// Logisim project 4位先行进位电路.circ as structural Verilog: 1 circuit, main circuit 4位先行进位电路
// CLA74182
module \_4位先行进位电路  (
  input  G4,
  input  P4,
  input  G3,
  input  P3,
  input  G2,
  input  P2,
  input  G1,
  input  P1,
  input  Cin,
  output C4,
  output C3,
  output C2,
  output C1,
  output G_star,
  output P_star
);

  wire and_2_out, and_3_out, and_4_out, and_5_out, and_6_out, and_7_out, and_8_out, and_9_out, and_10_out,
       and_11_out;

  and and_1 (P_star, P4, P3, P2, P1);
  or or_1 (G_star, G4, and_2_out, and_3_out, and_4_out);
  and and_2 (and_2_out, P4, G3);
  and and_3 (and_3_out, P4, P3, G2);
  or or_2 (C4, G4, and_2_out, and_3_out, and_4_out, and_5_out);
  and and_4 (and_4_out, P4, P3, P2, G1);
  and and_5 (and_5_out, P4, P3, P2, P1, Cin);
  or or_3 (C3, G3, and_6_out, and_7_out, and_8_out);
  and and_6 (and_6_out, P3, G2);
  and and_7 (and_7_out, P3, P2, G1);
  and and_8 (and_8_out, P3, P2, P1, Cin);
  or or_4 (C2, G2, and_9_out, and_10_out);
  and and_9 (and_9_out, P2, G1);
  and and_10 (and_10_out, P2, P1, Cin);
  or or_5 (C1, G1, and_11_out);
  and and_11 (and_11_out, P1, Cin);

  // Notes on the sheet:
  //   P1: pull=down
  //   G2: pull=down
  //   P3: pull=down
  //   P2: pull=down
  //   G3: pull=down
  //   G1: pull=down
  //   Cin: pull=down
  //   P4: pull=down
  //   G4: pull=down
  //   输入引脚区
  //   请根据以上引脚以及隧道信号设计完成74LS182先行进位电路，尽可能使用多输入逻辑门，并分析电路延迟
  //   4位先行进位电路
  //   输出引脚区
endmodule
