// Logisim project 4位快速加法器.circ as structural Verilog: 2 circuits, main circuit 4位先行进位电路
module \_4位先行进位电路  (
  input  G4,
  input  P4,
  input  G3,
  input  P3,
  input  G2,
  input  P2,
  input  G1,
  input  P1,
  input  Cin,
  output C4,
  output C3,
  output C2,
  output C1,
  output G_star,
  output P_star
);

  wire and_2_out, and_3_out, and_4_out, and_5_out, and_6_out, and_7_out, and_8_out, and_9_out, and_10_out,
       and_11_out;

  and and_1 (P_star, P4, P3, P2, P1);
  or or_1 (G_star, G4, and_3_out, and_2_out, and_4_out);
  and and_2 (and_2_out, P4, P3, G2);
  and and_3 (and_3_out, P4, G3);
  or or_2 (C4, G4, and_3_out, and_2_out, and_4_out, and_5_out);
  and and_4 (and_4_out, P4, P3, P2, G1);
  and and_5 (and_5_out, P4, P3, P2, P1, Cin);
  or or_3 (C3, G3, and_6_out, and_7_out, and_8_out);
  and and_6 (and_6_out, P3, G2);
  and and_7 (and_7_out, P3, P2, G1);
  and and_8 (and_8_out, P3, P2, P1, Cin);
  or or_4 (C2, G2, and_9_out, and_10_out);
  and and_9 (and_9_out, P2, G1);
  and and_10 (and_10_out, P2, P1, Cin);
  or or_5 (C1, G1, and_11_out);
  and and_11 (and_11_out, P1, Cin);

  // Notes on the sheet:
  //   G3: pull=down
  //   G1: pull=down
  //   P4: pull=down
  //   G4: pull=down
  //   P1: pull=down
  //   P3: pull=down
  //   Cin: pull=down
  //   P2: pull=down
  //   G2: pull=down
  //   输入引脚区
  //   请根据以上引脚以及隧道信号设计完成74LS182先行进位电路，尽可能使用多输入逻辑门，并分析电路延迟
  //   4位先行进位电路
  //   输出引脚区
endmodule

module \_4位快速加法器  (
  input  [3:0] X,
  input  [3:0] Y,
  input  C0,
  output [3:0] S,
  output C4,
  output C3,
  output G_star,
  output P_star
);

  wire and_1_out, and_2_out, and_3_out, and_4_out, \n4位先行进位电路_1_c1 , \n4位先行进位电路_1_c2 , xor_2_out, xor_3_out,
       xor_5_out, xor_8_out;

  \_4位先行进位电路  \u_4位先行进位电路_1  (
    .G4(and_1_out), .P4(xor_2_out), .G3(and_2_out), .P3(xor_3_out), .G2(and_3_out), .P2(xor_5_out),
    .G1(and_4_out), .P1(xor_8_out), .Cin(C0), .C4(C4), .C3(C3), .C2(\n4位先行进位电路_1_c2 ), .C1(\n4位先行进位电路_1_c1 ),
    .G_star(G_star), .P_star(P_star));
  and and_1 (and_1_out, X[3], Y[3]);
  xor xor_1 (S[3], C3, xor_2_out);
  xor xor_2 (xor_2_out, X[3], Y[3]);
  and and_2 (and_2_out, X[2], Y[2]);
  xor xor_3 (xor_3_out, X[2], Y[2]);
  xor xor_4 (S[2], \n4位先行进位电路_1_c2 , xor_3_out);
  and and_3 (and_3_out, X[1], Y[1]);
  xor xor_5 (xor_5_out, X[1], Y[1]);
  xor xor_6 (S[1], \n4位先行进位电路_1_c1 , xor_5_out);
  and and_4 (and_4_out, X[0], Y[0]);
  // Probe on X
  // Probe on Y
  // Probe on S
  xor xor_7 (S[0], xor_8_out, C0);
  xor xor_8 (xor_8_out, X[0], Y[0]);
  // Probe on X
  // Probe on Y
  // Probe on S

  // Notes on the sheet:
  //   C0: pull=down
  //   X: pull=down
  //   Y: pull=down
  //   输入引脚区
  //   输出引脚区
  //   功能说明:4位Adder  S=X+Y，C4、C3分别为最高位、次高位进位位，C0为进位输入， G* P*为成组进位生成传递函数
  //   4位快速加法器
  //   +
  //   =
  //   有符号加法
  //   +
  //   =
  //   无符号加法
endmodule
