// Logisim project 8位串行加法器.circ as structural Verilog: 4 circuits, main circuit 1位全加器（1）
module \_8位串行加法器_1  (
  input  [7:0] X,
  input  [7:0] Y,
  input  Cin,
  output [7:0] S,
  output Cout,
  output out_6
);

  wire \n1位全加器_1_2_cout , \n1位全加器_1_3_cout , \n1位全加器_1_4_cout , \n1位全加器_1_5_cout , \n1位全加器_1_6_cout ,
       \n1位全加器_1_7_cout , \n1位全加器_1_8_cout ;

  xor xor_1 (out_6, Cout, \n1位全加器_1_2_cout );
  \_1位全加器_1  \u_1位全加器_1_1  (.Cout(Cout), .Si(S[7]), .Cin(\n1位全加器_1_2_cout ), .Xi(X[7]), .Yi(Y[7]));
  \_1位全加器_1  \u_1位全加器_1_2  (.Cout(\n1位全加器_1_2_cout ), .Si(S[6]), .Cin(\n1位全加器_1_3_cout ), .Xi(X[6]), .Yi(Y[6]));
  \_1位全加器_1  \u_1位全加器_1_3  (.Cout(\n1位全加器_1_3_cout ), .Si(S[5]), .Cin(\n1位全加器_1_4_cout ), .Xi(X[5]), .Yi(Y[5]));
  \_1位全加器_1  \u_1位全加器_1_4  (.Cout(\n1位全加器_1_4_cout ), .Si(S[4]), .Cin(\n1位全加器_1_5_cout ), .Xi(X[4]), .Yi(Y[4]));
  \_1位全加器_1  \u_1位全加器_1_5  (.Cout(\n1位全加器_1_5_cout ), .Si(S[3]), .Cin(\n1位全加器_1_6_cout ), .Xi(X[3]), .Yi(Y[3]));
  \_1位全加器_1  \u_1位全加器_1_6  (.Cout(\n1位全加器_1_6_cout ), .Si(S[2]), .Cin(\n1位全加器_1_7_cout ), .Xi(X[2]), .Yi(Y[2]));
  // Probe on X
  // Probe on Y
  // Probe on S
  \_1位全加器_1  \u_1位全加器_1_7  (.Cout(\n1位全加器_1_7_cout ), .Si(S[1]), .Cin(\n1位全加器_1_8_cout ), .Xi(X[1]), .Yi(Y[1]));
  // Probe on X
  // Probe on Y
  // Probe on S
  \_1位全加器_1  \u_1位全加器_1_8  (.Cout(\n1位全加器_1_8_cout ), .Si(S[0]), .Cin(Cin), .Xi(X[0]), .Yi(Y[0]));

  // Other names for the same wires on the sheet: OF = out_6

  // Notes on the sheet:
  //   Y: pull=down
  //   Cin: pull=down
  //   X: pull=down
  //   输入引脚区
  //   符号位
  //   8位串行加法器（1）
  //   输出引脚区
  //   Overflow
  //   +
  //   有符号加法
  //   +
  //   =
  //   无符号加法
endmodule

module \_8位串行加法器_2  (
  input  [7:0] X,
  input  [7:0] Y,
  input  Cin,
  output [7:0] S,
  output Cout,
  output out_6
);

  wire \n1位全加器_2_2_cout , \n1位全加器_2_3_cout , \n1位全加器_2_4_cout , \n1位全加器_2_5_cout , \n1位全加器_2_6_cout ,
       \n1位全加器_2_7_cout , \n1位全加器_2_8_cout ;

  xor xor_1 (out_6, Cout, \n1位全加器_2_2_cout );
  \_1位全加器_2  \u_1位全加器_2_1  (.Cout(Cout), .Si(S[7]), .Cin(\n1位全加器_2_2_cout ), .Xi(X[7]), .Yi(Y[7]));
  \_1位全加器_2  \u_1位全加器_2_2  (.Cout(\n1位全加器_2_2_cout ), .Si(S[6]), .Cin(\n1位全加器_2_3_cout ), .Xi(X[6]), .Yi(Y[6]));
  \_1位全加器_2  \u_1位全加器_2_3  (.Cout(\n1位全加器_2_3_cout ), .Si(S[5]), .Cin(\n1位全加器_2_4_cout ), .Xi(X[5]), .Yi(Y[5]));
  \_1位全加器_2  \u_1位全加器_2_4  (.Cout(\n1位全加器_2_4_cout ), .Si(S[4]), .Cin(\n1位全加器_2_5_cout ), .Xi(X[4]), .Yi(Y[4]));
  \_1位全加器_2  \u_1位全加器_2_5  (.Cout(\n1位全加器_2_5_cout ), .Si(S[3]), .Cin(\n1位全加器_2_6_cout ), .Xi(X[3]), .Yi(Y[3]));
  \_1位全加器_2  \u_1位全加器_2_6  (.Cout(\n1位全加器_2_6_cout ), .Si(S[2]), .Cin(\n1位全加器_2_7_cout ), .Xi(X[2]), .Yi(Y[2]));
  \_1位全加器_2  \u_1位全加器_2_7  (.Cout(\n1位全加器_2_7_cout ), .Si(S[1]), .Cin(\n1位全加器_2_8_cout ), .Xi(X[1]), .Yi(Y[1]));
  // Probe on X
  // Probe on Y
  // Probe on S
  \_1位全加器_2  \u_1位全加器_2_8  (.Cout(\n1位全加器_2_8_cout ), .Si(S[0]), .Cin(Cin), .Xi(X[0]), .Yi(Y[0]));
  // Probe on X
  // Probe on Y
  // Probe on S

  // Other names for the same wires on the sheet: OF = out_6

  // Notes on the sheet:
  //   X: pull=down
  //   Y: pull=down
  //   Cin: pull=down
  //   输入引脚区
  //   符号位
  //   8位串行加法器（2）
  //   输出引脚区
  //   Overflow
  //   +
  //   有符号加法
  //   +
  //   =
  //   无符号加法
endmodule

// FA1
module \_1位全加器_1  (
  input  Cin,
  input  Xi,
  input  Yi,
  output Cout,
  output Si
);

  wire AND_2_out, AND_out, XOR_2_out;

  or OR (Cout, AND_out, AND_2_out);
  and AND (AND_out, Xi, Yi);
  and AND_2 (AND_2_out, Cin, XOR_2_out);
  xor XOR (Si, Cin, XOR_2_out);
  xor XOR_2 (XOR_2_out, Xi, Yi);

  // Notes on the sheet:
  //   Cin: pull=down
  //   Xi: pull=down
  //   Yi: pull=down
  //   Si = Xi ^ Yi ^ Cin
  //   Cout = Xi Yi + Cin (Xi ^ Yi)
  //   1位全加器（1）（FA）
endmodule

// FA2
module \_1位全加器_2  (
  input  Cin,
  input  Xi,
  input  Yi,
  output Cout,
  output Si
);

  wire AND_2_out, AND_3_out, AND_out, XOR_2_out;

  and AND (AND_out, Cin, Xi);
  or OR (Cout, AND_out, AND_2_out, AND_3_out);
  and AND_2 (AND_2_out, Cin, Yi);
  and AND_3 (AND_3_out, Xi, Yi);
  xor XOR (Si, Cin, XOR_2_out);
  xor XOR_2 (XOR_2_out, Xi, Yi);

  // Notes on the sheet:
  //   Cin: pull=down
  //   Yi: pull=down
  //   Xi: pull=down
  //   Cout = Xi Yi + Cin (Xi +Yi)
  //   Si = Xi ^ Yi ^ Cin
  //   1位全加器（2）（FA）
endmodule
