// Logisim project 8位无符号一位乘法器.circ as structural Verilog: 3 circuits, main circuit 8位无符号一位乘法器
module \_8位无符号一位乘法器  (
  input  [7:0] X,
  input  [7:0] Y,
  output [15:0] \乘积 
);

  wire comparator_1_eq, d_ff_1_q, not_1_out, RST, \时钟_out ;
  wire [0:0] \n8位串行加法器_1_s ;
  wire [3:0] counter_1_q;
  wire [7:0] multiplexer_1_out, multiplexer_2_out, \n8位串行加法器_1_cout ;

  // Probe on X
  Clock #(.highDuration(1), .lowDuration(1)) \u_时钟  (.out(\时钟_out ));
  // Probe on Y
  // Probe on \乘积 [15:8]
  Register #(.width(8), .trigger("rising"), .Select("low")) register_1 (
    .D(\n8位串行加法器_1_cout ), .en(not_1_out), .Q(\乘积 [15:8]), .clk(\时钟_out ), .clr(RST));
  \_8位串行加法器  \u_8位串行加法器_1  (
    .X(\乘积 [15:8]), .Y(multiplexer_1_out), .Cin(1'b0), .S({\n8位串行加法器_1_cout [6:0], \n8位串行加法器_1_s [0]}),
    .Cout(\n8位串行加法器_1_cout [7]));  // open: out_6
  Multiplexer #(.select(1), .width(8), .disabled("Z"), .enable("false")) multiplexer_1 (
    .in0({8{1'b0}}), .in1(X), .out(multiplexer_1_out), .sel(\乘积 [0]));
  Button \u_复位  (.out(RST));
  Multiplexer #(.select(1), .width(8), .disabled("Z"), .enable("false")) multiplexer_2 (
    .in0(Y), .in1({\n8位串行加法器_1_s [0], \乘积 [7:1]}), .out(multiplexer_2_out), .sel(d_ff_1_q));
  // Probe on \乘积 [7:0]
  Register #(.width(8), .trigger("rising"), .Select("low")) Y_2 (
    .D(multiplexer_2_out), .en(not_1_out), .Q(\乘积 [7:0]), .clk(\时钟_out ), .clr(RST));
  Counter #(.width(4), .max('hf), .ongoal("wrap"), .trigger("rising"), .behavior("old")) counter_1 (
    .count(not_1_out), .Q(counter_1_q), .clk(\时钟_out ), .clr(RST));  // open: load, D, carry, preset
  D_Flip_Flop #(.trigger("rising"), .Pre_Clr_Positions("LEGACY"), .NegatePresetClear("false"), .enable("true"), .NewFFLayout("false")) d_ff_1 (
    .clk(\时钟_out ), .D(1'b1), .Q(d_ff_1_q), .reset(RST));  // open: Qn, preset, en
  // Probe on \乘积 
  not not_1 (not_1_out, comparator_1_eq);
  Comparator #(.width(4), .mode("unsigned")) comparator_1 (
    .a(counter_1_q), .b(4'b1001), .eq(comparator_1_eq));  // open: gt, lt
  // Probe on X
  // Probe on Y
  // Probe on \乘积 

  // Notes on the sheet:
  //   ∑
  //   输入输出引脚区
  //   功能说明: 8位无符号一位乘法器                输入：X、Y为8位无符号数               输出：乘积=X*Y，为16位无符号数
  //   8位无符号数一位乘法器
  //   ×
  //   =
endmodule

// FA
module \_1位全加器FA  (
  input  Cin,
  input  Xi,
  input  Yi,
  output Cout,
  output Si
);

  wire AND_2_out, AND_out, XOR_2_out;

  or OR (Cout, AND_out, AND_2_out);
  and AND (AND_out, Xi, Yi);
  and AND_2 (AND_2_out, Cin, XOR_2_out);
  xor XOR (Si, Cin, XOR_2_out);
  xor XOR_2 (XOR_2_out, Xi, Yi);

  // Notes on the sheet:
  //   Yi: pull=down
  //   Cin: pull=down
  //   Xi: pull=down
  //   1位全加器（FA）
  //   Si = Xi ^ Yi ^ Cin
  //   Cout = Xi Yi + Cin (Xi ^ Yi)
endmodule

module \_8位串行加法器  (
  input  [7:0] X,
  input  [7:0] Y,
  input  Cin,
  output [7:0] S,
  output Cout,
  output out_6
);

  wire \n1位全加器fa_2_cout , \n1位全加器fa_3_cout , \n1位全加器fa_4_cout , \n1位全加器fa_5_cout , \n1位全加器fa_6_cout ,
       \n1位全加器fa_7_cout , \n1位全加器fa_8_cout ;

  xor xor_1 (out_6, Cout, \n1位全加器fa_2_cout );
  \_1位全加器FA  \u_1位全加器fa_1  (.Cout(Cout), .Si(S[7]), .Cin(\n1位全加器fa_2_cout ), .Xi(X[7]), .Yi(Y[7]));
  \_1位全加器FA  \u_1位全加器fa_2  (.Cout(\n1位全加器fa_2_cout ), .Si(S[6]), .Cin(\n1位全加器fa_3_cout ), .Xi(X[6]), .Yi(Y[6]));
  \_1位全加器FA  \u_1位全加器fa_3  (.Cout(\n1位全加器fa_3_cout ), .Si(S[5]), .Cin(\n1位全加器fa_4_cout ), .Xi(X[5]), .Yi(Y[5]));
  \_1位全加器FA  \u_1位全加器fa_4  (.Cout(\n1位全加器fa_4_cout ), .Si(S[4]), .Cin(\n1位全加器fa_5_cout ), .Xi(X[4]), .Yi(Y[4]));
  \_1位全加器FA  \u_1位全加器fa_5  (.Cout(\n1位全加器fa_5_cout ), .Si(S[3]), .Cin(\n1位全加器fa_6_cout ), .Xi(X[3]), .Yi(Y[3]));
  \_1位全加器FA  \u_1位全加器fa_6  (.Cout(\n1位全加器fa_6_cout ), .Si(S[2]), .Cin(\n1位全加器fa_7_cout ), .Xi(X[2]), .Yi(Y[2]));
  // Probe on X
  // Probe on Y
  // Probe on S
  \_1位全加器FA  \u_1位全加器fa_7  (.Cout(\n1位全加器fa_7_cout ), .Si(S[1]), .Cin(\n1位全加器fa_8_cout ), .Xi(X[1]), .Yi(Y[1]));
  // Probe on X
  // Probe on Y
  // Probe on S
  \_1位全加器FA  \u_1位全加器fa_8  (.Cout(\n1位全加器fa_8_cout ), .Si(S[0]), .Cin(Cin), .Xi(X[0]), .Yi(Y[0]));

  // Other names for the same wires on the sheet: OF = out_6

  // Notes on the sheet:
  //   Y: pull=down
  //   X: pull=down
  //   Cin: pull=down
  //   输入引脚区
  //   符号位
  //   8位串行加法器
  //   输出引脚区
  //   Overflow
  //   +
  //   有符号加法
  //   +
  //   =
  //   无符号加法
endmodule
