// Logisim project 8位补码一位乘法器.circ as structural Verilog: 3 circuits, main circuit 1位全加器FA
module \_8位补码一位乘法器  (
  input  [7:0] X,
  input  [7:0] Y,
  output [15:0] \乘积 
);

  wire and_1_out, clock_1_out, comparator_1_eq, d_ff_1_q, not_2_out, RST, XYZ, XZ, YZ;
  wire [0:0] \n8位串行加法器_1_s_2 ;
  wire [1:0] PS;
  wire [1:1] Yn_1_2_q;
  wire [3:0] counter_1_q;
  wire [7:0] multiplexer_1_out, multiplexer_2_out, \n8位串行加法器_1_s , not_1_out;
  wire [14:0] PX_star, PY_star;
  wire [15:0] multiplexer_3_out, \乘积_star ;
  wire [15:15] negator_1_out, negator_2_out, PX;

  // Probe on X
  Clock #(.highDuration(1), .lowDuration(1)) clock_1 (.out(clock_1_out));
  // Probe on Y
  Register #(.width(8), .trigger("rising"), .Select("low")) register (
    .D({{2{\n8位串行加法器_1_s [7]}}, \n8位串行加法器_1_s [5:0]}), .en(not_2_out), .Q(\乘积_star [15:8]),
    .clk(clock_1_out), .clr(RST));
  Button \u_复位  (.out(RST));
  // Probe on \乘积_star [15:8]
  Multiplexer #(.select(1), .width(8), .disabled("Z"), .enable("false")) multiplexer_1 (
    .in0(Y), .in1({\n8位串行加法器_1_s_2 [0], \乘积_star [7:1]}), .out(multiplexer_1_out), .sel(d_ff_1_q));
  \_8位串行加法器  \u_8位串行加法器_1  (
    .X(\乘积_star [15:8]), .Y(multiplexer_2_out), .Cin(and_1_out),
    .S({\n8位串行加法器_1_s [7], \n8位串行加法器_1_s [5:0], \n8位串行加法器_1_s_2 [0]}));  // open: Cout, out_6
  Multiplexer #(.select(2), .width(8), .disabled("Z"), .enable("false")) multiplexer_2 (
    .in0({8{1'b0}}), .in1(not_1_out), .in2(X), .in3({8{1'b0}}), .out(multiplexer_2_out),
    .sel({Yn_1_2_q[1], \乘积_star [0]}));
  assign not_1_out = ~X;  // NOT_Gate not_1, 8 bits wide
  // Probe on \乘积_star [7:0]
  Register #(.width(8), .trigger("rising"), .Select("low")) Y_2 (
    .D(multiplexer_1_out), .en(not_2_out), .Q(\乘积_star [7:0]), .clk(clock_1_out), .clr(RST));
  and and_1 (and_1_out, ~Yn_1_2_q[1], \乘积_star [0]);  // AND_Gate
  Counter #(.width(4), .max('hf), .ongoal("wrap"), .trigger("rising"), .behavior("old")) counter_1 (
    .count(not_2_out), .Q(counter_1_q), .clk(clock_1_out), .clr(RST));  // open: load, D, carry, preset
  // Probe on \乘积 
  // Probe on Yn_1_2_q[1]
  Register #(.width(1), .trigger("rising"), .Select("low")) Yn_1_2 (
    .D(\乘积_star [0]), .en(not_2_out), .Q(Yn_1_2_q[1]), .clk(clock_1_out), .clr(RST));
  Comparator #(.width(4), .mode("unsigned")) comparator_1 (
    .a(counter_1_q), .b(4'b1001), .eq(comparator_1_eq));  // open: gt, lt
  D_Flip_Flop #(.trigger("rising"), .Pre_Clr_Positions("LEGACY"), .NegatePresetClear("false"), .enable("true"), .NewFFLayout("false")) d_ff_1 (
    .clk(clock_1_out), .D(1'b1), .Q(d_ff_1_q), .reset(RST));  // open: Qn, preset, en
  not not_2 (not_2_out, comparator_1_eq);
  xor xor_1 (PX[15], X[7], Y[7]);
  Comparator #(.width(8), .mode("twosComplement")) comparator_2 (.a(X), .b(8'h80), .eq(PS[0]));  // open: gt, lt
  Comparator #(.width(8), .mode("twosComplement")) comparator_3 (.a(Y), .b(8'h80), .eq(PS[1]));  // open: gt, lt
  or or_1 (XZ, X[0], X[1], X[2], X[3], X[4], X[5], X[6], X[7]);
  Multiplexer #(.select(2), .width(16), .disabled("Z"), .enable("false")) multiplexer_3 (
    .in0(\乘积_star ), .in1({PX[15], PY_star}), .in2({PX[15], PX_star}), .in3(16'h4000),
    .out(multiplexer_3_out), .sel(PS));
  // Probe on X
  // Probe on Y
  // Probe on \乘积 
  or or_2 (YZ, Y[0], Y[1], Y[2], Y[3], Y[4], Y[5], Y[6], Y[7]);
  xor xor_2 (XYZ, XZ, YZ);
  Negator #(.width(16)) negator_1 (.in({PX[15], X, {7{1'b0}}}), .out({negator_1_out[15], PX_star}));
  Negator #(.width(16)) negator_2 (.in({PX[15], Y, {7{1'b0}}}), .out({negator_2_out[15], PY_star}));
  Multiplexer #(.select(1), .width(16), .disabled("Z"), .enable("false")) multiplexer_4 (
    .in0(multiplexer_3_out), .in1({16{1'b0}}), .out(\乘积 ), .sel(XYZ));

  // Other names for the same wires on the sheet: PX[14:7] = X; SX = X[7]; PY[15:7] = {PX[15], Y}; SY = Y[7];
  //   PX_star[15] = PX[15]; PY_star[15] = PX[15]; SP = PX[15]

  // Notes on the sheet:
  //   8位补码一位乘法器
  //   输入输出引脚区
  //   功能说明: 8位补码一位乘法器                输入：X、Y，8位补码             输出：乘积=X×Y，16位补码
  //   ×
  //   =
endmodule

// FA
module \_1位全加器FA  (
  input  Cin,
  input  Xi,
  input  Yi,
  output Cout,
  output Si
);

  wire AND_2_out, AND_out, XOR_2_out;

  or OR (Cout, AND_out, AND_2_out);
  and AND (AND_out, Xi, Yi);
  and AND_2 (AND_2_out, Cin, XOR_2_out);
  xor XOR (Si, Cin, XOR_2_out);
  xor XOR_2 (XOR_2_out, Xi, Yi);

  // Notes on the sheet:
  //   Yi: pull=down
  //   Xi: pull=down
  //   Cin: pull=down
  //   1位全加器（FA）
  //   Si = Xi ^ Yi ^ Cin
  //   Cout = Xi Yi + Cin (Xi ^ Yi)
endmodule

module \_8位串行加法器  (
  input  [7:0] X,
  input  [7:0] Y,
  input  Cin,
  output [7:0] S,
  output Cout,
  output out_6
);

  wire \n1位全加器fa_2_cout , \n1位全加器fa_3_cout , \n1位全加器fa_4_cout , \n1位全加器fa_5_cout , \n1位全加器fa_6_cout ,
       \n1位全加器fa_7_cout , \n1位全加器fa_8_cout ;

  xor xor_1 (out_6, Cout, \n1位全加器fa_2_cout );
  \_1位全加器FA  \u_1位全加器fa_1  (.Cout(Cout), .Si(S[7]), .Cin(\n1位全加器fa_2_cout ), .Xi(X[7]), .Yi(Y[7]));
  \_1位全加器FA  \u_1位全加器fa_2  (.Cout(\n1位全加器fa_2_cout ), .Si(S[6]), .Cin(\n1位全加器fa_3_cout ), .Xi(X[6]), .Yi(Y[6]));
  \_1位全加器FA  \u_1位全加器fa_3  (.Cout(\n1位全加器fa_3_cout ), .Si(S[5]), .Cin(\n1位全加器fa_4_cout ), .Xi(X[5]), .Yi(Y[5]));
  \_1位全加器FA  \u_1位全加器fa_4  (.Cout(\n1位全加器fa_4_cout ), .Si(S[4]), .Cin(\n1位全加器fa_5_cout ), .Xi(X[4]), .Yi(Y[4]));
  \_1位全加器FA  \u_1位全加器fa_5  (.Cout(\n1位全加器fa_5_cout ), .Si(S[3]), .Cin(\n1位全加器fa_6_cout ), .Xi(X[3]), .Yi(Y[3]));
  \_1位全加器FA  \u_1位全加器fa_6  (.Cout(\n1位全加器fa_6_cout ), .Si(S[2]), .Cin(\n1位全加器fa_7_cout ), .Xi(X[2]), .Yi(Y[2]));
  // Probe on X
  // Probe on Y
  // Probe on S
  \_1位全加器FA  \u_1位全加器fa_7  (.Cout(\n1位全加器fa_7_cout ), .Si(S[1]), .Cin(\n1位全加器fa_8_cout ), .Xi(X[1]), .Yi(Y[1]));
  // Probe on X
  // Probe on Y
  // Probe on S
  \_1位全加器FA  \u_1位全加器fa_8  (.Cout(\n1位全加器fa_8_cout ), .Si(S[0]), .Cin(Cin), .Xi(X[0]), .Yi(Y[0]));

  // Other names for the same wires on the sheet: OF = out_6

  // Notes on the sheet:
  //   X: pull=down
  //   Cin: pull=down
  //   Y: pull=down
  //   输入引脚区
  //   符号位
  //   8位串行加法器
  //   输出引脚区
  //   Overflow
  //   +
  //   有符号加法
  //   +
  //   =
  //   无符号加法
endmodule
