// Logisim project 桶型移位器.circ as structural Verilog: 1 circuit, main circuit 桶形移位器
module \桶形移位器  (
  input  [31:0] X,
  input  [4:0] Y,
  output [31:0] Z
);

  wire [31:0] multiplexer_1_out, multiplexer_2_out, multiplexer_3_out, multiplexer_4_out, shifter_1_out,
       shifter_2_out, shifter_3_out, shifter_4_out, shifter_5_out;

  Shifter #(.width(32), .shift("ll")) shifter_1 (.in(X), .\dist (5'b00001), .out(shifter_1_out));
  Multiplexer #(.select(1), .width(32), .disabled("Z"), .enable("false")) multiplexer_1 (
    .in0(X), .in1(shifter_1_out), .out(multiplexer_1_out), .sel(Y[0]));
  Multiplexer #(.select(1), .width(32), .disabled("Z"), .enable("false")) multiplexer_2 (
    .in0(multiplexer_1_out), .in1(shifter_2_out), .out(multiplexer_2_out), .sel(Y[1]));
  Shifter #(.width(32), .shift("ll")) shifter_2 (.in(multiplexer_1_out), .\dist (5'b00010), .out(shifter_2_out));
  Shifter #(.width(32), .shift("ll")) shifter_3 (.in(multiplexer_2_out), .\dist (5'b00100), .out(shifter_3_out));
  Multiplexer #(.select(1), .width(32), .disabled("Z"), .enable("false")) multiplexer_3 (
    .in0(multiplexer_2_out), .in1(shifter_3_out), .out(multiplexer_3_out), .sel(Y[2]));
  Shifter #(.width(32), .shift("ll")) shifter_4 (.in(multiplexer_3_out), .\dist (5'b01000), .out(shifter_4_out));
  Multiplexer #(.select(1), .width(32), .disabled("Z"), .enable("false")) multiplexer_4 (
    .in0(multiplexer_3_out), .in1(shifter_4_out), .out(multiplexer_4_out), .sel(Y[3]));
  Shifter #(.width(32), .shift("ll")) shifter_5 (.in(multiplexer_4_out), .\dist (5'b10000), .out(shifter_5_out));
  Multiplexer #(.select(1), .width(32), .disabled("Z"), .enable("false")) multiplexer_5 (
    .in0(multiplexer_4_out), .in1(shifter_5_out), .out(Z), .sel(Y[4]));

  // Notes on the sheet:
  //   输入：X(32位)，Y(5位)                     输出：Z(32位)=X<<Y
  //   桶型移位器
endmodule
