// Logisim project 13位随机干扰电路.circ as structural Verilog: 1 circuit, main circuit 随机干扰电路
// 随机干扰
module \随机干扰电路  (
  input  CLK,
  input  [12:0] \_13位输入 ,
  output [12:0] \随机加扰屏蔽字 ,
  output [12:0] \加扰后数据 
);

  wire comparator_1_eq, not_1_out, pull_resistor_1_node, \随机信号_5_out ;
  wire [1:0] pull_resistor_2_node, \随机信号_4_out ;
  wire [3:0] \随机信号_2_out , \随机信号_3_out , \随机信号_out ;
  wire [15:0] \_1位加扰A , decoder_3_out0;
  wire [21:0] \_1位加扰 , \_2位加扰 , \_3位加扰 , multiplexer_1_out, multiplexer_2_out, multiplexer_4_out;
  wire [21:6] \_1位加扰B ;
  wire [21:13] multiplexer_3_out;

  Random #(.width(4), .seed(0), .trigger("rising")) \u_随机信号  (.clk(CLK), .out(\随机信号_out ));  // open: next, clr
  Decoder #(.select(4), .tristate("false"), .disabled("Z"), .enable("false")) decoder_1 (
    .out0(\_1位加扰A [0]), .out1(\_1位加扰A [1]), .out2(\_1位加扰A [2]), .out3(\_1位加扰A [3]), .out4(\_1位加扰A [4]),
    .out5(\_1位加扰A [5]), .out6(\_1位加扰A [6]), .out7(\_1位加扰A [7]), .out8(\_1位加扰A [8]), .out9(\_1位加扰A [9]),
    .out10(\_1位加扰A [10]), .out11(\_1位加扰A [11]), .out12(\_1位加扰A [12]), .out13(\_1位加扰A [13]),
    .out14(\_1位加扰A [14]), .out15(\_1位加扰A [15]), .sel(\随机信号_out ));
  Random #(.width(4), .seed(18), .trigger("rising")) \u_随机信号_2  (.clk(CLK), .out(\随机信号_2_out ));  // open: next, clr
  Decoder #(.select(4), .tristate("false"), .disabled("Z"), .enable("false")) decoder_2 (
    .out0(\_1位加扰B [6]), .out1(\_1位加扰B [7]), .out2(\_1位加扰B [8]), .out3(\_1位加扰B [9]), .out4(\_1位加扰B [10]),
    .out5(\_1位加扰B [11]), .out6(\_1位加扰B [12]), .out7(\_1位加扰B [13]), .out8(\_1位加扰B [14]), .out9(\_1位加扰B [15]),
    .out10(\_1位加扰B [16]), .out11(\_1位加扰B [17]), .out12(\_1位加扰B [18]), .out13(\_1位加扰B [19]),
    .out14(\_1位加扰B [20]), .out15(\_1位加扰B [21]), .sel(\随机信号_2_out ));
  Decoder #(.select(4), .tristate("false"), .disabled("Z"), .enable("false")) decoder_3 (
    .out0(decoder_3_out0[0]), .out1(decoder_3_out0[1]), .out2(decoder_3_out0[2]), .out3(decoder_3_out0[3]),
    .out4(decoder_3_out0[4]), .out5(decoder_3_out0[5]), .out6(decoder_3_out0[6]), .out7(decoder_3_out0[7]),
    .out8(decoder_3_out0[8]), .out9(decoder_3_out0[9]), .out10(decoder_3_out0[10]),
    .out11(decoder_3_out0[11]), .out12(decoder_3_out0[12]), .out13(decoder_3_out0[13]),
    .out14(decoder_3_out0[14]), .out15(decoder_3_out0[15]), .sel(\随机信号_3_out ));
  Random #(.width(4), .seed(3), .trigger("rising")) \u_随机信号_3  (.clk(CLK), .out(\随机信号_3_out ));  // open: next, clr
  Random #(.width(2), .seed(21), .trigger("rising")) \u_随机信号_4  (.clk(CLK), .out(\随机信号_4_out ));  // open: next, clr
  Random #(.width(1), .seed(31), .trigger("rising")) \u_随机信号_5  (.clk(CLK), .out(\随机信号_5_out ));  // open: next, clr
  Pull_Resistor #(.pull(0)) pull_resistor_1 (.node(pull_resistor_1_node));
  Multiplexer #(.select(1), .width(22), .disabled("Z"), .enable("false")) multiplexer_1 (
    .in0({\_1位加扰B , {6{1'b0}}}), .in1(\_3位加扰 ), .out(multiplexer_1_out), .sel(pull_resistor_1_node));
  Pull_Resistor #(.pull(1)) pull_resistor_2 (.node(pull_resistor_2_node));
  Multiplexer #(.select(2), .width(22), .disabled("Z"), .enable("false")) multiplexer_2 (
    .in0({22{1'b0}}), .in1({{6{1'b0}}, \_1位加扰A }), .in2(\_2位加扰 ), .in3(multiplexer_1_out),
    .out(multiplexer_2_out), .sel(\随机信号_4_out ));
  Multiplexer #(.select(2), .width(22), .disabled("Z"), .enable("false")) multiplexer_3 (
    .in0({22{1'b0}}), .in1(\_1位加扰 ), .in2(\_2位加扰 ), .in3(multiplexer_2_out),
    .out({multiplexer_3_out, \随机加扰屏蔽字 }), .sel(pull_resistor_2_node));
  Comparator #(.width(22), .mode("unsigned")) comparator_1 (
    .a({{6{1'b0}}, \_1位加扰A }), .b({\_1位加扰B , {6{1'b0}}}), .eq(comparator_1_eq));  // open: gt, lt
  not not_1 (not_1_out, comparator_1_eq);
  Multiplexer #(.select(1), .width(22), .disabled("Z"), .enable("false")) multiplexer_4 (
    .in0(22'h1), .in1({{6{1'b0}}, \_1位加扰A }), .out(multiplexer_4_out), .sel(not_1_out));
  assign \_2位加扰  = multiplexer_4_out ^ {\_1位加扰B , {6{1'b0}}};  // XOR_Gate xor_1, 22 bits wide
  assign \_3位加扰  = \_2位加扰  ^ {decoder_3_out0, {6{1'b0}}};  // XOR_Gate xor_2, 22 bits wide
  Multiplexer #(.select(1), .width(22), .disabled("Z"), .enable("false")) multiplexer_5 (
    .in0(multiplexer_4_out), .in1({\_1位加扰B , {6{1'b0}}}), .out(\_1位加扰 ), .sel(\随机信号_5_out ));
  assign \加扰后数据  = \随机加扰屏蔽字  ^ \_13位输入 ;  // XOR_Gate xor_3, 13 bits wide
  // also tied to GND on the sheet: pull_resistor_1_node
  // also tied to VCC on the sheet: {pull_resistor_2_node[0], pull_resistor_2_node[1]}

  // Notes on the sheet:
  //   随机干扰电路
endmodule
