// Logisim project 循环冗余校验码（串行）实验1.circ as structural Verilog: 5 circuits, main circuit CRC串行编解码测试实验1
module \CRC串行编解码测试实验1  (
  input  [2:0] \原始数据 ,
  input  [6:0] \干扰项 ,
  output [2:0] \接收数据 
);

  wire comparator_1_eq, \crc串行编码电路1_封装用_1_out_7 , \crc串行解码电路1_封装用_1_out_8 , \复位1_out , \复位2_out , \时钟1_out ,
       \时钟2_out , \装入1_out , \装入2_out ;
  wire [3:0] \crc串行编码电路1_封装用_1_余数 , \crc串行解码电路1_封装用_1_余数 ;
  wire [6:0] \crc串行编码电路1_封装用_1_crc码 , \crc串行解码电路1_封装用_1_纠正后的crc码 , xor_1_out;

  // Probe on \crc串行编码电路1_封装用_1_余数 
  Button \u_复位1  (.out(\复位1_out ));
  LED #(.active("true")) \u_余数生成1  (.in(\crc串行编码电路1_封装用_1_out_7 ));
  \CRC串行编码电路1_封装用  \crc串行编码电路1_封装用_1  (
    .\原始数据 (\原始数据 ), .\复位 (\复位1_out ), .\装入 (\装入1_out ), .\时钟 (\时钟1_out ), .\余数 (\crc串行编码电路1_封装用_1_余数 ),
    .\CRC码 (\crc串行编码电路1_封装用_1_crc码 ), .out_7(\crc串行编码电路1_封装用_1_out_7 ));
  Button \u_装入1  (.out(\装入1_out ));
  Button \u_时钟1  (.out(\时钟1_out ));
  // Probe on \crc串行编码电路1_封装用_1_crc码 
  assign xor_1_out = \crc串行编码电路1_封装用_1_crc码  ^ \干扰项 ;  // XOR_Gate xor_1, 7 bits wide
  // Probe on xor_1_out
  // Probe on \crc串行解码电路1_封装用_1_余数 
  LED #(.active("true")) \u_余数生成2  (.in(\crc串行解码电路1_封装用_1_out_8 ));
  \CRC串行解码电路1_封装用  \crc串行解码电路1_封装用_1  (
    .\CRC码 (xor_1_out), .\复位 (\复位2_out ), .\装入 (\装入2_out ), .\时钟 (\时钟2_out ), .\余数 (\crc串行解码电路1_封装用_1_余数 ),
    .\纠正后的CRC码 (\crc串行解码电路1_封装用_1_纠正后的crc码 ), .\纠正后的数据 (\接收数据 ), .out_8(\crc串行解码电路1_封装用_1_out_8 ));
  Button \u_复位2  (.out(\复位2_out ));
  Button \u_装入2  (.out(\装入2_out ));
  Button \u_时钟2  (.out(\时钟2_out ));
  // Probe on \crc串行解码电路1_封装用_1_纠正后的crc码 
  Comparator #(.width(3), .mode("twosComplement")) comparator_1 (
    .a(\原始数据 ), .b(\接收数据 ), .eq(comparator_1_eq));  // open: gt, lt
  LED #(.active("true")) \u_数据正确  (.in(comparator_1_eq));

  // Notes on the sheet:
  //   第二步：设置干扰项（只设置1个1）
  //   第五步：重复第二步（设置2个1）、第三步，此时“数据正确”指示灯不亮（接收数据不等于原始数据，无法纠正2位错）
  //   第一步：首先设置3位原始数据，然后按“复位1”按钮，再按“装入1”按钮，再按“时钟1”按钮多次，直到“余数生成1”指示灯变红色
  //   第三步：按“复位2”按钮，再按“装入2”按钮，再按“时钟2”按钮多次，直到“余数生成2”指示灯变红色；此时“数据正确”指示灯应为红色（可以纠正1位错）
  //   电路功能：测试CRC串行编解码电路的功能                       输入：3位原始数据、7位干扰项                      输出：3位接收数据（纠错后的数据）、数据正确指示灯
  //   第四步：重复第二步（设置另外位置的1，仍然为1个1）、第三步，直到干扰项的7个位置都测试过，7种情况下“数据正确”指示灯都是红色（可以纠正1位错）
  //   CRC串行编解码测试实验1
endmodule

module \CRC串行编码电路1  (
  input  [2:0] \原始数据 ,
  output [3:0] \余数 ,
  output [6:0] \CRC码 ,
  output out_4
);

  wire and_1_out, comparator_2_eq, \D触发器_2_q , \D触发器_3_q , \D触发器_4_q , multiplexer_1_out, multiplexer_2_out,
       not_1_out, not_2_out, or_1_out, R0, R1, R2, R3, shift_register_1_out, \复位_out , \时钟_out , \装入_out ,
       \计数器_2_q ;
  wire [2:0] \计数器_q ;

  Button \u_复位  (.out(\复位_out ));
  Button \u_装入  (.out(\装入_out ));
  Button \u_时钟  (.out(\时钟_out ));
  and and_1 (and_1_out, \装入_out , multiplexer_2_out);
  LED #(.active("true")) \u_余数生成指示灯  (.in(out_4));
  or or_1 (or_1_out, and_1_out, \时钟_out );
  Shift_Register #(.width(1), .length(3), .parallel("true"), .trigger("rising")) shift_register_1 (
    .in(1'b0), .clk(or_1_out), .out(shift_register_1_out), .load(multiplexer_2_out), .clr(\复位_out ),
    .d0(\原始数据 [0]), .d1(\原始数据 [1]), .d2(\原始数据 [2]));  // open: shift, q0, q1, q2
  Counter #(.width(3), .max('h7), .ongoal("wrap"), .trigger("rising"), .behavior("old")) \u_计数器  (
    .count(multiplexer_1_out), .Q(\计数器_q ), .clk(or_1_out), .clr(multiplexer_2_out));  // open: load, D, carry, preset
  xor xor_1 (R0, \D触发器_4_q , shift_register_1_out);
  Comparator #(.width(3), .mode("unsigned")) comparator_1 (.a(\计数器_q ), .b(3'b110), .eq(out_4));  // open: gt, lt
  not not_1 (not_1_out, out_4);
  Counter #(.width(1), .max('h1), .ongoal("wrap"), .trigger("rising"), .behavior("old")) \u_计数器_2  (
    .count(multiplexer_2_out), .Q(\计数器_2_q ), .clk(and_1_out), .clr(\复位_out ));  // open: load, D, carry, preset
  assign \余数  = {4{out_4}} & {R3, R2, R1, R0};  // AND_Gate and_2, 4 bits wide
  D_Flip_Flop #(.trigger("rising"), .Pre_Clr_Positions("LEGACY"), .NegatePresetClear("false"), .enable("true"), .NewFFLayout("false")) \D触发器  (
    .clk(or_1_out), .D(R0), .Q(R1), .en(multiplexer_1_out), .reset(\复位_out ));  // open: Qn, preset
  Multiplexer #(.select(1), .width(1), .disabled("Z"), .enable("false")) multiplexer_1 (
    .in0(1'b1), .in1(not_1_out), .out(multiplexer_1_out), .sel(1'b1));
  Comparator #(.width(1), .mode("unsigned")) comparator_2 (
    .a(\计数器_2_q ), .b(1'b1), .eq(comparator_2_eq));  // open: gt, lt
  Multiplexer #(.select(1), .width(1), .disabled("Z"), .enable("false")) multiplexer_2 (
    .in0(1'b1), .in1(not_2_out), .out(multiplexer_2_out), .sel(1'b1));
  not not_2 (not_2_out, comparator_2_eq);
  D_Flip_Flop #(.trigger("rising"), .Pre_Clr_Positions("LEGACY"), .NegatePresetClear("false"), .enable("true"), .NewFFLayout("false")) \D触发器_2  (
    .clk(or_1_out), .D(R1), .Q(\D触发器_2_q ), .en(multiplexer_1_out), .reset(\复位_out ));  // open: Qn, preset
  xor xor_2 (R2, \D触发器_4_q , \D触发器_2_q );
  D_Flip_Flop #(.trigger("rising"), .Pre_Clr_Positions("LEGACY"), .NegatePresetClear("false"), .enable("true"), .NewFFLayout("false")) \D触发器_3  (
    .clk(or_1_out), .D(R2), .Q(\D触发器_3_q ), .en(multiplexer_1_out), .reset(\复位_out ));  // open: Qn, preset
  assign \CRC码  = {\原始数据 , R3, R2, R1, R0} & {7{out_4}};  // AND_Gate and_3, 7 bits wide
  xor xor_3 (R3, \D触发器_4_q , \D触发器_3_q );
  D_Flip_Flop #(.trigger("rising"), .Pre_Clr_Positions("LEGACY"), .NegatePresetClear("false"), .enable("true"), .NewFFLayout("false")) \D触发器_4  (
    .clk(or_1_out), .D(R3), .Q(\D触发器_4_q ), .en(multiplexer_1_out), .reset(\复位_out ));  // open: Qn, preset

  // Other names for the same wires on the sheet: C0 = \原始数据 [0]; C1 = \原始数据 [1]; C2 = \原始数据 [2]; LED = out_4

  // Notes on the sheet:
  //   移位寄存器
  //   0
  //   x
  //   1*
  //   比较器
  //   比较器
  //   1
  //   0*
  //   x
  //   2
  //   x
  //   1*
  //   第二步：按“复位”按钮
  //   第三步：按“装入”按钮
  //   第一步：置左上角的原始数据（例如：110）
  //   生成的余数=1001
  //   3
  //   1*
  //   x
  //   CRC串行编码电路1（生成多项式=11101）
  //   原始数据=3位；余数=4位；CRC码=原始数据3位+余数4位
  //   第四步：按“时钟”按钮多次，直到“余数生成指示灯”变红
  //   生成的CRC码在右上角（1101001）
  //   4
  //   x
  //   1*
endmodule

module \CRC串行解码电路1  (
  input  [6:0] \CRC码 ,
  output [3:0] \余数 ,
  output [6:0] \纠错后的CRC码 ,
  output [2:0] \纠错后的数据 ,
  output out_5
);

  wire and_1_out, and_2_out, and_3_out, and_4_out, and_5_out, and_6_out, and_8_out, and_9_out, and_10_out,
       C0_prime, C1_prime, C2_prime, C3_prime, C4_prime, C5_prime, C6_prime, CLK, CLR, comparator_1_eq,
       comparator_2_eq, comparator_3_eq, comparator_4_eq, comparator_5_eq, comparator_6_eq, comparator_7_eq,
       comparator_8_eq, comparator_9_eq, comparator_10_eq, comparator_11_eq, comparator_12_eq,
       comparator_13_eq, comparator_14_eq, comparator_15_eq, comparator_17_eq, comparator_18_eq,
       comparator_19_eq, \D触发器_2_q , \D触发器_3_q , \D触发器_4_q , multiplexer_1_out, multiplexer_2_out, not_1_out,
       not_2_out, not_3_out, or_1_out, or_2_out, R0, R1, R2, R3, shift_register_1_out, Stop, \装入_out ,
       \计数器_2_q ;
  wire [2:0] \计数器_q ;
  wire [3:0] R, \计数器_3_q ;

  LED #(.active("true")) \u_余数生成指示灯  (.in(out_5));
  Comparator #(.width(4), .mode("unsigned")) comparator_1 (.a(R), .b(4'b0000), .eq(comparator_1_eq));  // open: gt, lt
  Comparator #(.width(4), .mode("unsigned")) comparator_2 (.a(R), .b(4'b0011), .eq(comparator_2_eq));  // open: gt, lt
  Button \u_复位  (.out(CLR));
  Button \u_装入  (.out(\装入_out ));
  Button \u_时钟  (.out(CLK));
  and and_1 (and_1_out, out_5, comparator_1_eq);
  LED #(.active("true")) \u_无错  (.in(and_1_out));
  and and_2 (and_2_out, \装入_out , multiplexer_2_out);
  Comparator #(.width(4), .mode("unsigned")) comparator_3 (.a(R), .b(4'b1110), .eq(comparator_3_eq));  // open: gt, lt
  Comparator #(.width(4), .mode("unsigned")) comparator_4 (.a(R), .b(4'b0101), .eq(comparator_4_eq));  // open: gt, lt
  or or_1 (or_1_out, and_2_out, CLK);
  and and_3 (and_3_out, out_5, comparator_3_eq);
  LED #(.active("true")) \u_第7位错  (.in(and_3_out));
  xor xor_1 (C6_prime, comparator_3_eq, \CRC码 [6]);
  and and_4 (and_4_out, out_5, comparator_5_eq);
  LED #(.active("true")) \u_第6位错  (.in(and_4_out));
  Comparator #(.width(4), .mode("unsigned")) comparator_5 (.a(R), .b(4'b0111), .eq(comparator_5_eq));  // open: gt, lt
  Comparator #(.width(4), .mode("unsigned")) comparator_6 (.a(R), .b(4'b0110), .eq(comparator_6_eq));  // open: gt, lt
  Shift_Register #(.width(1), .length(7), .parallel("true"), .trigger("rising")) shift_register_1 (
    .in(1'b0), .clk(or_1_out), .out(shift_register_1_out), .load(multiplexer_2_out), .clr(CLR),
    .d0(\CRC码 [0]), .d1(\CRC码 [1]), .d2(\CRC码 [2]), .d3(\CRC码 [3]), .d4(\CRC码 [4]), .d5(\CRC码 [5]),
    .d6(\CRC码 [6]));  // open: shift, q0, q1, q2, q3, q4, q5, q6
  Counter #(.width(3), .max('h7), .ongoal("wrap"), .trigger("rising"), .behavior("old")) \u_计数器  (
    .count(multiplexer_1_out), .Q(\计数器_q ), .clk(or_1_out), .clr(multiplexer_2_out));  // open: load, D, carry, preset
  Comparator #(.width(4), .mode("unsigned")) comparator_7 (.a(R), .b(4'b1101), .eq(comparator_7_eq));  // open: gt, lt
  xor xor_2 (C5_prime, comparator_5_eq, \CRC码 [5]);
  xor xor_3 (R0, \D触发器_4_q , shift_register_1_out);
  Comparator #(.width(3), .mode("unsigned")) comparator_8 (
    .a(\计数器_q ), .b(3'b110), .eq(comparator_8_eq));  // open: gt, lt
  Counter #(.width(1), .max('h1), .ongoal("wrap"), .trigger("rising"), .behavior("old")) \u_计数器_2  (
    .count(multiplexer_2_out), .Q(\计数器_2_q ), .clk(and_2_out), .clr(CLR));  // open: load, D, carry, preset
  and and_5 (and_5_out, out_5, comparator_7_eq);
  LED #(.active("true")) \u_第5位错  (.in(and_5_out));
  xor xor_4 (C4_prime, comparator_7_eq, \CRC码 [4]);
  Comparator #(.width(4), .mode("unsigned")) comparator_9 (.a(R), .b(4'b1001), .eq(comparator_9_eq));  // open: gt, lt
  or or_2 (or_2_out, comparator_2_eq, comparator_4_eq, comparator_6_eq, comparator_9_eq, comparator_12_eq, comparator_14_eq, comparator_17_eq, comparator_19_eq);
  LED #(.active("true")) \u_两位或多位错  (.in(or_2_out));
  Register #(.width(4), .trigger("rising"), .Select("low")) \u_寄存器  (
    .D({R3, R2, R1, R0}), .en(Stop), .Q(R), .clk(CLK), .clr(CLR));
  Multiplexer #(.select(1), .width(1), .disabled("Z"), .enable("false")) multiplexer_1 (
    .in0(1'b1), .in1(not_1_out), .out(multiplexer_1_out), .sel(1'b1));
  not not_1 (not_1_out, comparator_8_eq);
  Comparator #(.width(1), .mode("unsigned")) comparator_10 (
    .a(\计数器_2_q ), .b(1'b1), .eq(comparator_10_eq));  // open: gt, lt
  Comparator #(.width(4), .mode("unsigned")) comparator_11 (.a(R), .b(4'b1000), .eq(comparator_11_eq));  // open: gt, lt
  D_Flip_Flop #(.trigger("rising"), .Pre_Clr_Positions("LEGACY"), .NegatePresetClear("false"), .enable("true"), .NewFFLayout("false")) \D触发器  (
    .clk(or_1_out), .D(R0), .Q(R1), .en(multiplexer_1_out), .reset(CLR));  // open: Qn, preset
  Multiplexer #(.select(1), .width(1), .disabled("Z"), .enable("false")) multiplexer_2 (
    .in0(1'b1), .in1(not_2_out), .out(multiplexer_2_out), .sel(1'b1));
  not not_2 (not_2_out, comparator_10_eq);
  and and_6 (and_6_out, out_5, comparator_11_eq);
  LED #(.active("true")) \u_第4位错  (.in(and_6_out));
  xor xor_5 (C3_prime, comparator_11_eq, \CRC码 [3]);
  Comparator #(.width(4), .mode("unsigned")) comparator_12 (.a(R), .b(4'b1010), .eq(comparator_12_eq));  // open: gt, lt
  assign \余数  = R & {4{out_5}};  // AND_Gate and_7, 4 bits wide
  Comparator #(.width(4), .mode("unsigned")) comparator_13 (.a(R), .b(4'b0100), .eq(comparator_13_eq));  // open: gt, lt
  xor xor_6 (R2, \D触发器_4_q , \D触发器_2_q );
  D_Flip_Flop #(.trigger("rising"), .Pre_Clr_Positions("LEGACY"), .NegatePresetClear("false"), .enable("true"), .NewFFLayout("false")) \D触发器_2  (
    .clk(or_1_out), .D(R1), .Q(\D触发器_2_q ), .en(multiplexer_1_out), .reset(CLR));  // open: Qn, preset
  and and_8 (and_8_out, out_5, comparator_13_eq);
  LED #(.active("true")) \u_第3位错  (.in(and_8_out));
  xor xor_7 (C2_prime, comparator_13_eq, \CRC码 [2]);
  Comparator #(.width(4), .mode("unsigned")) comparator_14 (.a(R), .b(4'b1011), .eq(comparator_14_eq));  // open: gt, lt
  Counter #(.width(4), .max('hf), .ongoal("wrap"), .trigger("rising"), .behavior("old")) \u_计数器_3  (
    .count(Stop), .Q(\计数器_3_q ), .clk(or_1_out), .clr(CLR));  // open: load, D, carry, preset
  and and_9 (and_9_out, out_5, comparator_15_eq);
  Comparator #(.width(4), .mode("unsigned")) comparator_15 (.a(R), .b(4'b0010), .eq(comparator_15_eq));  // open: gt, lt
  xor xor_8 (R3, \D触发器_4_q , \D触发器_3_q );
  D_Flip_Flop #(.trigger("rising"), .Pre_Clr_Positions("LEGACY"), .NegatePresetClear("false"), .enable("true"), .NewFFLayout("false")) \D触发器_3  (
    .clk(or_1_out), .D(R2), .Q(\D触发器_3_q ), .en(multiplexer_1_out), .reset(CLR));  // open: Qn, preset
  Comparator #(.width(4), .mode("unsigned")) comparator_16 (.a(\计数器_3_q ), .b(4'b1000), .eq(out_5));  // open: gt, lt
  not not_3 (not_3_out, out_5);
  LED #(.active("true")) \u_第2位错  (.in(and_9_out));
  xor xor_9 (C1_prime, comparator_15_eq, \CRC码 [1]);
  Comparator #(.width(4), .mode("unsigned")) comparator_17 (.a(R), .b(4'b1100), .eq(comparator_17_eq));  // open: gt, lt
  Multiplexer #(.select(1), .width(1), .disabled("Z"), .enable("false")) multiplexer_3 (
    .in0(1'b1), .in1(not_3_out), .out(Stop), .sel(1'b1));
  and and_10 (and_10_out, out_5, comparator_18_eq);
  LED #(.active("true")) \u_第1位错  (.in(and_10_out));
  Comparator #(.width(4), .mode("unsigned")) comparator_18 (.a(R), .b(4'b0001), .eq(comparator_18_eq));  // open: gt, lt
  Comparator #(.width(4), .mode("unsigned")) comparator_19 (.a(R), .b(4'b1111), .eq(comparator_19_eq));  // open: gt, lt
  D_Flip_Flop #(.trigger("rising"), .Pre_Clr_Positions("LEGACY"), .NegatePresetClear("false"), .enable("true"), .NewFFLayout("false")) \D触发器_4  (
    .clk(or_1_out), .D(R3), .Q(\D触发器_4_q ), .en(multiplexer_1_out), .reset(CLR));  // open: Qn, preset
  xor xor_10 (C0_prime, comparator_18_eq, \CRC码 [0]);
  assign \纠错后的CRC码  = {C6_prime, C5_prime, C4_prime, C3_prime, C2_prime, C1_prime, C0_prime} & {7{out_5}};  // AND_Gate and_11, 7 bits wide
  assign \纠错后的数据  = {C6_prime, C5_prime, C4_prime} & {3{out_5}};  // AND_Gate and_12, 3 bits wide

  // Other names for the same wires on the sheet: LED = out_5; C0 = \CRC码 [0]; C1 = \CRC码 [1]; C2 = \CRC码 [2];
  //   C3 = \CRC码 [3]; C4 = \CRC码 [4]; C5 = \CRC码 [5]; C6 = \CRC码 [6]

  // Notes on the sheet:
  //   第二步：按“复位”按钮
  //   第三步：按“装入”按钮
  //   重复第二、三、四步
  //   第一步：置左上角的CRC码（如：1101001）
  //   第四步：按“时钟”按钮多次，直到“余数生成指示灯”变红
  //   第五步：置有一位错的CRC码（如：0101001）
  //   重复第二、三、四步
  //   此时余数=1110，下面的“第7位错”指示灯变红
  //   纠正后的CRC码见右上角
  //   第六步：置有两位错的CRC码（如：0001001）
  //   此时，下面的“两位或多位错”指示灯变红
  //   此时余数=0000，下面的“无错”指示灯变红，表示无错
  //   比较器
  //   比较器
  //   比较器
  //   比较器
  //   比较器
  //   比较器
  //   移位寄存器
  //   比较器
  //   比较器
  //   0
  //   x
  //   1*
  //   比较器
  //   比较器
  //   比较器
  //   比较器
  //   1
  //   x
  //   0*
  //   比较器
  //   比较器
  //   2
  //   1*
  //   x
  //   比较器
  //   比较器
  //   比较器
  //   3
  //   x
  //   1*
  //   CRC串行解码电路1（生成多项式=11101）
  //   原始数据=3位；余数=4位；CRC码=原始数据3位+余数4位
  //   比较器
  //   比较器
  //   4
  //   1*
  //   x
endmodule

// CRC编码
module \CRC串行编码电路1_封装用  (
  input  [2:0] \原始数据 ,
  input  \复位 ,
  input  \装入 ,
  input  \时钟 ,
  output [3:0] \余数 ,
  output [6:0] \CRC码 ,
  output out_7
);

  wire and_1_out, comparator_2_eq, \D触发器_2_q , \D触发器_3_q , \D触发器_4_q , multiplexer_1_out, multiplexer_2_out,
       not_1_out, not_2_out, or_1_out, R0, R1, R2, R3, shift_register_1_out, \计数器_2_q ;
  wire [2:0] \计数器_q ;

  and and_1 (and_1_out, \装入 , multiplexer_2_out);
  LED #(.active("true")) \u_余数生成指示灯  (.in(out_7));
  or or_1 (or_1_out, and_1_out, \时钟 );
  Shift_Register #(.width(1), .length(3), .parallel("true"), .trigger("rising")) shift_register_1 (
    .in(1'b0), .clk(or_1_out), .out(shift_register_1_out), .load(multiplexer_2_out), .clr(\复位 ),
    .d0(\原始数据 [0]), .d1(\原始数据 [1]), .d2(\原始数据 [2]));  // open: shift, q0, q1, q2
  Counter #(.width(3), .max('h7), .ongoal("wrap"), .trigger("rising"), .behavior("old")) \u_计数器  (
    .count(multiplexer_1_out), .Q(\计数器_q ), .clk(or_1_out), .clr(multiplexer_2_out));  // open: load, D, carry, preset
  xor xor_1 (R0, \D触发器_4_q , shift_register_1_out);
  Comparator #(.width(3), .mode("unsigned")) comparator_1 (.a(\计数器_q ), .b(3'b110), .eq(out_7));  // open: gt, lt
  not not_1 (not_1_out, out_7);
  Counter #(.width(1), .max('h1), .ongoal("wrap"), .trigger("rising"), .behavior("old")) \u_计数器_2  (
    .count(multiplexer_2_out), .Q(\计数器_2_q ), .clk(and_1_out), .clr(\复位 ));  // open: load, D, carry, preset
  assign \余数  = {4{out_7}} & {R3, R2, R1, R0};  // AND_Gate and_2, 4 bits wide
  D_Flip_Flop #(.trigger("rising"), .Pre_Clr_Positions("LEGACY"), .NegatePresetClear("false"), .enable("true"), .NewFFLayout("false")) \D触发器  (
    .clk(or_1_out), .D(R0), .Q(R1), .en(multiplexer_1_out), .reset(\复位 ));  // open: Qn, preset
  Multiplexer #(.select(1), .width(1), .disabled("Z"), .enable("false")) multiplexer_1 (
    .in0(1'b1), .in1(not_1_out), .out(multiplexer_1_out), .sel(1'b1));
  Comparator #(.width(1), .mode("unsigned")) comparator_2 (
    .a(\计数器_2_q ), .b(1'b1), .eq(comparator_2_eq));  // open: gt, lt
  Multiplexer #(.select(1), .width(1), .disabled("Z"), .enable("false")) multiplexer_2 (
    .in0(1'b1), .in1(not_2_out), .out(multiplexer_2_out), .sel(1'b1));
  not not_2 (not_2_out, comparator_2_eq);
  D_Flip_Flop #(.trigger("rising"), .Pre_Clr_Positions("LEGACY"), .NegatePresetClear("false"), .enable("true"), .NewFFLayout("false")) \D触发器_2  (
    .clk(or_1_out), .D(R1), .Q(\D触发器_2_q ), .en(multiplexer_1_out), .reset(\复位 ));  // open: Qn, preset
  xor xor_2 (R2, \D触发器_4_q , \D触发器_2_q );
  D_Flip_Flop #(.trigger("rising"), .Pre_Clr_Positions("LEGACY"), .NegatePresetClear("false"), .enable("true"), .NewFFLayout("false")) \D触发器_3  (
    .clk(or_1_out), .D(R2), .Q(\D触发器_3_q ), .en(multiplexer_1_out), .reset(\复位 ));  // open: Qn, preset
  assign \CRC码  = {\原始数据 , R3, R2, R1, R0} & {7{out_7}};  // AND_Gate and_3, 7 bits wide
  xor xor_3 (R3, \D触发器_4_q , \D触发器_3_q );
  D_Flip_Flop #(.trigger("rising"), .Pre_Clr_Positions("LEGACY"), .NegatePresetClear("false"), .enable("true"), .NewFFLayout("false")) \D触发器_4  (
    .clk(or_1_out), .D(R3), .Q(\D触发器_4_q ), .en(multiplexer_1_out), .reset(\复位 ));  // open: Qn, preset

  // Other names for the same wires on the sheet: C0 = \原始数据 [0]; C1 = \原始数据 [1]; C2 = \原始数据 [2]; LED = out_7

  // Notes on the sheet:
  //   移位寄存器
  //   0
  //   x
  //   1*
  //   比较器
  //   比较器
  //   1
  //   x
  //   0*
  //   2
  //   x
  //   1*
  //   第二步：按“复位”按钮
  //   第三步：按“装入”按钮
  //   第一步：置左上角的原始数据（例如：110）
  //   生成的余数=1001
  //   生成的CRC码在右上角（1101001）
  //   3
  //   x
  //   1*
  //   CRC串行编码电路1（生成多项式=11101）
  //   原始数据=3位；余数=4位；CRC码=原始数据3位+余数4位
  //   第四步：按“时钟”按钮多次，直到“余数生成指示灯”变红
  //   4
  //   1*
  //   x
endmodule

// CRC解码
module \CRC串行解码电路1_封装用  (
  input  [6:0] \CRC码 ,
  input  \复位 ,
  input  \装入 ,
  input  \时钟 ,
  output [3:0] \余数 ,
  output [6:0] \纠正后的CRC码 ,
  output [2:0] \纠正后的数据 ,
  output out_8
);

  wire and_1_out, and_2_out, and_3_out, and_4_out, and_5_out, and_6_out, and_8_out, and_9_out, and_10_out,
       C0_prime, C1_prime, C2_prime, C3_prime, C4_prime, C5_prime, C6_prime, comparator_1_eq,
       comparator_2_eq, comparator_3_eq, comparator_4_eq, comparator_5_eq, comparator_6_eq, comparator_7_eq,
       comparator_8_eq, comparator_9_eq, comparator_10_eq, comparator_11_eq, comparator_12_eq,
       comparator_13_eq, comparator_14_eq, comparator_15_eq, comparator_17_eq, comparator_18_eq,
       comparator_19_eq, \D触发器_2_q , \D触发器_3_q , \D触发器_4_q , multiplexer_1_out, multiplexer_2_out, not_1_out,
       not_2_out, not_3_out, or_1_out, or_2_out, R0, R1, R2, R3, shift_register_1_out, Stop, \计数器_2_q ;
  wire [2:0] \计数器_q ;
  wire [3:0] R, \计数器_3_q ;

  LED #(.active("true")) \u_余数生成指示灯  (.in(out_8));
  Comparator #(.width(4), .mode("unsigned")) comparator_1 (.a(R), .b(4'b0000), .eq(comparator_1_eq));  // open: gt, lt
  Comparator #(.width(4), .mode("unsigned")) comparator_2 (.a(R), .b(4'b0011), .eq(comparator_2_eq));  // open: gt, lt
  and and_1 (and_1_out, out_8, comparator_1_eq);
  LED #(.active("true")) \u_无错  (.in(and_1_out));
  and and_2 (and_2_out, \装入 , multiplexer_2_out);
  Comparator #(.width(4), .mode("unsigned")) comparator_3 (.a(R), .b(4'b1110), .eq(comparator_3_eq));  // open: gt, lt
  Comparator #(.width(4), .mode("unsigned")) comparator_4 (.a(R), .b(4'b0101), .eq(comparator_4_eq));  // open: gt, lt
  or or_1 (or_1_out, and_2_out, \时钟 );
  and and_3 (and_3_out, out_8, comparator_3_eq);
  LED #(.active("true")) \u_第7位错  (.in(and_3_out));
  xor xor_1 (C6_prime, comparator_3_eq, \CRC码 [6]);
  and and_4 (and_4_out, out_8, comparator_5_eq);
  LED #(.active("true")) \u_第6位错  (.in(and_4_out));
  Comparator #(.width(4), .mode("unsigned")) comparator_5 (.a(R), .b(4'b0111), .eq(comparator_5_eq));  // open: gt, lt
  Comparator #(.width(4), .mode("unsigned")) comparator_6 (.a(R), .b(4'b0110), .eq(comparator_6_eq));  // open: gt, lt
  Shift_Register #(.width(1), .length(7), .parallel("true"), .trigger("rising")) shift_register_1 (
    .in(1'b0), .clk(or_1_out), .out(shift_register_1_out), .load(multiplexer_2_out), .clr(\复位 ),
    .d0(\CRC码 [0]), .d1(\CRC码 [1]), .d2(\CRC码 [2]), .d3(\CRC码 [3]), .d4(\CRC码 [4]), .d5(\CRC码 [5]),
    .d6(\CRC码 [6]));  // open: shift, q0, q1, q2, q3, q4, q5, q6
  Counter #(.width(3), .max('h7), .ongoal("wrap"), .trigger("rising"), .behavior("old")) \u_计数器  (
    .count(multiplexer_1_out), .Q(\计数器_q ), .clk(or_1_out), .clr(multiplexer_2_out));  // open: load, D, carry, preset
  Comparator #(.width(4), .mode("unsigned")) comparator_7 (.a(R), .b(4'b1101), .eq(comparator_7_eq));  // open: gt, lt
  xor xor_2 (C5_prime, comparator_5_eq, \CRC码 [5]);
  xor xor_3 (R0, \D触发器_4_q , shift_register_1_out);
  Comparator #(.width(3), .mode("unsigned")) comparator_8 (
    .a(\计数器_q ), .b(3'b110), .eq(comparator_8_eq));  // open: gt, lt
  Counter #(.width(1), .max('h1), .ongoal("wrap"), .trigger("rising"), .behavior("old")) \u_计数器_2  (
    .count(multiplexer_2_out), .Q(\计数器_2_q ), .clk(and_2_out), .clr(\复位 ));  // open: load, D, carry, preset
  and and_5 (and_5_out, out_8, comparator_7_eq);
  LED #(.active("true")) \u_第5位错  (.in(and_5_out));
  xor xor_4 (C4_prime, comparator_7_eq, \CRC码 [4]);
  Comparator #(.width(4), .mode("unsigned")) comparator_9 (.a(R), .b(4'b1001), .eq(comparator_9_eq));  // open: gt, lt
  or or_2 (or_2_out, comparator_2_eq, comparator_4_eq, comparator_6_eq, comparator_9_eq, comparator_12_eq, comparator_14_eq, comparator_17_eq, comparator_19_eq);
  LED #(.active("true")) \u_两位或多位错  (.in(or_2_out));
  Register #(.width(4), .trigger("rising"), .Select("low")) \u_寄存器  (
    .D({R3, R2, R1, R0}), .en(Stop), .Q(R), .clk(\时钟 ), .clr(\复位 ));
  Multiplexer #(.select(1), .width(1), .disabled("Z"), .enable("false")) multiplexer_1 (
    .in0(1'b1), .in1(not_1_out), .out(multiplexer_1_out), .sel(1'b1));
  not not_1 (not_1_out, comparator_8_eq);
  Comparator #(.width(1), .mode("unsigned")) comparator_10 (
    .a(\计数器_2_q ), .b(1'b1), .eq(comparator_10_eq));  // open: gt, lt
  Comparator #(.width(4), .mode("unsigned")) comparator_11 (.a(R), .b(4'b1000), .eq(comparator_11_eq));  // open: gt, lt
  D_Flip_Flop #(.trigger("rising"), .Pre_Clr_Positions("LEGACY"), .NegatePresetClear("false"), .enable("true"), .NewFFLayout("false")) \D触发器  (
    .clk(or_1_out), .D(R0), .Q(R1), .en(multiplexer_1_out), .reset(\复位 ));  // open: Qn, preset
  Multiplexer #(.select(1), .width(1), .disabled("Z"), .enable("false")) multiplexer_2 (
    .in0(1'b1), .in1(not_2_out), .out(multiplexer_2_out), .sel(1'b1));
  not not_2 (not_2_out, comparator_10_eq);
  and and_6 (and_6_out, out_8, comparator_11_eq);
  LED #(.active("true")) \u_第4位错  (.in(and_6_out));
  xor xor_5 (C3_prime, comparator_11_eq, \CRC码 [3]);
  Comparator #(.width(4), .mode("unsigned")) comparator_12 (.a(R), .b(4'b1010), .eq(comparator_12_eq));  // open: gt, lt
  assign \余数  = R & {4{out_8}};  // AND_Gate and_7, 4 bits wide
  Comparator #(.width(4), .mode("unsigned")) comparator_13 (.a(R), .b(4'b0100), .eq(comparator_13_eq));  // open: gt, lt
  xor xor_6 (R2, \D触发器_4_q , \D触发器_2_q );
  D_Flip_Flop #(.trigger("rising"), .Pre_Clr_Positions("LEGACY"), .NegatePresetClear("false"), .enable("true"), .NewFFLayout("false")) \D触发器_2  (
    .clk(or_1_out), .D(R1), .Q(\D触发器_2_q ), .en(multiplexer_1_out), .reset(\复位 ));  // open: Qn, preset
  and and_8 (and_8_out, out_8, comparator_13_eq);
  LED #(.active("true")) \u_第3位错  (.in(and_8_out));
  xor xor_7 (C2_prime, comparator_13_eq, \CRC码 [2]);
  Comparator #(.width(4), .mode("unsigned")) comparator_14 (.a(R), .b(4'b1011), .eq(comparator_14_eq));  // open: gt, lt
  Counter #(.width(4), .max('hf), .ongoal("wrap"), .trigger("rising"), .behavior("old")) \u_计数器_3  (
    .count(Stop), .Q(\计数器_3_q ), .clk(or_1_out), .clr(\复位 ));  // open: load, D, carry, preset
  and and_9 (and_9_out, out_8, comparator_15_eq);
  Comparator #(.width(4), .mode("unsigned")) comparator_15 (.a(R), .b(4'b0010), .eq(comparator_15_eq));  // open: gt, lt
  xor xor_8 (R3, \D触发器_4_q , \D触发器_3_q );
  D_Flip_Flop #(.trigger("rising"), .Pre_Clr_Positions("LEGACY"), .NegatePresetClear("false"), .enable("true"), .NewFFLayout("false")) \D触发器_3  (
    .clk(or_1_out), .D(R2), .Q(\D触发器_3_q ), .en(multiplexer_1_out), .reset(\复位 ));  // open: Qn, preset
  not not_3 (not_3_out, out_8);
  Comparator #(.width(4), .mode("unsigned")) comparator_16 (.a(\计数器_3_q ), .b(4'b1000), .eq(out_8));  // open: gt, lt
  LED #(.active("true")) \u_第2位错  (.in(and_9_out));
  xor xor_9 (C1_prime, comparator_15_eq, \CRC码 [1]);
  Comparator #(.width(4), .mode("unsigned")) comparator_17 (.a(R), .b(4'b1100), .eq(comparator_17_eq));  // open: gt, lt
  Multiplexer #(.select(1), .width(1), .disabled("Z"), .enable("false")) multiplexer_3 (
    .in0(1'b1), .in1(not_3_out), .out(Stop), .sel(1'b1));
  and and_10 (and_10_out, out_8, comparator_18_eq);
  LED #(.active("true")) \u_第1位错  (.in(and_10_out));
  Comparator #(.width(4), .mode("unsigned")) comparator_18 (.a(R), .b(4'b0001), .eq(comparator_18_eq));  // open: gt, lt
  Comparator #(.width(4), .mode("unsigned")) comparator_19 (.a(R), .b(4'b1111), .eq(comparator_19_eq));  // open: gt, lt
  D_Flip_Flop #(.trigger("rising"), .Pre_Clr_Positions("LEGACY"), .NegatePresetClear("false"), .enable("true"), .NewFFLayout("false")) \D触发器_4  (
    .clk(or_1_out), .D(R3), .Q(\D触发器_4_q ), .en(multiplexer_1_out), .reset(\复位 ));  // open: Qn, preset
  xor xor_10 (C0_prime, comparator_18_eq, \CRC码 [0]);
  assign \纠正后的CRC码  = {C6_prime, C5_prime, C4_prime, C3_prime, C2_prime, C1_prime, C0_prime} & {7{out_8}};  // AND_Gate and_11, 7 bits wide
  assign \纠正后的数据  = {C6_prime, C5_prime, C4_prime} & {3{out_8}};  // AND_Gate and_12, 3 bits wide

  // Other names for the same wires on the sheet: LED = out_8; CLK = \时钟 ; CLR = \复位 ; C0 = \CRC码 [0]; C1 = \CRC码 [1];
  //   C2 = \CRC码 [2]; C3 = \CRC码 [3]; C4 = \CRC码 [4]; C5 = \CRC码 [5]; C6 = \CRC码 [6]

  // Notes on the sheet:
  //   第二步：按“复位”按钮
  //   第三步：按“装入”按钮
  //   第一步：置左上角的CRC码（如：1101001）
  //   第四步：按“时钟”按钮多次，直到“余数生成指示灯”变红
  //   第五步：置有一位错的CRC码（如：0101001）
  //   重复第二、三、四步
  //   此时余数=1110，下面的“第7位错”指示灯变红
  //   纠正后的CRC码见右上角
  //   第六步：置有两位错的CRC码（如：0001001）
  //   重复第二、三、四步
  //   此时，下面的“两位或多位错”指示灯变红
  //   此时余数=0000，下面的“无错”指示灯变红，表示无错
  //   比较器
  //   比较器
  //   比较器
  //   比较器
  //   比较器
  //   比较器
  //   移位寄存器
  //   比较器
  //   比较器
  //   0
  //   1*
  //   x
  //   比较器
  //   比较器
  //   比较器
  //   比较器
  //   1
  //   0*
  //   x
  //   比较器
  //   比较器
  //   2
  //   x
  //   1*
  //   比较器
  //   比较器
  //   比较器
  //   3
  //   x
  //   1*
  //   CRC串行解码电路1（生成多项式=11101）
  //   原始数据=3位；余数=4位；CRC码=原始数据3位+余数4位
  //   比较器
  //   比较器
  //   4
  //   1*
  //   x
endmodule
