// Logisim project 8位补码一位乘法器（用8位无符号一位乘法器实现）(挑战性实验）.circ as structural Verilog: 4 circuits, main circuit 8位补码一位乘法器（用8位无符号数一位乘法器实现）
module \_8位补码一位乘法器_用8位无符号数一位乘法器实现  (
  input  [7:0] X,
  input  [7:0] Y,
  output [15:0] \乘积 
);

  wire CLK, comparator_1_eq, comparator_2_eq, END, RST, X_0, Y_0, ZERO;
  wire [6:0] negator_1_out, negator_2_out, X_star, Y_star;
  wire [7:0] multiplexer_3_out, multiplexer_4_out;
  wire [14:0] multiplexer_5_out, negator_3_out;
  wire [15:0] P;
  wire [15:15] P_star;

  // Probe on X
  // Probe on Y
  Button \u_复位  (.out(RST));
  Multiplexer #(.select(1), .width(7), .disabled("Z"), .enable("false")) multiplexer_1 (
    .in0(X[6:0]), .in1(negator_1_out), .out(X_star), .sel(X[7]));
  Negator #(.width(7)) negator_1 (.in(X[6:0]), .out(negator_1_out));
  Multiplexer #(.select(1), .width(7), .disabled("Z"), .enable("false")) multiplexer_2 (
    .in0(Y[6:0]), .in1(negator_2_out), .out(Y_star), .sel(Y[7]));
  Negator #(.width(7)) negator_2 (.in(Y[6:0]), .out(negator_2_out));
  or or_1 (ZERO, X_0, Y_0);
  Button \u_时钟  (.out(CLK));
  Comparator #(.width(8), .mode("twosComplement")) comparator_1 (
    .a(X), .b(8'h80), .eq(comparator_1_eq));  // open: gt, lt
  // Probe on \乘积 
  Multiplexer #(.select(1), .width(8), .disabled("Z"), .enable("false")) multiplexer_3 (
    .in0({1'b0, X_star}), .in1(8'h80), .out(multiplexer_3_out), .sel(comparator_1_eq));
  Comparator #(.width(8), .mode("twosComplement")) comparator_2 (
    .a(Y), .b(8'h80), .eq(comparator_2_eq));  // open: gt, lt
  \_8位无符号数一位乘法器  \u_8位无符号数一位乘法器_1  (
    .X(multiplexer_3_out), .Y(multiplexer_4_out), .\乘积 ({P_star[15], P[14:0]}), .RST(RST), .CLK(CLK),
    .out_5(END));
  Multiplexer #(.select(1), .width(8), .disabled("Z"), .enable("false")) multiplexer_4 (
    .in0({1'b0, Y_star}), .in1(8'h80), .out(multiplexer_4_out), .sel(comparator_2_eq));
  LED #(.active("true")) led_1 (.in(END));
  Negator #(.width(15)) negator_3 (.in(P[14:0]), .out(negator_3_out));
  nor nor_1 (X_0, X[0], X[1], X[2], X[3], X[4], X[5], X[6], X[7]);
  nor nor_2 (Y_0, Y[0], Y[1], Y[2], Y[3], Y[4], Y[5], Y[6], Y[7]);
  Multiplexer #(.select(1), .width(15), .disabled("Z"), .enable("false")) multiplexer_5 (
    .in0(P[14:0]), .in1(negator_3_out), .out(multiplexer_5_out), .sel(P[15]));
  // Probe on X
  // Probe on Y
  // Probe on \乘积 
  xor xor_1 (P[15], X[7], Y[7]);
  Multiplexer #(.select(1), .width(16), .disabled("Z"), .enable("false")) multiplexer_6 (
    .in0({P[15], multiplexer_5_out}), .in1({16{1'b0}}), .out(\乘积 ), .sel(ZERO));

  // Other names for the same wires on the sheet: P_star[14:0] = P[14:0]; X6_0[6:0] = X[6:0];
  //   X原码[7:0] = {X[7], X_star}; Y6_0[6:0] = Y[6:0]; Y原码[7:0] = {Y[7], Y_star}

  // Notes on the sheet:
  //   转换为无符号
  //   补码转原码
  //   输入引脚区
  //   首先设置X、Y值，然后按“复位”按钮，接下去按“CLK”按钮多次，直到“END”指示灯变红，此时观看乘积是不是正确？
  //   功能说明: 8位补码一位乘法器（用8位无符号数一位乘法器实现）                输入：X、Y 为8位补码               输出：乘积=X*Y 为16位补码
  //   检测是否有0
  //   输出引脚区
  //   8位补码一位乘法器（用8位无符号数一位乘法器实现）
  //   ×
  //   =
  //   检测是否有0
  //   无符号结果转补码以及特判
  //   By 黄勖
endmodule

// 8位无符号一位乘法器
module \_8位无符号数一位乘法器  (
  input  [7:0] X,
  input  [7:0] Y,
  input  RST,
  input  CLK,
  output out_5,
  output [15:0] \乘积 
);

  wire comparator_1_eq, d_ff_1_q, not_1_out;
  wire [0:0] \n8位串行加法器_1_s ;
  wire [3:0] counter_1_q;
  wire [7:0] multiplexer_1_out, multiplexer_2_out, \n8位串行加法器_1_cout ;

  // Probe on \乘积 [15:8]
  Register #(.width(8), .trigger("rising"), .Select("low")) register_1 (
    .D(\n8位串行加法器_1_cout ), .en(not_1_out), .Q(\乘积 [15:8]), .clk(CLK), .clr(RST));
  \_8位串行加法器  \u_8位串行加法器_1  (
    .X(\乘积 [15:8]), .Y(multiplexer_1_out), .Cin(1'b0), .S({\n8位串行加法器_1_cout [6:0], \n8位串行加法器_1_s [0]}),
    .Cout(\n8位串行加法器_1_cout [7]));  // open: out_6
  Multiplexer #(.select(1), .width(8), .disabled("Z"), .enable("false")) multiplexer_1 (
    .in0({8{1'b0}}), .in1(X), .out(multiplexer_1_out), .sel(\乘积 [0]));
  Multiplexer #(.select(1), .width(8), .disabled("Z"), .enable("false")) multiplexer_2 (
    .in0(Y), .in1({\n8位串行加法器_1_s [0], \乘积 [7:1]}), .out(multiplexer_2_out), .sel(d_ff_1_q));
  // Probe on \乘积 [7:0]
  Register #(.width(8), .trigger("rising"), .Select("low")) Y_2 (
    .D(multiplexer_2_out), .en(not_1_out), .Q(\乘积 [7:0]), .clk(CLK), .clr(RST));
  Counter #(.width(4), .max('hf), .ongoal("wrap"), .trigger("rising"), .behavior("old")) counter_1 (
    .count(not_1_out), .Q(counter_1_q), .clk(CLK), .clr(RST));  // open: load, D, carry, preset
  D_Flip_Flop #(.trigger("rising"), .Pre_Clr_Positions("LEGACY"), .NegatePresetClear("false"), .enable("true"), .NewFFLayout("false")) d_ff_1 (
    .clk(CLK), .D(1'b1), .Q(d_ff_1_q), .reset(RST));  // open: Qn, preset, en
  Comparator #(.width(4), .mode("unsigned")) comparator_1 (
    .a(counter_1_q), .b(4'b1001), .eq(comparator_1_eq));  // open: gt, lt
  not not_1 (not_1_out, comparator_1_eq);
  not not_2 (out_5, not_1_out);
  // Probe on X
  // Probe on Y
  // Probe on \乘积 

  // Other names for the same wires on the sheet: END = out_5

  // Notes on the sheet:
  //   输入引脚区
  //   ∑
  //   功能说明: 8位无符号数一位乘法器                输入：X、Y 为8位无符号数               输出：乘积=X*Y 为16位无符号数
  //   首先设置X、Y值，然后按“复位”按钮，接下去按“CLK”按钮多次，直到“END”指示灯变红，此时观看乘积是不是正确？
  //   8位无符号数一位乘法器
  //   输出引脚区
  //   ×
  //   =
endmodule

module \_8位串行加法器  (
  input  [7:0] X,
  input  [7:0] Y,
  input  Cin,
  output [7:0] S,
  output Cout,
  output out_6
);

  wire \n1位全加器_fa_2_cout , \n1位全加器_fa_3_cout , \n1位全加器_fa_4_cout , \n1位全加器_fa_5_cout , \n1位全加器_fa_6_cout ,
       \n1位全加器_fa_7_cout , \n1位全加器_fa_8_cout ;

  xor xor_1 (out_6, Cout, \n1位全加器_fa_2_cout );
  \_1位全加器_FA  \u_1位全加器_fa_1  (.Cout(Cout), .Si(S[7]), .Cin(\n1位全加器_fa_2_cout ), .Xi(X[7]), .Yi(Y[7]));
  \_1位全加器_FA  \u_1位全加器_fa_2  (.Cout(\n1位全加器_fa_2_cout ), .Si(S[6]), .Cin(\n1位全加器_fa_3_cout ), .Xi(X[6]), .Yi(Y[6]));
  \_1位全加器_FA  \u_1位全加器_fa_3  (.Cout(\n1位全加器_fa_3_cout ), .Si(S[5]), .Cin(\n1位全加器_fa_4_cout ), .Xi(X[5]), .Yi(Y[5]));
  \_1位全加器_FA  \u_1位全加器_fa_4  (.Cout(\n1位全加器_fa_4_cout ), .Si(S[4]), .Cin(\n1位全加器_fa_5_cout ), .Xi(X[4]), .Yi(Y[4]));
  \_1位全加器_FA  \u_1位全加器_fa_5  (.Cout(\n1位全加器_fa_5_cout ), .Si(S[3]), .Cin(\n1位全加器_fa_6_cout ), .Xi(X[3]), .Yi(Y[3]));
  \_1位全加器_FA  \u_1位全加器_fa_6  (.Cout(\n1位全加器_fa_6_cout ), .Si(S[2]), .Cin(\n1位全加器_fa_7_cout ), .Xi(X[2]), .Yi(Y[2]));
  // Probe on X
  // Probe on Y
  // Probe on S
  \_1位全加器_FA  \u_1位全加器_fa_7  (.Cout(\n1位全加器_fa_7_cout ), .Si(S[1]), .Cin(\n1位全加器_fa_8_cout ), .Xi(X[1]), .Yi(Y[1]));
  // Probe on X
  // Probe on Y
  // Probe on S
  \_1位全加器_FA  \u_1位全加器_fa_8  (.Cout(\n1位全加器_fa_8_cout ), .Si(S[0]), .Cin(Cin), .Xi(X[0]), .Yi(Y[0]));

  // Other names for the same wires on the sheet: OF = out_6

  // Notes on the sheet:
  //   Y: pull=down
  //   X: pull=down
  //   Cin: pull=down
  //   输入引脚区
  //   符号位
  //   输出引脚区
  //   8位串行加法器
  //   OF
  //   +
  //   有符号加法
  //   +
  //   =
  //   无符号加法
endmodule

// FA
module \_1位全加器_FA  (
  input  Cin,
  input  Xi,
  input  Yi,
  output Cout,
  output Si
);

  wire AND_2_out, AND_out, XOR_2_out;

  and AND (AND_out, Xi, Yi);
  or OR (Cout, AND_out, AND_2_out);
  and AND_2 (AND_2_out, Cin, XOR_2_out);
  xor XOR (Si, Cin, XOR_2_out);
  xor XOR_2 (XOR_2_out, Xi, Yi);

  // Notes on the sheet:
  //   Yi: pull=down
  //   Xi: pull=down
  //   Cin: pull=down
  //   Cout = Xi Yi + Cin (Xi ^ Yi)
  //   Si = Xi ^ Yi ^ Cin
  //   1位全加器（FA）
endmodule
