// Logisim project 串行加法器.circ as structural Verilog: 6 circuits, main circuit 1位全加器（FA1）
module \_8位串行加法器_1  (
  input  [7:0] X,
  input  [7:0] Y,
  input  Cin,
  output [7:0] S,
  output Cout,
  output out_6
);

  wire \n1位全加器_fa1_2_cout , \n1位全加器_fa1_3_cout , \n1位全加器_fa1_4_cout , \n1位全加器_fa1_5_cout ,
       \n1位全加器_fa1_6_cout , \n1位全加器_fa1_7_cout , \n1位全加器_fa1_8_cout ;

  xor xor_1 (out_6, Cout, \n1位全加器_fa1_2_cout );
  \_1位全加器_FA1  \u_1位全加器_fa1_1  (.Cout(Cout), .Si(S[7]), .Cin(\n1位全加器_fa1_2_cout ), .Xi(X[7]), .Yi(Y[7]));
  \_1位全加器_FA1  \u_1位全加器_fa1_2  (.Cout(\n1位全加器_fa1_2_cout ), .Si(S[6]), .Cin(\n1位全加器_fa1_3_cout ), .Xi(X[6]), .Yi(Y[6]));
  \_1位全加器_FA1  \u_1位全加器_fa1_3  (.Cout(\n1位全加器_fa1_3_cout ), .Si(S[5]), .Cin(\n1位全加器_fa1_4_cout ), .Xi(X[5]), .Yi(Y[5]));
  \_1位全加器_FA1  \u_1位全加器_fa1_4  (.Cout(\n1位全加器_fa1_4_cout ), .Si(S[4]), .Cin(\n1位全加器_fa1_5_cout ), .Xi(X[4]), .Yi(Y[4]));
  \_1位全加器_FA1  \u_1位全加器_fa1_5  (.Cout(\n1位全加器_fa1_5_cout ), .Si(S[3]), .Cin(\n1位全加器_fa1_6_cout ), .Xi(X[3]), .Yi(Y[3]));
  \_1位全加器_FA1  \u_1位全加器_fa1_6  (.Cout(\n1位全加器_fa1_6_cout ), .Si(S[2]), .Cin(\n1位全加器_fa1_7_cout ), .Xi(X[2]), .Yi(Y[2]));
  // Probe on X
  // Probe on Y
  // Probe on S
  \_1位全加器_FA1  \u_1位全加器_fa1_7  (.Cout(\n1位全加器_fa1_7_cout ), .Si(S[1]), .Cin(\n1位全加器_fa1_8_cout ), .Xi(X[1]), .Yi(Y[1]));
  // Probe on X
  // Probe on Y
  // Probe on S
  \_1位全加器_FA1  \u_1位全加器_fa1_8  (.Cout(\n1位全加器_fa1_8_cout ), .Si(S[0]), .Cin(Cin), .Xi(X[0]), .Yi(Y[0]));

  // Other names for the same wires on the sheet: OF = out_6

  // Notes on the sheet:
  //   Y: pull=down
  //   Cin: pull=down
  //   X: pull=down
  //   输入引脚区
  //   符号位
  //   输出引脚区
  //   8位串行加法器（1）
  //   Overflow
  //   +
  //   有符号加法
  //   +
  //   =
  //   无符号加法
endmodule

module \_8位串行加法器_2  (
  input  [7:0] X,
  input  [7:0] Y,
  input  Cin,
  output [7:0] S,
  output Cout,
  output out_6
);

  wire \n1位全加器_fa2_2_cout , \n1位全加器_fa2_3_cout , \n1位全加器_fa2_4_cout , \n1位全加器_fa2_5_cout ,
       \n1位全加器_fa2_6_cout , \n1位全加器_fa2_7_cout , \n1位全加器_fa2_8_cout ;

  xor xor_1 (out_6, Cout, \n1位全加器_fa2_2_cout );
  \_1位全加器_FA2  \u_1位全加器_fa2_1  (.Cout(Cout), .Si(S[7]), .Cin(\n1位全加器_fa2_2_cout ), .Xi(X[7]), .Yi(Y[7]));
  \_1位全加器_FA2  \u_1位全加器_fa2_2  (.Cout(\n1位全加器_fa2_2_cout ), .Si(S[6]), .Cin(\n1位全加器_fa2_3_cout ), .Xi(X[6]), .Yi(Y[6]));
  \_1位全加器_FA2  \u_1位全加器_fa2_3  (.Cout(\n1位全加器_fa2_3_cout ), .Si(S[5]), .Cin(\n1位全加器_fa2_4_cout ), .Xi(X[5]), .Yi(Y[5]));
  \_1位全加器_FA2  \u_1位全加器_fa2_4  (.Cout(\n1位全加器_fa2_4_cout ), .Si(S[4]), .Cin(\n1位全加器_fa2_5_cout ), .Xi(X[4]), .Yi(Y[4]));
  \_1位全加器_FA2  \u_1位全加器_fa2_5  (.Cout(\n1位全加器_fa2_5_cout ), .Si(S[3]), .Cin(\n1位全加器_fa2_6_cout ), .Xi(X[3]), .Yi(Y[3]));
  \_1位全加器_FA2  \u_1位全加器_fa2_6  (.Cout(\n1位全加器_fa2_6_cout ), .Si(S[2]), .Cin(\n1位全加器_fa2_7_cout ), .Xi(X[2]), .Yi(Y[2]));
  \_1位全加器_FA2  \u_1位全加器_fa2_7  (.Cout(\n1位全加器_fa2_7_cout ), .Si(S[1]), .Cin(\n1位全加器_fa2_8_cout ), .Xi(X[1]), .Yi(Y[1]));
  // Probe on X
  // Probe on Y
  // Probe on S
  \_1位全加器_FA2  \u_1位全加器_fa2_8  (.Cout(\n1位全加器_fa2_8_cout ), .Si(S[0]), .Cin(Cin), .Xi(X[0]), .Yi(Y[0]));
  // Probe on X
  // Probe on Y
  // Probe on S

  // Other names for the same wires on the sheet: OF = out_6

  // Notes on the sheet:
  //   X: pull=down
  //   Cin: pull=down
  //   Y: pull=down
  //   输入引脚区
  //   符号位
  //   输出引脚区
  //   8位串行加法器（2）
  //   Overflow
  //   +
  //   有符号加法
  //   +
  //   =
  //   无符号加法
endmodule

module \_8位串行可控加减法器_1  (
  input  [7:0] X,
  input  [7:0] Y,
  input  Sub,
  output [7:0] S,
  output Cout,
  output OF
);

  wire \n1位全加器_fa1_2_cout , \n1位全加器_fa1_3_cout , \n1位全加器_fa1_4_cout , \n1位全加器_fa1_5_cout ,
       \n1位全加器_fa1_6_cout , \n1位全加器_fa1_7_cout , \n1位全加器_fa1_8_cout , xor_2_out, xor_3_out, xor_4_out,
       xor_5_out, xor_6_out, xor_7_out, xor_8_out, xor_9_out;
  wire [8:0] \运算指示 ;

  Multiplexer #(.select(1), .width(9), .disabled("Z"), .enable("false")) multiplexer_1 (
    .in0(9'hba), .in1(9'h92), .out(\运算指示 ), .sel(Sub));
  xor xor_1 (OF, Cout, \n1位全加器_fa1_2_cout );
  \_1位全加器_FA1  \u_1位全加器_fa1_1  (.Cout(Cout), .Si(S[7]), .Cin(\n1位全加器_fa1_2_cout ), .Xi(X[7]), .Yi(xor_3_out));
  \_1位全加器_FA1  \u_1位全加器_fa1_2  (
    .Cout(\n1位全加器_fa1_2_cout ), .Si(S[6]), .Cin(\n1位全加器_fa1_3_cout ), .Xi(X[6]), .Yi(xor_2_out));
  xor xor_2 (xor_2_out, Sub, Y[6]);
  xor xor_3 (xor_3_out, Sub, Y[7]);
  \_1位全加器_FA1  \u_1位全加器_fa1_3  (
    .Cout(\n1位全加器_fa1_3_cout ), .Si(S[5]), .Cin(\n1位全加器_fa1_4_cout ), .Xi(X[5]), .Yi(xor_4_out));
  xor xor_4 (xor_4_out, Sub, Y[5]);
  \_1位全加器_FA1  \u_1位全加器_fa1_4  (
    .Cout(\n1位全加器_fa1_4_cout ), .Si(S[4]), .Cin(\n1位全加器_fa1_5_cout ), .Xi(X[4]), .Yi(xor_5_out));
  xor xor_5 (xor_5_out, Sub, Y[4]);
  \_1位全加器_FA1  \u_1位全加器_fa1_5  (
    .Cout(\n1位全加器_fa1_5_cout ), .Si(S[3]), .Cin(\n1位全加器_fa1_7_cout ), .Xi(X[3]), .Yi(xor_7_out));
  xor xor_6 (xor_6_out, Sub, Y[2]);
  xor xor_7 (xor_7_out, Sub, Y[3]);
  \_1位全加器_FA1  \u_1位全加器_fa1_6  (
    .Cout(\n1位全加器_fa1_6_cout ), .Si(S[1]), .Cin(\n1位全加器_fa1_8_cout ), .Xi(X[1]), .Yi(xor_8_out));
  \_1位全加器_FA1  \u_1位全加器_fa1_7  (
    .Cout(\n1位全加器_fa1_7_cout ), .Si(S[2]), .Cin(\n1位全加器_fa1_6_cout ), .Xi(X[2]), .Yi(xor_6_out));
  xor xor_8 (xor_8_out, Sub, Y[1]);
  // Probe on X
  // Probe on Y
  // Probe on S
  \_1位全加器_FA1  \u_1位全加器_fa1_8  (.Cout(\n1位全加器_fa1_8_cout ), .Si(S[0]), .Cin(Sub), .Xi(X[0]), .Yi(xor_9_out));
  xor xor_9 (xor_9_out, Sub, Y[0]);
  DotMatrix #(.inputtype("column"), .matrixcols(3), .matrixrows(3), .persist(0), .dotshape("square")) dotmatrix_1 (
    .col0(\运算指示 [8:6]), .col1(\运算指示 [5:3]), .col2(\运算指示 [2:0]));
  // Probe on X
  // Probe on Y
  // Probe on S

  // Notes on the sheet:
  //   S: pull=down
  //   OF: pull=down
  //   Y: pull=down
  //   Cout: pull=down
  //   Sub: pull=down
  //   X: pull=down
  //   输入引脚区
  //   符号位
  //   输出引脚区
  //   功能说明：8位串行可控加减法器          Sub=0：S=X+Y     Sub=1：S=X-Y        Cout为最高位进位位，OF为有符号溢出标志
  //   8位串行可控加减法器（1）
  //   =
  //   有符号
  //   =
  //   无符号
endmodule

module \_8位串行可控加减法器_2  (
  input  [7:0] X,
  input  [7:0] Y,
  input  Sub,
  output [7:0] S,
  output Cout,
  output OF
);

  wire \n1位全加器_fa2_2_cout , \n1位全加器_fa2_3_cout , \n1位全加器_fa2_4_cout , \n1位全加器_fa2_5_cout ,
       \n1位全加器_fa2_6_cout , \n1位全加器_fa2_7_cout , \n1位全加器_fa2_8_cout , xor_2_out, xor_3_out, xor_4_out,
       xor_5_out, xor_6_out, xor_7_out, xor_8_out, xor_9_out;
  wire [8:0] \运算指示 ;

  Multiplexer #(.select(1), .width(9), .disabled("Z"), .enable("false")) multiplexer_1 (
    .in0(9'hba), .in1(9'h92), .out(\运算指示 ), .sel(Sub));
  xor xor_1 (OF, Cout, \n1位全加器_fa2_2_cout );
  \_1位全加器_FA2  \u_1位全加器_fa2_1  (.Cout(Cout), .Si(S[7]), .Cin(\n1位全加器_fa2_2_cout ), .Xi(X[7]), .Yi(xor_3_out));
  \_1位全加器_FA2  \u_1位全加器_fa2_2  (
    .Cout(\n1位全加器_fa2_2_cout ), .Si(S[6]), .Cin(\n1位全加器_fa2_3_cout ), .Xi(X[6]), .Yi(xor_2_out));
  xor xor_2 (xor_2_out, Sub, Y[6]);
  xor xor_3 (xor_3_out, Sub, Y[7]);
  \_1位全加器_FA2  \u_1位全加器_fa2_3  (
    .Cout(\n1位全加器_fa2_3_cout ), .Si(S[5]), .Cin(\n1位全加器_fa2_4_cout ), .Xi(X[5]), .Yi(xor_4_out));
  \_1位全加器_FA2  \u_1位全加器_fa2_4  (
    .Cout(\n1位全加器_fa2_4_cout ), .Si(S[4]), .Cin(\n1位全加器_fa2_5_cout ), .Xi(X[4]), .Yi(xor_5_out));
  xor xor_4 (xor_4_out, Sub, Y[5]);
  \_1位全加器_FA2  \u_1位全加器_fa2_5  (
    .Cout(\n1位全加器_fa2_5_cout ), .Si(S[3]), .Cin(\n1位全加器_fa2_6_cout ), .Xi(X[3]), .Yi(xor_6_out));
  xor xor_5 (xor_5_out, Sub, Y[4]);
  \_1位全加器_FA2  \u_1位全加器_fa2_6  (
    .Cout(\n1位全加器_fa2_6_cout ), .Si(S[2]), .Cin(\n1位全加器_fa2_7_cout ), .Xi(X[2]), .Yi(xor_7_out));
  xor xor_6 (xor_6_out, Sub, Y[3]);
  xor xor_7 (xor_7_out, Sub, Y[2]);
  \_1位全加器_FA2  \u_1位全加器_fa2_7  (
    .Cout(\n1位全加器_fa2_7_cout ), .Si(S[1]), .Cin(\n1位全加器_fa2_8_cout ), .Xi(X[1]), .Yi(xor_8_out));
  xor xor_8 (xor_8_out, Sub, Y[1]);
  // Probe on X
  // Probe on Y
  // Probe on S
  \_1位全加器_FA2  \u_1位全加器_fa2_8  (.Cout(\n1位全加器_fa2_8_cout ), .Si(S[0]), .Cin(Sub), .Xi(X[0]), .Yi(xor_9_out));
  xor xor_9 (xor_9_out, Sub, Y[0]);
  DotMatrix #(.inputtype("column"), .matrixcols(3), .matrixrows(3), .persist(0), .dotshape("square")) dotmatrix_1 (
    .col0(\运算指示 [8:6]), .col1(\运算指示 [5:3]), .col2(\运算指示 [2:0]));
  // Probe on X
  // Probe on Y
  // Probe on S

  // Notes on the sheet:
  //   Y: pull=down
  //   Cout: pull=down
  //   Sub: pull=down
  //   OF: pull=down
  //   S: pull=down
  //   X: pull=down
  //   输入引脚区
  //   符号位
  //   输出引脚区
  //   功能说明：8位串行可控加减法器          Sub=0：S=X+Y     Sub=1：S=X-Y        Cout为最高位进位位，OF为有符号溢出标志
  //   8位串行可控加减法器（2）
  //   =
  //   有符号
  //   =
  //   无符号
endmodule

// FA1
module \_1位全加器_FA1  (
  input  Cin,
  input  Xi,
  input  Yi,
  output Cout,
  output Si
);

  wire AND_2_out, AND_out, XOR_2_out;

  or OR (Cout, AND_out, AND_2_out);
  and AND (AND_out, Xi, Yi);
  and AND_2 (AND_2_out, Cin, XOR_2_out);
  xor XOR (Si, Cin, XOR_2_out);
  xor XOR_2 (XOR_2_out, Xi, Yi);

  // Notes on the sheet:
  //   Yi: pull=down
  //   Xi: pull=down
  //   Cin: pull=down
  //   Si = Xi ^ Yi ^ Cin
  //   Cout = Xi Yi + Cin (Xi ^ Yi)
  //   1位全加器（FA1）
endmodule

// FA2
module \_1位全加器_FA2  (
  input  Cin,
  input  Xi,
  input  Yi,
  output Cout,
  output Si
);

  wire AND_2_out, AND_3_out, AND_out, XOR_2_out;

  and AND (AND_out, Cin, Xi);
  or OR (Cout, AND_out, AND_2_out, AND_3_out);
  and AND_2 (AND_2_out, Cin, Yi);
  and AND_3 (AND_3_out, Xi, Yi);
  xor XOR (Si, Cin, XOR_2_out);
  xor XOR_2 (XOR_2_out, Xi, Yi);

  // Notes on the sheet:
  //   Cin: pull=down
  //   Yi: pull=down
  //   Xi: pull=down
  //   Si = Xi ^ Yi ^ Cin
  //   Cout = Xi Yi + Cin Xi + Cin Yi
  //   1位全加器（FA2）
endmodule
