// Logisim project 阵列乘法器.circ as structural Verilog: 6 circuits, main circuit 5位无符号阵列乘法器（横向）
// 5位阵列乘法器（斜向）
module \_5位无符号阵列乘法器_斜向  (
  input  [4:0] X,
  input  [4:0] Y,
  output [9:0] \乘积 
);

  wire \n1位全加器fa_2_cout , \n1位全加器fa_2_si , \n1位全加器fa_3_cout , \n1位全加器fa_4_cout , \n1位全加器fa_4_si ,
       \n1位全加器fa_5_cout , \n1位全加器fa_5_si , \n1位全加器fa_6_cout , \n1位全加器fa_7_cout , \n1位全加器fa_7_si ,
       \n1位全加器fa_8_cout , \n1位全加器fa_8_si , \n1位全加器fa_9_cout , \n1位全加器fa_9_si , \n1位全加器fa_10_cout ,
       \n1位全加器fa_11_cout , \n1位全加器fa_11_si , \n1位全加器fa_12_cout , \n1位全加器fa_12_si , \n1位全加器fa_13_cout ,
       \n1位全加器fa_13_si , \n1位全加器fa_14_cout , \n1位全加器fa_15_cout , \n1位全加器fa_15_si , \n1位全加器fa_16_cout ,
       \n1位全加器fa_16_si , \n1位全加器fa_17_cout , \n1位全加器fa_18_cout , \n1位全加器fa_18_si , \n1位全加器fa_19_cout ,
       \n1位全加器fa_20_cout , X0Y1, X0Y2, X0Y3, X0Y4, X1Y0, X1Y1, X1Y2, X1Y3, X1Y4, X2Y0, X2Y1, X2Y2, X2Y3,
       X2Y4, X3Y0, X3Y1, X3Y2, X3Y3, X3Y4, X4Y0, X4Y1, X4Y2, X4Y3, X4Y4;

  \_1位全加器FA  \u_1位全加器fa_1  (.Cout(\乘积 [9]), .Si(\乘积 [8]), .Cin(\n1位全加器fa_2_cout ), .Xi(\n1位全加器fa_3_cout ), .Yi(X4Y4));
  \与门阵列  \u_与门阵列_1  (
    .X(X), .XY4({X4Y4, X3Y4, X2Y4, X1Y4, X0Y4}), .XY3({X4Y3, X3Y3, X2Y3, X1Y3, X0Y3}),
    .XY2({X4Y2, X3Y2, X2Y2, X1Y2, X0Y2}), .XY1({X4Y1, X3Y1, X2Y1, X1Y1, X0Y1}),
    .XY0({X4Y0, X3Y0, X2Y0, X1Y0, \乘积 [0]}), .Y(Y));
  \_1位全加器FA  \u_1位全加器fa_2  (
    .Cout(\n1位全加器fa_2_cout ), .Si(\n1位全加器fa_2_si ), .Cin(\n1位全加器fa_4_cout ), .Xi(X3Y4), .Yi(X4Y3));
  \_1位全加器FA  \u_1位全加器fa_3  (
    .Cout(\n1位全加器fa_3_cout ), .Si(\乘积 [7]), .Cin(\n1位全加器fa_5_cout ), .Xi(\n1位全加器fa_6_cout ),
    .Yi(\n1位全加器fa_2_si ));
  \_1位全加器FA  \u_1位全加器fa_4  (
    .Cout(\n1位全加器fa_4_cout ), .Si(\n1位全加器fa_4_si ), .Cin(\n1位全加器fa_7_cout ), .Xi(X3Y3), .Yi(X4Y2));
  \_1位全加器FA  \u_1位全加器fa_5  (
    .Cout(\n1位全加器fa_5_cout ), .Si(\n1位全加器fa_5_si ), .Cin(\n1位全加器fa_8_cout ), .Xi(X2Y4), .Yi(\n1位全加器fa_4_si ));
  \_1位全加器FA  \u_1位全加器fa_6  (
    .Cout(\n1位全加器fa_6_cout ), .Si(\乘积 [6]), .Cin(\n1位全加器fa_9_cout ), .Xi(\n1位全加器fa_10_cout ),
    .Yi(\n1位全加器fa_5_si ));
  \_1位全加器FA  \u_1位全加器fa_7  (
    .Cout(\n1位全加器fa_7_cout ), .Si(\n1位全加器fa_7_si ), .Cin(\n1位全加器fa_11_cout ), .Xi(X3Y2), .Yi(X4Y1));
  \_1位全加器FA  \u_1位全加器fa_8  (
    .Cout(\n1位全加器fa_8_cout ), .Si(\n1位全加器fa_8_si ), .Cin(\n1位全加器fa_12_cout ), .Xi(X2Y3), .Yi(\n1位全加器fa_7_si ));
  \_1位全加器FA  \u_1位全加器fa_9  (
    .Cout(\n1位全加器fa_9_cout ), .Si(\n1位全加器fa_9_si ), .Cin(\n1位全加器fa_13_cout ), .Xi(X1Y4), .Yi(\n1位全加器fa_8_si ));
  \_1位全加器FA  \u_1位全加器fa_10  (
    .Cout(\n1位全加器fa_10_cout ), .Si(\乘积 [5]), .Cin(\n1位全加器fa_14_cout ), .Xi(1'b0), .Yi(\n1位全加器fa_9_si ));
  \_1位全加器FA  \u_1位全加器fa_11  (.Cout(\n1位全加器fa_11_cout ), .Si(\n1位全加器fa_11_si ), .Cin(1'b0), .Xi(X3Y1), .Yi(X4Y0));
  \_1位全加器FA  \u_1位全加器fa_12  (
    .Cout(\n1位全加器fa_12_cout ), .Si(\n1位全加器fa_12_si ), .Cin(\n1位全加器fa_15_cout ), .Xi(X2Y2),
    .Yi(\n1位全加器fa_11_si ));
  \_1位全加器FA  \u_1位全加器fa_13  (
    .Cout(\n1位全加器fa_13_cout ), .Si(\n1位全加器fa_13_si ), .Cin(\n1位全加器fa_16_cout ), .Xi(X1Y3),
    .Yi(\n1位全加器fa_12_si ));
  \_1位全加器FA  \u_1位全加器fa_14  (
    .Cout(\n1位全加器fa_14_cout ), .Si(\乘积 [4]), .Cin(\n1位全加器fa_17_cout ), .Xi(X0Y4), .Yi(\n1位全加器fa_13_si ));
  \_1位全加器FA  \u_1位全加器fa_15  (.Cout(\n1位全加器fa_15_cout ), .Si(\n1位全加器fa_15_si ), .Cin(1'b0), .Xi(X2Y1), .Yi(X3Y0));
  \_1位全加器FA  \u_1位全加器fa_16  (
    .Cout(\n1位全加器fa_16_cout ), .Si(\n1位全加器fa_16_si ), .Cin(\n1位全加器fa_18_cout ), .Xi(X1Y2),
    .Yi(\n1位全加器fa_15_si ));
  \_1位全加器FA  \u_1位全加器fa_17  (
    .Cout(\n1位全加器fa_17_cout ), .Si(\乘积 [3]), .Cin(\n1位全加器fa_19_cout ), .Xi(X0Y3), .Yi(\n1位全加器fa_16_si ));
  \_1位全加器FA  \u_1位全加器fa_18  (.Cout(\n1位全加器fa_18_cout ), .Si(\n1位全加器fa_18_si ), .Cin(1'b0), .Xi(X1Y1), .Yi(X2Y0));
  \_1位全加器FA  \u_1位全加器fa_19  (
    .Cout(\n1位全加器fa_19_cout ), .Si(\乘积 [2]), .Cin(\n1位全加器fa_20_cout ), .Xi(X0Y2), .Yi(\n1位全加器fa_18_si ));
  \_1位全加器FA  \u_1位全加器fa_20  (.Cout(\n1位全加器fa_20_cout ), .Si(\乘积 [1]), .Cin(1'b0), .Xi(X0Y1), .Yi(X1Y0));
  // Probe on X
  // Probe on Y
  // Probe on \乘积 

  // Other names for the same wires on the sheet: P[9:0] = \乘积 ; P0 = \乘积 [0]; X0Y0 = \乘积 [0];
  //   XY0[4:0] = {X4Y0, X3Y0, X2Y0, X1Y0, \乘积 [0]}; P1 = \乘积 [1]; P2 = \乘积 [2]; P3 = \乘积 [3]; P4 = \乘积 [4];
  //   P5 = \乘积 [5]; P6 = \乘积 [6]; P7 = \乘积 [7]; P8 = \乘积 [8]; P9 = \乘积 [9]; XY1[4:0] = {X4Y1, X3Y1, X2Y1, X1Y1, X0Y1};
  //   XY2[4:0] = {X4Y2, X3Y2, X2Y2, X1Y2, X0Y2}; XY3[4:0] = {X4Y3, X3Y3, X2Y3, X1Y3, X0Y3};
  //   XY4[4:0] = {X4Y4, X3Y4, X2Y4, X1Y4, X0Y4}

  // Notes on the sheet:
  //   X: pull=down
  //   Y: pull=down
  //   输入引脚区
  //   输出引脚区
  //   ×
  //   =
  //   5位无符号阵列乘法器（斜向）
  //   验证
endmodule

// 5位阵列乘法器（横向）
module \_5位无符号阵列乘法器_横向  (
  input  [4:0] X,
  input  [4:0] Y,
  output [9:0] \乘积 
);

  wire \n1位全加器fa_2_cout , \n1位全加器fa_2_si , \n1位全加器fa_3_cout , \n1位全加器fa_4_cout , \n1位全加器fa_4_si ,
       \n1位全加器fa_5_cout , \n1位全加器fa_5_si , \n1位全加器fa_6_cout , \n1位全加器fa_7_cout , \n1位全加器fa_7_si ,
       \n1位全加器fa_8_cout , \n1位全加器fa_8_si , \n1位全加器fa_9_cout , \n1位全加器fa_9_si , \n1位全加器fa_10_cout ,
       \n1位全加器fa_11_cout , \n1位全加器fa_11_si , \n1位全加器fa_12_cout , \n1位全加器fa_12_si , \n1位全加器fa_13_cout ,
       \n1位全加器fa_13_si , \n1位全加器fa_14_cout , \n1位全加器fa_15_cout , \n1位全加器fa_15_si , \n1位全加器fa_16_cout ,
       \n1位全加器fa_16_si , \n1位全加器fa_17_cout , \n1位全加器fa_18_cout , \n1位全加器fa_18_si , \n1位全加器fa_19_cout ,
       \n1位全加器fa_20_cout , X0Y1, X0Y2, X0Y3, X0Y4, X1Y0, X1Y1, X1Y2, X1Y3, X1Y4, X2Y0, X2Y1, X2Y2, X2Y3,
       X2Y4, X3Y0, X3Y1, X3Y2, X3Y3, X3Y4, X4Y0, X4Y1, X4Y2, X4Y3, X4Y4;

  \_1位全加器FA  \u_1位全加器fa_1  (.Cout(\乘积 [9]), .Si(\乘积 [8]), .Cin(X4Y4), .Xi(\n1位全加器fa_3_cout ), .Yi(\n1位全加器fa_2_cout ));
  \与门阵列  \u_与门阵列_1  (
    .X(X), .XY4({X4Y4, X3Y4, X2Y4, X1Y4, X0Y4}), .XY3({X4Y3, X3Y3, X2Y3, X1Y3, X0Y3}),
    .XY2({X4Y2, X3Y2, X2Y2, X1Y2, X0Y2}), .XY1({X4Y1, X3Y1, X2Y1, X1Y1, X0Y1}),
    .XY0({X4Y0, X3Y0, X2Y0, X1Y0, \乘积 [0]}), .Y(Y));
  \_1位全加器FA  \u_1位全加器fa_2  (
    .Cout(\n1位全加器fa_2_cout ), .Si(\n1位全加器fa_2_si ), .Cin(X4Y3), .Xi(\n1位全加器fa_5_cout ), .Yi(\n1位全加器fa_4_cout ));
  \_1位全加器FA  \u_1位全加器fa_3  (
    .Cout(\n1位全加器fa_3_cout ), .Si(\乘积 [7]), .Cin(X3Y4), .Xi(\n1位全加器fa_6_cout ), .Yi(\n1位全加器fa_2_si ));
  \_1位全加器FA  \u_1位全加器fa_4  (
    .Cout(\n1位全加器fa_4_cout ), .Si(\n1位全加器fa_4_si ), .Cin(X4Y2), .Xi(\n1位全加器fa_8_cout ), .Yi(\n1位全加器fa_7_cout ));
  \_1位全加器FA  \u_1位全加器fa_5  (
    .Cout(\n1位全加器fa_5_cout ), .Si(\n1位全加器fa_5_si ), .Cin(X3Y3), .Xi(\n1位全加器fa_9_cout ), .Yi(\n1位全加器fa_4_si ));
  \_1位全加器FA  \u_1位全加器fa_6  (
    .Cout(\n1位全加器fa_6_cout ), .Si(\乘积 [6]), .Cin(X2Y4), .Xi(\n1位全加器fa_10_cout ), .Yi(\n1位全加器fa_5_si ));
  \_1位全加器FA  \u_1位全加器fa_7  (
    .Cout(\n1位全加器fa_7_cout ), .Si(\n1位全加器fa_7_si ), .Cin(X4Y1), .Xi(\n1位全加器fa_11_cout ), .Yi(1'b0));
  \_1位全加器FA  \u_1位全加器fa_8  (
    .Cout(\n1位全加器fa_8_cout ), .Si(\n1位全加器fa_8_si ), .Cin(X3Y2), .Xi(\n1位全加器fa_12_cout ), .Yi(\n1位全加器fa_7_si ));
  \_1位全加器FA  \u_1位全加器fa_9  (
    .Cout(\n1位全加器fa_9_cout ), .Si(\n1位全加器fa_9_si ), .Cin(X2Y3), .Xi(\n1位全加器fa_13_cout ), .Yi(\n1位全加器fa_8_si ));
  \_1位全加器FA  \u_1位全加器fa_10  (
    .Cout(\n1位全加器fa_10_cout ), .Si(\乘积 [5]), .Cin(X1Y4), .Xi(\n1位全加器fa_14_cout ), .Yi(\n1位全加器fa_9_si ));
  \_1位全加器FA  \u_1位全加器fa_11  (
    .Cout(\n1位全加器fa_11_cout ), .Si(\n1位全加器fa_11_si ), .Cin(X3Y1), .Xi(\n1位全加器fa_15_cout ), .Yi(X4Y0));
  \_1位全加器FA  \u_1位全加器fa_12  (
    .Cout(\n1位全加器fa_12_cout ), .Si(\n1位全加器fa_12_si ), .Cin(X2Y2), .Xi(\n1位全加器fa_16_cout ),
    .Yi(\n1位全加器fa_11_si ));
  \_1位全加器FA  \u_1位全加器fa_13  (
    .Cout(\n1位全加器fa_13_cout ), .Si(\n1位全加器fa_13_si ), .Cin(X1Y3), .Xi(\n1位全加器fa_17_cout ),
    .Yi(\n1位全加器fa_12_si ));
  \_1位全加器FA  \u_1位全加器fa_14  (.Cout(\n1位全加器fa_14_cout ), .Si(\乘积 [4]), .Cin(X0Y4), .Xi(1'b0), .Yi(\n1位全加器fa_13_si ));
  \_1位全加器FA  \u_1位全加器fa_15  (
    .Cout(\n1位全加器fa_15_cout ), .Si(\n1位全加器fa_15_si ), .Cin(X2Y1), .Xi(\n1位全加器fa_18_cout ), .Yi(X3Y0));
  \_1位全加器FA  \u_1位全加器fa_16  (
    .Cout(\n1位全加器fa_16_cout ), .Si(\n1位全加器fa_16_si ), .Cin(X1Y2), .Xi(\n1位全加器fa_19_cout ),
    .Yi(\n1位全加器fa_15_si ));
  \_1位全加器FA  \u_1位全加器fa_17  (.Cout(\n1位全加器fa_17_cout ), .Si(\乘积 [3]), .Cin(X0Y3), .Xi(1'b0), .Yi(\n1位全加器fa_16_si ));
  \_1位全加器FA  \u_1位全加器fa_18  (
    .Cout(\n1位全加器fa_18_cout ), .Si(\n1位全加器fa_18_si ), .Cin(X1Y1), .Xi(\n1位全加器fa_20_cout ), .Yi(X2Y0));
  \_1位全加器FA  \u_1位全加器fa_19  (.Cout(\n1位全加器fa_19_cout ), .Si(\乘积 [2]), .Cin(X0Y2), .Xi(1'b0), .Yi(\n1位全加器fa_18_si ));
  \_1位全加器FA  \u_1位全加器fa_20  (.Cout(\n1位全加器fa_20_cout ), .Si(\乘积 [1]), .Cin(X0Y1), .Xi(1'b0), .Yi(X1Y0));
  // Probe on X
  // Probe on Y
  // Probe on \乘积 

  // Other names for the same wires on the sheet: P[9:0] = \乘积 ; P0 = \乘积 [0]; X0Y0 = \乘积 [0];
  //   XY0[4:0] = {X4Y0, X3Y0, X2Y0, X1Y0, \乘积 [0]}; P1 = \乘积 [1]; P2 = \乘积 [2]; P3 = \乘积 [3]; P4 = \乘积 [4];
  //   P5 = \乘积 [5]; P6 = \乘积 [6]; P7 = \乘积 [7]; P8 = \乘积 [8]; P9 = \乘积 [9]; XY1[4:0] = {X4Y1, X3Y1, X2Y1, X1Y1, X0Y1};
  //   XY2[4:0] = {X4Y2, X3Y2, X2Y2, X1Y2, X0Y2}; XY3[4:0] = {X4Y3, X3Y3, X2Y3, X1Y3, X0Y3};
  //   XY4[4:0] = {X4Y4, X3Y4, X2Y4, X1Y4, X0Y4}

  // Notes on the sheet:
  //   X: pull=down
  //   Y: pull=down
  //   输入引脚区
  //   输出引脚区
  //   ×
  //   =
  //   5位无符号阵列乘法器（横向）
  //   验证
endmodule

module \_6位原码阵列乘法器  (
  input  [5:0] X,
  input  [5:0] Y,
  output [10:0] P
);

  wire [4:0] negator_1_out, negator_2_out, \X真值 , \Y真值 ;
  wire [9:0] negator_3_out, \P真值 ;

  \_5位无符号阵列乘法器_斜向  \u_5位无符号阵列乘法器_斜向_1  (.\乘积 (P[9:0]), .X(Y[4:0]), .Y(X[4:0]));
  xor xor_1 (P[10], X[5], Y[5]);
  Negator #(.width(5)) negator_1 (.in(X[4:0]), .out(negator_1_out));
  Negator #(.width(5)) negator_2 (.in(Y[4:0]), .out(negator_2_out));
  Negator #(.width(10)) negator_3 (.in(P[9:0]), .out(negator_3_out));
  // Probe on {X[5], \X真值 }
  // Probe on {Y[5], \Y真值 }
  // Probe on {P[10], \P真值 }
  Multiplexer #(.select(1), .width(5), .disabled("Z"), .enable("false")) multiplexer_1 (
    .in0(X[4:0]), .in1(negator_1_out), .out(\X真值 ), .sel(X[5]));
  Multiplexer #(.select(1), .width(5), .disabled("Z"), .enable("false")) multiplexer_2 (
    .in0(Y[4:0]), .in1(negator_2_out), .out(\Y真值 ), .sel(Y[5]));
  Multiplexer #(.select(1), .width(10), .disabled("Z"), .enable("false")) multiplexer_3 (
    .in0(P[9:0]), .in1(negator_3_out), .out(\P真值 ), .sel(P[10]));

  // Other names for the same wires on the sheet: P_t[9:0] = P[9:0]; Pf = P[10]; P真值[10] = P[10]; X4_0[4:0] = X[4:0];
  //   X真值[5] = X[5]; Y4_0[4:0] = Y[4:0]; Y真值[5] = Y[5]

  // Notes on the sheet:
  //   输入引脚区
  //   6位原码阵列乘法器
  //    功能说明：6位原码阵列乘法器          输入：X（6位原码）、Y（6位原码）          输出：P（11位原码）= X×Y
  //   输出引脚区
  //   验证
  //   ×
  //   =
endmodule

module \_6位补码阵列乘法器  (
  input  [5:0] X,
  input  [5:0] Y,
  output [11:0] P
);

  wire _0, _1024, X_0, X__32, Y_0, Y__32;
  wire [4:0] negator_1_out, negator_2_out;
  wire [9:0] minus_32X, minus_32Y, \n5位无符号阵列乘法器_斜向_1_乘积 , negator_3_out, negator_4_out, negator_5_out;
  wire [9:5] _32_X, _32_Y;
  wire [11:0] ANS, multiplexer_6_out, multiplexer_7_out, multiplexer_8_out;

  Negator #(.width(5)) negator_1 (.in(X[4:0]), .out(negator_1_out));
  Negator #(.width(5)) negator_2 (.in(Y[4:0]), .out(negator_2_out));
  Negator #(.width(10)) negator_3 (.in({_32_X, {5{1'b0}}}), .out(negator_3_out));
  // Probe on _32_X
  Multiplexer #(.select(1), .width(5), .disabled("Z"), .enable("false")) multiplexer_1 (
    .in0(X[4:0]), .in1(negator_1_out), .out(_32_X), .sel(X[5]));
  // Probe on _32_Y
  Multiplexer #(.select(1), .width(5), .disabled("Z"), .enable("false")) multiplexer_2 (
    .in0(Y[4:0]), .in1(negator_2_out), .out(_32_Y), .sel(Y[5]));
  Multiplexer #(.select(1), .width(10), .disabled("Z"), .enable("false")) multiplexer_3 (
    .in0({_32_X, {5{1'b0}}}), .in1(negator_3_out), .out(minus_32X), .sel(P[11]));
  \_5位无符号阵列乘法器_斜向  \u_5位无符号阵列乘法器_斜向_1  (.\乘积 (\n5位无符号阵列乘法器_斜向_1_乘积 ), .X(_32_X), .Y(_32_Y));
  Negator #(.width(10)) negator_4 (.in(\n5位无符号阵列乘法器_斜向_1_乘积 ), .out(negator_4_out));
  xor xor_1 (P[11], X[5], Y[5]);
  Negator #(.width(10)) negator_5 (.in({_32_Y, {5{1'b0}}}), .out(negator_5_out));
  // Probe on X
  // Probe on Y
  // Probe on ANS
  Multiplexer #(.select(1), .width(10), .disabled("Z"), .enable("false")) multiplexer_4 (
    .in0(\n5位无符号阵列乘法器_斜向_1_乘积 ), .in1(negator_4_out), .out(P[9:0]), .sel(P[11]));
  Multiplexer #(.select(1), .width(10), .disabled("Z"), .enable("false")) multiplexer_5 (
    .in0({_32_Y, {5{1'b0}}}), .in1(negator_5_out), .out(minus_32Y), .sel(P[11]));
  Multiplexer #(.select(1), .width(12), .disabled("Z"), .enable("false")) multiplexer_6 (
    .in0({{2{P[11]}}, P[9:0]}), .in1({{2{P[11]}}, minus_32Y}), .out(multiplexer_6_out), .sel(X__32));
  nor nor_1 (X_0, X[0], X[1], X[2], X[3], X[4], X[5]);
  Comparator #(.width(6), .mode("twosComplement")) comparator_1 (.a(X), .b(6'b100000), .eq(X__32));  // open: gt, lt
  Multiplexer #(.select(1), .width(12), .disabled("Z"), .enable("false")) multiplexer_7 (
    .in0(multiplexer_6_out), .in1({{2{P[11]}}, minus_32X}), .out(multiplexer_7_out), .sel(Y__32));
  nor nor_2 (Y_0, Y[0], Y[1], Y[2], Y[3], Y[4], Y[5]);
  or or_1 (_0, X_0, Y_0);
  Comparator #(.width(6), .mode("twosComplement")) comparator_2 (.a(Y), .b(6'b100000), .eq(Y__32));  // open: gt, lt
  and and_1 (_1024, X__32, Y__32);
  Multiplexer #(.select(1), .width(12), .disabled("Z"), .enable("false")) multiplexer_8 (
    .in0(multiplexer_7_out), .in1(12'h400), .out(multiplexer_8_out), .sel(_1024));
  Multiplexer #(.select(1), .width(12), .disabled("Z"), .enable("false")) multiplexer_9 (
    .in0(multiplexer_8_out), .in1({12{1'b0}}), .out(ANS), .sel(_0));

  assign P[10] = P[11];

  // Other names for the same wires on the sheet: X_t[4:0] = _32_X; Y_t[4:0] = _32_Y; minus_32X[11:10] = {2{P[11]}};
  //   minus_32Y[11:10] = {2{P[11]}}; P10 = P[11]; P9_0[9:0] = P[9:0]; X4_0[4:0] = X[4:0]; Y4_0[4:0] = Y[4:0]

  // Notes on the sheet:
  //   输入引脚区
  //   6位补码阵列乘法器
  //   求X和Y的绝对值
  //   求P的绝对值
  //    功能说明：6位补码阵列乘法器          输入：X（6位补码）、Y（6位补码）          输出：P（12位补码）= X×Y
  //   求-32特殊情况答案
  //   输出引脚区
  //   验证
  //   ×
  //   =
  //   判断是否为0
  //   判断X和Y是否为-32
  //   更正P的值
endmodule

module \与门阵列  (
  input  [4:0] X,
  input  [4:0] Y,
  output [4:0] XY0,
  output [4:0] XY1,
  output [4:0] XY2,
  output [4:0] XY3,
  output [4:0] XY4
);

  and and_1 (XY0[4], X[4], Y[0]);
  and and_2 (XY1[4], X[4], Y[1]);
  and and_3 (XY2[4], X[4], Y[2]);
  and and_4 (XY3[4], X[4], Y[3]);
  and and_5 (XY4[4], X[4], Y[4]);
  and and_6 (XY0[2], X[2], Y[0]);
  and and_7 (XY0[3], X[3], Y[0]);
  and and_8 (XY1[2], X[2], Y[1]);
  and and_9 (XY1[3], X[3], Y[1]);
  and and_10 (XY2[2], X[2], Y[2]);
  and and_11 (XY2[3], X[3], Y[2]);
  and and_12 (XY3[3], X[3], Y[3]);
  and and_13 (XY3[2], X[2], Y[3]);
  and and_14 (XY4[3], X[3], Y[4]);
  and and_15 (XY4[2], X[2], Y[4]);
  and and_16 (XY0[1], X[1], Y[0]);
  and and_17 (XY1[1], X[1], Y[1]);
  and and_18 (XY2[1], X[1], Y[2]);
  and and_19 (XY3[1], X[1], Y[3]);
  and and_20 (XY4[1], X[1], Y[4]);
  and and_21 (XY0[0], X[0], Y[0]);
  and and_22 (XY1[0], X[0], Y[1]);
  and and_23 (XY2[0], X[0], Y[2]);
  and and_24 (XY3[0], X[0], Y[3]);
  and and_25 (XY4[0], X[0], Y[4]);

  // Other names for the same wires on the sheet: X0Y0 = XY0[0]; X1Y0 = XY0[1]; X2Y0 = XY0[2]; X3Y0 = XY0[3];
  //   X4Y0 = XY0[4]; X0Y1 = XY1[0]; X1Y1 = XY1[1]; X2Y1 = XY1[2]; X3Y1 = XY1[3]; X4Y1 = XY1[4]; X0Y2 = XY2[0];
  //   X1Y2 = XY2[1]; X2Y2 = XY2[2]; X3Y2 = XY2[3]; X4Y2 = XY2[4]; X0Y3 = XY3[0]; X1Y3 = XY3[1]; X2Y3 = XY3[2];
  //   X3Y3 = XY3[3]; X4Y3 = XY3[4]; X0Y4 = XY4[0]; X1Y4 = XY4[1]; X2Y4 = XY4[2]; X3Y4 = XY4[3]; X4Y4 = XY4[4]

  // Notes on the sheet:
  //   5位乘法与门阵列
endmodule

module \_1位全加器FA  (
  input  Cin,
  input  Xi,
  input  Yi,
  output Cout,
  output Si
);

  wire AND_2_out, AND_out, XOR_2_out;

  or OR (Cout, AND_out, AND_2_out);
  and AND (AND_out, Xi, Yi);
  and AND_2 (AND_2_out, Cin, XOR_2_out);
  xor XOR (Si, Cin, XOR_2_out);
  xor XOR_2 (XOR_2_out, Xi, Yi);

  // Notes on the sheet:
  //   Cout = Xi Yi + Cin (Xi ^ Yi)
  //   Si = Xi ^ Yi ^ Cin
  //   1位全加器（FA）
endmodule
