// Logisim project cache 设计实验.circ as structural Verilog: 8 circuits, main circuit cache（直接相联映射）电路（4个cache块）
// 直接相联cache
module \cache_直接相联映射_电路_4个cache块  (
  input  [15:0] Addr,
  input  [31:0] BlockDataIn,
  input  BlkDataReady,
  input  CLK,
  output Miss,
  output [7:0] DataOut
);

  wire and_2_out, and_3_out, and_4_out, and_5_out, comparator_1_eq, Hit, L0, L1, L2, L3, Valid, VALID_2_q,
       VALID_3_q, VALID_4_q, VALID_q;
  wire [11:0] TAG_2_q, TAG_3_q, TAG_4_q, TAG_q, TagData;
  wire [31:0] DATA_COPY_2_q, DATA_COPY_3_q, DATA_COPY_q, SlotData, \数据块副本_q ;

  Multiplexer #(.select(2), .width(8), .disabled("Z"), .enable("true")) multiplexer_1 (
    .in0(SlotData[7:0]), .in1(SlotData[15:8]), .in2(SlotData[23:16]), .in3(SlotData[31:24]), .out(DataOut),
    .sel(Addr[1:0]), .en(Hit));
  assign Valid = L0 ? VALID_q : 1'bz;  // Controlled_Buffer controlled_buffer_1
  Register #(.width(1), .trigger("rising"), .Select("low")) u_VALID (
    .D(1'b1), .en(and_2_out), .Q(VALID_q), .clk(CLK));  // open: clr
  assign Valid = L1 ? VALID_2_q : 1'bz;  // Controlled_Buffer controlled_buffer_2
  Register #(.width(1), .trigger("rising"), .Select("low")) VALID_2 (
    .D(1'b1), .en(and_3_out), .Q(VALID_2_q), .clk(CLK));  // open: clr
  assign Valid = L2 ? VALID_3_q : 1'bz;  // Controlled_Buffer controlled_buffer_3
  Register #(.width(1), .trigger("rising"), .Select("low")) VALID_3 (
    .D(1'b1), .en(and_4_out), .Q(VALID_3_q), .clk(CLK));  // open: clr
  assign Valid = L3 ? VALID_4_q : 1'bz;  // Controlled_Buffer controlled_buffer_4
  Register #(.width(1), .trigger("rising"), .Select("low")) VALID_4 (
    .D(1'b1), .en(and_5_out), .Q(VALID_4_q), .clk(CLK));  // open: clr
  Register #(.width(12), .trigger("rising"), .Select("low")) TAG (
    .D(Addr[15:4]), .en(and_2_out), .Q(TAG_q), .clk(CLK));  // open: clr
  Register #(.width(12), .trigger("rising"), .Select("low")) TAG_2 (
    .D(Addr[15:4]), .en(and_3_out), .Q(TAG_2_q), .clk(CLK));  // open: clr
  Register #(.width(12), .trigger("rising"), .Select("low")) TAG_3 (
    .D(Addr[15:4]), .en(and_4_out), .Q(TAG_3_q), .clk(CLK));  // open: clr
  Register #(.width(12), .trigger("rising"), .Select("low")) TAG_4 (
    .D(Addr[15:4]), .en(and_5_out), .Q(TAG_4_q), .clk(CLK));  // open: clr
  Decoder #(.select(2), .tristate("false"), .disabled(0), .enable("false")) decoder_1 (
    .out0(L0), .out1(L1), .out2(L2), .out3(L3), .sel(Addr[3:2]));
  assign TagData = L0 ? TAG_q : 12'bz;  // Controlled_Buffer controlled_buffer_5
  assign TagData = L1 ? TAG_2_q : 12'bz;  // Controlled_Buffer controlled_buffer_6
  assign TagData = L2 ? TAG_3_q : 12'bz;  // Controlled_Buffer controlled_buffer_7
  assign TagData = L3 ? TAG_4_q : 12'bz;  // Controlled_Buffer controlled_buffer_8
  Comparator #(.width(12), .mode("twosComplement")) comparator_1 (
    .a(Addr[15:4]), .b(TagData), .eq(comparator_1_eq));  // open: gt, lt
  and and_1 (Hit, comparator_1_eq, Valid);
  Register #(.width(32), .trigger("rising"), .Select("low")) \u_数据块副本  (
    .D(BlockDataIn), .en(and_2_out), .Q(\数据块副本_q ), .clk(CLK));  // open: clr
  assign SlotData = L0 ? \数据块副本_q  : 32'bz;  // Controlled_Buffer controlled_buffer_9
  Register #(.width(32), .trigger("rising"), .Select("low")) DATA_COPY (
    .D(BlockDataIn), .en(and_3_out), .Q(DATA_COPY_q), .clk(CLK));  // open: clr
  assign SlotData = L1 ? DATA_COPY_q : 32'bz;  // Controlled_Buffer controlled_buffer_10
  assign SlotData = L2 ? DATA_COPY_2_q : 32'bz;  // Controlled_Buffer controlled_buffer_11
  Register #(.width(32), .trigger("rising"), .Select("low")) DATA_COPY_2 (
    .D(BlockDataIn), .en(and_4_out), .Q(DATA_COPY_2_q), .clk(CLK));  // open: clr
  assign SlotData = L3 ? DATA_COPY_3_q : 32'bz;  // Controlled_Buffer controlled_buffer_12
  Register #(.width(32), .trigger("rising"), .Select("low")) DATA_COPY_3 (
    .D(BlockDataIn), .en(and_5_out), .Q(DATA_COPY_3_q), .clk(CLK));  // open: clr
  not not_1 (Miss, Hit);
  and and_2 (and_2_out, L0, BlkDataReady);
  and and_3 (and_3_out, L1, BlkDataReady);
  and and_4 (and_4_out, L2, BlkDataReady);
  and and_5 (and_5_out, L3, BlkDataReady);

  // Other names for the same wires on the sheet: Blk[31:0] = BlockDataIn; BlkReady = BlkDataReady;
  //   Offset[1:0] = Addr[1:0]; 字节地址[15:0] = Addr; Index[1:0] = Addr[3:2]; Tag[11:0] = Addr[15:4]

  // Notes on the sheet:
  //   输入引脚区
  //   标记位
  //   有效位
  //   三态门控制多行输出
  //   行选中
  //   cache（直接相联映射）电路（4个cache块）
  //   块数据输出
  //   输出引脚区
endmodule

// 直接相联cache
module \cache_直接相联映射_电路_16个cache块  (
  input  [15:0] Addr,
  input  [31:0] BlockDataIn,
  input  BlkDataReady,
  input  CLK,
  output Miss,
  output [7:0] DataOut
);

  wire and_2_out, and_3_out, and_4_out, and_5_out, and_6_out, and_7_out, and_8_out, and_9_out, and_10_out,
       and_11_out, and_12_out, and_13_out, and_14_out, and_15_out, and_16_out, and_17_out, comparator_1_eq,
       Hit, L0, L1, L2, L3, L4, L5, L6, L7, L8, L9, L10, L11, L12, L13, L14, L15, Valid, VALID_2_q,
       VALID_3_q, VALID_4_q, VALID_5_q, VALID_6_q, VALID_7_q, VALID_8_q, VALID_9_q, VALID_10_q, VALID_11_q,
       VALID_12_q, VALID_13_q, VALID_14_q, VALID_15_q, VALID_16_q, VALID_q;
  wire [9:0] TAG_2_q, TAG_3_q, TAG_4_q, TAG_5_q, TAG_6_q, TAG_7_q, TAG_8_q, TAG_9_q, TAG_10_q, TAG_11_q,
       TAG_12_q, TAG_13_q, TAG_14_q, TAG_15_q, TAG_16_q, TAG_q, TagData;
  wire [31:0] DATA_COPY_2_q, DATA_COPY_3_q, DATA_COPY_4_q, DATA_COPY_5_q, DATA_COPY_6_q, DATA_COPY_7_q,
       DATA_COPY_8_q, DATA_COPY_9_q, DATA_COPY_10_q, DATA_COPY_11_q, DATA_COPY_12_q, DATA_COPY_13_q,
       DATA_COPY_14_q, DATA_COPY_q, SlotData, \数据块副本_2_q , \数据块副本_q ;

  Register #(.width(1), .trigger("rising"), .Select("low")) u_VALID (
    .D(1'b1), .en(and_2_out), .Q(VALID_q), .clk(CLK));  // open: clr
  Register #(.width(1), .trigger("rising"), .Select("low")) VALID_2 (
    .D(1'b1), .en(and_3_out), .Q(VALID_2_q), .clk(CLK));  // open: clr
  Register #(.width(1), .trigger("rising"), .Select("low")) VALID_3 (
    .D(1'b1), .en(and_4_out), .Q(VALID_3_q), .clk(CLK));  // open: clr
  Register #(.width(1), .trigger("rising"), .Select("low")) VALID_4 (
    .D(1'b1), .en(and_5_out), .Q(VALID_4_q), .clk(CLK));  // open: clr
  Register #(.width(1), .trigger("rising"), .Select("low")) VALID_5 (
    .D(1'b1), .en(and_6_out), .Q(VALID_5_q), .clk(CLK));  // open: clr
  Register #(.width(1), .trigger("rising"), .Select("low")) VALID_6 (
    .D(1'b1), .en(and_7_out), .Q(VALID_6_q), .clk(CLK));  // open: clr
  Register #(.width(1), .trigger("rising"), .Select("low")) VALID_7 (
    .D(1'b1), .en(and_8_out), .Q(VALID_7_q), .clk(CLK));  // open: clr
  Register #(.width(1), .trigger("rising"), .Select("low")) VALID_8 (
    .D(1'b1), .en(and_9_out), .Q(VALID_8_q), .clk(CLK));  // open: clr
  Multiplexer #(.select(2), .width(8), .disabled("Z"), .enable("true")) multiplexer_1 (
    .in0(SlotData[7:0]), .in1(SlotData[15:8]), .in2(SlotData[23:16]), .in3(SlotData[31:24]), .out(DataOut),
    .sel(Addr[1:0]), .en(Hit));
  assign Valid = L0 ? VALID_q : 1'bz;  // Controlled_Buffer controlled_buffer_1
  assign Valid = L1 ? VALID_2_q : 1'bz;  // Controlled_Buffer controlled_buffer_2
  assign Valid = L2 ? VALID_3_q : 1'bz;  // Controlled_Buffer controlled_buffer_3
  assign Valid = L3 ? VALID_4_q : 1'bz;  // Controlled_Buffer controlled_buffer_4
  assign Valid = L4 ? VALID_5_q : 1'bz;  // Controlled_Buffer controlled_buffer_5
  assign Valid = L5 ? VALID_6_q : 1'bz;  // Controlled_Buffer controlled_buffer_6
  assign Valid = L6 ? VALID_7_q : 1'bz;  // Controlled_Buffer controlled_buffer_7
  assign Valid = L7 ? VALID_8_q : 1'bz;  // Controlled_Buffer controlled_buffer_8
  assign TagData = L0 ? TAG_q : 10'bz;  // Controlled_Buffer controlled_buffer_9
  Register #(.width(10), .trigger("rising"), .Select("low")) TAG (
    .D(Addr[15:6]), .en(and_2_out), .Q(TAG_q), .clk(CLK));  // open: clr
  assign TagData = L1 ? TAG_2_q : 10'bz;  // Controlled_Buffer controlled_buffer_10
  Register #(.width(10), .trigger("rising"), .Select("low")) TAG_2 (
    .D(Addr[15:6]), .en(and_3_out), .Q(TAG_2_q), .clk(CLK));  // open: clr
  Register #(.width(10), .trigger("rising"), .Select("low")) TAG_3 (
    .D(Addr[15:6]), .en(and_4_out), .Q(TAG_3_q), .clk(CLK));  // open: clr
  assign TagData = L2 ? TAG_3_q : 10'bz;  // Controlled_Buffer controlled_buffer_11
  assign TagData = L3 ? TAG_4_q : 10'bz;  // Controlled_Buffer controlled_buffer_12
  Register #(.width(10), .trigger("rising"), .Select("low")) TAG_4 (
    .D(Addr[15:6]), .en(and_5_out), .Q(TAG_4_q), .clk(CLK));  // open: clr
  Register #(.width(10), .trigger("rising"), .Select("low")) TAG_5 (
    .D(Addr[15:6]), .en(and_6_out), .Q(TAG_5_q), .clk(CLK));  // open: clr
  assign TagData = L4 ? TAG_5_q : 10'bz;  // Controlled_Buffer controlled_buffer_13
  Register #(.width(10), .trigger("rising"), .Select("low")) TAG_6 (
    .D(Addr[15:6]), .en(and_7_out), .Q(TAG_6_q), .clk(CLK));  // open: clr
  assign TagData = L5 ? TAG_6_q : 10'bz;  // Controlled_Buffer controlled_buffer_14
  Register #(.width(10), .trigger("rising"), .Select("low")) TAG_7 (
    .D(Addr[15:6]), .en(and_8_out), .Q(TAG_7_q), .clk(CLK));  // open: clr
  assign TagData = L6 ? TAG_7_q : 10'bz;  // Controlled_Buffer controlled_buffer_15
  assign TagData = L7 ? TAG_8_q : 10'bz;  // Controlled_Buffer controlled_buffer_16
  Register #(.width(10), .trigger("rising"), .Select("low")) TAG_8 (
    .D(Addr[15:6]), .en(and_9_out), .Q(TAG_8_q), .clk(CLK));  // open: clr
  Decoder #(.select(4), .tristate("false"), .disabled(0), .enable("false")) decoder_1 (
    .out0(L0), .out1(L1), .out2(L2), .out3(L3), .out4(L4), .out5(L5), .out6(L6), .out7(L7), .out8(L8),
    .out9(L9), .out10(L10), .out11(L11), .out12(L12), .out13(L13), .out14(L14), .out15(L15), .sel(Addr[5:2]));
  Comparator #(.width(10), .mode("twosComplement")) comparator_1 (
    .a(Addr[15:6]), .b(TagData), .eq(comparator_1_eq));  // open: gt, lt
  and and_1 (Hit, comparator_1_eq, Valid);
  assign SlotData = L0 ? \数据块副本_q  : 32'bz;  // Controlled_Buffer controlled_buffer_17
  Register #(.width(32), .trigger("rising"), .Select("low")) \u_数据块副本  (
    .D(BlockDataIn), .en(and_2_out), .Q(\数据块副本_q ), .clk(CLK));  // open: clr
  Register #(.width(32), .trigger("rising"), .Select("low")) DATA_COPY (
    .D(BlockDataIn), .en(and_3_out), .Q(DATA_COPY_q), .clk(CLK));  // open: clr
  assign SlotData = L1 ? DATA_COPY_q : 32'bz;  // Controlled_Buffer controlled_buffer_18
  assign SlotData = L2 ? DATA_COPY_2_q : 32'bz;  // Controlled_Buffer controlled_buffer_19
  Register #(.width(32), .trigger("rising"), .Select("low")) DATA_COPY_2 (
    .D(BlockDataIn), .en(and_4_out), .Q(DATA_COPY_2_q), .clk(CLK));  // open: clr
  assign SlotData = L3 ? DATA_COPY_3_q : 32'bz;  // Controlled_Buffer controlled_buffer_20
  Register #(.width(32), .trigger("rising"), .Select("low")) DATA_COPY_3 (
    .D(BlockDataIn), .en(and_5_out), .Q(DATA_COPY_3_q), .clk(CLK));  // open: clr
  assign SlotData = L4 ? DATA_COPY_4_q : 32'bz;  // Controlled_Buffer controlled_buffer_21
  Register #(.width(32), .trigger("rising"), .Select("low")) DATA_COPY_4 (
    .D(BlockDataIn), .en(and_6_out), .Q(DATA_COPY_4_q), .clk(CLK));  // open: clr
  assign SlotData = L5 ? DATA_COPY_5_q : 32'bz;  // Controlled_Buffer controlled_buffer_22
  Register #(.width(32), .trigger("rising"), .Select("low")) DATA_COPY_5 (
    .D(BlockDataIn), .en(and_7_out), .Q(DATA_COPY_5_q), .clk(CLK));  // open: clr
  assign SlotData = L6 ? DATA_COPY_6_q : 32'bz;  // Controlled_Buffer controlled_buffer_23
  Register #(.width(32), .trigger("rising"), .Select("low")) DATA_COPY_6 (
    .D(BlockDataIn), .en(and_8_out), .Q(DATA_COPY_6_q), .clk(CLK));  // open: clr
  Register #(.width(32), .trigger("rising"), .Select("low")) DATA_COPY_7 (
    .D(BlockDataIn), .en(and_9_out), .Q(DATA_COPY_7_q), .clk(CLK));  // open: clr
  assign SlotData = L7 ? DATA_COPY_7_q : 32'bz;  // Controlled_Buffer controlled_buffer_24
  not not_1 (Miss, Hit);
  and and_2 (and_2_out, L0, BlkDataReady);
  and and_3 (and_3_out, L1, BlkDataReady);
  and and_4 (and_4_out, L2, BlkDataReady);
  and and_5 (and_5_out, L3, BlkDataReady);
  and and_6 (and_6_out, L4, BlkDataReady);
  and and_7 (and_7_out, L5, BlkDataReady);
  and and_8 (and_8_out, L6, BlkDataReady);
  and and_9 (and_9_out, L7, BlkDataReady);
  Register #(.width(1), .trigger("rising"), .Select("low")) VALID_9 (
    .D(1'b1), .en(and_10_out), .Q(VALID_9_q), .clk(CLK));  // open: clr
  assign Valid = L8 ? VALID_9_q : 1'bz;  // Controlled_Buffer controlled_buffer_25
  Register #(.width(1), .trigger("rising"), .Select("low")) VALID_10 (
    .D(1'b1), .en(and_11_out), .Q(VALID_10_q), .clk(CLK));  // open: clr
  assign Valid = L9 ? VALID_10_q : 1'bz;  // Controlled_Buffer controlled_buffer_26
  Register #(.width(1), .trigger("rising"), .Select("low")) VALID_11 (
    .D(1'b1), .en(and_12_out), .Q(VALID_11_q), .clk(CLK));  // open: clr
  assign Valid = L10 ? VALID_11_q : 1'bz;  // Controlled_Buffer controlled_buffer_27
  Register #(.width(1), .trigger("rising"), .Select("low")) VALID_12 (
    .D(1'b1), .en(and_13_out), .Q(VALID_12_q), .clk(CLK));  // open: clr
  assign Valid = L11 ? VALID_12_q : 1'bz;  // Controlled_Buffer controlled_buffer_28
  assign Valid = L12 ? VALID_13_q : 1'bz;  // Controlled_Buffer controlled_buffer_29
  Register #(.width(1), .trigger("rising"), .Select("low")) VALID_13 (
    .D(1'b1), .en(and_14_out), .Q(VALID_13_q), .clk(CLK));  // open: clr
  assign Valid = L13 ? VALID_14_q : 1'bz;  // Controlled_Buffer controlled_buffer_30
  Register #(.width(1), .trigger("rising"), .Select("low")) VALID_14 (
    .D(1'b1), .en(and_15_out), .Q(VALID_14_q), .clk(CLK));  // open: clr
  assign Valid = L14 ? VALID_15_q : 1'bz;  // Controlled_Buffer controlled_buffer_31
  Register #(.width(1), .trigger("rising"), .Select("low")) VALID_15 (
    .D(1'b1), .en(and_16_out), .Q(VALID_15_q), .clk(CLK));  // open: clr
  Register #(.width(1), .trigger("rising"), .Select("low")) VALID_16 (
    .D(1'b1), .en(and_17_out), .Q(VALID_16_q), .clk(CLK));  // open: clr
  assign Valid = L15 ? VALID_16_q : 1'bz;  // Controlled_Buffer controlled_buffer_32
  Register #(.width(10), .trigger("rising"), .Select("low")) TAG_9 (
    .D(Addr[15:6]), .en(and_10_out), .Q(TAG_9_q), .clk(CLK));  // open: clr
  Register #(.width(10), .trigger("rising"), .Select("low")) TAG_10 (
    .D(Addr[15:6]), .en(and_11_out), .Q(TAG_10_q), .clk(CLK));  // open: clr
  Register #(.width(10), .trigger("rising"), .Select("low")) TAG_11 (
    .D(Addr[15:6]), .en(and_12_out), .Q(TAG_11_q), .clk(CLK));  // open: clr
  Register #(.width(10), .trigger("rising"), .Select("low")) TAG_12 (
    .D(Addr[15:6]), .en(and_13_out), .Q(TAG_12_q), .clk(CLK));  // open: clr
  Register #(.width(10), .trigger("rising"), .Select("low")) TAG_13 (
    .D(Addr[15:6]), .en(and_14_out), .Q(TAG_13_q), .clk(CLK));  // open: clr
  Register #(.width(10), .trigger("rising"), .Select("low")) TAG_14 (
    .D(Addr[15:6]), .en(and_15_out), .Q(TAG_14_q), .clk(CLK));  // open: clr
  Register #(.width(10), .trigger("rising"), .Select("low")) TAG_15 (
    .D(Addr[15:6]), .en(and_16_out), .Q(TAG_15_q), .clk(CLK));  // open: clr
  Register #(.width(10), .trigger("rising"), .Select("low")) TAG_16 (
    .D(Addr[15:6]), .en(and_17_out), .Q(TAG_16_q), .clk(CLK));  // open: clr
  assign TagData = L8 ? TAG_9_q : 10'bz;  // Controlled_Buffer controlled_buffer_33
  assign TagData = L9 ? TAG_10_q : 10'bz;  // Controlled_Buffer controlled_buffer_34
  assign TagData = L10 ? TAG_11_q : 10'bz;  // Controlled_Buffer controlled_buffer_35
  assign TagData = L11 ? TAG_12_q : 10'bz;  // Controlled_Buffer controlled_buffer_36
  assign TagData = L12 ? TAG_13_q : 10'bz;  // Controlled_Buffer controlled_buffer_37
  assign TagData = L13 ? TAG_14_q : 10'bz;  // Controlled_Buffer controlled_buffer_38
  assign TagData = L14 ? TAG_15_q : 10'bz;  // Controlled_Buffer controlled_buffer_39
  assign TagData = L15 ? TAG_16_q : 10'bz;  // Controlled_Buffer controlled_buffer_40
  assign SlotData = L8 ? \数据块副本_2_q  : 32'bz;  // Controlled_Buffer controlled_buffer_41
  Register #(.width(32), .trigger("rising"), .Select("low")) \u_数据块副本_2  (
    .D(BlockDataIn), .en(and_10_out), .Q(\数据块副本_2_q ), .clk(CLK));  // open: clr
  Register #(.width(32), .trigger("rising"), .Select("low")) DATA_COPY_8 (
    .D(BlockDataIn), .en(and_11_out), .Q(DATA_COPY_8_q), .clk(CLK));  // open: clr
  assign SlotData = L9 ? DATA_COPY_8_q : 32'bz;  // Controlled_Buffer controlled_buffer_42
  Register #(.width(32), .trigger("rising"), .Select("low")) DATA_COPY_9 (
    .D(BlockDataIn), .en(and_12_out), .Q(DATA_COPY_9_q), .clk(CLK));  // open: clr
  assign SlotData = L10 ? DATA_COPY_9_q : 32'bz;  // Controlled_Buffer controlled_buffer_43
  Register #(.width(32), .trigger("rising"), .Select("low")) DATA_COPY_10 (
    .D(BlockDataIn), .en(and_13_out), .Q(DATA_COPY_10_q), .clk(CLK));  // open: clr
  assign SlotData = L11 ? DATA_COPY_10_q : 32'bz;  // Controlled_Buffer controlled_buffer_44
  assign SlotData = L12 ? DATA_COPY_11_q : 32'bz;  // Controlled_Buffer controlled_buffer_45
  Register #(.width(32), .trigger("rising"), .Select("low")) DATA_COPY_11 (
    .D(BlockDataIn), .en(and_14_out), .Q(DATA_COPY_11_q), .clk(CLK));  // open: clr
  assign SlotData = L13 ? DATA_COPY_12_q : 32'bz;  // Controlled_Buffer controlled_buffer_46
  Register #(.width(32), .trigger("rising"), .Select("low")) DATA_COPY_12 (
    .D(BlockDataIn), .en(and_15_out), .Q(DATA_COPY_12_q), .clk(CLK));  // open: clr
  assign SlotData = L14 ? DATA_COPY_13_q : 32'bz;  // Controlled_Buffer controlled_buffer_47
  Register #(.width(32), .trigger("rising"), .Select("low")) DATA_COPY_13 (
    .D(BlockDataIn), .en(and_16_out), .Q(DATA_COPY_13_q), .clk(CLK));  // open: clr
  assign SlotData = L15 ? DATA_COPY_14_q : 32'bz;  // Controlled_Buffer controlled_buffer_48
  Register #(.width(32), .trigger("rising"), .Select("low")) DATA_COPY_14 (
    .D(BlockDataIn), .en(and_17_out), .Q(DATA_COPY_14_q), .clk(CLK));  // open: clr
  and and_10 (and_10_out, L8, BlkDataReady);
  and and_11 (and_11_out, L9, BlkDataReady);
  and and_12 (and_12_out, L10, BlkDataReady);
  and and_13 (and_13_out, L11, BlkDataReady);
  and and_14 (and_14_out, L12, BlkDataReady);
  and and_15 (and_15_out, L13, BlkDataReady);
  and and_16 (and_16_out, L14, BlkDataReady);
  and and_17 (and_17_out, L15, BlkDataReady);

  // Other names for the same wires on the sheet: Blk[31:0] = BlockDataIn; BlkReady = BlkDataReady;
  //   Offset[1:0] = Addr[1:0]; 字节地址[15:0] = Addr; Index[3:0] = Addr[5:2]; Tag[9:0] = Addr[15:6]

  // Notes on the sheet:
  //   输入引脚区
  //   有效位
  //   三态门控制多行输出
  //   行选中
  //   标记位
  //   cache（直接相联映射）电路（16个cache块）
  //   块数据输出
  //   输出引脚区
  //   有效位
  //   行选中
  //   标记位
  //   三态门控制多行输出
  //   块数据输出
endmodule

module \Max2_归并比较_电路  (
  input  [15:0] Y,
  input  [15:0] X,
  input  [1:0] Y_num,
  input  [1:0] X_num,
  output [15:0] MAX,
  output [1:0] MAX_num
);

  wire comparator_1_eq, comparator_1_gt, or_1_out;

  Multiplexer #(.select(1), .width(16), .disabled("Z"), .enable("true")) multiplexer_1 (
    .in0(Y), .in1(X), .out(MAX), .sel(or_1_out), .en(1'b1));
  Comparator #(.width(16), .mode("unsigned")) comparator_1 (
    .a(X), .b(Y), .gt(comparator_1_gt), .eq(comparator_1_eq));  // open: lt
  or or_1 (or_1_out, comparator_1_gt, comparator_1_eq);
  Multiplexer #(.select(1), .width(2), .disabled("Z"), .enable("false")) multiplexer_2 (
    .in0(Y_num), .in1(X_num), .out(MAX_num), .sel(or_1_out));

  // Notes on the sheet:
  //   电路功能：输出两个输入中的较大值，并输出较大值的2位编号
  //   Max2（归并比较）电路
endmodule

module \Max3_归并比较_电路  (
  input  [15:0] Y,
  input  [15:0] X,
  input  [2:0] Y_num,
  input  [2:0] X_num,
  output [15:0] MAX,
  output [2:0] Max_num
);

  wire comparator_1_eq, comparator_1_gt, or_1_out;

  Multiplexer #(.select(1), .width(16), .disabled("Z"), .enable("false")) multiplexer_1 (
    .in0(Y), .in1(X), .out(MAX), .sel(or_1_out));
  Comparator #(.width(16), .mode("unsigned")) comparator_1 (
    .a(X), .b(Y), .gt(comparator_1_gt), .eq(comparator_1_eq));  // open: lt
  or or_1 (or_1_out, comparator_1_gt, comparator_1_eq);
  Multiplexer #(.select(1), .width(3), .disabled("Z"), .enable("false")) multiplexer_2 (
    .in0(Y_num), .in1(X_num), .out(Max_num), .sel(or_1_out));

  // Notes on the sheet:
  //   电路功能：输出两个输入中的较大值，并输出较大值的3位编号
  //   Max3（归并比较）电路
endmodule

module \cache块交换逻辑电路  (
  input  [15:0] Addr,
  input  [7:0] ByteDataIn,
  input  Miss,
  input  Enable,
  input  CLK,
  output [15:0] ByteAddrOut,
  output [31:0] BlockDataIn,
  output BlkDataReady
);

  wire \cache块交换状态机电路_1_byte0_ready , \cache块交换状态机电路_1_byte1_ready , \cache块交换状态机电路_1_byte2_ready ,
       \cache块交换状态机电路_1_byte3_ready ;
  wire [7:0] register_1_q, register_2_q, register_3_q, register_4_q;

  assign ByteAddrOut = \cache块交换状态机电路_1_byte0_ready  ? {Addr[15:2], 2'b00} : 16'bz;  // Controlled_Buffer controlled_buffer_1
  \cache块交换状态机电路  \cache块交换状态机电路_1  (
    .Clk(CLK), .Miss(Miss), .Byte0_Ready(\cache块交换状态机电路_1_byte0_ready ),
    .Byte1_Ready(\cache块交换状态机电路_1_byte1_ready ), .Byte2_Ready(\cache块交换状态机电路_1_byte2_ready ),
    .Byte3_Ready(\cache块交换状态机电路_1_byte3_ready ), .Byte0_Ready_2(BlkDataReady), .En(Enable));
  assign ByteAddrOut = \cache块交换状态机电路_1_byte1_ready  ? {Addr[15:2], 2'b01} : 16'bz;  // Controlled_Buffer controlled_buffer_2
  assign ByteAddrOut = \cache块交换状态机电路_1_byte2_ready  ? {Addr[15:2], 2'b10} : 16'bz;  // Controlled_Buffer controlled_buffer_3
  assign ByteAddrOut = \cache块交换状态机电路_1_byte3_ready  ? {Addr[15:2], 2'b11} : 16'bz;  // Controlled_Buffer controlled_buffer_4
  Register #(.width(8), .trigger("rising"), .Select("low")) register_1 (
    .D(ByteDataIn), .en(\cache块交换状态机电路_1_byte0_ready ), .Q(register_1_q), .clk(CLK));  // open: clr
  Register #(.width(8), .trigger("rising"), .Select("low")) register_2 (
    .D(ByteDataIn), .en(\cache块交换状态机电路_1_byte1_ready ), .Q(register_2_q), .clk(CLK));  // open: clr
  Register #(.width(8), .trigger("rising"), .Select("low")) register_3 (
    .D(ByteDataIn), .en(\cache块交换状态机电路_1_byte2_ready ), .Q(register_3_q), .clk(CLK));  // open: clr
  Register #(.width(8), .trigger("rising"), .Select("low")) register_4 (
    .D(ByteDataIn), .en(\cache块交换状态机电路_1_byte3_ready ), .Q(register_4_q), .clk(CLK));  // open: clr
  assign BlockDataIn = BlkDataReady ? {register_4_q, register_3_q, register_2_q, register_1_q} : 32'bz;  // Controlled_Buffer controlled_buffer_5

  // Notes on the sheet:
  //   cache块交换逻辑电路
  //   数据缓存寄存器
endmodule

module \cache块交换状态机电路  (
  input  En,
  input  Clk,
  input  Miss,
  output Byte0_Ready,
  output Byte1_Ready,
  output Byte2_Ready,
  output Byte3_Ready,
  output Byte0_Ready_2
);

  wire and_1_out, and_2_out, and_3_out, and_4_out, and_5_out, and_6_out, and_7_out, Next_Q0, Next_Q1,
       Next_Q2, Next_Q3, not_1_out, not_2_out, not_3_out, not_4_out, not_5_out, not_6_out, not_7_out,
       not_8_out, not_9_out, not_10_out, not_11_out, not_12_out, not_13_out, or_1_out, or_2_out, Q0, Q1, Q2,
       Q3;

  D_Flip_Flop #(.trigger("rising"), .Pre_Clr_Positions("LEGACY"), .NegatePresetClear("false"), .enable("true"), .NewFFLayout("false")) d_ff_1 (
    .clk(Clk), .D(Next_Q3), .Q(Q3), .en(En));  // open: Qn, preset, reset
  D_Flip_Flop #(.trigger("rising"), .Pre_Clr_Positions("LEGACY"), .NegatePresetClear("false"), .enable("true"), .NewFFLayout("false")) d_ff_2 (
    .clk(Clk), .D(Next_Q2), .Q(Q2), .en(En));  // open: Qn, preset, reset
  D_Flip_Flop #(.trigger("rising"), .Pre_Clr_Positions("LEGACY"), .NegatePresetClear("false"), .enable("true"), .NewFFLayout("false")) d_ff_3 (
    .clk(Clk), .D(Next_Q1), .Q(Q1), .en(En));  // open: Qn, preset, reset
  D_Flip_Flop #(.trigger("rising"), .Pre_Clr_Positions("LEGACY"), .NegatePresetClear("false"), .enable("true"), .NewFFLayout("false")) d_ff_4 (
    .clk(Clk), .D(Next_Q0), .Q(Q0), .en(En));  // open: Qn, preset, reset
  not not_1 (not_1_out, Q3);
  not not_2 (not_2_out, Q3);
  not not_3 (not_3_out, Q2);
  not not_4 (not_4_out, Q3);
  not not_5 (not_5_out, Q1);
  not not_6 (not_6_out, Q3);
  not not_7 (not_7_out, Q0);
  not not_8 (not_8_out, Q3);
  not not_9 (not_9_out, Q1);
  not not_10 (not_10_out, Q3);
  not not_11 (not_11_out, Q0);
  not not_12 (not_12_out, Q3);
  not not_13 (not_13_out, Q0);
  and and_1 (and_1_out, not_1_out, Q2, Q1, Q0);
  and and_2 (and_2_out, not_2_out, not_3_out, Q1, Q0);
  and and_3 (and_3_out, not_4_out, Q2, not_5_out);
  and and_4 (and_4_out, not_6_out, Q2, not_7_out);
  and and_5 (and_5_out, not_8_out, not_9_out, Q0);
  and and_6 (and_6_out, not_10_out, Q1, not_11_out);
  and and_7 (and_7_out, not_12_out, not_13_out);
  or or_1 (or_1_out, and_2_out, and_3_out, and_4_out);
  or or_2 (or_2_out, and_5_out, and_6_out);
  Decoder #(.select(4), .tristate("false"), .disabled(0), .enable("false")) decoder_1 (
    .out1(Byte0_Ready), .out3(Byte1_Ready), .out5(Byte2_Ready), .out7(Byte3_Ready), .out8(Byte0_Ready_2),
    .sel({Q3, Q2, Q1, Q0}));  // open: out0, out2, out4, out6, out9, out10, out11, out12, out13, out14, out15
  and and_8 (Next_Q3, and_1_out, Miss);
  and and_9 (Next_Q2, or_1_out, Miss);
  and and_10 (Next_Q1, Miss, or_2_out);
  and and_11 (Next_Q0, Miss, and_7_out);

  // Notes on the sheet:
  //   cache块交换状态机电路
endmodule

module \cache_直接相联映射_测试电路_4个cache块  (
  input  in_1
);

  wire and_2_out, Clk, comparator_1_lt, comparator_2_eq, comparator_3_eq, controlled_buffer_1_out, EN, Error,
       Go, Hit, Miss, or_1_out, RDY, Runing;
  wire [3:0] _1, _2, _3;
  wire [7:0] Dataout, \主存内容_data ;
  wire [9:0] \测试用例数 ;
  wire [15:0] adder_1_out, Addr, bit_extender_3_out, \cache块交换逻辑电路_1_byteaddrout , counter_1_q,
       subtractor_1_out, \命中次数 , \时钟周期数 , \校验和 , \缺失次数 , \访问次数 ;
  wire [31:0] bit_extender_1_out, bit_extender_2_out, BlkDataIn, divider_1_out, divider_2_out,
       multiplier_1_out;
  wire [31:4] divider_2_rem, divider_3_out, divider_3_rem;

  not not_1 (Hit, Miss);
  and and_1 (EN, Hit, Go);
  Clock #(.highDuration(1), .lowDuration(1)) clock_1 (.out(Clk));
  Counter #(.width(16), .max('hffff), .ongoal("wrap"), .trigger("rising"), .behavior("old")) counter_1 (
    .count(and_2_out), .Q(counter_1_q), .clk(Clk));  // open: load, D, carry, clr, preset
  and and_2 (and_2_out, Miss, RDY, Runing);
  Subtractor #(.width(16)) subtractor_1 (.a(\访问次数 ), .b(\缺失次数 ), .out(subtractor_1_out));  // open: bin, bout
  Comparator #(.width(16), .mode("twosComplement")) comparator_1 (
    .a(\访问次数 ), .b(\缺失次数 ), .lt(comparator_1_lt));  // open: gt, eq
  // Probe on \访问次数 
  // Probe on \测试用例数 
  Counter #(.width(10), .max('h3ff), .ongoal("wrap"), .trigger("rising"), .behavior("old")) \u_计数器  (
    .count(EN), .Q(\测试用例数 ), .clk(Clk));  // open: load, D, carry, clr, preset
  Register #(.width(16), .trigger("rising"), .Select("low")) register_1 (
    .D(counter_1_q), .en(EN), .Q(\缺失次数 ), .clk(Clk));  // open: clr
  Comparator #(.width(10), .mode("twosComplement")) comparator_2 (
    .a(\测试用例数 ), .b(10'h100), .eq(comparator_2_eq));  // open: gt, lt
  not not_2 (Runing, comparator_2_eq);
  Multiplexer #(.select(1), .width(16), .disabled(0), .enable("false")) multiplexer_1 (
    .in0(subtractor_1_out), .in1({16{1'b0}}), .out(\命中次数 ), .sel(comparator_1_lt));
  // Probe on \命中次数 
  // Probe on \时钟周期数 
  ROM #(.addrWidth(10), .dataWidth(16), .Select("high")) \u_主存地址  (.addr(\测试用例数 ), .data(Addr));
  Counter #(.width(16), .max('hffff), .ongoal("wrap"), .trigger("rising"), .behavior("old")) counter_2 (
    .count(EN), .Q(\访问次数 ), .clk(Clk));  // open: load, D, carry, clr, preset
  assign bit_extender_1_out = {{16{1'b0}}, \命中次数 };  // Bit_Extender bit_extender_1
  // Probe on Dataout
  Multiplier #(.width(32)) multiplier_1 (
    .a(bit_extender_1_out), .b(32'h64), .out(multiplier_1_out));  // open: cin, cout
  assign bit_extender_2_out = {{16{1'b0}}, \访问次数 };  // Bit_Extender bit_extender_2
  // Probe on \缺失次数 
  // Probe on \校验和 
  \cache_直接相联映射_电路_4个cache块  \cache_直接相联映射_电路_4个cache块_1  (
    .Addr(Addr), .BlockDataIn(BlkDataIn), .BlkDataReady(RDY), .CLK(Clk), .Miss(Miss), .DataOut(Dataout));
  assign bit_extender_3_out = {{8{1'b0}}, Dataout};  // Bit_Extender bit_extender_3
  Divider #(.width(32)) divider_1 (
    .a(multiplier_1_out), .b(bit_extender_2_out), .out(divider_1_out));  // open: upper, rem
  Adder #(.width(16)) adder_1 (.a(\校验和 ), .b(bit_extender_3_out), .out(adder_1_out));  // open: cin, cout
  LED #(.active("true")) \u_读数据出错  (.in(Error));
  Pull_Resistor #(.pull(1)) pull_resistor_1 (.node(Miss));
  LED #(.active("true")) \u_缺失  (.in(Miss));
  Register #(.width(16), .trigger("rising"), .Select("low")) \u_校验和  (
    .D(adder_1_out), .en(EN), .Q(\校验和 ), .clk(Clk));  // open: clr
  Divider #(.width(32)) divider_2 (
    .a(divider_1_out), .b(32'ha), .out(divider_2_out), .rem({divider_2_rem, _1}));  // open: upper
  \cache块交换逻辑电路  \cache块交换逻辑电路_1  (
    .Addr(Addr), .ByteDataIn(\主存内容_data ), .Miss(Miss), .Enable(Runing), .CLK(Clk),
    .ByteAddrOut(\cache块交换逻辑电路_1_byteaddrout ), .BlockDataIn(BlkDataIn), .BlkDataReady(RDY));
  // Probe on \校验和 
  Divider #(.width(32)) divider_3 (
    .a(divider_2_out), .b(32'ha), .out({divider_3_out, _3}), .rem({divider_3_rem, _2}));  // open: upper
  ROM #(.addrWidth(16), .dataWidth(8), .Select("high")) \u_主存内容  (
    .addr(\cache块交换逻辑电路_1_byteaddrout ), .data(\主存内容_data ));
  assign controlled_buffer_1_out = Hit ? comparator_3_eq : 1'bz;  // Controlled_Buffer controlled_buffer_1
  Comparator #(.width(8), .mode("twosComplement")) comparator_3 (
    .a(Addr[7:0]), .b(Dataout), .eq(comparator_3_eq));  // open: gt, lt
  Pull_Resistor #(.pull(1)) pull_resistor_2 (.node(controlled_buffer_1_out));
  Hex_Digit_Display hex_digit_display_1 (.value(_2));  // open: dp
  Hex_Digit_Display hex_digit_display_2 (.value(_3), .dp(1'b1));
  or or_1 (or_1_out, controlled_buffer_1_out, ~in_1);  // OR_Gate
  Counter #(.width(16), .max('hffff), .ongoal("wrap"), .trigger("rising"), .behavior("old")) counter_3 (
    .count(Runing), .Q(\时钟周期数 ), .clk(Clk));  // open: load, D, carry, clr, preset
  Hex_Digit_Display hex_digit_display_3 (.value(_1));  // open: dp
  // Probe on Addr
  LED #(.active("true")) led_1 (.in(RDY));
  // Probe on BlkDataIn
  // Probe on Dataout
  and and_3 (Go, Runing, or_1_out);
  not not_3 (Error, or_1_out);

  // Other names for the same wires on the sheet: 读错误暂停 = in_1

  // Notes on the sheet:
  //   contents of 主存地址 (hex, n*v repeats v):
  //   0 1 2 3 8 9 a b 10 11 12 13 20 21 22 23 8 9 a b 4 5 6 7 24 25 26 27 4 5 6 7 0 1 2 3 8 9 a b 8 9 a b
  //   20 21 22 23 28 29 2a 2b 24 25 26 27 4 5 6 7 24 25 26 27 0 1 2 3 8 9 a b 20 21 22 23 20 21 22 23 30
  //   31 32 33 4 5 6 7 24 25 26 27 4 5 6 7 0 1 2 3 8 9 a b 20 21 22 23 20 21 22 23 28 29 2a 2b 4 5 6 7 24
  //   25 26 27 24 25 26 27 0 1 2 3 8 9 a b 8 9 a b 20 21 22 23 30 31 32 33 4 5 6 7 24 25 26 27 24 25 26 27
  //   0 1 2 3 0 1 2 3 8 9 a b 20 21 22 23 28 29 2a 2b 4 5 6 7 24 25 26 27 4 5 6 7 0 1 2 3 8 9 a b 0 1 2 3
  //   20 21 22 23 30 31 32 33 24 25 26 27 4 5 6 7 24 25 26 27 0 1 2 3 8 9 a b 20 21 22 23 20 21 22 23 28
  //   29 2a 2b 4 5 6 7 24 25 26 27 4 5 6 7
  //   直接相联映射cache测试电路（4个cache块）
  //   命中率
  //   contents of 主存内容 (hex, n*v repeats v):
  //   0 1 2 3 4 5 6 7 8 9 a b c d e f 10 11 12 13 14 15 16 17 18 19 1a 1b 1c 1d 1e 1f 20 21 22 23 24 25 26
  //   27 28 29 2a 2b 2c 2d 2e 2f 30 31 32 33 34 35 36 37 38 39 3a 3b 3c 3d 3e 3f 40 41 42 43 44 45 46 47
  //   48 49 4a 4b 4c 4d 4e 4f 50 51 52 53 54 55 56 57 58 59 5a 5b 5c 5d 5e 5f 60 61 62 63 64 65 66 67 68
  //   69 6a 6b 6c 6d 6e 6f 70 71 72 73 74 75 76 77 78 79 7a 7b 7c 7d 7e 7f 80 81 82 83 84 85 86 87 88 89
  //   8a 8b 8c 8d 8e 8f 90 91 92 93 94 95 96 97 98 99 9a 9b 9c 9d 9e 9f a0 a1 a2 a3 a4 a5 a6 a7 a8 a9 aa
  //   ab ac ad ae af b0 b1 b2 b3 b4 b5 b6 b7 b8 b9 ba bb bc bd be bf c0 c1 c2 c3 c4 c5 c6 c7 c8 c9 ca cb
  //   cc cd ce cf d0 d1 d2 d3 d4 d5 d6 d7 d8 d9 da db dc dd de df e0 e1 e2 e3 e4 e5 e6 e7 e8 e9 ea eb ec
  //   ed ee ef f0 f1 f2 f3 f4 f5 f6 f7 f8 f9 fa fb fc fd fe ff 0 1 2 3 4 5 6 7 8 9 a b c d e f 10 11 12 13
  //   14 15 16 17 18 19 1a 1b 1c 1d 1e 1f 20 21 22 23 24 25 26 27 28 29 2a 2b 2c 2d 2e 2f 30 31 32 33 34
  //   35 36 37 38 39 3a 3b 3c 3d 3e 3f 40 41 42 43 44 45 46 47 48 49 4a 4b 4c 4d 4e 4f 50 51 52 53 54 55
  //   56 57 58 59 5a 5b 5c 5d 5e 5f 60 61 62 63 64 65 66 67 68 69 6a 6b 6c 6d 6e 6f 70 71 72 73 74 75 76
  //   77 78 79 7a 7b 7c 7d 7e 7f 80 81 82 83 84 85 86 87 88 89 8a 8b 8c 8d 8e 8f 90 91 92 93 94 95 96 97
  //   98 99 9a 9b 9c 9d 9e 9f a0 a1 a2 a3 a4 a5 a6 a7 a8 a9 aa ab ac ad ae af b0 b1 b2 b3 b4 b5 b6 b7 b8
  //   b9 ba bb bc bd be bf c0 c1 c2 c3 c4 c5 c6 c7 c8 c9 ca cb cc cd ce cf d0 d1 d2 d3 d4 d5 d6 d7 d8 d9
  //   da db dc dd de df e0 e1 e2 e3 e4 e5 e6 e7 e8 e9 ea eb ec ed ee ef f0 f1 f2 f3 f4 f5 f6 f7 f8 f9 fa
  //   fb fc fd fe ff 0 1 2 3 4 5 6 7 8 9 a b c d e f 10 11 12 13 14 15 16 17 18 19 1a 1b 1c 1d 1e 1f 20 21
  //   22 23 24 25 26 27 28 29 2a 2b 2c 2d 2e 2f 30 31 32 33 34 35 36 37 38 39 3a 3b 3c 3d 3e 3f 40 41 42
  //   43 44 45 46 47 48 49 4a 4b 4c 4d 4e 4f 50 51 52 53 54 55 56 57 58 59 5a 5b 5c 5d 5e 5f 60 61 62 63
  //   64 65 66 67 68 69 6a 6b 6c 6d 6e 6f 70 71 72 73 74 75 76 77 78 79 7a 7b 7c 7d 7e 7f 80 81 82 83 84
  //   85 86 87 88 89 8a 8b 8c 8d 8e 8f 90 91 92 93 94 95 96 97 98 99 9a 9b 9c 9d 9e 9f a0 a1 a2 a3 a4 a5
  //   a6 a7 a8 a9 aa ab ac ad ae af b0 b1 b2 b3 b4 b5 b6 b7 b8 b9 ba bb bc bd be bf c0 c1 c2 c3 c4 c5 c6
  //   c7 c8 c9 ca cb cc cd ce cf d0 d1 d2 d3 d4 d5 d6 d7 d8 d9 da db dc dd de df e0 e1 e2 e3 e4 e5 e6 e7
  //   e8 e9 ea eb ec ed ee ef f0 f1 f2 f3 f4 f5 f6 f7 f8 f9 fa fb fc fd fe ff 0 1 2 3 4 5 6 7 8 9 a b c d
  //   e f 10 11 12 13 14 15 16 17 18 19 1a 1b 1c 1d 1e 1f 20 21 22 23 24 25 26 27 28 29 2a 2b 2c 2d 2e 2f
  //   30 31 32 33 34 35 36 37 38 39 3a 3b 3c 3d 3e 3f 40 41 42 43 44 45 46 47 48 49 4a 4b 4c 4d 4e 4f 50
  //   51 52 53 54 55 56 57 58 59 5a 5b 5c 5d 5e 5f 60 61 62 63 64 65 66 67 68 69 6a 6b 6c 6d 6e 6f 70 71
  //   72 73 74 75 76 77 78 79 7a 7b 7c 7d 7e 7f 80 81 82 83 84 85 86 87 88 89 8a 8b 8c 8d 8e 8f 90 91 92
  //   93 94 95 96 97 98 99 9a 9b 9c 9d 9e 9f a0 a1 a2 a3 a4 a5 a6 a7 a8 a9 aa ab ac ad ae af b0 b1 b2 b3
  //   b4 b5 b6 b7 b8 b9 ba bb bc bd be bf c0 c1 c2 c3 c4 c5 c6 c7 c8 c9 ca cb cc cd ce cf d0 d1 d2 d3 d4
  //   d5 d6 d7 d8 d9 da db dc dd de df e0 e1 e2 e3 e4 e5 e6 e7 e8 e9 ea eb ec ed ee ef f0 f1 f2 f3 f4 f5
  //   f6 f7 f8 f9 fa fb fc fd fe ff 0 1 2 3 4 5 6 7 8 9 a b c d e f 10 11 12 13 14 15 16 17 18 19 1a 1b 1c
  //   1d 1e 1f 20 21 22 23 24 25 26 27 28 29 2a 2b 2c 2d 2e 2f 30 31 32 33 34 35 36 37 38 39 3a 3b 3c 3d
  //   3e 3f 40 41 42 43 44 45 46 47 48 49 4a 4b 4c 4d 4e 4f 50 51 52 53 54 55 56 57 58 59 5a 5b 5c 5d 5e
  //   5f 60 61 62 63 64 65 66 67 68 69 6a 6b 6c 6d 6e 6f 70 71 72 73 74 75 76 77 78 79 7a 7b 7c 7d 7e 7f
  //   80 81 82 83 84 85 86 87 88 89 8a 8b 8c 8d 8e 8f 90 91 92 93 94 95 96 97 98 99 9a 9b 9c 9d 9e 9f a0
  //   a1 a2 a3 a4 a5 a6 a7 a8 a9 aa ab ac ad ae af b0 b1 b2 b3 b4 b5 b6 b7 b8 b9 ba bb bc bd be bf c0 c1
  //   c2 c3 c4 c5 c6 c7 c8 c9 ca cb cc cd ce cf d0 d1 d2 d3 d4 d5 d6 d7 d8 d9 da db dc dd de df e0 e1 e2
  //   e3 e4 e5 e6 e7 e8 e9 ea eb ec ed ee ef f0 f1 f2 f3 f4 f5 f6 f7 f8 f9 fa fb fc fd fe ff
  //   cache模拟器
endmodule

module \cache_直接相联映射_测试电路_16个cache块  (
  input  in_1
);

  wire and_2_out, Clk, comparator_1_lt, comparator_2_eq, comparator_3_eq, controlled_buffer_1_out, EN, Error,
       Go, Hit, Miss, or_1_out, RDY, Runing;
  wire [3:0] _1, _2, _3;
  wire [7:0] Dataout, \主存内容_data ;
  wire [9:0] \测试用例数 ;
  wire [15:0] adder_1_out, Addr, bit_extender_3_out, \cache块交换逻辑电路_1_byteaddrout , counter_1_q,
       subtractor_1_out, \命中次数 , \时钟周期数 , \校验和 , \缺失次数 , \访问次数 ;
  wire [31:0] bit_extender_1_out, bit_extender_2_out, BlkDataIn, divider_1_out, divider_2_out,
       multiplier_1_out;
  wire [31:4] divider_2_rem, divider_3_out, divider_3_rem;

  not not_1 (Hit, Miss);
  and and_1 (EN, Hit, Go);
  Clock #(.highDuration(1), .lowDuration(1)) clock_1 (.out(Clk));
  Counter #(.width(16), .max('hffff), .ongoal("wrap"), .trigger("rising"), .behavior("old")) counter_1 (
    .count(and_2_out), .Q(counter_1_q), .clk(Clk));  // open: load, D, carry, clr, preset
  and and_2 (and_2_out, Miss, RDY, Runing);
  Subtractor #(.width(16)) subtractor_1 (.a(\访问次数 ), .b(\缺失次数 ), .out(subtractor_1_out));  // open: bin, bout
  Comparator #(.width(16), .mode("twosComplement")) comparator_1 (
    .a(\访问次数 ), .b(\缺失次数 ), .lt(comparator_1_lt));  // open: gt, eq
  // Probe on \访问次数 
  // Probe on \测试用例数 
  Counter #(.width(10), .max('h3ff), .ongoal("wrap"), .trigger("rising"), .behavior("old")) \u_计数器  (
    .count(EN), .Q(\测试用例数 ), .clk(Clk));  // open: load, D, carry, clr, preset
  Register #(.width(16), .trigger("rising"), .Select("low")) register_1 (
    .D(counter_1_q), .en(EN), .Q(\缺失次数 ), .clk(Clk));  // open: clr
  not not_2 (Runing, comparator_2_eq);
  Comparator #(.width(10), .mode("twosComplement")) comparator_2 (
    .a(\测试用例数 ), .b(10'h100), .eq(comparator_2_eq));  // open: gt, lt
  Multiplexer #(.select(1), .width(16), .disabled(0), .enable("false")) multiplexer_1 (
    .in0(subtractor_1_out), .in1({16{1'b0}}), .out(\命中次数 ), .sel(comparator_1_lt));
  // Probe on \命中次数 
  // Probe on \时钟周期数 
  ROM #(.addrWidth(10), .dataWidth(16), .Select("high")) \u_主存地址  (.addr(\测试用例数 ), .data(Addr));
  Counter #(.width(16), .max('hffff), .ongoal("wrap"), .trigger("rising"), .behavior("old")) counter_2 (
    .count(EN), .Q(\访问次数 ), .clk(Clk));  // open: load, D, carry, clr, preset
  assign bit_extender_1_out = {{16{1'b0}}, \命中次数 };  // Bit_Extender bit_extender_1
  // Probe on Dataout
  Multiplier #(.width(32)) multiplier_1 (
    .a(bit_extender_1_out), .b(32'h64), .out(multiplier_1_out));  // open: cin, cout
  assign bit_extender_2_out = {{16{1'b0}}, \访问次数 };  // Bit_Extender bit_extender_2
  // Probe on \缺失次数 
  // Probe on \校验和 
  \cache_直接相联映射_电路_16个cache块  \cache_直接相联映射_电路_16个cache块_1  (
    .Addr(Addr), .BlockDataIn(BlkDataIn), .BlkDataReady(RDY), .CLK(Clk), .Miss(Miss), .DataOut(Dataout));
  assign bit_extender_3_out = {{8{1'b0}}, Dataout};  // Bit_Extender bit_extender_3
  Divider #(.width(32)) divider_1 (
    .a(multiplier_1_out), .b(bit_extender_2_out), .out(divider_1_out));  // open: upper, rem
  Adder #(.width(16)) adder_1 (.a(\校验和 ), .b(bit_extender_3_out), .out(adder_1_out));  // open: cin, cout
  LED #(.active("true")) \u_读数据出错  (.in(Error));
  LED #(.active("true")) \u_缺失  (.in(Miss));
  Pull_Resistor #(.pull(1)) pull_resistor_1 (.node(Miss));
  Register #(.width(16), .trigger("rising"), .Select("low")) \u_校验和  (
    .D(adder_1_out), .en(EN), .Q(\校验和 ), .clk(Clk));  // open: clr
  Divider #(.width(32)) divider_2 (
    .a(divider_1_out), .b(32'ha), .out(divider_2_out), .rem({divider_2_rem, _1}));  // open: upper
  \cache块交换逻辑电路  \cache块交换逻辑电路_1  (
    .Addr(Addr), .ByteDataIn(\主存内容_data ), .Miss(Miss), .Enable(Runing), .CLK(Clk),
    .ByteAddrOut(\cache块交换逻辑电路_1_byteaddrout ), .BlockDataIn(BlkDataIn), .BlkDataReady(RDY));
  // Probe on \校验和 
  Divider #(.width(32)) divider_3 (
    .a(divider_2_out), .b(32'ha), .out({divider_3_out, _3}), .rem({divider_3_rem, _2}));  // open: upper
  ROM #(.addrWidth(16), .dataWidth(8), .Select("high")) \u_主存内容  (
    .addr(\cache块交换逻辑电路_1_byteaddrout ), .data(\主存内容_data ));
  assign controlled_buffer_1_out = Hit ? comparator_3_eq : 1'bz;  // Controlled_Buffer controlled_buffer_1
  Comparator #(.width(8), .mode("twosComplement")) comparator_3 (
    .a(Addr[7:0]), .b(Dataout), .eq(comparator_3_eq));  // open: gt, lt
  Pull_Resistor #(.pull(1)) pull_resistor_2 (.node(controlled_buffer_1_out));
  Hex_Digit_Display hex_digit_display_1 (.value(_3), .dp(1'b1));
  Hex_Digit_Display hex_digit_display_2 (.value(_2));  // open: dp
  or or_1 (or_1_out, controlled_buffer_1_out, ~in_1);  // OR_Gate
  Counter #(.width(16), .max('hffff), .ongoal("wrap"), .trigger("rising"), .behavior("old")) counter_3 (
    .count(Runing), .Q(\时钟周期数 ), .clk(Clk));  // open: load, D, carry, clr, preset
  Hex_Digit_Display hex_digit_display_3 (.value(_1));  // open: dp
  // Probe on Addr
  LED #(.active("true")) led_1 (.in(RDY));
  // Probe on BlkDataIn
  // Probe on Dataout
  and and_3 (Go, Runing, or_1_out);
  not not_3 (Error, or_1_out);

  // Other names for the same wires on the sheet: 读错误暂停 = in_1

  // Notes on the sheet:
  //   contents of 主存地址 (hex, n*v repeats v):
  //   0 1 2 3 8 9 a b 10 11 12 13 20 21 22 23 8 9 a b 4 5 6 7 24 25 26 27 4 5 6 7 0 1 2 3 8 9 a b 8 9 a b
  //   20 21 22 23 28 29 2a 2b 24 25 26 27 4 5 6 7 24 25 26 27 0 1 2 3 8 9 a b 20 21 22 23 20 21 22 23 30
  //   31 32 33 4 5 6 7 24 25 26 27 4 5 6 7 0 1 2 3 8 9 a b 20 21 22 23 20 21 22 23 28 29 2a 2b 4 5 6 7 24
  //   25 26 27 24 25 26 27 0 1 2 3 8 9 a b 8 9 a b 20 21 22 23 30 31 32 33 4 5 6 7 24 25 26 27 24 25 26 27
  //   0 1 2 3 0 1 2 3 8 9 a b 20 21 22 23 28 29 2a 2b 4 5 6 7 24 25 26 27 4 5 6 7 0 1 2 3 8 9 a b 0 1 2 3
  //   20 21 22 23 30 31 32 33 24 25 26 27 4 5 6 7 24 25 26 27 0 1 2 3 8 9 a b 20 21 22 23 20 21 22 23 28
  //   29 2a 2b 4 5 6 7 24 25 26 27 4 5 6 7
  //   直接相联映射cache测试电路（16个cache块）
  //   命中率
  //   contents of 主存内容 (hex, n*v repeats v):
  //   0 1 2 3 4 5 6 7 8 9 a b c d e f 10 11 12 13 14 15 16 17 18 19 1a 1b 1c 1d 1e 1f 20 21 22 23 24 25 26
  //   27 28 29 2a 2b 2c 2d 2e 2f 30 31 32 33 34 35 36 37 38 39 3a 3b 3c 3d 3e 3f 40 41 42 43 44 45 46 47
  //   48 49 4a 4b 4c 4d 4e 4f 50 51 52 53 54 55 56 57 58 59 5a 5b 5c 5d 5e 5f 60 61 62 63 64 65 66 67 68
  //   69 6a 6b 6c 6d 6e 6f 70 71 72 73 74 75 76 77 78 79 7a 7b 7c 7d 7e 7f 80 81 82 83 84 85 86 87 88 89
  //   8a 8b 8c 8d 8e 8f 90 91 92 93 94 95 96 97 98 99 9a 9b 9c 9d 9e 9f a0 a1 a2 a3 a4 a5 a6 a7 a8 a9 aa
  //   ab ac ad ae af b0 b1 b2 b3 b4 b5 b6 b7 b8 b9 ba bb bc bd be bf c0 c1 c2 c3 c4 c5 c6 c7 c8 c9 ca cb
  //   cc cd ce cf d0 d1 d2 d3 d4 d5 d6 d7 d8 d9 da db dc dd de df e0 e1 e2 e3 e4 e5 e6 e7 e8 e9 ea eb ec
  //   ed ee ef f0 f1 f2 f3 f4 f5 f6 f7 f8 f9 fa fb fc fd fe ff 0 1 2 3 4 5 6 7 8 9 a b c d e f 10 11 12 13
  //   14 15 16 17 18 19 1a 1b 1c 1d 1e 1f 20 21 22 23 24 25 26 27 28 29 2a 2b 2c 2d 2e 2f 30 31 32 33 34
  //   35 36 37 38 39 3a 3b 3c 3d 3e 3f 40 41 42 43 44 45 46 47 48 49 4a 4b 4c 4d 4e 4f 50 51 52 53 54 55
  //   56 57 58 59 5a 5b 5c 5d 5e 5f 60 61 62 63 64 65 66 67 68 69 6a 6b 6c 6d 6e 6f 70 71 72 73 74 75 76
  //   77 78 79 7a 7b 7c 7d 7e 7f 80 81 82 83 84 85 86 87 88 89 8a 8b 8c 8d 8e 8f 90 91 92 93 94 95 96 97
  //   98 99 9a 9b 9c 9d 9e 9f a0 a1 a2 a3 a4 a5 a6 a7 a8 a9 aa ab ac ad ae af b0 b1 b2 b3 b4 b5 b6 b7 b8
  //   b9 ba bb bc bd be bf c0 c1 c2 c3 c4 c5 c6 c7 c8 c9 ca cb cc cd ce cf d0 d1 d2 d3 d4 d5 d6 d7 d8 d9
  //   da db dc dd de df e0 e1 e2 e3 e4 e5 e6 e7 e8 e9 ea eb ec ed ee ef f0 f1 f2 f3 f4 f5 f6 f7 f8 f9 fa
  //   fb fc fd fe ff 0 1 2 3 4 5 6 7 8 9 a b c d e f 10 11 12 13 14 15 16 17 18 19 1a 1b 1c 1d 1e 1f 20 21
  //   22 23 24 25 26 27 28 29 2a 2b 2c 2d 2e 2f 30 31 32 33 34 35 36 37 38 39 3a 3b 3c 3d 3e 3f 40 41 42
  //   43 44 45 46 47 48 49 4a 4b 4c 4d 4e 4f 50 51 52 53 54 55 56 57 58 59 5a 5b 5c 5d 5e 5f 60 61 62 63
  //   64 65 66 67 68 69 6a 6b 6c 6d 6e 6f 70 71 72 73 74 75 76 77 78 79 7a 7b 7c 7d 7e 7f 80 81 82 83 84
  //   85 86 87 88 89 8a 8b 8c 8d 8e 8f 90 91 92 93 94 95 96 97 98 99 9a 9b 9c 9d 9e 9f a0 a1 a2 a3 a4 a5
  //   a6 a7 a8 a9 aa ab ac ad ae af b0 b1 b2 b3 b4 b5 b6 b7 b8 b9 ba bb bc bd be bf c0 c1 c2 c3 c4 c5 c6
  //   c7 c8 c9 ca cb cc cd ce cf d0 d1 d2 d3 d4 d5 d6 d7 d8 d9 da db dc dd de df e0 e1 e2 e3 e4 e5 e6 e7
  //   e8 e9 ea eb ec ed ee ef f0 f1 f2 f3 f4 f5 f6 f7 f8 f9 fa fb fc fd fe ff 0 1 2 3 4 5 6 7 8 9 a b c d
  //   e f 10 11 12 13 14 15 16 17 18 19 1a 1b 1c 1d 1e 1f 20 21 22 23 24 25 26 27 28 29 2a 2b 2c 2d 2e 2f
  //   30 31 32 33 34 35 36 37 38 39 3a 3b 3c 3d 3e 3f 40 41 42 43 44 45 46 47 48 49 4a 4b 4c 4d 4e 4f 50
  //   51 52 53 54 55 56 57 58 59 5a 5b 5c 5d 5e 5f 60 61 62 63 64 65 66 67 68 69 6a 6b 6c 6d 6e 6f 70 71
  //   72 73 74 75 76 77 78 79 7a 7b 7c 7d 7e 7f 80 81 82 83 84 85 86 87 88 89 8a 8b 8c 8d 8e 8f 90 91 92
  //   93 94 95 96 97 98 99 9a 9b 9c 9d 9e 9f a0 a1 a2 a3 a4 a5 a6 a7 a8 a9 aa ab ac ad ae af b0 b1 b2 b3
  //   b4 b5 b6 b7 b8 b9 ba bb bc bd be bf c0 c1 c2 c3 c4 c5 c6 c7 c8 c9 ca cb cc cd ce cf d0 d1 d2 d3 d4
  //   d5 d6 d7 d8 d9 da db dc dd de df e0 e1 e2 e3 e4 e5 e6 e7 e8 e9 ea eb ec ed ee ef f0 f1 f2 f3 f4 f5
  //   f6 f7 f8 f9 fa fb fc fd fe ff 0 1 2 3 4 5 6 7 8 9 a b c d e f 10 11 12 13 14 15 16 17 18 19 1a 1b 1c
  //   1d 1e 1f 20 21 22 23 24 25 26 27 28 29 2a 2b 2c 2d 2e 2f 30 31 32 33 34 35 36 37 38 39 3a 3b 3c 3d
  //   3e 3f 40 41 42 43 44 45 46 47 48 49 4a 4b 4c 4d 4e 4f 50 51 52 53 54 55 56 57 58 59 5a 5b 5c 5d 5e
  //   5f 60 61 62 63 64 65 66 67 68 69 6a 6b 6c 6d 6e 6f 70 71 72 73 74 75 76 77 78 79 7a 7b 7c 7d 7e 7f
  //   80 81 82 83 84 85 86 87 88 89 8a 8b 8c 8d 8e 8f 90 91 92 93 94 95 96 97 98 99 9a 9b 9c 9d 9e 9f a0
  //   a1 a2 a3 a4 a5 a6 a7 a8 a9 aa ab ac ad ae af b0 b1 b2 b3 b4 b5 b6 b7 b8 b9 ba bb bc bd be bf c0 c1
  //   c2 c3 c4 c5 c6 c7 c8 c9 ca cb cc cd ce cf d0 d1 d2 d3 d4 d5 d6 d7 d8 d9 da db dc dd de df e0 e1 e2
  //   e3 e4 e5 e6 e7 e8 e9 ea eb ec ed ee ef f0 f1 f2 f3 f4 f5 f6 f7 f8 f9 fa fb fc fd fe ff
  //   cache模拟器
endmodule
