// Logisim project 单总线结构MIPS处理器（硬布线控制器）（7条指令）.circ as structural Verilog: 8 circuits, main circuit 硬布线控制器
module \单总线结构MIPS处理器_硬布线控制器_数据通路  (
);

  wire Add, Add4, alu_1_equal, and_1_out, ARin, CLK, comparator_1_eq, DREin, DREout, DRin, DRout, equal,
       IR_A_out, IR_I26_out, IR_I_out, IRin, Jump, Mcal, Mex, Mif, not_1_out, PCin, PCout, PSWin, READ,
       RegDst, RegTgt, Rin, Rout, RST, Slt, T1, T2, T3, T4, Write, Xin, Zout;
  wire [4:0] registerfile_1_p4, registerfile_1_p5;
  wire [11:0] Clks, \指令数 ;
  wire [31:0] alu_1_result, AR_q, bit_extender_1_out, bit_extender_2_out, controlled_buffer_1_out,
       controlled_buffer_3_out, DR_q, IR, PC_q, ram_1_data, registerfile_1_p6, shifter_1_out, X_q, Z_q,
       \内部总线 ;

  // Probe on \指令数 
  LED #(.active("true")) led_1 (.in(Mif));
  Button u_RST (.out(RST));
  // Digital_Oscilloscope #(.nState(35), .frontlines("rising"), .showclock("true")) digital_oscilloscope_1: pin names not known; wires that end beside it: CLK, Mif, Mcal, Mex, T1, T2, T3, T4
  LED #(.active("true")) led_2 (.in(Mcal));
  LED #(.active("true")) led_3 (.in(Mex));
  Register #(.width(32), .trigger("rising"), .Select("low")) AR (.D(\内部总线 ), .en(ARin), .Q(AR_q), .clk(CLK), .clr(RST));
  Register #(.width(32), .trigger("rising"), .Select("low")) X (.D(\内部总线 ), .en(Xin), .Q(X_q), .clk(CLK), .clr(RST));
  // Probe on Clks
  LED #(.active("true")) led_4 (.in(T3));
  LED #(.active("true")) led_5 (.in(T2));
  LED #(.active("true")) led_6 (.in(T1));
  Clock #(.highDuration(1), .lowDuration(1)) u_CLK (.out(CLK));
  LED #(.active("true")) led_7 (.in(T4));
  RAM #(.addrWidth(10), .dataWidth(32), .bus("separate"), .Select("high")) ram_1 (
    .addr(AR_q[11:2]), .din(controlled_buffer_3_out), .data(ram_1_data), .str(Write), .clk(CLK), .ld(READ));  // open: sel, clr
  ALU alu_1 (
    .X(X_q), .Y(\内部总线 ), .Equal(alu_1_equal), .Result(alu_1_result), .ADD(Add), .ADD4(Add4), .J(Jump),
    .SLT(Slt));
  assign controlled_buffer_1_out = DRin ? \内部总线  : 32'bz;  // Controlled_Buffer controlled_buffer_1
  assign controlled_buffer_1_out = DREin ? ram_1_data : 32'bz;  // Controlled_Buffer controlled_buffer_2
  assign controlled_buffer_3_out = DREout ? DR_q : 32'bz;  // Controlled_Buffer controlled_buffer_3
  Register #(.width(32), .trigger("rising"), .Select("low")) PC (.D(\内部总线 ), .en(PCin), .Q(PC_q), .clk(CLK), .clr(RST));
  Register #(.width(32), .trigger("rising"), .Select("low")) DR (
    .D(controlled_buffer_1_out), .Q(DR_q), .clk(CLK), .clr(RST));  // open: en
  Register #(.width(1), .trigger("rising"), .Select("low")) PSW (
    .D(alu_1_equal), .en(PSWin), .Q(equal), .clk(CLK), .clr(RST));
  Register #(.width(32), .trigger("rising"), .Select("low")) Z (
    .D(alu_1_result), .Q(Z_q), .clk(CLK), .clr(RST));  // open: en
  assign \内部总线  = PCout ? PC_q : 32'bz;  // Controlled_Buffer controlled_buffer_4
  assign \内部总线  = DRout ? DR_q : 32'bz;  // Controlled_Buffer controlled_buffer_5
  assign \内部总线  = Zout ? Z_q : 32'bz;  // Controlled_Buffer controlled_buffer_6
  Register #(.width(32), .trigger("rising"), .Select("low")) u_IR (.D(\内部总线 ), .en(IRin), .Q(IR), .clk(CLK), .clr(RST));
  assign \内部总线  = IR_I_out ? bit_extender_2_out : 32'bz;  // Controlled_Buffer controlled_buffer_7
  assign \内部总线  = IR_A_out ? shifter_1_out : 32'bz;  // Controlled_Buffer controlled_buffer_8
  assign \内部总线  = IR_I26_out ? bit_extender_1_out : 32'bz;  // Controlled_Buffer controlled_buffer_9
  \硬布线控制器  \u_硬布线控制器_1  (
    .\状态节拍信号 ({T4, T3, T2, T1, Mex, Mcal, Mif}), .CLK(CLK), .IR(IR),
    .ControlBus({IR_I26_out, Jump, PCout, DRout, Zout, Rout, IR_I_out, IR_A_out, DREout, PCin, ARin, DREin, DRin, Xin, Rin, IRin, PSWin, RegTgt, RegDst, Add, Add4, Slt, READ, Write}),
    .EQUAL(equal), .RST(RST));
  assign bit_extender_1_out = {{6{IR[25]}}, IR[25:0]};  // Bit_Extender bit_extender_1
  // RegisterFile registerfile_1: pin names not known; wires that end beside it: \内部总线 , CLK, Rin, registerfile_1_p4, registerfile_1_p5, registerfile_1_p6
  assign bit_extender_2_out = {{16{IR[15]}}, IR[15:0]};  // Bit_Extender bit_extender_2
  assign \内部总线  = Rout ? registerfile_1_p6 : 32'bz;  // Controlled_Buffer controlled_buffer_10
  Multiplexer #(.select(1), .width(5), .disabled("Z"), .enable("false")) multiplexer_1 (
    .in0(IR[25:21]), .in1(IR[20:16]), .out(registerfile_1_p5), .sel(RegTgt));
  Multiplexer #(.select(1), .width(5), .disabled("Z"), .enable("false")) multiplexer_2 (
    .in0(IR[20:16]), .in1(IR[15:11]), .out(registerfile_1_p4), .sel(RegDst));
  Comparator #(.width(32), .mode("twosComplement")) comparator_1 (
    .a(IR), .b(32'h1000ffff), .eq(comparator_1_eq));  // open: gt, lt
  Counter #(.width(12), .max('hfff), .ongoal("wrap"), .trigger("falling"), .behavior("new")) counter_1 (
    .count(not_1_out), .Q(Clks), .clk(CLK), .clr(RST));  // open: load, D, carry, preset, down
  not not_1 (not_1_out, comparator_1_eq);
  Shifter #(.width(32), .shift("ll")) shifter_1 (.in(bit_extender_2_out), .\dist (5'b00010), .out(shifter_1_out));
  Counter #(.width(12), .max('hfff), .ongoal("wrap"), .trigger("falling"), .behavior("old")) counter_2 (
    .count(and_1_out), .Q(\指令数 ), .clk(CLK), .clr(RST));  // open: load, D, carry, preset
  and and_1 (and_1_out, not_1_out, Mif, T1);

  // Other names for the same wires on the sheet: rd[4:0] = IR[15:11]; rt[4:0] = IR[20:16]; rs[4:0] = IR[25:21];
  //   控制信号[23:0] = {IR_I26_out, Jump, PCout, DRout, Zout, Rout, IR_I_out, IR_A_out, DREout, PCin, ARin, DREin, DRin, Xin, Rin, IRin, PSWin, RegTgt, RegDst, Add, Add4, Slt, READ, Write};
  //   状态节拍信号[6:0] = {T4, T3, T2, T1, Mex, Mcal, Mif}

  // Notes on the sheet:
  //   指令数
  //   RAM
  //   外部总线
  //   时钟周期数
  //   内部总线
  //   支持LW、SW、BEQ、SLT、ADDI、ADD、J等7条指令
  //   单总线结构 MIPS 处理器（硬布线控制器）数据通路
  //   Immidate32
  //   BranchAddress32
endmodule

module \硬布线控制器  (
  input  CLK,
  input  [31:0] IR,
  input  EQUAL,
  input  RST,
  output [6:0] \状态节拍信号 ,
  output [23:0] ControlBus
);

  wire ADD, ADDI, BEQ, J, LW, not_1_out, Other;
  wire [3:0] \状态寄存器_q , \状态机_1_n0 ;
  wire [5:2] OCInput;

  Register #(.width(4), .trigger("rising"), .Select("low")) \u_状态寄存器  (
    .D(\状态机_1_n0 ), .Q(\状态寄存器_q ), .clk(not_1_out), .clr(RST));  // open: en
  not not_1 (not_1_out, CLK);
  \状态机  \u_状态机_1  (
    .LW(LW), .N3(\状态机_1_n0 [3]), .SW(OCInput[5]), .BEQ(BEQ), .SLT(OCInput[2]), .ADDI(ADDI), .ADD(ADD), .J(J),
    .S3(\状态寄存器_q [3]), .S2(\状态寄存器_q [2]), .S1(\状态寄存器_q [1]), .S0(\状态寄存器_q [0]), .N2(\状态机_1_n0 [2]),
    .N1(\状态机_1_n0 [1]), .N0(\状态机_1_n0 [0]));
  \输出函数  \u_输出函数_1  (
    .S3(\状态寄存器_q [3]), .S2(\状态寄存器_q [2]), .S1(\状态寄存器_q [1]), .S0(\状态寄存器_q [0]), .Mif(\状态节拍信号 [0]),
    .Mcal(\状态节拍信号 [1]), .Mex(\状态节拍信号 [2]), .T1(\状态节拍信号 [3]), .T2(\状态节拍信号 [4]), .T3(\状态节拍信号 [5]),
    .T4(\状态节拍信号 [6]));
  \指令译码器  \u_指令译码器_1  (
    .IR(IR), .LW(LW), .SW(OCInput[5]), .BEQ(BEQ), .ADDI(ADDI), .SLT(OCInput[2]), .OtherInstr(Other),
    .ADD(ADD), .J(J));
  \硬布线控制器组合逻辑单元  \u_硬布线控制器组合逻辑单元_1  (
    .SLT(OCInput[2]), .IRI26out(ControlBus[23]), .ADDI(ADDI), .Jump(ControlBus[22]), .LW(LW),
    .SW(OCInput[5]), .Pcout(ControlBus[21]), .BEQ(BEQ), .ADD(ADD), .DRout(ControlBus[20]), .J(J),
    .Mif(\状态节拍信号 [0]), .Mcal(\状态节拍信号 [1]), .Mex(\状态节拍信号 [2]), .T1(\状态节拍信号 [3]), .Zout(ControlBus[19]),
    .T2(\状态节拍信号 [4]), .T3(\状态节拍信号 [5]), .T4(\状态节拍信号 [6]), .EQUAL(EQUAL), .Rout(ControlBus[18]),
    .IRiout(ControlBus[17]), .IRaout(ControlBus[16]), .DREout(ControlBus[15]), .Pcin(ControlBus[14]),
    .ARin(ControlBus[13]), .DREin(ControlBus[12]), .DRin(ControlBus[11]), .Xin(ControlBus[10]),
    .Rin(ControlBus[9]), .IRin(ControlBus[8]), .PSWin(ControlBus[7]), .RegTgt(ControlBus[6]),
    .RegDst(ControlBus[5]), .Add_2(ControlBus[4]), .Add4(ControlBus[3]), .Slt_2(ControlBus[2]),
    .READ(ControlBus[1]), .WRITE(ControlBus[0]));

  // Other names for the same wires on the sheet: Write = ControlBus[0]; READ = ControlBus[1]; Slt_t = ControlBus[2];
  //   Add4 = ControlBus[3]; Add_t = ControlBus[4]; RegDst = ControlBus[5]; RegTgt = ControlBus[6];
  //   PSWin = ControlBus[7]; IRin = ControlBus[8]; Rin = ControlBus[9]; Xin = ControlBus[10]; DRin = ControlBus[11];
  //   DREin = ControlBus[12]; ARin = ControlBus[13]; PCin = ControlBus[14]; DREout = ControlBus[15];
  //   IR_A_out = ControlBus[16]; IR_I_out = ControlBus[17]; Rout = ControlBus[18]; Zout = ControlBus[19];
  //   DRout = ControlBus[20]; PCout = ControlBus[21]; Jump = ControlBus[22]; IR_I26_out = ControlBus[23];
  //   OCInput (some bits) = {EQUAL, \状态节拍信号 , BEQ, LW, ADDI, ADD, J}; SLT = OCInput[2]; SW = OCInput[5];
  //   Mif = \状态节拍信号 [0]; Mcal = \状态节拍信号 [1]; Mex = \状态节拍信号 [2]; T1 = \状态节拍信号 [3]; T2 = \状态节拍信号 [4]; T3 = \状态节拍信号 [5];
  //   T4 = \状态节拍信号 [6]; 指令字[31:0] = IR

  // Notes on the sheet:
  //   指令译码信号
  //   次态
  //   输入引脚
  //   现态
  //   现态
  //   次态
  //   输出引脚
  //   时序发生器
  //   硬布线控制器
  //   指令译码信号
  //   硬布线控制器组合逻辑单元
  //   指令译码
endmodule

module \指令译码器  (
  input  [31:0] IR,
  output LW,
  output SW,
  output BEQ,
  output ADDI,
  output SLT,
  output OtherInstr,
  output ADD,
  output J
);

  wire comparator_6_eq, comparator_7_eq, comparator_8_eq;

  Comparator #(.width(6), .mode("twosComplement")) comparator_1 (
    .a(IR[31:26]), .b(6'b100011), .eq(LW));  // open: gt, lt
  Comparator #(.width(6), .mode("twosComplement")) comparator_2 (
    .a(IR[31:26]), .b(6'b101011), .eq(SW));  // open: gt, lt
  Comparator #(.width(6), .mode("twosComplement")) comparator_3 (.a(6'b000010), .b(IR[31:26]), .eq(J));  // open: gt, lt
  Comparator #(.width(6), .mode("twosComplement")) comparator_4 (
    .a(IR[31:26]), .b(6'b000100), .eq(BEQ));  // open: gt, lt
  Comparator #(.width(6), .mode("twosComplement")) comparator_5 (
    .a(IR[31:26]), .b(6'b001000), .eq(ADDI));  // open: gt, lt
  Comparator #(.width(6), .mode("twosComplement")) comparator_6 (
    .a(IR[31:26]), .b({6{1'b0}}), .eq(comparator_6_eq));  // open: gt, lt
  Comparator #(.width(6), .mode("twosComplement")) comparator_7 (
    .a(IR[5:0]), .b(6'b101010), .eq(comparator_7_eq));  // open: gt, lt
  and and_1 (SLT, comparator_7_eq, comparator_6_eq);
  and and_2 (ADD, comparator_6_eq, comparator_8_eq);
  Comparator #(.width(6), .mode("twosComplement")) comparator_8 (
    .a(IR[5:0]), .b(6'b100000), .eq(comparator_8_eq));  // open: gt, lt
  nor nor_1 (OtherInstr, J, ADD, BEQ, SW, LW, ADDI, SLT);

  // Other names for the same wires on the sheet: FUNCT[5:0] = IR[5:0]; OP[5:0] = IR[31:26]

  // Notes on the sheet:
  //   输入引脚
  //   指令译码器（ID）
  //   输出引脚
endmodule

module \状态机  (
  input  LW,
  input  SW,
  input  BEQ,
  input  SLT,
  input  ADDI,
  input  ADD,
  input  J,
  input  S3,
  input  S2,
  input  S1,
  input  S0,
  output N3,
  output N2,
  output N1,
  output N0
);

  wire and_2_out, and_3_out, and_4_out, and_5_out, and_6_out, and_7_out, and_8_out, and_9_out, and_10_out,
       and_11_out, and_12_out, and_13_out, and_14_out, and_15_out, and_16_out, and_17_out, and_18_out,
       and_19_out, and_20_out, and_21_out, and_22_out, and_23_out, not_1_out, not_2_out, not_3_out,
       not_4_out, not_5_out, not_6_out, not_7_out, not_8_out, not_9_out, not_10_out, not_11_out, not_12_out,
       not_13_out, not_14_out, not_15_out, not_16_out, not_17_out, not_18_out, not_19_out, not_20_out,
       not_21_out, not_22_out, not_23_out, not_24_out, not_25_out, not_26_out, not_27_out, not_28_out,
       not_29_out, not_30_out, not_31_out, not_32_out, not_33_out, not_34_out, not_35_out, not_36_out,
       not_37_out, not_38_out, not_39_out, not_40_out, not_41_out, not_42_out, not_43_out, not_44_out,
       not_45_out, not_46_out, not_47_out, not_48_out, not_49_out, not_50_out, not_51_out, not_52_out;

  not not_1 (not_1_out, S3);
  not not_2 (not_2_out, S3);
  not not_3 (not_3_out, S2);
  not not_4 (not_4_out, S3);
  not not_5 (not_5_out, S2);
  not not_6 (not_6_out, S3);
  not not_7 (not_7_out, S2);
  not not_8 (not_8_out, S3);
  not not_9 (not_9_out, S2);
  not not_10 (not_10_out, S3);
  not not_11 (not_11_out, S2);
  not not_12 (not_12_out, S3);
  not not_13 (not_13_out, S2);
  not not_14 (not_14_out, S3);
  not not_15 (not_15_out, S2);
  not not_16 (not_16_out, S3);
  not not_17 (not_17_out, S1);
  not not_18 (not_18_out, S0);
  not not_19 (not_19_out, S3);
  not not_20 (not_20_out, S1);
  not not_21 (not_21_out, S3);
  not not_22 (not_22_out, S0);
  not not_23 (not_23_out, S3);
  not not_24 (not_24_out, S2);
  not not_25 (not_25_out, S1);
  not not_26 (not_26_out, S3);
  not not_27 (not_27_out, S2);
  not not_28 (not_28_out, S0);
  not not_29 (not_29_out, S3);
  not not_30 (not_30_out, S2);
  not not_31 (not_31_out, S3);
  not not_32 (not_32_out, S2);
  not not_33 (not_33_out, S3);
  not not_34 (not_34_out, S2);
  not not_35 (not_35_out, S3);
  not not_36 (not_36_out, S2);
  not not_37 (not_37_out, S3);
  not not_38 (not_38_out, S1);
  not not_39 (not_39_out, S3);
  not not_40 (not_40_out, S0);
  not not_41 (not_41_out, S3);
  not not_42 (not_42_out, S2);
  not not_43 (not_43_out, S1);
  not not_44 (not_44_out, S0);
  not not_45 (not_45_out, S3);
  not not_46 (not_46_out, S2);
  not not_47 (not_47_out, S0);
  not not_48 (not_48_out, S3);
  not not_49 (not_49_out, S1);
  not not_50 (not_50_out, S0);
  not not_51 (not_51_out, S3);
  not not_52 (not_52_out, S0);
  and and_1 (N3, not_1_out, S2, S1, S0);
  and and_2 (and_2_out, not_2_out, not_3_out, S1, S0, LW);
  and and_3 (and_3_out, not_4_out, not_5_out, S1, S0, SW);
  and and_4 (and_4_out, not_6_out, not_7_out, S1, S0, BEQ);
  and and_5 (and_5_out, not_8_out, not_9_out, S1, S0, SLT);
  and and_6 (and_6_out, not_10_out, not_11_out, S1, S0, ADDI);
  and and_7 (and_7_out, not_12_out, not_13_out, S1, S0, ADD);
  and and_8 (and_8_out, not_14_out, not_15_out, S1, S0, J);
  and and_9 (and_9_out, not_16_out, S2, not_17_out, not_18_out);
  and and_10 (and_10_out, not_19_out, S2, not_20_out, S0);
  and and_11 (and_11_out, not_21_out, S2, S1, not_22_out);
  and and_12 (and_12_out, not_23_out, not_24_out, not_25_out, S0);
  and and_13 (and_13_out, not_26_out, not_27_out, S1, not_28_out);
  and and_14 (and_14_out, not_29_out, not_30_out, S1, S0, SLT);
  and and_15 (and_15_out, not_31_out, not_32_out, S1, S0, ADDI);
  and and_16 (and_16_out, not_33_out, not_34_out, S1, S0, ADD);
  and and_17 (and_17_out, not_35_out, not_36_out, S1, S0, J);
  and and_18 (and_18_out, not_37_out, S2, not_38_out, S0);
  and and_19 (and_19_out, not_39_out, S2, S1, not_40_out);
  and and_20 (and_20_out, not_41_out, not_42_out, not_43_out, not_44_out);
  and and_21 (and_21_out, not_45_out, not_46_out, S1, not_47_out);
  and and_22 (and_22_out, not_48_out, S2, not_49_out, not_50_out);
  and and_23 (and_23_out, not_51_out, S2, S1, not_52_out);
  or or_1 (N0, and_20_out, and_21_out, and_22_out, and_23_out);
  or or_2 (N2, and_2_out, and_3_out, and_4_out, and_5_out, and_6_out, and_7_out, and_8_out, and_9_out, and_10_out, and_11_out);
  or or_3 (N1, and_12_out, and_13_out, and_14_out, and_15_out, and_16_out, and_17_out, and_18_out, and_19_out);
endmodule

module \输出函数  (
  input  S3,
  input  S2,
  input  S1,
  input  S0,
  output Mif,
  output Mcal,
  output Mex,
  output T1,
  output T2,
  output T3,
  output T4
);

  wire and_3_out, and_4_out, and_5_out, and_6_out, and_7_out, and_8_out, and_9_out, and_10_out, and_11_out,
       and_12_out, not_1_out, not_2_out, not_3_out, not_4_out, not_5_out, not_6_out, not_7_out, not_8_out,
       not_9_out, not_10_out, not_11_out, not_12_out, not_13_out, not_14_out, not_15_out, not_16_out,
       not_17_out, not_18_out, not_19_out, not_20_out, not_21_out, not_22_out, not_23_out, not_24_out,
       not_25_out, not_26_out, not_27_out, not_28_out;

  not not_1 (not_1_out, S3);
  and and_1 (Mif, not_1_out, not_2_out);
  not not_2 (not_2_out, S2);
  not not_3 (not_3_out, S3);
  and and_2 (Mcal, not_3_out, S2, not_4_out);
  not not_4 (not_4_out, S1);
  not not_5 (not_5_out, S3);
  not not_6 (not_6_out, S2);
  not not_7 (not_7_out, S1);
  not not_8 (not_8_out, S0);
  not not_9 (not_9_out, S3);
  not not_10 (not_10_out, S1);
  not not_11 (not_11_out, S0);
  not not_12 (not_12_out, S3);
  not not_13 (not_13_out, S0);
  not not_14 (not_14_out, S2);
  not not_15 (not_15_out, S1);
  not not_16 (not_16_out, S3);
  not not_17 (not_17_out, S1);
  not not_18 (not_18_out, S3);
  not not_19 (not_19_out, S2);
  not not_20 (not_20_out, S0);
  not not_21 (not_21_out, S3);
  not not_22 (not_22_out, S2);
  not not_23 (not_23_out, S0);
  not not_24 (not_24_out, S2);
  not not_25 (not_25_out, S1);
  not not_26 (not_26_out, S0);
  not not_27 (not_27_out, S3);
  not not_28 (not_28_out, S2);
  and and_3 (and_3_out, not_5_out, S2, S1);
  or or_1 (Mex, and_3_out, and_4_out);
  and and_4 (and_4_out, S3, not_6_out, not_7_out, not_8_out);
  and and_5 (and_5_out, not_9_out, not_10_out, not_11_out);
  and and_6 (and_6_out, not_12_out, S2, not_13_out);
  or or_2 (T1, and_5_out, and_6_out, and_7_out);
  and and_7 (and_7_out, S3, not_14_out, not_15_out, S0);
  and and_8 (and_8_out, not_16_out, not_17_out, S0);
  and and_9 (and_9_out, not_18_out, S2, S0);
  or or_3 (T2, and_8_out, and_9_out, and_10_out);
  and and_10 (and_10_out, S3, not_19_out, S1, not_20_out);
  and and_11 (and_11_out, not_21_out, not_22_out, S1, not_23_out);
  or or_4 (T3, and_11_out, and_12_out);
  and and_12 (and_12_out, S3, not_24_out, not_25_out, not_26_out);
  and and_13 (T4, not_27_out, not_28_out, S1, S0);

  // Notes on the sheet:
  //   输出函数
endmodule

module \硬布线控制器组合逻辑单元  (
  input  SLT,
  input  ADDI,
  input  LW,
  input  SW,
  input  BEQ,
  input  ADD,
  input  J,
  input  Mif,
  input  Mcal,
  input  Mex,
  input  T1,
  input  T2,
  input  T3,
  input  T4,
  input  EQUAL,
  output IRI26out,
  output Jump,
  output Pcout,
  output DRout,
  output Zout,
  output Rout,
  output IRiout,
  output IRaout,
  output DREout,
  output Pcin,
  output ARin,
  output DREin,
  output DRin,
  output Xin,
  output Rin,
  output IRin,
  output PSWin,
  output RegTgt,
  output RegDst,
  output Add_2,
  output Add4,
  output Slt_2,
  output READ,
  output WRITE
);

  wire and_3_out, and_4_out, and_5_out, and_6_out, and_7_out, and_8_out, and_9_out, and_10_out, and_11_out,
       and_12_out, and_13_out, and_14_out, and_15_out, and_16_out, and_17_out, and_18_out, and_19_out,
       and_20_out, and_21_out, and_22_out, and_23_out, and_24_out, and_25_out, and_26_out, and_27_out,
       and_28_out, and_31_out, and_32_out, and_33_out, and_34_out, and_35_out, and_36_out, and_37_out,
       and_38_out, and_40_out, and_41_out, and_42_out, and_43_out, and_44_out, and_45_out, and_46_out,
       and_47_out, and_48_out, and_49_out, and_50_out, and_51_out, and_52_out, and_55_out, and_56_out,
       and_57_out, and_58_out, and_59_out, and_60_out, and_61_out, and_62_out, and_63_out, and_64_out,
       and_65_out, and_68_out, and_69_out;

  and and_1 (IRI26out, Mex, T2, J);
  and and_2 (Jump, Mex, T2, J);
  and and_3 (and_3_out, Mif, T1);
  and and_4 (and_4_out, Mex, T1, BEQ);
  and and_5 (and_5_out, Mex, T1, J);
  and and_6 (and_6_out, Mif, T4);
  and and_7 (and_7_out, LW, Mex, T3);
  and and_8 (and_8_out, Mif, T3);
  and and_9 (and_9_out, Mex, T1, LW);
  and and_10 (and_10_out, Mex, T1, SW);
  and and_11 (and_11_out, Mex, T3, BEQ, EQUAL);
  and and_12 (and_12_out, Mex, T3, SLT);
  and and_13 (and_13_out, Mex, T3, ADDI);
  and and_14 (and_14_out, Mex, T3, ADD);
  and and_15 (and_15_out, Mex, T3, J);
  and and_16 (and_16_out, ADD, Mex, T2);
  and and_17 (and_17_out, ADD, Mex, T1);
  and and_18 (and_18_out, BEQ, Mcal, T2);
  and and_19 (and_19_out, BEQ, Mcal, T1);
  and and_20 (and_20_out, SW, Mex, T2);
  and and_21 (and_21_out, SW, Mcal, T1);
  and and_22 (and_22_out, LW, Mcal, T1);
  and and_23 (and_23_out, ADDI, Mex, T1);
  and and_24 (and_24_out, SLT, Mex, T2);
  and and_25 (and_25_out, SLT, Mex, T1);
  and and_26 (and_26_out, SW, Mcal, T2);
  and and_27 (and_27_out, LW, Mcal, T2);
  and and_28 (and_28_out, ADDI, Mex, T2);
  and and_29 (IRaout, BEQ, Mex, T2);
  and and_30 (DREout, SW, Mex, T3);
  and and_31 (and_31_out, Mif, T3);
  and and_32 (and_32_out, Mex, T3, BEQ, EQUAL);
  and and_33 (and_33_out, Mex, T3, J);
  and and_34 (and_34_out, Mif, T1);
  and and_35 (and_35_out, SW, Mex, T1);
  and and_36 (and_36_out, LW, Mex, T1);
  and and_37 (and_37_out, Mif, T3);
  and and_38 (and_38_out, LW, Mex, T2);
  and and_39 (DRin, SW, Mex, T2);
  and and_40 (and_40_out, Mif, T1);
  and and_41 (and_41_out, Mcal, T1, LW);
  and and_42 (and_42_out, Mcal, T1, SW);
  and and_43 (and_43_out, Mcal, T1, BEQ);
  and and_44 (and_44_out, Mex, T1, BEQ);
  and and_45 (and_45_out, Mex, T1, SLT);
  and and_46 (and_46_out, Mex, T1, ADDI);
  and and_47 (and_47_out, Mex, T1, ADD);
  and and_48 (and_48_out, Mex, T1, J);
  and and_49 (and_49_out, ADD, Mex, T3);
  and and_50 (and_50_out, LW, Mex, T3);
  and and_51 (and_51_out, ADDI, Mex, T3);
  and and_52 (and_52_out, SLT, Mex, T3);
  and and_53 (IRin, Mif, T4);
  and and_54 (PSWin, BEQ, Mcal, T2);
  and and_55 (and_55_out, ADD, Mex, T2);
  and and_56 (and_56_out, BEQ, Mcal, T2);
  and and_57 (and_57_out, SW, Mex, T2);
  and and_58 (and_58_out, SLT, Mex, T2);
  and and_59 (and_59_out, ADD, Mex, T3);
  and and_60 (and_60_out, SLT, Mex, T3);
  and and_61 (and_61_out, ADD, Mex, T2);
  and and_62 (and_62_out, BEQ, Mex, T2);
  and and_63 (and_63_out, SW, Mcal, T2);
  and and_64 (and_64_out, LW, Mcal, T2);
  and and_65 (and_65_out, ADDI, Mex, T2);
  and and_66 (Add4, Mif, T2);
  and and_67 (Slt_2, SLT, Mex, T2);
  and and_68 (and_68_out, Mif, T3);
  and and_69 (and_69_out, LW, Mex, T2);
  and and_70 (WRITE, SW, Mex, T3);
  or or_1 (Pcout, and_3_out, and_4_out, and_5_out);
  or or_2 (DRout, and_6_out, and_7_out);
  or or_3 (IRiout, and_26_out, and_27_out, and_28_out);
  or or_4 (Pcin, and_31_out, and_32_out, and_33_out);
  or or_5 (ARin, and_34_out, and_35_out, and_36_out);
  or or_6 (DREin, and_37_out, and_38_out);
  or or_7 (Rin, and_49_out, and_50_out, and_51_out, and_52_out);
  or or_8 (RegTgt, and_55_out, and_56_out, and_57_out, and_58_out);
  or or_9 (RegDst, and_59_out, and_60_out);
  or or_10 (Add_2, and_61_out, and_62_out, and_63_out, and_64_out, and_65_out);
  or or_11 (READ, and_68_out, and_69_out);
  or or_12 (Zout, and_8_out, and_9_out, and_10_out, and_11_out, and_12_out, and_13_out, and_14_out, and_15_out);
  or or_13 (Rout, and_16_out, and_17_out, and_18_out, and_19_out, and_20_out, and_21_out, and_22_out, and_23_out, and_24_out, and_25_out);
  or or_14 (Xin, and_40_out, and_41_out, and_42_out, and_43_out, and_44_out, and_45_out, and_46_out, and_47_out, and_48_out);
endmodule

module ALU (
  input  ADD,
  input  ADD4,
  input  [31:0] X,
  input  [31:0] Y,
  input  J,
  input  SLT,
  output Equal,
  output [31:0] Result
);

  wire [0:0] comparator_1_lt;
  wire [1:0] priority_encoder_1_out;
  wire [31:0] adder_1_out, adder_2_out, shifter_1_out;

  Pull_Resistor #(.pull(0)) pull_resistor_1 (.node(Y));
  Adder #(.width(32)) adder_1 (.a(X), .b(Y), .out(adder_1_out));  // open: cin, cout
  Adder #(.width(32)) adder_2 (.a(X), .b(32'h4), .out(adder_2_out));  // open: cin, cout
  Shifter #(.width(32), .shift("ll")) shifter_1 (.in(Y), .\dist (5'b00010), .out(shifter_1_out));
  Comparator #(.width(32), .mode("twosComplement")) comparator_1 (
    .a(X), .b(Y), .eq(Equal), .lt(comparator_1_lt[0]));  // open: gt
  Priority_Encoder #(.select(2), .disabled("Z")) priority_encoder_1 (
    .in0(ADD), .in1(ADD4), .in2(J), .in3(SLT), .out(priority_encoder_1_out));  // open: gs, en_out, en_in
  Pull_Resistor #(.pull(0)) pull_resistor_2 (.node(priority_encoder_1_out));
  Multiplexer #(.select(2), .width(32), .disabled("Z"), .enable("false")) multiplexer_1 (
    .in0(adder_1_out), .in1(adder_2_out), .in2({adder_2_out[31:28], shifter_1_out[27:0]}),
    .in3({{31{1'b0}}, comparator_1_lt[0]}), .out(Result), .sel(priority_encoder_1_out));

  // Notes on the sheet:
  //   输入引脚
  //   算术逻辑单元（ALU）
  //   输出引脚
endmodule

module \测试电路  (
  input  LW,
  input  SW,
  input  BEQ,
  input  SLT,
  input  ADDI,
  input  ADD,
  input  J,
  input  [3:0] \现态 ,
  input  [3:0] \现态_2 ,
  output [3:0] \次态 
);

  wire \输出函数_1_mcal , \输出函数_1_mex , \输出函数_1_mif , \输出函数_1_t1 , \输出函数_1_t2 , \输出函数_1_t3 , \输出函数_1_t4 ;

  \状态机  \u_状态机_1  (
    .LW(LW), .N3(\次态 [3]), .SW(SW), .BEQ(BEQ), .SLT(SLT), .ADDI(ADDI), .ADD(ADD), .J(J), .S3(\现态 [3]),
    .S2(\现态 [2]), .S1(\现态 [1]), .S0(\现态 [0]), .N2(\次态 [2]), .N1(\次态 [1]), .N0(\次态 [0]));
  LED #(.active("true")) Mif (.in(\输出函数_1_mif ));
  \输出函数  \u_输出函数_1  (
    .S3(\现态_2 [3]), .S2(\现态_2 [2]), .S1(\现态_2 [1]), .S0(\现态_2 [0]), .Mif(\输出函数_1_mif ), .Mcal(\输出函数_1_mcal ),
    .Mex(\输出函数_1_mex ), .T1(\输出函数_1_t1 ), .T2(\输出函数_1_t2 ), .T3(\输出函数_1_t3 ), .T4(\输出函数_1_t4 ));
  LED #(.active("true")) Mcal (.in(\输出函数_1_mcal ));
  LED #(.active("true")) Mex (.in(\输出函数_1_mex ));
  LED #(.active("true")) T1 (.in(\输出函数_1_t1 ));
  LED #(.active("true")) T2 (.in(\输出函数_1_t2 ));
  LED #(.active("true")) T3 (.in(\输出函数_1_t3 ));
  LED #(.active("true")) T4 (.in(\输出函数_1_t4 ));
endmodule
