// Logisim project cache设计实验.circ as structural Verilog: 10 circuits, main circuit cache（直接相联映射）电路（4个cache块）
module \cache_直接相联映射_电路_4个cache块  (
  input  [15:0] Addr,
  input  [31:0] BlockDataIn,
  input  BlkDataReady,
  input  CLK,
  output Miss,
  output [7:0] DataOut
);

  wire and_2_out, and_3_out, and_4_out, and_5_out, comparator_1_eq, Hit, L0, L1, L2, L3, Valid, VALID_2_q,
       VALID_3_q, VALID_4_q, VALID_q;
  wire [11:0] TAG_2_q, TAG_3_q, TAG_4_q, TAG_q, TagData;
  wire [31:0] DATA_COPY_2_q, DATA_COPY_3_q, DATA_COPY_4_q, DATA_COPY_q, SlotData;

  Multiplexer #(.select(2), .width(8), .disabled("Z"), .enable("true")) multiplexer_1 (
    .in0(SlotData[7:0]), .in1(SlotData[15:8]), .in2(SlotData[23:16]), .in3(SlotData[31:24]), .out(DataOut),
    .sel(Addr[1:0]), .en(Hit));
  assign Valid = L0 ? VALID_q : 1'bz;  // Controlled_Buffer controlled_buffer_1
  Register #(.width(1), .trigger("rising"), .Select("low")) u_VALID (
    .D(1'b1), .en(and_2_out), .Q(VALID_q), .clk(CLK));  // open: clr
  Register #(.width(1), .trigger("rising"), .Select("low")) VALID_2 (
    .D(1'b1), .en(and_3_out), .Q(VALID_2_q), .clk(CLK));  // open: clr
  assign Valid = L1 ? VALID_2_q : 1'bz;  // Controlled_Buffer controlled_buffer_2
  assign Valid = L2 ? VALID_3_q : 1'bz;  // Controlled_Buffer controlled_buffer_3
  Register #(.width(1), .trigger("rising"), .Select("low")) VALID_3 (
    .D(1'b1), .en(and_4_out), .Q(VALID_3_q), .clk(CLK));  // open: clr
  assign Valid = L3 ? VALID_4_q : 1'bz;  // Controlled_Buffer controlled_buffer_4
  Register #(.width(1), .trigger("rising"), .Select("low")) VALID_4 (
    .D(1'b1), .en(and_5_out), .Q(VALID_4_q), .clk(CLK));  // open: clr
  Register #(.width(12), .trigger("rising"), .Select("low")) TAG (
    .D(Addr[15:4]), .en(and_2_out), .Q(TAG_q), .clk(CLK));  // open: clr
  Register #(.width(12), .trigger("rising"), .Select("low")) TAG_2 (
    .D(Addr[15:4]), .en(and_3_out), .Q(TAG_2_q), .clk(CLK));  // open: clr
  Register #(.width(12), .trigger("rising"), .Select("low")) TAG_3 (
    .D(Addr[15:4]), .en(and_4_out), .Q(TAG_3_q), .clk(CLK));  // open: clr
  Register #(.width(12), .trigger("rising"), .Select("low")) TAG_4 (
    .D(Addr[15:4]), .en(and_5_out), .Q(TAG_4_q), .clk(CLK));  // open: clr
  assign TagData = L0 ? TAG_q : 12'bz;  // Controlled_Buffer controlled_buffer_5
  assign TagData = L1 ? TAG_2_q : 12'bz;  // Controlled_Buffer controlled_buffer_6
  assign TagData = L2 ? TAG_3_q : 12'bz;  // Controlled_Buffer controlled_buffer_7
  assign TagData = L3 ? TAG_4_q : 12'bz;  // Controlled_Buffer controlled_buffer_8
  Comparator #(.width(12), .mode("twosComplement")) comparator_1 (
    .a(Addr[15:4]), .b(TagData), .eq(comparator_1_eq));  // open: gt, lt
  Decoder #(.select(2), .tristate("false"), .disabled(0), .enable("false")) decoder_1 (
    .out0(L0), .out1(L1), .out2(L2), .out3(L3), .sel(Addr[3:2]));
  and and_1 (Hit, comparator_1_eq, Valid);
  assign SlotData = L0 ? DATA_COPY_q : 32'bz;  // Controlled_Buffer controlled_buffer_9
  Register #(.width(32), .trigger("rising"), .Select("low")) DATA_COPY (
    .D(BlockDataIn), .en(and_2_out), .Q(DATA_COPY_q), .clk(CLK));  // open: clr
  assign SlotData = L1 ? DATA_COPY_2_q : 32'bz;  // Controlled_Buffer controlled_buffer_10
  Register #(.width(32), .trigger("rising"), .Select("low")) DATA_COPY_2 (
    .D(BlockDataIn), .en(and_3_out), .Q(DATA_COPY_2_q), .clk(CLK));  // open: clr
  Register #(.width(32), .trigger("rising"), .Select("low")) DATA_COPY_3 (
    .D(BlockDataIn), .en(and_4_out), .Q(DATA_COPY_3_q), .clk(CLK));  // open: clr
  assign SlotData = L2 ? DATA_COPY_3_q : 32'bz;  // Controlled_Buffer controlled_buffer_11
  Register #(.width(32), .trigger("rising"), .Select("low")) DATA_COPY_4 (
    .D(BlockDataIn), .en(and_5_out), .Q(DATA_COPY_4_q), .clk(CLK));  // open: clr
  assign SlotData = L3 ? DATA_COPY_4_q : 32'bz;  // Controlled_Buffer controlled_buffer_12
  not not_1 (Miss, Hit);
  and and_2 (and_2_out, L0, BlkDataReady);
  and and_3 (and_3_out, L1, BlkDataReady);
  and and_4 (and_4_out, L2, BlkDataReady);
  and and_5 (and_5_out, L3, BlkDataReady);

  // Other names for the same wires on the sheet: Blk[31:0] = BlockDataIn; BlkReady = BlkDataReady;
  //   Offset[1:0] = Addr[1:0]; 字节地址[15:0] = Addr; Index[1:0] = Addr[3:2]; Tag[11:0] = Addr[15:4]

  // Notes on the sheet:
  //   输入引脚区
  //   标记位
  //   有效位
  //   行选中
  //   cache（直接相联映射）电路（4个cache块）
  //   输出引脚区
endmodule

module \直接相联映射_4个cache块_测试电路  (
  input  in_1
);

  wire and_2_out, Clk, comparator_1_lt, comparator_2_eq, comparator_3_eq, controlled_buffer_1_out, EN, Error,
       Go, Hit, Miss, or_1_out, RDY, Runing;
  wire [3:0] _1, _2, _3;
  wire [7:0] Dataout, \主存内容_data ;
  wire [9:0] \测试用例数 ;
  wire [15:0] adder_1_out, Addr, bit_extender_3_out, \cache块交换逻辑电路_1_byteaddrout , counter_1_q,
       subtractor_1_out, \命中次数 , \时钟周期数 , \校验和 , \缺失次数 , \访问次数 ;
  wire [31:0] bit_extender_1_out, bit_extender_2_out, BlkDataIn, divider_1_out, divider_2_out,
       multiplier_1_out;
  wire [31:4] divider_2_rem, divider_3_out, divider_3_rem;

  not not_1 (Hit, Miss);
  and and_1 (EN, Hit, Go);
  Clock #(.highDuration(1), .lowDuration(1)) clock_1 (.out(Clk));
  Counter #(.width(16), .max('hffff), .ongoal("wrap"), .trigger("rising"), .behavior("old")) counter_1 (
    .count(and_2_out), .Q(counter_1_q), .clk(Clk));  // open: load, D, carry, clr, preset
  and and_2 (and_2_out, Miss, RDY, Runing);
  Subtractor #(.width(16)) subtractor_1 (.a(\访问次数 ), .b(\缺失次数 ), .out(subtractor_1_out));  // open: bin, bout
  Comparator #(.width(16), .mode("twosComplement")) comparator_1 (
    .a(\访问次数 ), .b(\缺失次数 ), .lt(comparator_1_lt));  // open: gt, eq
  // Probe on \访问次数 
  // Probe on \测试用例数 
  Counter #(.width(10), .max('h3ff), .ongoal("wrap"), .trigger("rising"), .behavior("old")) \u_计数器  (
    .count(EN), .Q(\测试用例数 ), .clk(Clk));  // open: load, D, carry, clr, preset
  Register #(.width(16), .trigger("rising"), .Select("low")) register_1 (
    .D(counter_1_q), .en(EN), .Q(\缺失次数 ), .clk(Clk));  // open: clr
  not not_2 (Runing, comparator_2_eq);
  Comparator #(.width(10), .mode("twosComplement")) comparator_2 (
    .a(\测试用例数 ), .b(10'h100), .eq(comparator_2_eq));  // open: gt, lt
  Multiplexer #(.select(1), .width(16), .disabled(0), .enable("false")) multiplexer_1 (
    .in0(subtractor_1_out), .in1({16{1'b0}}), .out(\命中次数 ), .sel(comparator_1_lt));
  // Probe on \命中次数 
  // Probe on \时钟周期数 
  ROM #(.addrWidth(10), .dataWidth(16), .Select("high")) \u_主存地址  (.addr(\测试用例数 ), .data(Addr));
  Counter #(.width(16), .max('hffff), .ongoal("wrap"), .trigger("rising"), .behavior("old")) counter_2 (
    .count(EN), .Q(\访问次数 ), .clk(Clk));  // open: load, D, carry, clr, preset
  assign bit_extender_1_out = {{16{1'b0}}, \命中次数 };  // Bit_Extender bit_extender_1
  // Probe on Dataout
  Multiplier #(.width(32)) multiplier_1 (
    .a(bit_extender_1_out), .b(32'h64), .out(multiplier_1_out));  // open: cin, cout
  assign bit_extender_2_out = {{16{1'b0}}, \访问次数 };  // Bit_Extender bit_extender_2
  // Probe on \缺失次数 
  // Probe on \校验和 
  \cache_直接相联映射_电路_4个cache块  \cache_直接相联映射_电路_4个cache块_1  (
    .Miss(Miss), .Addr(Addr), .BlockDataIn(BlkDataIn), .DataOut(Dataout), .BlkDataReady(RDY), .CLK(Clk));
  assign bit_extender_3_out = {{8{1'b0}}, Dataout};  // Bit_Extender bit_extender_3
  Divider #(.width(32)) divider_1 (
    .a(multiplier_1_out), .b(bit_extender_2_out), .out(divider_1_out));  // open: upper, rem
  Adder #(.width(16)) adder_1 (.a(\校验和 ), .b(bit_extender_3_out), .out(adder_1_out));  // open: cin, cout
  LED #(.active("true")) \u_读数据出错  (.in(Error));
  Pull_Resistor #(.pull(1)) pull_resistor_1 (.node(Miss));
  LED #(.active("true")) \u_缺失  (.in(Miss));
  Register #(.width(16), .trigger("rising"), .Select("low")) \u_校验和  (
    .D(adder_1_out), .en(EN), .Q(\校验和 ), .clk(Clk));  // open: clr
  Divider #(.width(32)) divider_2 (
    .a(divider_1_out), .b(32'ha), .out(divider_2_out), .rem({divider_2_rem, _1}));  // open: upper
  \cache块交换逻辑电路  \cache块交换逻辑电路_1  (
    .Addr(Addr), .CLK(Clk), .ByteAddrOut(\cache块交换逻辑电路_1_byteaddrout ), .ByteDataIn(\主存内容_data ),
    .Miss(Miss), .BlkDataReady(RDY), .BlockDataIn(BlkDataIn), .Enable(Runing));
  // Probe on \校验和 
  Divider #(.width(32)) divider_3 (
    .a(divider_2_out), .b(32'ha), .out({divider_3_out, _3}), .rem({divider_3_rem, _2}));  // open: upper
  ROM #(.addrWidth(16), .dataWidth(8), .Select("high")) \u_主存内容  (
    .addr(\cache块交换逻辑电路_1_byteaddrout ), .data(\主存内容_data ));
  Comparator #(.width(8), .mode("twosComplement")) comparator_3 (
    .a(Addr[7:0]), .b(Dataout), .eq(comparator_3_eq));  // open: gt, lt
  assign controlled_buffer_1_out = Hit ? comparator_3_eq : 1'bz;  // Controlled_Buffer controlled_buffer_1
  Pull_Resistor #(.pull(1)) pull_resistor_2 (.node(controlled_buffer_1_out));
  Hex_Digit_Display hex_digit_display_1 (.value(_2));  // open: dp
  Hex_Digit_Display hex_digit_display_2 (.value(_3), .dp(1'b1));
  or or_1 (or_1_out, controlled_buffer_1_out, ~in_1);  // OR_Gate
  Counter #(.width(16), .max('hffff), .ongoal("wrap"), .trigger("rising"), .behavior("old")) counter_3 (
    .count(Runing), .Q(\时钟周期数 ), .clk(Clk));  // open: load, D, carry, clr, preset
  Hex_Digit_Display hex_digit_display_3 (.value(_1));  // open: dp
  // Probe on Addr
  LED #(.active("true")) led_1 (.in(RDY));
  // Probe on BlkDataIn
  // Probe on Dataout
  and and_3 (Go, Runing, or_1_out);
  not not_3 (Error, or_1_out);

  // Other names for the same wires on the sheet: 读错误暂停 = in_1

  // Notes on the sheet:
  //   contents of 主存地址 (hex, n*v repeats v):
  //   0 1 2 3 8 9 a b 10 11 12 13 20 21 22 23 8 9 a b 4 5 6 7 24 25 26 27 4 5 6 7 0 1 2 3 8 9 a b 8 9 a b
  //   20 21 22 23 28 29 2a 2b 24 25 26 27 4 5 6 7 24 25 26 27 0 1 2 3 8 9 a b 20 21 22 23 20 21 22 23 30
  //   31 32 33 4 5 6 7 24 25 26 27 4 5 6 7 0 1 2 3 8 9 a b 20 21 22 23 20 21 22 23 28 29 2a 2b 4 5 6 7 24
  //   25 26 27 24 25 26 27 0 1 2 3 8 9 a b 8 9 a b 20 21 22 23 30 31 32 33 4 5 6 7 24 25 26 27 24 25 26 27
  //   0 1 2 3 0 1 2 3 8 9 a b 20 21 22 23 28 29 2a 2b 4 5 6 7 24 25 26 27 4 5 6 7 0 1 2 3 8 9 a b 0 1 2 3
  //   20 21 22 23 30 31 32 33 24 25 26 27 4 5 6 7 24 25 26 27 0 1 2 3 8 9 a b 20 21 22 23 20 21 22 23 28
  //   29 2a 2b 4 5 6 7 24 25 26 27 4 5 6 7
  //   直接相联映射cache测试电路
  //   命中率
  //   contents of 主存内容 (hex, n*v repeats v):
  //   0 1 2 3 4 5 6 7 8 9 a b c d e f 10 11 12 13 14 15 16 17 18 19 1a 1b 1c 1d 1e 1f 20 21 22 23 24 25 26
  //   27 28 29 2a 2b 2c 2d 2e 2f 30 31 32 33 34 35 36 37 38 39 3a 3b 3c 3d 3e 3f 40 41 42 43 44 45 46 47
  //   48 49 4a 4b 4c 4d 4e 4f 50 51 52 53 54 55 56 57 58 59 5a 5b 5c 5d 5e 5f 60 61 62 63 64 65 66 67 68
  //   69 6a 6b 6c 6d 6e 6f 70 71 72 73 74 75 76 77 78 79 7a 7b 7c 7d 7e 7f 80 81 82 83 84 85 86 87 88 89
  //   8a 8b 8c 8d 8e 8f 90 91 92 93 94 95 96 97 98 99 9a 9b 9c 9d 9e 9f a0 a1 a2 a3 a4 a5 a6 a7 a8 a9 aa
  //   ab ac ad ae af b0 b1 b2 b3 b4 b5 b6 b7 b8 b9 ba bb bc bd be bf c0 c1 c2 c3 c4 c5 c6 c7 c8 c9 ca cb
  //   cc cd ce cf d0 d1 d2 d3 d4 d5 d6 d7 d8 d9 da db dc dd de df e0 e1 e2 e3 e4 e5 e6 e7 e8 e9 ea eb ec
  //   ed ee ef f0 f1 f2 f3 f4 f5 f6 f7 f8 f9 fa fb fc fd fe ff 0 1 2 3 4 5 6 7 8 9 a b c d e f 10 11 12 13
  //   14 15 16 17 18 19 1a 1b 1c 1d 1e 1f 20 21 22 23 24 25 26 27 28 29 2a 2b 2c 2d 2e 2f 30 31 32 33 34
  //   35 36 37 38 39 3a 3b 3c 3d 3e 3f 40 41 42 43 44 45 46 47 48 49 4a 4b 4c 4d 4e 4f 50 51 52 53 54 55
  //   56 57 58 59 5a 5b 5c 5d 5e 5f 60 61 62 63 64 65 66 67 68 69 6a 6b 6c 6d 6e 6f 70 71 72 73 74 75 76
  //   77 78 79 7a 7b 7c 7d 7e 7f 80 81 82 83 84 85 86 87 88 89 8a 8b 8c 8d 8e 8f 90 91 92 93 94 95 96 97
  //   98 99 9a 9b 9c 9d 9e 9f a0 a1 a2 a3 a4 a5 a6 a7 a8 a9 aa ab ac ad ae af b0 b1 b2 b3 b4 b5 b6 b7 b8
  //   b9 ba bb bc bd be bf c0 c1 c2 c3 c4 c5 c6 c7 c8 c9 ca cb cc cd ce cf d0 d1 d2 d3 d4 d5 d6 d7 d8 d9
  //   da db dc dd de df e0 e1 e2 e3 e4 e5 e6 e7 e8 e9 ea eb ec ed ee ef f0 f1 f2 f3 f4 f5 f6 f7 f8 f9 fa
  //   fb fc fd fe ff 0 1 2 3 4 5 6 7 8 9 a b c d e f 10 11 12 13 14 15 16 17 18 19 1a 1b 1c 1d 1e 1f 20 21
  //   22 23 24 25 26 27 28 29 2a 2b 2c 2d 2e 2f 30 31 32 33 34 35 36 37 38 39 3a 3b 3c 3d 3e 3f 40 41 42
  //   43 44 45 46 47 48 49 4a 4b 4c 4d 4e 4f 50 51 52 53 54 55 56 57 58 59 5a 5b 5c 5d 5e 5f 60 61 62 63
  //   64 65 66 67 68 69 6a 6b 6c 6d 6e 6f 70 71 72 73 74 75 76 77 78 79 7a 7b 7c 7d 7e 7f 80 81 82 83 84
  //   85 86 87 88 89 8a 8b 8c 8d 8e 8f 90 91 92 93 94 95 96 97 98 99 9a 9b 9c 9d 9e 9f a0 a1 a2 a3 a4 a5
  //   a6 a7 a8 a9 aa ab ac ad ae af b0 b1 b2 b3 b4 b5 b6 b7 b8 b9 ba bb bc bd be bf c0 c1 c2 c3 c4 c5 c6
  //   c7 c8 c9 ca cb cc cd ce cf d0 d1 d2 d3 d4 d5 d6 d7 d8 d9 da db dc dd de df e0 e1 e2 e3 e4 e5 e6 e7
  //   e8 e9 ea eb ec ed ee ef f0 f1 f2 f3 f4 f5 f6 f7 f8 f9 fa fb fc fd fe ff 0 1 2 3 4 5 6 7 8 9 a b c d
  //   e f 10 11 12 13 14 15 16 17 18 19 1a 1b 1c 1d 1e 1f 20 21 22 23 24 25 26 27 28 29 2a 2b 2c 2d 2e 2f
  //   30 31 32 33 34 35 36 37 38 39 3a 3b 3c 3d 3e 3f 40 41 42 43 44 45 46 47 48 49 4a 4b 4c 4d 4e 4f 50
  //   51 52 53 54 55 56 57 58 59 5a 5b 5c 5d 5e 5f 60 61 62 63 64 65 66 67 68 69 6a 6b 6c 6d 6e 6f 70 71
  //   72 73 74 75 76 77 78 79 7a 7b 7c 7d 7e 7f 80 81 82 83 84 85 86 87 88 89 8a 8b 8c 8d 8e 8f 90 91 92
  //   93 94 95 96 97 98 99 9a 9b 9c 9d 9e 9f a0 a1 a2 a3 a4 a5 a6 a7 a8 a9 aa ab ac ad ae af b0 b1 b2 b3
  //   b4 b5 b6 b7 b8 b9 ba bb bc bd be bf c0 c1 c2 c3 c4 c5 c6 c7 c8 c9 ca cb cc cd ce cf d0 d1 d2 d3 d4
  //   d5 d6 d7 d8 d9 da db dc dd de df e0 e1 e2 e3 e4 e5 e6 e7 e8 e9 ea eb ec ed ee ef f0 f1 f2 f3 f4 f5
  //   f6 f7 f8 f9 fa fb fc fd fe ff 0 1 2 3 4 5 6 7 8 9 a b c d e f 10 11 12 13 14 15 16 17 18 19 1a 1b 1c
  //   1d 1e 1f 20 21 22 23 24 25 26 27 28 29 2a 2b 2c 2d 2e 2f 30 31 32 33 34 35 36 37 38 39 3a 3b 3c 3d
  //   3e 3f 40 41 42 43 44 45 46 47 48 49 4a 4b 4c 4d 4e 4f 50 51 52 53 54 55 56 57 58 59 5a 5b 5c 5d 5e
  //   5f 60 61 62 63 64 65 66 67 68 69 6a 6b 6c 6d 6e 6f 70 71 72 73 74 75 76 77 78 79 7a 7b 7c 7d 7e 7f
  //   80 81 82 83 84 85 86 87 88 89 8a 8b 8c 8d 8e 8f 90 91 92 93 94 95 96 97 98 99 9a 9b 9c 9d 9e 9f a0
  //   a1 a2 a3 a4 a5 a6 a7 a8 a9 aa ab ac ad ae af b0 b1 b2 b3 b4 b5 b6 b7 b8 b9 ba bb bc bd be bf c0 c1
  //   c2 c3 c4 c5 c6 c7 c8 c9 ca cb cc cd ce cf d0 d1 d2 d3 d4 d5 d6 d7 d8 d9 da db dc dd de df e0 e1 e2
  //   e3 e4 e5 e6 e7 e8 e9 ea eb ec ed ee ef f0 f1 f2 f3 f4 f5 f6 f7 f8 f9 fa fb fc fd fe ff
  //   cache模拟器
endmodule

module \cache_直接相联映射_电路_16个cache块  (
  input  [15:0] Addr,
  input  [31:0] BlockDataIn,
  input  BlkDataReady,
  input  CLK,
  output Miss,
  output [7:0] DataOut
);

  wire and_2_out, and_3_out, and_4_out, and_5_out, and_6_out, and_7_out, and_8_out, and_9_out, and_10_out,
       and_11_out, and_12_out, and_13_out, and_14_out, and_15_out, and_16_out, and_17_out, comparator_1_eq,
       Hit, L0, L1, L2, L3, L4, L5, L6, L7, L8, L9, L10, L11, L12, L13, L14, L15, undriven, Valid, VALID_2_q,
       VALID_3_q, VALID_4_q, VALID_5_q, VALID_6_q, VALID_7_q, VALID_8_q, VALID_9_q, VALID_10_q, VALID_11_q,
       VALID_12_q, VALID_13_q, VALID_14_q, VALID_15_q, VALID_16_q, VALID_q;
  wire [9:0] TAG_2_q, TAG_3_q, TAG_4_q, TAG_5_q, TAG_6_q, TAG_7_q, TAG_8_q, TAG_9_q, TAG_10_q, TAG_11_q,
       TAG_12_q, TAG_13_q, TAG_14_q, TAG_15_q, TAG_16_q, TAG_q, TagData;
  wire [31:0] DATA_COPY_2_q, DATA_COPY_3_q, DATA_COPY_4_q, DATA_COPY_5_q, DATA_COPY_6_q, DATA_COPY_7_q,
       DATA_COPY_8_q, DATA_COPY_9_q, DATA_COPY_10_q, DATA_COPY_11_q, DATA_COPY_12_q, DATA_COPY_13_q,
       DATA_COPY_14_q, DATA_COPY_15_q, DATA_COPY_16_q, DATA_COPY_q, SlotData;

  Multiplexer #(.select(2), .width(8), .disabled("Z"), .enable("true")) multiplexer_1 (
    .in0(SlotData[7:0]), .in1(SlotData[15:8]), .in2(SlotData[23:16]), .in3(SlotData[31:24]), .out(DataOut),
    .sel(Addr[1:0]), .en(Hit));
  Register #(.width(1), .trigger("rising"), .Select("low")) u_VALID (
    .D(1'b1), .en(and_2_out), .Q(VALID_q), .clk(CLK));  // open: clr
  assign Valid = L0 ? VALID_q : 1'bz;  // Controlled_Buffer controlled_buffer_1
  Register #(.width(1), .trigger("rising"), .Select("low")) VALID_2 (
    .D(1'b1), .en(and_3_out), .Q(VALID_2_q), .clk(CLK));  // open: clr
  assign Valid = L1 ? VALID_2_q : 1'bz;  // Controlled_Buffer controlled_buffer_2
  Register #(.width(1), .trigger("rising"), .Select("low")) VALID_3 (
    .D(1'b1), .en(and_4_out), .Q(VALID_3_q), .clk(CLK));  // open: clr
  assign Valid = L2 ? VALID_3_q : 1'bz;  // Controlled_Buffer controlled_buffer_3
  Register #(.width(1), .trigger("rising"), .Select("low")) VALID_4 (
    .D(1'b1), .en(and_5_out), .Q(VALID_4_q), .clk(CLK));  // open: clr
  assign Valid = L3 ? VALID_4_q : 1'bz;  // Controlled_Buffer controlled_buffer_4
  Register #(.width(1), .trigger("rising"), .Select("low")) VALID_5 (
    .D(1'b1), .en(and_6_out), .Q(VALID_5_q), .clk(CLK));  // open: clr
  assign Valid = L4 ? VALID_5_q : 1'bz;  // Controlled_Buffer controlled_buffer_5
  Register #(.width(1), .trigger("rising"), .Select("low")) VALID_6 (
    .D(1'b1), .en(and_7_out), .Q(VALID_6_q), .clk(CLK));  // open: clr
  assign Valid = L5 ? VALID_6_q : 1'bz;  // Controlled_Buffer controlled_buffer_6
  Register #(.width(1), .trigger("rising"), .Select("low")) VALID_7 (
    .D(1'b1), .en(and_8_out), .Q(VALID_7_q), .clk(CLK));  // open: clr
  assign Valid = L6 ? VALID_7_q : 1'bz;  // Controlled_Buffer controlled_buffer_7
  Register #(.width(1), .trigger("rising"), .Select("low")) VALID_8 (
    .D(1'b1), .en(and_9_out), .Q(VALID_8_q), .clk(CLK));  // open: clr
  assign Valid = L7 ? VALID_8_q : 1'bz;  // Controlled_Buffer controlled_buffer_8
  // Probe on Addr[5:2]
  Register #(.width(10), .trigger("rising"), .Select("low")) TAG (
    .D(Addr[15:6]), .en(and_2_out), .Q(TAG_q), .clk(CLK));  // open: clr
  Register #(.width(10), .trigger("rising"), .Select("low")) TAG_2 (
    .D(Addr[15:6]), .en(and_3_out), .Q(TAG_2_q), .clk(CLK));  // open: clr
  Register #(.width(10), .trigger("rising"), .Select("low")) TAG_3 (
    .D(Addr[15:6]), .en(and_4_out), .Q(TAG_3_q), .clk(CLK));  // open: clr
  Register #(.width(10), .trigger("rising"), .Select("low")) TAG_4 (
    .D(Addr[15:6]), .en(and_5_out), .Q(TAG_4_q), .clk(CLK));  // open: clr
  Register #(.width(10), .trigger("rising"), .Select("low")) TAG_5 (
    .D(Addr[15:6]), .en(and_6_out), .Q(TAG_5_q), .clk(CLK));  // open: clr
  Register #(.width(10), .trigger("rising"), .Select("low")) TAG_6 (
    .D(Addr[15:6]), .en(and_7_out), .Q(TAG_6_q), .clk(CLK));  // open: clr
  Register #(.width(10), .trigger("rising"), .Select("low")) TAG_7 (
    .D(Addr[15:6]), .en(and_8_out), .Q(TAG_7_q), .clk(CLK));  // open: clr
  Register #(.width(10), .trigger("rising"), .Select("low")) TAG_8 (
    .D(Addr[15:6]), .en(and_9_out), .Q(TAG_8_q), .clk(CLK));  // open: clr
  Decoder #(.select(4), .tristate("false"), .disabled("Z"), .enable("false")) decoder_1 (
    .out0(L0), .out1(L1), .out2(L2), .out3(L3), .out4(L4), .out5(L5), .out6(L6), .out7(L7), .out8(L8),
    .out9(L9), .out10(L10), .out11(L11), .out12(L12), .out13(L13), .out14(L14), .out15(L15), .sel(Addr[5:2]));
  assign TagData = L0 ? TAG_q : 10'bz;  // Controlled_Buffer controlled_buffer_9
  assign TagData = L1 ? TAG_2_q : 10'bz;  // Controlled_Buffer controlled_buffer_10
  assign TagData = L2 ? TAG_3_q : 10'bz;  // Controlled_Buffer controlled_buffer_11
  assign TagData = L3 ? TAG_4_q : 10'bz;  // Controlled_Buffer controlled_buffer_12
  assign TagData = L4 ? TAG_5_q : 10'bz;  // Controlled_Buffer controlled_buffer_13
  assign TagData = L5 ? TAG_6_q : 10'bz;  // Controlled_Buffer controlled_buffer_14
  assign TagData = L6 ? TAG_7_q : 10'bz;  // Controlled_Buffer controlled_buffer_15
  assign TagData = L7 ? TAG_8_q : 10'bz;  // Controlled_Buffer controlled_buffer_16
  Comparator #(.width(10), .mode("twosComplement")) comparator_1 (
    .a(Addr[15:6]), .b(TagData), .eq(comparator_1_eq));  // open: gt, lt
  and and_1 (Hit, comparator_1_eq, Valid);
  assign SlotData = L0 ? DATA_COPY_q : 32'bz;  // Controlled_Buffer controlled_buffer_17
  Register #(.width(32), .trigger("rising"), .Select("low")) DATA_COPY (
    .D(BlockDataIn), .en(and_2_out), .Q(DATA_COPY_q), .clk(CLK));  // open: clr
  assign SlotData = L1 ? DATA_COPY_2_q : 32'bz;  // Controlled_Buffer controlled_buffer_18
  Register #(.width(32), .trigger("rising"), .Select("low")) DATA_COPY_2 (
    .D(BlockDataIn), .en(and_3_out), .Q(DATA_COPY_2_q), .clk(CLK));  // open: clr
  assign SlotData = L2 ? DATA_COPY_3_q : 32'bz;  // Controlled_Buffer controlled_buffer_19
  Register #(.width(32), .trigger("rising"), .Select("low")) DATA_COPY_3 (
    .D(BlockDataIn), .en(and_4_out), .Q(DATA_COPY_3_q), .clk(CLK));  // open: clr
  assign SlotData = L3 ? DATA_COPY_4_q : 32'bz;  // Controlled_Buffer controlled_buffer_20
  Register #(.width(32), .trigger("rising"), .Select("low")) DATA_COPY_4 (
    .D(BlockDataIn), .en(and_5_out), .Q(DATA_COPY_4_q), .clk(CLK));  // open: clr
  Register #(.width(32), .trigger("rising"), .Select("low")) DATA_COPY_5 (
    .D(BlockDataIn), .en(and_6_out), .Q(DATA_COPY_5_q), .clk(CLK));  // open: clr
  assign SlotData = L4 ? DATA_COPY_5_q : 32'bz;  // Controlled_Buffer controlled_buffer_21
  Register #(.width(32), .trigger("rising"), .Select("low")) DATA_COPY_6 (
    .D(BlockDataIn), .en(and_7_out), .Q(DATA_COPY_6_q), .clk(CLK));  // open: clr
  assign SlotData = L5 ? DATA_COPY_6_q : 32'bz;  // Controlled_Buffer controlled_buffer_22
  assign SlotData = L6 ? DATA_COPY_7_q : 32'bz;  // Controlled_Buffer controlled_buffer_23
  Register #(.width(32), .trigger("rising"), .Select("low")) DATA_COPY_7 (
    .D(BlockDataIn), .en(and_8_out), .Q(DATA_COPY_7_q), .clk(CLK));  // open: clr
  assign SlotData = L7 ? DATA_COPY_8_q : 32'bz;  // Controlled_Buffer controlled_buffer_24
  Register #(.width(32), .trigger("rising"), .Select("low")) DATA_COPY_8 (
    .D(BlockDataIn), .en(and_9_out), .Q(DATA_COPY_8_q), .clk(CLK));  // open: clr
  not not_1 (Miss, Hit);
  and and_2 (and_2_out, L0, BlkDataReady);
  and and_3 (and_3_out, L1, BlkDataReady);
  and and_4 (and_4_out, L2, BlkDataReady);
  and and_5 (and_5_out, L3, BlkDataReady);
  and and_6 (and_6_out, L4, BlkDataReady);
  and and_7 (and_7_out, L5, BlkDataReady);
  and and_8 (and_8_out, L6, BlkDataReady);
  and and_9 (and_9_out, L7, BlkDataReady);
  Register #(.width(1), .trigger("rising"), .Select("low")) VALID_9 (
    .D(1'b1), .en(and_10_out), .Q(VALID_9_q), .clk(CLK), .preset(undriven));  // open: clr, cs
  Register #(.width(1), .trigger("rising"), .Select("low")) VALID_10 (
    .D(1'b1), .en(and_11_out), .Q(VALID_10_q), .clk(CLK));  // open: clr
  Register #(.width(1), .trigger("rising"), .Select("low")) VALID_11 (
    .D(1'b1), .en(and_12_out), .Q(VALID_11_q), .clk(CLK));  // open: clr
  Register #(.width(1), .trigger("rising"), .Select("low")) VALID_12 (
    .D(1'b1), .en(and_13_out), .Q(VALID_12_q), .clk(CLK));  // open: clr
  Register #(.width(1), .trigger("rising"), .Select("low")) VALID_13 (
    .D(1'b1), .en(and_14_out), .Q(VALID_13_q), .clk(CLK));  // open: clr
  Register #(.width(1), .trigger("rising"), .Select("low")) VALID_14 (
    .D(1'b1), .en(and_15_out), .Q(VALID_14_q), .clk(CLK));  // open: clr
  Register #(.width(1), .trigger("rising"), .Select("low")) VALID_15 (
    .D(1'b1), .en(and_16_out), .Q(VALID_15_q), .clk(CLK));  // open: clr
  Register #(.width(1), .trigger("rising"), .Select("low")) VALID_16 (
    .D(1'b1), .en(and_17_out), .Q(VALID_16_q), .clk(CLK));  // open: clr
  assign Valid = L8 ? VALID_9_q : 1'bz;  // Controlled_Buffer controlled_buffer_25
  assign Valid = L9 ? VALID_10_q : 1'bz;  // Controlled_Buffer controlled_buffer_26
  assign Valid = L10 ? VALID_11_q : 1'bz;  // Controlled_Buffer controlled_buffer_27
  assign Valid = L11 ? VALID_12_q : 1'bz;  // Controlled_Buffer controlled_buffer_28
  assign Valid = L12 ? VALID_13_q : 1'bz;  // Controlled_Buffer controlled_buffer_29
  assign Valid = L13 ? VALID_14_q : 1'bz;  // Controlled_Buffer controlled_buffer_30
  assign Valid = L14 ? VALID_15_q : 1'bz;  // Controlled_Buffer controlled_buffer_31
  assign Valid = L15 ? VALID_16_q : 1'bz;  // Controlled_Buffer controlled_buffer_32
  Register #(.width(10), .trigger("rising"), .Select("low")) TAG_9 (
    .D(Addr[15:6]), .en(and_10_out), .Q(TAG_9_q), .clk(CLK));  // open: clr
  assign TagData = L8 ? TAG_9_q : 10'bz;  // Controlled_Buffer controlled_buffer_33
  assign TagData = L9 ? TAG_10_q : 10'bz;  // Controlled_Buffer controlled_buffer_34
  Register #(.width(10), .trigger("rising"), .Select("low")) TAG_10 (
    .D(Addr[15:6]), .en(and_11_out), .Q(TAG_10_q), .clk(CLK));  // open: clr
  Register #(.width(10), .trigger("rising"), .Select("low")) TAG_11 (
    .D(Addr[15:6]), .en(and_12_out), .Q(TAG_11_q), .clk(CLK));  // open: clr
  assign TagData = L10 ? TAG_11_q : 10'bz;  // Controlled_Buffer controlled_buffer_35
  Register #(.width(10), .trigger("rising"), .Select("low")) TAG_12 (
    .D(Addr[15:6]), .en(and_13_out), .Q(TAG_12_q), .clk(CLK));  // open: clr
  assign TagData = L11 ? TAG_12_q : 10'bz;  // Controlled_Buffer controlled_buffer_36
  assign TagData = L12 ? TAG_13_q : 10'bz;  // Controlled_Buffer controlled_buffer_37
  Register #(.width(10), .trigger("rising"), .Select("low")) TAG_13 (
    .D(Addr[15:6]), .en(and_14_out), .Q(TAG_13_q), .clk(CLK));  // open: clr
  assign TagData = L13 ? TAG_14_q : 10'bz;  // Controlled_Buffer controlled_buffer_38
  Register #(.width(10), .trigger("rising"), .Select("low")) TAG_14 (
    .D(Addr[15:6]), .en(and_15_out), .Q(TAG_14_q), .clk(CLK));  // open: clr
  assign TagData = L14 ? TAG_15_q : 10'bz;  // Controlled_Buffer controlled_buffer_39
  Register #(.width(10), .trigger("rising"), .Select("low")) TAG_15 (
    .D(Addr[15:6]), .en(and_16_out), .Q(TAG_15_q), .clk(CLK));  // open: clr
  Register #(.width(10), .trigger("rising"), .Select("low")) TAG_16 (
    .D(Addr[15:6]), .en(and_17_out), .Q(TAG_16_q), .clk(CLK));  // open: clr
  assign TagData = L15 ? TAG_16_q : 10'bz;  // Controlled_Buffer controlled_buffer_40
  Register #(.width(32), .trigger("rising"), .Select("low")) DATA_COPY_9 (
    .D(BlockDataIn), .en(and_10_out), .Q(DATA_COPY_9_q), .clk(CLK));  // open: clr
  Register #(.width(32), .trigger("rising"), .Select("low")) DATA_COPY_10 (
    .D(BlockDataIn), .en(and_11_out), .Q(DATA_COPY_10_q), .clk(CLK));  // open: clr
  Register #(.width(32), .trigger("rising"), .Select("low")) DATA_COPY_11 (
    .D(BlockDataIn), .en(and_12_out), .Q(DATA_COPY_11_q), .clk(CLK));  // open: clr
  Register #(.width(32), .trigger("rising"), .Select("low")) DATA_COPY_12 (
    .D(BlockDataIn), .en(and_13_out), .Q(DATA_COPY_12_q), .clk(CLK));  // open: clr
  Register #(.width(32), .trigger("rising"), .Select("low")) DATA_COPY_13 (
    .D(BlockDataIn), .en(and_14_out), .Q(DATA_COPY_13_q), .clk(CLK));  // open: clr
  Register #(.width(32), .trigger("rising"), .Select("low")) DATA_COPY_14 (
    .D(BlockDataIn), .en(and_15_out), .Q(DATA_COPY_14_q), .clk(CLK));  // open: clr
  Register #(.width(32), .trigger("rising"), .Select("low")) DATA_COPY_15 (
    .D(BlockDataIn), .en(and_16_out), .Q(DATA_COPY_15_q), .clk(CLK));  // open: clr
  Register #(.width(32), .trigger("rising"), .Select("low")) DATA_COPY_16 (
    .D(BlockDataIn), .en(and_17_out), .Q(DATA_COPY_16_q), .clk(CLK));  // open: clr
  assign SlotData = L8 ? DATA_COPY_9_q : 32'bz;  // Controlled_Buffer controlled_buffer_41
  assign SlotData = L9 ? DATA_COPY_10_q : 32'bz;  // Controlled_Buffer controlled_buffer_42
  assign SlotData = L10 ? DATA_COPY_11_q : 32'bz;  // Controlled_Buffer controlled_buffer_43
  assign SlotData = L11 ? DATA_COPY_12_q : 32'bz;  // Controlled_Buffer controlled_buffer_44
  assign SlotData = L12 ? DATA_COPY_13_q : 32'bz;  // Controlled_Buffer controlled_buffer_45
  assign SlotData = L13 ? DATA_COPY_14_q : 32'bz;  // Controlled_Buffer controlled_buffer_46
  assign SlotData = L14 ? DATA_COPY_15_q : 32'bz;  // Controlled_Buffer controlled_buffer_47
  assign SlotData = L15 ? DATA_COPY_16_q : 32'bz;  // Controlled_Buffer controlled_buffer_48
  and and_10 (and_10_out, L8, BlkDataReady);
  and and_11 (and_11_out, L9, BlkDataReady);
  and and_12 (and_12_out, L10, BlkDataReady);
  and and_13 (and_13_out, L11, BlkDataReady);
  and and_14 (and_14_out, L12, BlkDataReady);
  and and_15 (and_15_out, L13, BlkDataReady);
  and and_16 (and_16_out, L14, BlkDataReady);
  and and_17 (and_17_out, L15, BlkDataReady);

  // Other names for the same wires on the sheet: Blk[31:0] = BlockDataIn; BlkReady = BlkDataReady;
  //   Offset[1:0] = Addr[1:0]; 字节地址[15:0] = Addr; Index[3:0] = Addr[5:2]; Tag[9:0] = Addr[15:6]

  // Notes on the sheet:
  //   输入引脚区
  //   标记位
  //   有效位
  //   行选中
  //   cache（直接相联映射）电路（16个cache块）
  //   输出引脚区
  //   有效位
  //   行选中
  //   标记位
endmodule

module \直接相联映射_16个cache块_测试电路  (
  input  in_1
);

  wire and_2_out, Clk, comparator_1_lt, comparator_2_eq, comparator_3_eq, controlled_buffer_1_out, EN, Error,
       Go, Hit, Miss, or_1_out, RDY, Runing;
  wire [3:0] _1, _2, _3;
  wire [7:0] Dataout, \主存内容_data ;
  wire [9:0] \测试用例数 ;
  wire [15:0] adder_1_out, Addr, bit_extender_3_out, \cache块交换逻辑电路_1_byteaddrout , counter_1_q,
       subtractor_1_out, \命中次数 , \时钟周期数 , \校验和 , \缺失次数 , \访问次数 ;
  wire [31:0] bit_extender_1_out, bit_extender_2_out, BlkDataIn, divider_1_out, divider_2_out,
       multiplier_1_out;
  wire [31:4] divider_2_rem, divider_3_out, divider_3_rem;

  not not_1 (Hit, Miss);
  and and_1 (EN, Hit, Go);
  Clock #(.highDuration(1), .lowDuration(1)) clock_1 (.out(Clk));
  Counter #(.width(16), .max('hffff), .ongoal("wrap"), .trigger("rising"), .behavior("old")) counter_1 (
    .count(and_2_out), .Q(counter_1_q), .clk(Clk));  // open: load, D, carry, clr, preset
  and and_2 (and_2_out, Miss, RDY, Runing);
  Subtractor #(.width(16)) subtractor_1 (.a(\访问次数 ), .b(\缺失次数 ), .out(subtractor_1_out));  // open: bin, bout
  Comparator #(.width(16), .mode("twosComplement")) comparator_1 (
    .a(\访问次数 ), .b(\缺失次数 ), .lt(comparator_1_lt));  // open: gt, eq
  // Probe on \访问次数 
  // Probe on \测试用例数 
  Counter #(.width(10), .max('h3ff), .ongoal("wrap"), .trigger("rising"), .behavior("old")) \u_计数器  (
    .count(EN), .Q(\测试用例数 ), .clk(Clk));  // open: load, D, carry, clr, preset
  Register #(.width(16), .trigger("rising"), .Select("low")) register_1 (
    .D(counter_1_q), .en(EN), .Q(\缺失次数 ), .clk(Clk));  // open: clr
  Comparator #(.width(10), .mode("twosComplement")) comparator_2 (
    .a(\测试用例数 ), .b(10'h100), .eq(comparator_2_eq));  // open: gt, lt
  not not_2 (Runing, comparator_2_eq);
  Multiplexer #(.select(1), .width(16), .disabled(0), .enable("false")) multiplexer_1 (
    .in0(subtractor_1_out), .in1({16{1'b0}}), .out(\命中次数 ), .sel(comparator_1_lt));
  // Probe on \命中次数 
  // Probe on \时钟周期数 
  ROM #(.addrWidth(10), .dataWidth(16), .Select("high")) \u_主存地址  (.addr(\测试用例数 ), .data(Addr));
  Counter #(.width(16), .max('hffff), .ongoal("wrap"), .trigger("rising"), .behavior("old")) counter_2 (
    .count(EN), .Q(\访问次数 ), .clk(Clk));  // open: load, D, carry, clr, preset
  assign bit_extender_1_out = {{16{1'b0}}, \命中次数 };  // Bit_Extender bit_extender_1
  // Probe on Dataout
  Multiplier #(.width(32)) multiplier_1 (
    .a(bit_extender_1_out), .b(32'h64), .out(multiplier_1_out));  // open: cin, cout
  assign bit_extender_2_out = {{16{1'b0}}, \访问次数 };  // Bit_Extender bit_extender_2
  // Probe on \缺失次数 
  // Probe on \校验和 
  \cache_直接相联映射_电路_16个cache块  \cache_直接相联映射_电路_16个cache块_1  (
    .Addr(Addr), .BlockDataIn(BlkDataIn), .BlkDataReady(RDY), .CLK(Clk), .Miss(Miss), .DataOut(Dataout));
  assign bit_extender_3_out = {{8{1'b0}}, Dataout};  // Bit_Extender bit_extender_3
  Divider #(.width(32)) divider_1 (
    .a(multiplier_1_out), .b(bit_extender_2_out), .out(divider_1_out));  // open: upper, rem
  Adder #(.width(16)) adder_1 (.a(\校验和 ), .b(bit_extender_3_out), .out(adder_1_out));  // open: cin, cout
  LED #(.active("true")) \u_读数据出错  (.in(Error));
  Pull_Resistor #(.pull(1)) pull_resistor_1 (.node(Miss));
  LED #(.active("true")) \u_缺失  (.in(Miss));
  Register #(.width(16), .trigger("rising"), .Select("low")) \u_校验和  (
    .D(adder_1_out), .en(EN), .Q(\校验和 ), .clk(Clk));  // open: clr
  Divider #(.width(32)) divider_2 (
    .a(divider_1_out), .b(32'ha), .out(divider_2_out), .rem({divider_2_rem, _1}));  // open: upper
  \cache块交换逻辑电路  \cache块交换逻辑电路_1  (
    .Addr(Addr), .CLK(Clk), .ByteAddrOut(\cache块交换逻辑电路_1_byteaddrout ), .ByteDataIn(\主存内容_data ),
    .Miss(Miss), .BlkDataReady(RDY), .BlockDataIn(BlkDataIn), .Enable(Runing));
  // Probe on \校验和 
  Divider #(.width(32)) divider_3 (
    .a(divider_2_out), .b(32'ha), .out({divider_3_out, _3}), .rem({divider_3_rem, _2}));  // open: upper
  ROM #(.addrWidth(16), .dataWidth(8), .Select("high")) \u_主存内容  (
    .addr(\cache块交换逻辑电路_1_byteaddrout ), .data(\主存内容_data ));
  assign controlled_buffer_1_out = Hit ? comparator_3_eq : 1'bz;  // Controlled_Buffer controlled_buffer_1
  Comparator #(.width(8), .mode("twosComplement")) comparator_3 (
    .a(Addr[7:0]), .b(Dataout), .eq(comparator_3_eq));  // open: gt, lt
  Pull_Resistor #(.pull(1)) pull_resistor_2 (.node(controlled_buffer_1_out));
  Hex_Digit_Display hex_digit_display_1 (.value(_3), .dp(1'b1));
  Hex_Digit_Display hex_digit_display_2 (.value(_2));  // open: dp
  or or_1 (or_1_out, controlled_buffer_1_out, ~in_1);  // OR_Gate
  Counter #(.width(16), .max('hffff), .ongoal("wrap"), .trigger("rising"), .behavior("old")) counter_3 (
    .count(Runing), .Q(\时钟周期数 ), .clk(Clk));  // open: load, D, carry, clr, preset
  Hex_Digit_Display hex_digit_display_3 (.value(_1));  // open: dp
  // Probe on Addr
  LED #(.active("true")) led_1 (.in(RDY));
  // Probe on BlkDataIn
  // Probe on Dataout
  and and_3 (Go, Runing, or_1_out);
  not not_3 (Error, or_1_out);

  // Other names for the same wires on the sheet: 读错误暂停 = in_1

  // Notes on the sheet:
  //   contents of 主存地址 (hex, n*v repeats v):
  //   0 1 2 3 8 9 a b 10 11 12 13 20 21 22 23 8 9 a b 4 5 6 7 24 25 26 27 4 5 6 7 0 1 2 3 8 9 a b 8 9 a b
  //   20 21 22 23 28 29 2a 2b 24 25 26 27 4 5 6 7 24 25 26 27 0 1 2 3 8 9 a b 20 21 22 23 20 21 22 23 30
  //   31 32 33 4 5 6 7 24 25 26 27 4 5 6 7 0 1 2 3 8 9 a b 20 21 22 23 20 21 22 23 28 29 2a 2b 4 5 6 7 24
  //   25 26 27 24 25 26 27 0 1 2 3 8 9 a b 8 9 a b 20 21 22 23 30 31 32 33 4 5 6 7 24 25 26 27 24 25 26 27
  //   0 1 2 3 0 1 2 3 8 9 a b 20 21 22 23 28 29 2a 2b 4 5 6 7 24 25 26 27 4 5 6 7 0 1 2 3 8 9 a b 0 1 2 3
  //   20 21 22 23 30 31 32 33 24 25 26 27 4 5 6 7 24 25 26 27 0 1 2 3 8 9 a b 20 21 22 23 20 21 22 23 28
  //   29 2a 2b 4 5 6 7 24 25 26 27 4 5 6 7
  //   直接相联映射cache测试电路
  //   命中率
  //   contents of 主存内容 (hex, n*v repeats v):
  //   0 1 2 3 4 5 6 7 8 9 a b c d e f 10 11 12 13 14 15 16 17 18 19 1a 1b 1c 1d 1e 1f 20 21 22 23 24 25 26
  //   27 28 29 2a 2b 2c 2d 2e 2f 30 31 32 33 34 35 36 37 38 39 3a 3b 3c 3d 3e 3f 40 41 42 43 44 45 46 47
  //   48 49 4a 4b 4c 4d 4e 4f 50 51 52 53 54 55 56 57 58 59 5a 5b 5c 5d 5e 5f 60 61 62 63 64 65 66 67 68
  //   69 6a 6b 6c 6d 6e 6f 70 71 72 73 74 75 76 77 78 79 7a 7b 7c 7d 7e 7f 80 81 82 83 84 85 86 87 88 89
  //   8a 8b 8c 8d 8e 8f 90 91 92 93 94 95 96 97 98 99 9a 9b 9c 9d 9e 9f a0 a1 a2 a3 a4 a5 a6 a7 a8 a9 aa
  //   ab ac ad ae af b0 b1 b2 b3 b4 b5 b6 b7 b8 b9 ba bb bc bd be bf c0 c1 c2 c3 c4 c5 c6 c7 c8 c9 ca cb
  //   cc cd ce cf d0 d1 d2 d3 d4 d5 d6 d7 d8 d9 da db dc dd de df e0 e1 e2 e3 e4 e5 e6 e7 e8 e9 ea eb ec
  //   ed ee ef f0 f1 f2 f3 f4 f5 f6 f7 f8 f9 fa fb fc fd fe ff 0 1 2 3 4 5 6 7 8 9 a b c d e f 10 11 12 13
  //   14 15 16 17 18 19 1a 1b 1c 1d 1e 1f 20 21 22 23 24 25 26 27 28 29 2a 2b 2c 2d 2e 2f 30 31 32 33 34
  //   35 36 37 38 39 3a 3b 3c 3d 3e 3f 40 41 42 43 44 45 46 47 48 49 4a 4b 4c 4d 4e 4f 50 51 52 53 54 55
  //   56 57 58 59 5a 5b 5c 5d 5e 5f 60 61 62 63 64 65 66 67 68 69 6a 6b 6c 6d 6e 6f 70 71 72 73 74 75 76
  //   77 78 79 7a 7b 7c 7d 7e 7f 80 81 82 83 84 85 86 87 88 89 8a 8b 8c 8d 8e 8f 90 91 92 93 94 95 96 97
  //   98 99 9a 9b 9c 9d 9e 9f a0 a1 a2 a3 a4 a5 a6 a7 a8 a9 aa ab ac ad ae af b0 b1 b2 b3 b4 b5 b6 b7 b8
  //   b9 ba bb bc bd be bf c0 c1 c2 c3 c4 c5 c6 c7 c8 c9 ca cb cc cd ce cf d0 d1 d2 d3 d4 d5 d6 d7 d8 d9
  //   da db dc dd de df e0 e1 e2 e3 e4 e5 e6 e7 e8 e9 ea eb ec ed ee ef f0 f1 f2 f3 f4 f5 f6 f7 f8 f9 fa
  //   fb fc fd fe ff 0 1 2 3 4 5 6 7 8 9 a b c d e f 10 11 12 13 14 15 16 17 18 19 1a 1b 1c 1d 1e 1f 20 21
  //   22 23 24 25 26 27 28 29 2a 2b 2c 2d 2e 2f 30 31 32 33 34 35 36 37 38 39 3a 3b 3c 3d 3e 3f 40 41 42
  //   43 44 45 46 47 48 49 4a 4b 4c 4d 4e 4f 50 51 52 53 54 55 56 57 58 59 5a 5b 5c 5d 5e 5f 60 61 62 63
  //   64 65 66 67 68 69 6a 6b 6c 6d 6e 6f 70 71 72 73 74 75 76 77 78 79 7a 7b 7c 7d 7e 7f 80 81 82 83 84
  //   85 86 87 88 89 8a 8b 8c 8d 8e 8f 90 91 92 93 94 95 96 97 98 99 9a 9b 9c 9d 9e 9f a0 a1 a2 a3 a4 a5
  //   a6 a7 a8 a9 aa ab ac ad ae af b0 b1 b2 b3 b4 b5 b6 b7 b8 b9 ba bb bc bd be bf c0 c1 c2 c3 c4 c5 c6
  //   c7 c8 c9 ca cb cc cd ce cf d0 d1 d2 d3 d4 d5 d6 d7 d8 d9 da db dc dd de df e0 e1 e2 e3 e4 e5 e6 e7
  //   e8 e9 ea eb ec ed ee ef f0 f1 f2 f3 f4 f5 f6 f7 f8 f9 fa fb fc fd fe ff 0 1 2 3 4 5 6 7 8 9 a b c d
  //   e f 10 11 12 13 14 15 16 17 18 19 1a 1b 1c 1d 1e 1f 20 21 22 23 24 25 26 27 28 29 2a 2b 2c 2d 2e 2f
  //   30 31 32 33 34 35 36 37 38 39 3a 3b 3c 3d 3e 3f 40 41 42 43 44 45 46 47 48 49 4a 4b 4c 4d 4e 4f 50
  //   51 52 53 54 55 56 57 58 59 5a 5b 5c 5d 5e 5f 60 61 62 63 64 65 66 67 68 69 6a 6b 6c 6d 6e 6f 70 71
  //   72 73 74 75 76 77 78 79 7a 7b 7c 7d 7e 7f 80 81 82 83 84 85 86 87 88 89 8a 8b 8c 8d 8e 8f 90 91 92
  //   93 94 95 96 97 98 99 9a 9b 9c 9d 9e 9f a0 a1 a2 a3 a4 a5 a6 a7 a8 a9 aa ab ac ad ae af b0 b1 b2 b3
  //   b4 b5 b6 b7 b8 b9 ba bb bc bd be bf c0 c1 c2 c3 c4 c5 c6 c7 c8 c9 ca cb cc cd ce cf d0 d1 d2 d3 d4
  //   d5 d6 d7 d8 d9 da db dc dd de df e0 e1 e2 e3 e4 e5 e6 e7 e8 e9 ea eb ec ed ee ef f0 f1 f2 f3 f4 f5
  //   f6 f7 f8 f9 fa fb fc fd fe ff 0 1 2 3 4 5 6 7 8 9 a b c d e f 10 11 12 13 14 15 16 17 18 19 1a 1b 1c
  //   1d 1e 1f 20 21 22 23 24 25 26 27 28 29 2a 2b 2c 2d 2e 2f 30 31 32 33 34 35 36 37 38 39 3a 3b 3c 3d
  //   3e 3f 40 41 42 43 44 45 46 47 48 49 4a 4b 4c 4d 4e 4f 50 51 52 53 54 55 56 57 58 59 5a 5b 5c 5d 5e
  //   5f 60 61 62 63 64 65 66 67 68 69 6a 6b 6c 6d 6e 6f 70 71 72 73 74 75 76 77 78 79 7a 7b 7c 7d 7e 7f
  //   80 81 82 83 84 85 86 87 88 89 8a 8b 8c 8d 8e 8f 90 91 92 93 94 95 96 97 98 99 9a 9b 9c 9d 9e 9f a0
  //   a1 a2 a3 a4 a5 a6 a7 a8 a9 aa ab ac ad ae af b0 b1 b2 b3 b4 b5 b6 b7 b8 b9 ba bb bc bd be bf c0 c1
  //   c2 c3 c4 c5 c6 c7 c8 c9 ca cb cc cd ce cf d0 d1 d2 d3 d4 d5 d6 d7 d8 d9 da db dc dd de df e0 e1 e2
  //   e3 e4 e5 e6 e7 e8 e9 ea eb ec ed ee ef f0 f1 f2 f3 f4 f5 f6 f7 f8 f9 fa fb fc fd fe ff
  //   cache模拟器
endmodule

module \cache_4路组相联映射_电路_16个cache块  (
  input  BlkDataReady,
  input  [31:0] BlockDataIn,
  input  [15:0] Addr,
  input  CLK,
  output Miss,
  output [7:0] DataOut
);

  wire and_1_out, and_2_out, and_3_out, and_4_out, and_5_out, and_6_out, and_7_out, and_8_out, and_9_out,
       and_10_out, and_11_out, and_12_out, and_13_out, and_14_out, and_15_out, and_16_out, and_17_out,
       and_18_out, and_19_out, and_20_out, and_21_out, and_22_out, and_23_out, and_24_out, and_29_out,
       and_30_out, and_31_out, and_32_out, and_33_out, and_34_out, and_35_out, and_36_out, comparator_1_eq,
       comparator_2_eq, comparator_3_eq, comparator_4_eq, Hit, L0, L1, L2, L3, not_2_out, not_3_out,
       not_4_out, not_5_out, priority_encoder_1_gs, R0, R1, R2, R3, Set0, Set1, Set2, Set3, V0, V1, V2, V3,
       VALID_2_q, VALID_3_q, VALID_4_q, VALID_5_q, VALID_6_q, VALID_7_q, VALID_8_q, VALID_9_q, VALID_10_q,
       VALID_11_q, VALID_12_q, VALID_13_q, VALID_14_q, VALID_15_q, VALID_16_q, VALID_q;
  wire [1:0] \max2_归并比较_电路_1_max_num , \max2_归并比较_电路_2_max_num , \max2_归并比较_电路_3_max_num , multiplexer_2_out,
       not_6_out, priority_encoder_1_out;
  wire [11:0] Tag0, Tag1, Tag2, Tag3, \标记位_2_q , \标记位_3_q , \标记位_4_q , \标记位_5_q , \标记位_6_q , \标记位_7_q ,
       \标记位_8_q , \标记位_9_q , \标记位_10_q , \标记位_11_q , \标记位_12_q , \标记位_13_q , \标记位_14_q , \标记位_15_q ,
       \标记位_16_q , \标记位_q ;
  wire [15:0] C0, C1, C2, C3, \max2_归并比较_电路_1_max , \max2_归并比较_电路_2_max , \淘汰标志位_2_q , \淘汰标志位_3_q ,
       \淘汰标志位_4_q , \淘汰标志位_5_q , \淘汰标志位_6_q , \淘汰标志位_7_q , \淘汰标志位_8_q , \淘汰标志位_9_q , \淘汰标志位_10_q ,
       \淘汰标志位_11_q , \淘汰标志位_12_q , \淘汰标志位_13_q , \淘汰标志位_14_q , \淘汰标志位_15_q , \淘汰标志位_16_q , \淘汰标志位_q ;
  wire [31:0] SlotData, \数据块副本_2_q , \数据块副本_3_q , \数据块副本_4_q , \数据块副本_5_q , \数据块副本_6_q , \数据块副本_7_q ,
       \数据块副本_8_q , \数据块副本_9_q , \数据块副本_10_q , \数据块副本_11_q , \数据块副本_12_q , \数据块副本_13_q , \数据块副本_14_q ,
       \数据块副本_15_q , \数据块副本_16_q , \数据块副本_q ;

  Register #(.width(1), .trigger("rising"), .Select("low")) VALID (
    .D(1'b1), .en(and_1_out), .Q(VALID_q), .clk(CLK));  // open: clr
  Register #(.width(1), .trigger("rising"), .Select("low")) VALID_2 (
    .D(1'b1), .en(and_2_out), .Q(VALID_2_q), .clk(CLK));  // open: clr
  Register #(.width(1), .trigger("rising"), .Select("low")) VALID_3 (
    .D(1'b1), .en(and_3_out), .Q(VALID_3_q), .clk(CLK));  // open: clr
  Register #(.width(1), .trigger("rising"), .Select("low")) VALID_4 (
    .D(1'b1), .en(and_4_out), .Q(VALID_4_q), .clk(CLK));  // open: clr
  Register #(.width(1), .trigger("rising"), .Select("low")) VALID_5 (
    .D(1'b1), .en(and_5_out), .Q(VALID_5_q), .clk(CLK));  // open: clr
  Register #(.width(1), .trigger("rising"), .Select("low")) VALID_6 (
    .D(1'b1), .en(and_6_out), .Q(VALID_6_q), .clk(CLK));  // open: clr
  Register #(.width(1), .trigger("rising"), .Select("low")) VALID_7 (
    .D(1'b1), .en(and_7_out), .Q(VALID_7_q), .clk(CLK));  // open: clr
  Register #(.width(1), .trigger("rising"), .Select("low")) VALID_8 (
    .D(1'b1), .en(and_8_out), .Q(VALID_8_q), .clk(CLK));  // open: clr
  assign V0 = Set0 ? VALID_q : 1'bz;  // Controlled_Buffer controlled_buffer_1
  and and_1 (and_1_out, Set0, R0);
  assign V1 = Set0 ? VALID_2_q : 1'bz;  // Controlled_Buffer controlled_buffer_2
  and and_2 (and_2_out, Set0, R1);
  assign V2 = Set0 ? VALID_3_q : 1'bz;  // Controlled_Buffer controlled_buffer_3
  and and_3 (and_3_out, Set0, R2);
  assign V3 = Set0 ? VALID_4_q : 1'bz;  // Controlled_Buffer controlled_buffer_4
  and and_4 (and_4_out, Set0, R3);
  assign V0 = Set1 ? VALID_5_q : 1'bz;  // Controlled_Buffer controlled_buffer_5
  and and_5 (and_5_out, Set1, R0);
  assign V1 = Set1 ? VALID_6_q : 1'bz;  // Controlled_Buffer controlled_buffer_6
  and and_6 (and_6_out, Set1, R1);
  assign V2 = Set1 ? VALID_7_q : 1'bz;  // Controlled_Buffer controlled_buffer_7
  and and_7 (and_7_out, Set1, R2);
  assign V3 = Set1 ? VALID_8_q : 1'bz;  // Controlled_Buffer controlled_buffer_8
  and and_8 (and_8_out, Set1, R3);
  Multiplexer #(.select(2), .width(8), .disabled("Z"), .enable("true")) multiplexer_1 (
    .in0(SlotData[7:0]), .in1(SlotData[15:8]), .in2(SlotData[23:16]), .in3(SlotData[31:24]), .out(DataOut),
    .sel(Addr[1:0]), .en(Hit));
  Register #(.width(12), .trigger("rising"), .Select("low")) \u_标记位  (
    .D(Addr[15:4]), .en(and_1_out), .Q(\标记位_q ), .clk(CLK));  // open: clr
  Register #(.width(12), .trigger("rising"), .Select("low")) \u_标记位_2  (
    .D(Addr[15:4]), .en(and_2_out), .Q(\标记位_2_q ), .clk(CLK));  // open: clr
  Register #(.width(12), .trigger("rising"), .Select("low")) \u_标记位_3  (
    .D(Addr[15:4]), .en(and_3_out), .Q(\标记位_3_q ), .clk(CLK));  // open: clr
  Register #(.width(12), .trigger("rising"), .Select("low")) \u_标记位_4  (
    .D(Addr[15:4]), .en(and_4_out), .Q(\标记位_4_q ), .clk(CLK));  // open: clr
  Register #(.width(12), .trigger("rising"), .Select("low")) \u_标记位_5  (
    .D(Addr[15:4]), .en(and_5_out), .Q(\标记位_5_q ), .clk(CLK));  // open: clr
  Register #(.width(12), .trigger("rising"), .Select("low")) \u_标记位_6  (
    .D(Addr[15:4]), .en(and_6_out), .Q(\标记位_6_q ), .clk(CLK));  // open: clr
  Register #(.width(12), .trigger("rising"), .Select("low")) \u_标记位_7  (
    .D(Addr[15:4]), .en(and_7_out), .Q(\标记位_7_q ), .clk(CLK));  // open: clr
  Register #(.width(12), .trigger("rising"), .Select("low")) \u_标记位_8  (
    .D(Addr[15:4]), .en(and_8_out), .Q(\标记位_8_q ), .clk(CLK));  // open: clr
  assign Tag0 = Set0 ? \标记位_q  : 12'bz;  // Controlled_Buffer controlled_buffer_9
  assign Tag1 = Set0 ? \标记位_2_q  : 12'bz;  // Controlled_Buffer controlled_buffer_10
  assign Tag2 = Set0 ? \标记位_3_q  : 12'bz;  // Controlled_Buffer controlled_buffer_11
  assign Tag3 = Set0 ? \标记位_4_q  : 12'bz;  // Controlled_Buffer controlled_buffer_12
  assign Tag0 = Set1 ? \标记位_5_q  : 12'bz;  // Controlled_Buffer controlled_buffer_13
  assign Tag1 = Set1 ? \标记位_6_q  : 12'bz;  // Controlled_Buffer controlled_buffer_14
  assign Tag2 = Set1 ? \标记位_7_q  : 12'bz;  // Controlled_Buffer controlled_buffer_15
  assign Tag3 = Set1 ? \标记位_8_q  : 12'bz;  // Controlled_Buffer controlled_buffer_16
  not not_1 (Miss, Hit);
  Decoder #(.select(2), .tristate("false"), .disabled("Z"), .enable("false")) decoder_1 (
    .out0(Set0), .out1(Set1), .out2(Set2), .out3(Set3), .sel(Addr[3:2]));
  assign C0 = Set0 ? \淘汰标志位_q  : 16'bz;  // Controlled_Buffer controlled_buffer_17
  Counter #(.width(16), .max('hffff), .ongoal("wrap"), .trigger("rising"), .behavior("old")) \u_淘汰标志位  (
    .count(Hit), .Q(\淘汰标志位_q ), .clk(CLK), .clr(and_9_out));  // open: load, D, carry, preset
  Counter #(.width(16), .max('hffff), .ongoal("wrap"), .trigger("rising"), .behavior("old")) \u_淘汰标志位_2  (
    .count(Hit), .Q(\淘汰标志位_2_q ), .clk(CLK), .clr(and_10_out));  // open: load, D, carry, preset
  assign C1 = Set0 ? \淘汰标志位_2_q  : 16'bz;  // Controlled_Buffer controlled_buffer_18
  Counter #(.width(16), .max('hffff), .ongoal("wrap"), .trigger("rising"), .behavior("old")) \u_淘汰标志位_3  (
    .count(Hit), .Q(\淘汰标志位_3_q ), .clk(CLK), .clr(and_11_out));  // open: load, D, carry, preset
  assign C2 = Set0 ? \淘汰标志位_3_q  : 16'bz;  // Controlled_Buffer controlled_buffer_19
  Counter #(.width(16), .max('hffff), .ongoal("wrap"), .trigger("rising"), .behavior("old")) \u_淘汰标志位_4  (
    .count(Hit), .Q(\淘汰标志位_4_q ), .clk(CLK), .clr(and_12_out));  // open: load, D, carry, preset
  assign C3 = Set0 ? \淘汰标志位_4_q  : 16'bz;  // Controlled_Buffer controlled_buffer_20
  Counter #(.width(16), .max('hffff), .ongoal("wrap"), .trigger("rising"), .behavior("old")) \u_淘汰标志位_5  (
    .count(Hit), .Q(\淘汰标志位_5_q ), .clk(CLK), .clr(and_13_out));  // open: load, D, carry, preset
  assign C0 = Set1 ? \淘汰标志位_5_q  : 16'bz;  // Controlled_Buffer controlled_buffer_21
  assign C1 = Set1 ? \淘汰标志位_6_q  : 16'bz;  // Controlled_Buffer controlled_buffer_22
  Counter #(.width(16), .max('hffff), .ongoal("wrap"), .trigger("rising"), .behavior("old")) \u_淘汰标志位_6  (
    .count(Hit), .Q(\淘汰标志位_6_q ), .clk(CLK), .clr(and_14_out));  // open: load, D, carry, preset
  Counter #(.width(16), .max('hffff), .ongoal("wrap"), .trigger("rising"), .behavior("old")) \u_淘汰标志位_7  (
    .count(Hit), .Q(\淘汰标志位_7_q ), .clk(CLK), .clr(and_15_out));  // open: load, D, carry, preset
  assign C2 = Set1 ? \淘汰标志位_7_q  : 16'bz;  // Controlled_Buffer controlled_buffer_23
  assign C3 = Set1 ? \淘汰标志位_8_q  : 16'bz;  // Controlled_Buffer controlled_buffer_24
  Counter #(.width(16), .max('hffff), .ongoal("wrap"), .trigger("rising"), .behavior("old")) \u_淘汰标志位_8  (
    .count(Hit), .Q(\淘汰标志位_8_q ), .clk(CLK), .clr(and_16_out));  // open: load, D, carry, preset
  or or_1 (Hit, L0, L1, L2, L3);
  Register #(.width(32), .trigger("rising"), .Select("low")) \u_数据块副本  (
    .D(BlockDataIn), .en(and_1_out), .Q(\数据块副本_q ), .clk(CLK));  // open: clr
  Register #(.width(32), .trigger("rising"), .Select("low")) \u_数据块副本_2  (
    .D(BlockDataIn), .en(and_2_out), .Q(\数据块副本_2_q ), .clk(CLK));  // open: clr
  Register #(.width(32), .trigger("rising"), .Select("low")) \u_数据块副本_3  (
    .D(BlockDataIn), .en(and_3_out), .Q(\数据块副本_3_q ), .clk(CLK));  // open: clr
  Register #(.width(32), .trigger("rising"), .Select("low")) \u_数据块副本_4  (
    .D(BlockDataIn), .en(and_4_out), .Q(\数据块副本_4_q ), .clk(CLK));  // open: clr
  Register #(.width(32), .trigger("rising"), .Select("low")) \u_数据块副本_5  (
    .D(BlockDataIn), .en(and_5_out), .Q(\数据块副本_5_q ), .clk(CLK));  // open: clr
  Register #(.width(32), .trigger("rising"), .Select("low")) \u_数据块副本_6  (
    .D(BlockDataIn), .en(and_6_out), .Q(\数据块副本_6_q ), .clk(CLK));  // open: clr
  Register #(.width(32), .trigger("rising"), .Select("low")) \u_数据块副本_7  (
    .D(BlockDataIn), .en(and_7_out), .Q(\数据块副本_7_q ), .clk(CLK));  // open: clr
  Register #(.width(32), .trigger("rising"), .Select("low")) \u_数据块副本_8  (
    .D(BlockDataIn), .en(and_8_out), .Q(\数据块副本_8_q ), .clk(CLK));  // open: clr
  assign SlotData = and_9_out ? \数据块副本_q  : 32'bz;  // Controlled_Buffer controlled_buffer_25
  and and_9 (and_9_out, L0, Set0);
  assign SlotData = and_10_out ? \数据块副本_2_q  : 32'bz;  // Controlled_Buffer controlled_buffer_26
  and and_10 (and_10_out, L1, Set0);
  assign SlotData = and_11_out ? \数据块副本_3_q  : 32'bz;  // Controlled_Buffer controlled_buffer_27
  and and_11 (and_11_out, L2, Set0);
  assign SlotData = and_12_out ? \数据块副本_4_q  : 32'bz;  // Controlled_Buffer controlled_buffer_28
  and and_12 (and_12_out, L3, Set0);
  assign SlotData = and_13_out ? \数据块副本_5_q  : 32'bz;  // Controlled_Buffer controlled_buffer_29
  and and_13 (and_13_out, L0, Set1);
  assign SlotData = and_14_out ? \数据块副本_6_q  : 32'bz;  // Controlled_Buffer controlled_buffer_30
  and and_14 (and_14_out, L1, Set1);
  assign SlotData = and_15_out ? \数据块副本_7_q  : 32'bz;  // Controlled_Buffer controlled_buffer_31
  and and_15 (and_15_out, L2, Set1);
  assign SlotData = and_16_out ? \数据块副本_8_q  : 32'bz;  // Controlled_Buffer controlled_buffer_32
  and and_16 (and_16_out, L3, Set1);
  assign V0 = Set2 ? VALID_9_q : 1'bz;  // Controlled_Buffer controlled_buffer_33
  Register #(.width(1), .trigger("rising"), .Select("low")) VALID_9 (
    .D(1'b1), .en(and_17_out), .Q(VALID_9_q), .clk(CLK));  // open: clr
  and and_17 (and_17_out, Set2, R0);
  Register #(.width(1), .trigger("rising"), .Select("low")) VALID_10 (
    .D(1'b1), .en(and_18_out), .Q(VALID_10_q), .clk(CLK));  // open: clr
  assign V1 = Set2 ? VALID_10_q : 1'bz;  // Controlled_Buffer controlled_buffer_34
  and and_18 (and_18_out, Set2, R1);
  Register #(.width(1), .trigger("rising"), .Select("low")) VALID_11 (
    .D(1'b1), .en(and_19_out), .Q(VALID_11_q), .clk(CLK));  // open: clr
  assign V2 = Set2 ? VALID_11_q : 1'bz;  // Controlled_Buffer controlled_buffer_35
  and and_19 (and_19_out, Set2, R2);
  assign V3 = Set2 ? VALID_12_q : 1'bz;  // Controlled_Buffer controlled_buffer_36
  Register #(.width(1), .trigger("rising"), .Select("low")) VALID_12 (
    .D(1'b1), .en(and_20_out), .Q(VALID_12_q), .clk(CLK));  // open: clr
  and and_20 (and_20_out, Set2, R3);
  assign V0 = Set3 ? VALID_13_q : 1'bz;  // Controlled_Buffer controlled_buffer_37
  Register #(.width(1), .trigger("rising"), .Select("low")) VALID_13 (
    .D(1'b1), .en(and_21_out), .Q(VALID_13_q), .clk(CLK));  // open: clr
  and and_21 (and_21_out, Set3, R0);
  Register #(.width(1), .trigger("rising"), .Select("low")) VALID_14 (
    .D(1'b1), .en(and_22_out), .Q(VALID_14_q), .clk(CLK));  // open: clr
  assign V1 = Set3 ? VALID_14_q : 1'bz;  // Controlled_Buffer controlled_buffer_38
  and and_22 (and_22_out, Set3, R1);
  assign V2 = Set3 ? VALID_15_q : 1'bz;  // Controlled_Buffer controlled_buffer_39
  Register #(.width(1), .trigger("rising"), .Select("low")) VALID_15 (
    .D(1'b1), .en(and_23_out), .Q(VALID_15_q), .clk(CLK));  // open: clr
  and and_23 (and_23_out, Set3, R2);
  assign V3 = Set3 ? VALID_16_q : 1'bz;  // Controlled_Buffer controlled_buffer_40
  Register #(.width(1), .trigger("rising"), .Select("low")) VALID_16 (
    .D(1'b1), .en(and_24_out), .Q(VALID_16_q), .clk(CLK));  // open: clr
  and and_24 (and_24_out, Set3, R3);
  Comparator #(.width(12), .mode("twosComplement")) comparator_1 (
    .a(Addr[15:4]), .b(Tag0), .eq(comparator_1_eq));  // open: gt, lt
  Comparator #(.width(12), .mode("twosComplement")) comparator_2 (
    .a(Addr[15:4]), .b(Tag1), .eq(comparator_2_eq));  // open: gt, lt
  Comparator #(.width(12), .mode("twosComplement")) comparator_3 (
    .a(Addr[15:4]), .b(Tag2), .eq(comparator_3_eq));  // open: gt, lt
  Comparator #(.width(12), .mode("twosComplement")) comparator_4 (
    .a(Addr[15:4]), .b(Tag3), .eq(comparator_4_eq));  // open: gt, lt
  \Max2_归并比较_电路  \max2_归并比较_电路_1  (
    .Y(C1), .X(C0), .Y_num(2'b01), .X_num(2'b00), .MAX(\max2_归并比较_电路_1_max ),
    .MAX_num(\max2_归并比较_电路_1_max_num ));
  \Max2_归并比较_电路  \max2_归并比较_电路_2  (
    .Y(C3), .X(C2), .Y_num(2'b11), .X_num(2'b10), .MAX(\max2_归并比较_电路_2_max ),
    .MAX_num(\max2_归并比较_电路_2_max_num ));
  not not_2 (not_2_out, V0);
  not not_3 (not_3_out, V1);
  not not_4 (not_4_out, V2);
  not not_5 (not_5_out, V3);
  and and_25 (L0, V0, comparator_1_eq);
  and and_26 (L1, V1, comparator_2_eq);
  and and_27 (L2, V2, comparator_3_eq);
  and and_28 (L3, V3, comparator_4_eq);
  Priority_Encoder #(.select(2), .disabled("Z")) priority_encoder_1 (
    .in0(not_5_out), .in1(not_4_out), .in2(not_3_out), .in3(not_2_out), .out(priority_encoder_1_out),
    .gs(priority_encoder_1_gs));  // open: en_out, en_in
  assign Tag0 = Set2 ? \标记位_9_q  : 12'bz;  // Controlled_Buffer controlled_buffer_41
  Register #(.width(12), .trigger("rising"), .Select("low")) \u_标记位_9  (
    .D(Addr[15:4]), .en(and_17_out), .Q(\标记位_9_q ), .clk(CLK));  // open: clr
  Register #(.width(12), .trigger("rising"), .Select("low")) \u_标记位_10  (
    .D(Addr[15:4]), .en(and_18_out), .Q(\标记位_10_q ), .clk(CLK));  // open: clr
  assign Tag1 = Set2 ? \标记位_10_q  : 12'bz;  // Controlled_Buffer controlled_buffer_42
  assign Tag2 = Set2 ? \标记位_11_q  : 12'bz;  // Controlled_Buffer controlled_buffer_43
  Register #(.width(12), .trigger("rising"), .Select("low")) \u_标记位_11  (
    .D(Addr[15:4]), .en(and_19_out), .Q(\标记位_11_q ), .clk(CLK));  // open: clr
  assign Tag3 = Set2 ? \标记位_12_q  : 12'bz;  // Controlled_Buffer controlled_buffer_44
  Register #(.width(12), .trigger("rising"), .Select("low")) \u_标记位_12  (
    .D(Addr[15:4]), .en(and_20_out), .Q(\标记位_12_q ), .clk(CLK));  // open: clr
  assign Tag0 = Set3 ? \标记位_13_q  : 12'bz;  // Controlled_Buffer controlled_buffer_45
  Register #(.width(12), .trigger("rising"), .Select("low")) \u_标记位_13  (
    .D(Addr[15:4]), .en(and_21_out), .Q(\标记位_13_q ), .clk(CLK));  // open: clr
  Register #(.width(12), .trigger("rising"), .Select("low")) \u_标记位_14  (
    .D(Addr[15:4]), .en(and_22_out), .Q(\标记位_14_q ), .clk(CLK));  // open: clr
  assign Tag1 = Set3 ? \标记位_14_q  : 12'bz;  // Controlled_Buffer controlled_buffer_46
  Register #(.width(12), .trigger("rising"), .Select("low")) \u_标记位_15  (
    .D(Addr[15:4]), .en(and_23_out), .Q(\标记位_15_q ), .clk(CLK));  // open: clr
  assign Tag2 = Set3 ? \标记位_15_q  : 12'bz;  // Controlled_Buffer controlled_buffer_47
  assign Tag3 = Set3 ? \标记位_16_q  : 12'bz;  // Controlled_Buffer controlled_buffer_48
  Register #(.width(12), .trigger("rising"), .Select("low")) \u_标记位_16  (
    .D(Addr[15:4]), .en(and_24_out), .Q(\标记位_16_q ), .clk(CLK));  // open: clr
  \Max2_归并比较_电路  \max2_归并比较_电路_3  (
    .Y(\max2_归并比较_电路_2_max ), .X(\max2_归并比较_电路_1_max ), .Y_num(\max2_归并比较_电路_2_max_num ),
    .X_num(\max2_归并比较_电路_1_max_num ), .MAX_num(\max2_归并比较_电路_3_max_num ));  // open: MAX
  assign not_6_out = ~priority_encoder_1_out;  // NOT_Gate not_6, 2 bits wide
  Multiplexer #(.select(1), .width(2), .disabled("Z"), .enable("false")) multiplexer_2 (
    .in0(\max2_归并比较_电路_3_max_num ), .in1(not_6_out), .out(multiplexer_2_out), .sel(priority_encoder_1_gs));
  Decoder #(.select(2), .tristate("false"), .disabled(0), .enable("true")) decoder_2 (
    .out0(R0), .out1(R1), .out2(R2), .out3(R3), .sel(multiplexer_2_out), .en(BlkDataReady));
  Counter #(.width(16), .max('hffff), .ongoal("wrap"), .trigger("rising"), .behavior("old")) \u_淘汰标志位_9  (
    .count(Hit), .Q(\淘汰标志位_9_q ), .clk(CLK), .clr(and_29_out));  // open: load, D, carry, preset
  Counter #(.width(16), .max('hffff), .ongoal("wrap"), .trigger("rising"), .behavior("old")) \u_淘汰标志位_10  (
    .count(Hit), .Q(\淘汰标志位_10_q ), .clk(CLK), .clr(and_30_out));  // open: load, D, carry, preset
  Counter #(.width(16), .max('hffff), .ongoal("wrap"), .trigger("rising"), .behavior("old")) \u_淘汰标志位_11  (
    .count(Hit), .Q(\淘汰标志位_11_q ), .clk(CLK), .clr(and_31_out));  // open: load, D, carry, preset
  Counter #(.width(16), .max('hffff), .ongoal("wrap"), .trigger("rising"), .behavior("old")) \u_淘汰标志位_12  (
    .count(Hit), .Q(\淘汰标志位_12_q ), .clk(CLK), .clr(and_32_out));  // open: load, D, carry, preset
  Counter #(.width(16), .max('hffff), .ongoal("wrap"), .trigger("rising"), .behavior("old")) \u_淘汰标志位_13  (
    .count(Hit), .Q(\淘汰标志位_13_q ), .clk(CLK), .clr(and_33_out));  // open: load, D, carry, preset
  Counter #(.width(16), .max('hffff), .ongoal("wrap"), .trigger("rising"), .behavior("old")) \u_淘汰标志位_14  (
    .count(Hit), .Q(\淘汰标志位_14_q ), .clk(CLK), .clr(and_34_out));  // open: load, D, carry, preset
  Counter #(.width(16), .max('hffff), .ongoal("wrap"), .trigger("rising"), .behavior("old")) \u_淘汰标志位_15  (
    .count(Hit), .Q(\淘汰标志位_15_q ), .clk(CLK), .clr(and_35_out));  // open: load, D, carry, preset
  Counter #(.width(16), .max('hffff), .ongoal("wrap"), .trigger("rising"), .behavior("old")) \u_淘汰标志位_16  (
    .count(Hit), .Q(\淘汰标志位_16_q ), .clk(CLK), .clr(and_36_out));  // open: load, D, carry, preset
  assign C0 = Set2 ? \淘汰标志位_9_q  : 16'bz;  // Controlled_Buffer controlled_buffer_49
  assign C1 = Set2 ? \淘汰标志位_10_q  : 16'bz;  // Controlled_Buffer controlled_buffer_50
  assign C2 = Set2 ? \淘汰标志位_11_q  : 16'bz;  // Controlled_Buffer controlled_buffer_51
  assign C3 = Set2 ? \淘汰标志位_12_q  : 16'bz;  // Controlled_Buffer controlled_buffer_52
  assign C0 = Set3 ? \淘汰标志位_13_q  : 16'bz;  // Controlled_Buffer controlled_buffer_53
  assign C1 = Set3 ? \淘汰标志位_14_q  : 16'bz;  // Controlled_Buffer controlled_buffer_54
  assign C2 = Set3 ? \淘汰标志位_15_q  : 16'bz;  // Controlled_Buffer controlled_buffer_55
  assign C3 = Set3 ? \淘汰标志位_16_q  : 16'bz;  // Controlled_Buffer controlled_buffer_56
  Register #(.width(32), .trigger("rising"), .Select("low")) \u_数据块副本_9  (
    .D(BlockDataIn), .en(and_17_out), .Q(\数据块副本_9_q ), .clk(CLK));  // open: clr
  assign SlotData = and_29_out ? \数据块副本_9_q  : 32'bz;  // Controlled_Buffer controlled_buffer_57
  and and_29 (and_29_out, L0, Set2);
  Register #(.width(32), .trigger("rising"), .Select("low")) \u_数据块副本_10  (
    .D(BlockDataIn), .en(and_18_out), .Q(\数据块副本_10_q ), .clk(CLK));  // open: clr
  assign SlotData = and_30_out ? \数据块副本_10_q  : 32'bz;  // Controlled_Buffer controlled_buffer_58
  and and_30 (and_30_out, L1, Set2);
  Register #(.width(32), .trigger("rising"), .Select("low")) \u_数据块副本_11  (
    .D(BlockDataIn), .en(and_19_out), .Q(\数据块副本_11_q ), .clk(CLK));  // open: clr
  assign SlotData = and_31_out ? \数据块副本_11_q  : 32'bz;  // Controlled_Buffer controlled_buffer_59
  and and_31 (and_31_out, L2, Set2);
  assign SlotData = and_32_out ? \数据块副本_12_q  : 32'bz;  // Controlled_Buffer controlled_buffer_60
  Register #(.width(32), .trigger("rising"), .Select("low")) \u_数据块副本_12  (
    .D(BlockDataIn), .en(and_20_out), .Q(\数据块副本_12_q ), .clk(CLK));  // open: clr
  and and_32 (and_32_out, L3, Set2);
  Register #(.width(32), .trigger("rising"), .Select("low")) \u_数据块副本_13  (
    .D(BlockDataIn), .en(and_21_out), .Q(\数据块副本_13_q ), .clk(CLK));  // open: clr
  assign SlotData = and_33_out ? \数据块副本_13_q  : 32'bz;  // Controlled_Buffer controlled_buffer_61
  and and_33 (and_33_out, L0, Set3);
  Register #(.width(32), .trigger("rising"), .Select("low")) \u_数据块副本_14  (
    .D(BlockDataIn), .en(and_22_out), .Q(\数据块副本_14_q ), .clk(CLK));  // open: clr
  assign SlotData = and_34_out ? \数据块副本_14_q  : 32'bz;  // Controlled_Buffer controlled_buffer_62
  and and_34 (and_34_out, L1, Set3);
  assign SlotData = and_35_out ? \数据块副本_15_q  : 32'bz;  // Controlled_Buffer controlled_buffer_63
  Register #(.width(32), .trigger("rising"), .Select("low")) \u_数据块副本_15  (
    .D(BlockDataIn), .en(and_23_out), .Q(\数据块副本_15_q ), .clk(CLK));  // open: clr
  and and_35 (and_35_out, L2, Set3);
  Register #(.width(32), .trigger("rising"), .Select("low")) \u_数据块副本_16  (
    .D(BlockDataIn), .en(and_24_out), .Q(\数据块副本_16_q ), .clk(CLK));  // open: clr
  assign SlotData = and_36_out ? \数据块副本_16_q  : 32'bz;  // Controlled_Buffer controlled_buffer_64
  and and_36 (and_36_out, L3, Set3);

  // Other names for the same wires on the sheet: Blk[31:0] = BlockDataIn; BlkReady = BlkDataReady;
  //   Offset[1:0] = Addr[1:0]; 字节地址[15:0] = Addr; Index[1:0] = Addr[3:2]; Tag[11:0] = Addr[15:4]

  // Notes on the sheet:
  //   输入引脚区
  //   cache（4路组相联映射）电路(16个cache块)
  //   输出引脚区
endmodule

module \_4路相联映射_16个cache块_测试电路  (
  input  in_1
);

  wire and_2_out, Clk, comparator_1_lt, comparator_2_eq, comparator_3_eq, controlled_buffer_1_out, EN, Error,
       Go, Hit, Miss, or_1_out, RDY, Runing;
  wire [3:0] _1, _2, _3;
  wire [7:0] Dataout, \主存内容_data ;
  wire [9:0] \测试用例数 ;
  wire [15:0] adder_1_out, Addr, bit_extender_3_out, \cache块交换逻辑电路_1_byteaddrout , counter_1_q,
       subtractor_1_out, \命中次数 , \时钟周期数 , \校验和 , \缺失次数 , \访问次数 ;
  wire [31:0] bit_extender_1_out, bit_extender_2_out, BlkDataIn, divider_1_out, divider_2_out,
       multiplier_1_out;
  wire [31:4] divider_2_rem, divider_3_out, divider_3_rem;

  not not_1 (Hit, Miss);
  and and_1 (EN, Hit, Go);
  Clock #(.highDuration(1), .lowDuration(1)) clock_1 (.out(Clk));
  Counter #(.width(16), .max('hffff), .ongoal("wrap"), .trigger("rising"), .behavior("old")) counter_1 (
    .count(and_2_out), .Q(counter_1_q), .clk(Clk));  // open: load, D, carry, clr, preset
  and and_2 (and_2_out, Miss, RDY, Runing);
  Subtractor #(.width(16)) subtractor_1 (.a(\访问次数 ), .b(\缺失次数 ), .out(subtractor_1_out));  // open: bin, bout
  Comparator #(.width(16), .mode("twosComplement")) comparator_1 (
    .a(\访问次数 ), .b(\缺失次数 ), .lt(comparator_1_lt));  // open: gt, eq
  // Probe on \访问次数 
  // Probe on \测试用例数 
  Counter #(.width(10), .max('h3ff), .ongoal("wrap"), .trigger("rising"), .behavior("old")) \u_计数器  (
    .count(EN), .Q(\测试用例数 ), .clk(Clk));  // open: load, D, carry, clr, preset
  Register #(.width(16), .trigger("rising"), .Select("low")) register_1 (
    .D(counter_1_q), .en(EN), .Q(\缺失次数 ), .clk(Clk));  // open: clr
  not not_2 (Runing, comparator_2_eq);
  Comparator #(.width(10), .mode("twosComplement")) comparator_2 (
    .a(\测试用例数 ), .b(10'h100), .eq(comparator_2_eq));  // open: gt, lt
  Multiplexer #(.select(1), .width(16), .disabled(0), .enable("false")) multiplexer_1 (
    .in0(subtractor_1_out), .in1({16{1'b0}}), .out(\命中次数 ), .sel(comparator_1_lt));
  // Probe on \命中次数 
  // Probe on \时钟周期数 
  ROM #(.addrWidth(10), .dataWidth(16), .Select("high")) \u_主存地址  (.addr(\测试用例数 ), .data(Addr));
  Counter #(.width(16), .max('hffff), .ongoal("wrap"), .trigger("rising"), .behavior("old")) counter_2 (
    .count(EN), .Q(\访问次数 ), .clk(Clk));  // open: load, D, carry, clr, preset
  assign bit_extender_1_out = {{16{1'b0}}, \命中次数 };  // Bit_Extender bit_extender_1
  // Probe on Dataout
  Multiplier #(.width(32)) multiplier_1 (
    .a(bit_extender_1_out), .b(32'h64), .out(multiplier_1_out));  // open: cin, cout
  assign bit_extender_2_out = {{16{1'b0}}, \访问次数 };  // Bit_Extender bit_extender_2
  // Probe on \缺失次数 
  // Probe on \校验和 
  \cache_4路组相联映射_电路_16个cache块  \cache_4路组相联映射_电路_16个cache块_1  (
    .Miss(Miss), .BlockDataIn(BlkDataIn), .Addr(Addr), .DataOut(Dataout), .BlkDataReady(RDY), .CLK(Clk));
  assign bit_extender_3_out = {{8{1'b0}}, Dataout};  // Bit_Extender bit_extender_3
  Divider #(.width(32)) divider_1 (
    .a(multiplier_1_out), .b(bit_extender_2_out), .out(divider_1_out));  // open: upper, rem
  Adder #(.width(16)) adder_1 (.a(\校验和 ), .b(bit_extender_3_out), .out(adder_1_out));  // open: cin, cout
  LED #(.active("true")) \u_读数据出错  (.in(Error));
  Pull_Resistor #(.pull(1)) pull_resistor_1 (.node(Miss));
  LED #(.active("true")) \u_缺失  (.in(Miss));
  Register #(.width(16), .trigger("rising"), .Select("low")) \u_校验和  (
    .D(adder_1_out), .en(EN), .Q(\校验和 ), .clk(Clk));  // open: clr
  Divider #(.width(32)) divider_2 (
    .a(divider_1_out), .b(32'ha), .out(divider_2_out), .rem({divider_2_rem, _1}));  // open: upper
  \cache块交换逻辑电路  \cache块交换逻辑电路_1  (
    .Addr(Addr), .CLK(Clk), .ByteAddrOut(\cache块交换逻辑电路_1_byteaddrout ), .ByteDataIn(\主存内容_data ),
    .Miss(Miss), .BlkDataReady(RDY), .BlockDataIn(BlkDataIn), .Enable(Runing));
  // Probe on \校验和 
  Divider #(.width(32)) divider_3 (
    .a(divider_2_out), .b(32'ha), .out({divider_3_out, _3}), .rem({divider_3_rem, _2}));  // open: upper
  ROM #(.addrWidth(16), .dataWidth(8), .Select("high")) \u_主存内容  (
    .addr(\cache块交换逻辑电路_1_byteaddrout ), .data(\主存内容_data ));
  Comparator #(.width(8), .mode("twosComplement")) comparator_3 (
    .a(Addr[7:0]), .b(Dataout), .eq(comparator_3_eq));  // open: gt, lt
  assign controlled_buffer_1_out = Hit ? comparator_3_eq : 1'bz;  // Controlled_Buffer controlled_buffer_1
  Pull_Resistor #(.pull(1)) pull_resistor_2 (.node(controlled_buffer_1_out));
  Hex_Digit_Display hex_digit_display_1 (.value(_3), .dp(1'b1));
  Hex_Digit_Display hex_digit_display_2 (.value(_2));  // open: dp
  or or_1 (or_1_out, controlled_buffer_1_out, ~in_1);  // OR_Gate
  Counter #(.width(16), .max('hffff), .ongoal("wrap"), .trigger("rising"), .behavior("old")) counter_3 (
    .count(Runing), .Q(\时钟周期数 ), .clk(Clk));  // open: load, D, carry, clr, preset
  Hex_Digit_Display hex_digit_display_3 (.value(_1));  // open: dp
  // Probe on Addr
  LED #(.active("true")) led_1 (.in(RDY));
  // Probe on BlkDataIn
  // Probe on Dataout
  and and_3 (Go, Runing, or_1_out);
  not not_3 (Error, or_1_out);

  // Other names for the same wires on the sheet: 读错误暂停 = in_1

  // Notes on the sheet:
  //   contents of 主存地址 (hex, n*v repeats v):
  //   0 1 2 3 8 9 a b 10 11 12 13 20 21 22 23 8 9 a b 4 5 6 7 24 25 26 27 4 5 6 7 0 1 2 3 8 9 a b 8 9 a b
  //   20 21 22 23 28 29 2a 2b 24 25 26 27 4 5 6 7 24 25 26 27 0 1 2 3 8 9 a b 20 21 22 23 20 21 22 23 30
  //   31 32 33 4 5 6 7 24 25 26 27 4 5 6 7 0 1 2 3 8 9 a b 20 21 22 23 20 21 22 23 28 29 2a 2b 4 5 6 7 24
  //   25 26 27 24 25 26 27 0 1 2 3 8 9 a b 8 9 a b 20 21 22 23 30 31 32 33 4 5 6 7 24 25 26 27 24 25 26 27
  //   0 1 2 3 0 1 2 3 8 9 a b 20 21 22 23 28 29 2a 2b 4 5 6 7 24 25 26 27 4 5 6 7 0 1 2 3 8 9 a b 0 1 2 3
  //   20 21 22 23 30 31 32 33 24 25 26 27 4 5 6 7 24 25 26 27 0 1 2 3 8 9 a b 20 21 22 23 20 21 22 23 28
  //   29 2a 2b 4 5 6 7 24 25 26 27 4 5 6 7
  //   4路组相连映射cache测试电路
  //   命中率
  //   contents of 主存内容 (hex, n*v repeats v):
  //   0 1 2 3 4 5 6 7 8 9 a b c d e f 10 11 12 13 14 15 16 17 18 19 1a 1b 1c 1d 1e 1f 20 21 22 23 24 25 26
  //   27 28 29 2a 2b 2c 2d 2e 2f 30 31 32 33 34 35 36 37 38 39 3a 3b 3c 3d 3e 3f 40 41 42 43 44 45 46 47
  //   48 49 4a 4b 4c 4d 4e 4f 50 51 52 53 54 55 56 57 58 59 5a 5b 5c 5d 5e 5f 60 61 62 63 64 65 66 67 68
  //   69 6a 6b 6c 6d 6e 6f 70 71 72 73 74 75 76 77 78 79 7a 7b 7c 7d 7e 7f 80 81 82 83 84 85 86 87 88 89
  //   8a 8b 8c 8d 8e 8f 90 91 92 93 94 95 96 97 98 99 9a 9b 9c 9d 9e 9f a0 a1 a2 a3 a4 a5 a6 a7 a8 a9 aa
  //   ab ac ad ae af b0 b1 b2 b3 b4 b5 b6 b7 b8 b9 ba bb bc bd be bf c0 c1 c2 c3 c4 c5 c6 c7 c8 c9 ca cb
  //   cc cd ce cf d0 d1 d2 d3 d4 d5 d6 d7 d8 d9 da db dc dd de df e0 e1 e2 e3 e4 e5 e6 e7 e8 e9 ea eb ec
  //   ed ee ef f0 f1 f2 f3 f4 f5 f6 f7 f8 f9 fa fb fc fd fe ff 0 1 2 3 4 5 6 7 8 9 a b c d e f 10 11 12 13
  //   14 15 16 17 18 19 1a 1b 1c 1d 1e 1f 20 21 22 23 24 25 26 27 28 29 2a 2b 2c 2d 2e 2f 30 31 32 33 34
  //   35 36 37 38 39 3a 3b 3c 3d 3e 3f 40 41 42 43 44 45 46 47 48 49 4a 4b 4c 4d 4e 4f 50 51 52 53 54 55
  //   56 57 58 59 5a 5b 5c 5d 5e 5f 60 61 62 63 64 65 66 67 68 69 6a 6b 6c 6d 6e 6f 70 71 72 73 74 75 76
  //   77 78 79 7a 7b 7c 7d 7e 7f 80 81 82 83 84 85 86 87 88 89 8a 8b 8c 8d 8e 8f 90 91 92 93 94 95 96 97
  //   98 99 9a 9b 9c 9d 9e 9f a0 a1 a2 a3 a4 a5 a6 a7 a8 a9 aa ab ac ad ae af b0 b1 b2 b3 b4 b5 b6 b7 b8
  //   b9 ba bb bc bd be bf c0 c1 c2 c3 c4 c5 c6 c7 c8 c9 ca cb cc cd ce cf d0 d1 d2 d3 d4 d5 d6 d7 d8 d9
  //   da db dc dd de df e0 e1 e2 e3 e4 e5 e6 e7 e8 e9 ea eb ec ed ee ef f0 f1 f2 f3 f4 f5 f6 f7 f8 f9 fa
  //   fb fc fd fe ff 0 1 2 3 4 5 6 7 8 9 a b c d e f 10 11 12 13 14 15 16 17 18 19 1a 1b 1c 1d 1e 1f 20 21
  //   22 23 24 25 26 27 28 29 2a 2b 2c 2d 2e 2f 30 31 32 33 34 35 36 37 38 39 3a 3b 3c 3d 3e 3f 40 41 42
  //   43 44 45 46 47 48 49 4a 4b 4c 4d 4e 4f 50 51 52 53 54 55 56 57 58 59 5a 5b 5c 5d 5e 5f 60 61 62 63
  //   64 65 66 67 68 69 6a 6b 6c 6d 6e 6f 70 71 72 73 74 75 76 77 78 79 7a 7b 7c 7d 7e 7f 80 81 82 83 84
  //   85 86 87 88 89 8a 8b 8c 8d 8e 8f 90 91 92 93 94 95 96 97 98 99 9a 9b 9c 9d 9e 9f a0 a1 a2 a3 a4 a5
  //   a6 a7 a8 a9 aa ab ac ad ae af b0 b1 b2 b3 b4 b5 b6 b7 b8 b9 ba bb bc bd be bf c0 c1 c2 c3 c4 c5 c6
  //   c7 c8 c9 ca cb cc cd ce cf d0 d1 d2 d3 d4 d5 d6 d7 d8 d9 da db dc dd de df e0 e1 e2 e3 e4 e5 e6 e7
  //   e8 e9 ea eb ec ed ee ef f0 f1 f2 f3 f4 f5 f6 f7 f8 f9 fa fb fc fd fe ff 0 1 2 3 4 5 6 7 8 9 a b c d
  //   e f 10 11 12 13 14 15 16 17 18 19 1a 1b 1c 1d 1e 1f 20 21 22 23 24 25 26 27 28 29 2a 2b 2c 2d 2e 2f
  //   30 31 32 33 34 35 36 37 38 39 3a 3b 3c 3d 3e 3f 40 41 42 43 44 45 46 47 48 49 4a 4b 4c 4d 4e 4f 50
  //   51 52 53 54 55 56 57 58 59 5a 5b 5c 5d 5e 5f 60 61 62 63 64 65 66 67 68 69 6a 6b 6c 6d 6e 6f 70 71
  //   72 73 74 75 76 77 78 79 7a 7b 7c 7d 7e 7f 80 81 82 83 84 85 86 87 88 89 8a 8b 8c 8d 8e 8f 90 91 92
  //   93 94 95 96 97 98 99 9a 9b 9c 9d 9e 9f a0 a1 a2 a3 a4 a5 a6 a7 a8 a9 aa ab ac ad ae af b0 b1 b2 b3
  //   b4 b5 b6 b7 b8 b9 ba bb bc bd be bf c0 c1 c2 c3 c4 c5 c6 c7 c8 c9 ca cb cc cd ce cf d0 d1 d2 d3 d4
  //   d5 d6 d7 d8 d9 da db dc dd de df e0 e1 e2 e3 e4 e5 e6 e7 e8 e9 ea eb ec ed ee ef f0 f1 f2 f3 f4 f5
  //   f6 f7 f8 f9 fa fb fc fd fe ff 0 1 2 3 4 5 6 7 8 9 a b c d e f 10 11 12 13 14 15 16 17 18 19 1a 1b 1c
  //   1d 1e 1f 20 21 22 23 24 25 26 27 28 29 2a 2b 2c 2d 2e 2f 30 31 32 33 34 35 36 37 38 39 3a 3b 3c 3d
  //   3e 3f 40 41 42 43 44 45 46 47 48 49 4a 4b 4c 4d 4e 4f 50 51 52 53 54 55 56 57 58 59 5a 5b 5c 5d 5e
  //   5f 60 61 62 63 64 65 66 67 68 69 6a 6b 6c 6d 6e 6f 70 71 72 73 74 75 76 77 78 79 7a 7b 7c 7d 7e 7f
  //   80 81 82 83 84 85 86 87 88 89 8a 8b 8c 8d 8e 8f 90 91 92 93 94 95 96 97 98 99 9a 9b 9c 9d 9e 9f a0
  //   a1 a2 a3 a4 a5 a6 a7 a8 a9 aa ab ac ad ae af b0 b1 b2 b3 b4 b5 b6 b7 b8 b9 ba bb bc bd be bf c0 c1
  //   c2 c3 c4 c5 c6 c7 c8 c9 ca cb cc cd ce cf d0 d1 d2 d3 d4 d5 d6 d7 d8 d9 da db dc dd de df e0 e1 e2
  //   e3 e4 e5 e6 e7 e8 e9 ea eb ec ed ee ef f0 f1 f2 f3 f4 f5 f6 f7 f8 f9 fa fb fc fd fe ff
  //   cache模拟器
endmodule

module \cache_8路组相联映射_电路_16个cache块  (
  input  BlkDataReady,
  input  [31:0] BlockDataIn,
  input  [15:0] Addr,
  input  CLK,
  output Miss,
  output [7:0] DataOut
);

  wire and_1_out, and_2_out, and_3_out, and_4_out, and_5_out, and_6_out, and_7_out, and_8_out, and_9_out,
       and_10_out, and_11_out, and_12_out, and_13_out, and_14_out, and_15_out, and_16_out, and_17_out,
       and_18_out, and_19_out, and_20_out, and_21_out, and_22_out, and_23_out, and_24_out, and_33_out,
       and_34_out, and_35_out, and_36_out, and_37_out, and_38_out, and_39_out, and_40_out, comparator_1_eq,
       comparator_2_eq, comparator_3_eq, comparator_4_eq, comparator_5_eq, comparator_6_eq, comparator_7_eq,
       comparator_8_eq, Hit, L0, L1, L2, L3, L4, L5, L6, L7, not_2_out, not_3_out, not_4_out, not_5_out,
       not_6_out, not_7_out, not_8_out, not_9_out, priority_encoder_1_gs, R0, R1, R2, R3, R4, R5, R6, R7,
       Set0, Set1, V0, V1, V2, V3, V4, V5, V6, V7, VALID_2_q, VALID_3_q, VALID_4_q, VALID_5_q, VALID_6_q,
       VALID_7_q, VALID_8_q, VALID_9_q, VALID_10_q, VALID_11_q, VALID_12_q, VALID_13_q, VALID_14_q,
       VALID_15_q, VALID_16_q, VALID_q;
  wire [2:0] \max3_归并比较_电路_1_max_num , \max3_归并比较_电路_2_max_num , \max3_归并比较_电路_3_max_num ,
       \max3_归并比较_电路_4_max_num , \max3_归并比较_电路_5_max_num , \max3_归并比较_电路_6_max_num ,
       \max3_归并比较_电路_7_max_num , multiplexer_2_out, priority_encoder_1_out;
  wire [12:0] Tag0, Tag1, Tag2, Tag3, Tag4, Tag5, Tag6, Tag7, \标记位_2_q , \标记位_3_q , \标记位_4_q , \标记位_5_q ,
       \标记位_6_q , \标记位_7_q , \标记位_8_q , \标记位_9_q , \标记位_10_q , \标记位_11_q , \标记位_12_q , \标记位_13_q ,
       \标记位_14_q , \标记位_15_q , \标记位_16_q , \标记位_q ;
  wire [15:0] C0, C1, C2, C3, C4, C5, C6, C7, \max3_归并比较_电路_1_max , \max3_归并比较_电路_2_max ,
       \max3_归并比较_电路_3_max , \max3_归并比较_电路_4_max , \max3_归并比较_电路_5_max , \max3_归并比较_电路_6_max , \淘汰标志位_2_q ,
       \淘汰标志位_3_q , \淘汰标志位_4_q , \淘汰标志位_5_q , \淘汰标志位_6_q , \淘汰标志位_7_q , \淘汰标志位_8_q , \淘汰标志位_9_q ,
       \淘汰标志位_10_q , \淘汰标志位_11_q , \淘汰标志位_12_q , \淘汰标志位_13_q , \淘汰标志位_14_q , \淘汰标志位_15_q , \淘汰标志位_16_q ,
       \淘汰标志位_q ;
  wire [31:0] SlotData, \数据块副本_2_q , \数据块副本_3_q , \数据块副本_4_q , \数据块副本_5_q , \数据块副本_6_q , \数据块副本_7_q ,
       \数据块副本_8_q , \数据块副本_9_q , \数据块副本_10_q , \数据块副本_11_q , \数据块副本_12_q , \数据块副本_13_q , \数据块副本_14_q ,
       \数据块副本_15_q , \数据块副本_16_q , \数据块副本_q ;

  // Probe on Addr
  Register #(.width(1), .trigger("rising"), .Select("low")) VALID (
    .D(1'b1), .en(and_1_out), .Q(VALID_q), .clk(CLK));  // open: clr
  Register #(.width(1), .trigger("rising"), .Select("low")) VALID_2 (
    .D(1'b1), .en(and_2_out), .Q(VALID_2_q), .clk(CLK));  // open: clr
  Register #(.width(1), .trigger("rising"), .Select("low")) VALID_3 (
    .D(1'b1), .en(and_3_out), .Q(VALID_3_q), .clk(CLK));  // open: clr
  Register #(.width(1), .trigger("rising"), .Select("low")) VALID_4 (
    .D(1'b1), .en(and_4_out), .Q(VALID_4_q), .clk(CLK));  // open: clr
  Register #(.width(1), .trigger("rising"), .Select("low")) VALID_5 (
    .D(1'b1), .en(and_5_out), .Q(VALID_5_q), .clk(CLK));  // open: clr
  Register #(.width(1), .trigger("rising"), .Select("low")) VALID_6 (
    .D(1'b1), .en(and_6_out), .Q(VALID_6_q), .clk(CLK));  // open: clr
  Register #(.width(1), .trigger("rising"), .Select("low")) VALID_7 (
    .D(1'b1), .en(and_7_out), .Q(VALID_7_q), .clk(CLK));  // open: clr
  Register #(.width(1), .trigger("rising"), .Select("low")) VALID_8 (
    .D(1'b1), .en(and_8_out), .Q(VALID_8_q), .clk(CLK));  // open: clr
  assign V0 = Set0 ? VALID_q : 1'bz;  // Controlled_Buffer controlled_buffer_1
  and and_1 (and_1_out, Set0, R0);
  assign V1 = Set0 ? VALID_2_q : 1'bz;  // Controlled_Buffer controlled_buffer_2
  and and_2 (and_2_out, Set0, R1);
  assign V2 = Set0 ? VALID_3_q : 1'bz;  // Controlled_Buffer controlled_buffer_3
  and and_3 (and_3_out, Set0, R2);
  assign V3 = Set0 ? VALID_4_q : 1'bz;  // Controlled_Buffer controlled_buffer_4
  and and_4 (and_4_out, Set0, R3);
  assign V4 = Set0 ? VALID_5_q : 1'bz;  // Controlled_Buffer controlled_buffer_5
  and and_5 (and_5_out, Set0, R4);
  assign V5 = Set0 ? VALID_6_q : 1'bz;  // Controlled_Buffer controlled_buffer_6
  and and_6 (and_6_out, Set0, R5);
  assign V6 = Set0 ? VALID_7_q : 1'bz;  // Controlled_Buffer controlled_buffer_7
  and and_7 (and_7_out, Set0, R6);
  assign V7 = Set0 ? VALID_8_q : 1'bz;  // Controlled_Buffer controlled_buffer_8
  and and_8 (and_8_out, Set0, R7);
  Multiplexer #(.select(2), .width(8), .disabled("Z"), .enable("true")) multiplexer_1 (
    .in0(SlotData[7:0]), .in1(SlotData[15:8]), .in2(SlotData[23:16]), .in3(SlotData[31:24]), .out(DataOut),
    .sel(Addr[1:0]), .en(Hit));
  Register #(.width(13), .trigger("rising"), .Select("low")) \u_标记位  (
    .D(Addr[15:3]), .en(and_1_out), .Q(\标记位_q ), .clk(CLK));  // open: clr
  Register #(.width(13), .trigger("rising"), .Select("low")) \u_标记位_2  (
    .D(Addr[15:3]), .en(and_2_out), .Q(\标记位_2_q ), .clk(CLK));  // open: clr
  Register #(.width(13), .trigger("rising"), .Select("low")) \u_标记位_3  (
    .D(Addr[15:3]), .en(and_3_out), .Q(\标记位_3_q ), .clk(CLK));  // open: clr
  Register #(.width(13), .trigger("rising"), .Select("low")) \u_标记位_4  (
    .D(Addr[15:3]), .en(and_4_out), .Q(\标记位_4_q ), .clk(CLK));  // open: clr
  Register #(.width(13), .trigger("rising"), .Select("low")) \u_标记位_5  (
    .D(Addr[15:3]), .en(and_5_out), .Q(\标记位_5_q ), .clk(CLK));  // open: clr
  Register #(.width(13), .trigger("rising"), .Select("low")) \u_标记位_6  (
    .D(Addr[15:3]), .en(and_6_out), .Q(\标记位_6_q ), .clk(CLK));  // open: clr
  Register #(.width(13), .trigger("rising"), .Select("low")) \u_标记位_7  (
    .D(Addr[15:3]), .en(and_7_out), .Q(\标记位_7_q ), .clk(CLK));  // open: clr
  Register #(.width(13), .trigger("rising"), .Select("low")) \u_标记位_8  (
    .D(Addr[15:3]), .en(and_8_out), .Q(\标记位_8_q ), .clk(CLK));  // open: clr
  assign Tag0 = Set0 ? \标记位_q  : 13'bz;  // Controlled_Buffer controlled_buffer_9
  assign Tag1 = Set0 ? \标记位_2_q  : 13'bz;  // Controlled_Buffer controlled_buffer_10
  assign Tag2 = Set0 ? \标记位_3_q  : 13'bz;  // Controlled_Buffer controlled_buffer_11
  assign Tag3 = Set0 ? \标记位_4_q  : 13'bz;  // Controlled_Buffer controlled_buffer_12
  assign Tag4 = Set0 ? \标记位_5_q  : 13'bz;  // Controlled_Buffer controlled_buffer_13
  assign Tag5 = Set0 ? \标记位_6_q  : 13'bz;  // Controlled_Buffer controlled_buffer_14
  assign Tag6 = Set0 ? \标记位_7_q  : 13'bz;  // Controlled_Buffer controlled_buffer_15
  assign Tag7 = Set0 ? \标记位_8_q  : 13'bz;  // Controlled_Buffer controlled_buffer_16
  not not_1 (Miss, Hit);
  Decoder #(.select(1), .tristate("false"), .disabled("Z"), .enable("false")) decoder_1 (
    .out0(Set0), .out1(Set1), .sel(Addr[2]));
  assign C0 = Set0 ? \淘汰标志位_q  : 16'bz;  // Controlled_Buffer controlled_buffer_17
  Counter #(.width(16), .max('hffff), .ongoal("wrap"), .trigger("rising"), .behavior("old")) \u_淘汰标志位  (
    .count(Hit), .Q(\淘汰标志位_q ), .clk(CLK), .clr(and_9_out));  // open: load, D, carry, preset
  assign C1 = Set0 ? \淘汰标志位_2_q  : 16'bz;  // Controlled_Buffer controlled_buffer_18
  Counter #(.width(16), .max('hffff), .ongoal("wrap"), .trigger("rising"), .behavior("old")) \u_淘汰标志位_2  (
    .count(Hit), .Q(\淘汰标志位_2_q ), .clk(CLK), .clr(and_10_out));  // open: load, D, carry, preset
  assign C2 = Set0 ? \淘汰标志位_3_q  : 16'bz;  // Controlled_Buffer controlled_buffer_19
  Counter #(.width(16), .max('hffff), .ongoal("wrap"), .trigger("rising"), .behavior("old")) \u_淘汰标志位_3  (
    .count(Hit), .Q(\淘汰标志位_3_q ), .clk(CLK), .clr(and_11_out));  // open: load, D, carry, preset
  Counter #(.width(16), .max('hffff), .ongoal("wrap"), .trigger("rising"), .behavior("old")) \u_淘汰标志位_4  (
    .count(Hit), .Q(\淘汰标志位_4_q ), .clk(CLK), .clr(and_12_out));  // open: load, D, carry, preset
  assign C3 = Set0 ? \淘汰标志位_4_q  : 16'bz;  // Controlled_Buffer controlled_buffer_20
  assign C4 = Set0 ? \淘汰标志位_5_q  : 16'bz;  // Controlled_Buffer controlled_buffer_21
  Counter #(.width(16), .max('hffff), .ongoal("wrap"), .trigger("rising"), .behavior("old")) \u_淘汰标志位_5  (
    .count(Hit), .Q(\淘汰标志位_5_q ), .clk(CLK), .clr(and_13_out));  // open: load, D, carry, preset
  Counter #(.width(16), .max('hffff), .ongoal("wrap"), .trigger("rising"), .behavior("old")) \u_淘汰标志位_6  (
    .count(Hit), .Q(\淘汰标志位_6_q ), .clk(CLK), .clr(and_14_out));  // open: load, D, carry, preset
  assign C5 = Set0 ? \淘汰标志位_6_q  : 16'bz;  // Controlled_Buffer controlled_buffer_22
  assign C6 = Set0 ? \淘汰标志位_7_q  : 16'bz;  // Controlled_Buffer controlled_buffer_23
  Counter #(.width(16), .max('hffff), .ongoal("wrap"), .trigger("rising"), .behavior("old")) \u_淘汰标志位_7  (
    .count(Hit), .Q(\淘汰标志位_7_q ), .clk(CLK), .clr(and_15_out));  // open: load, D, carry, preset
  Counter #(.width(16), .max('hffff), .ongoal("wrap"), .trigger("rising"), .behavior("old")) \u_淘汰标志位_8  (
    .count(Hit), .Q(\淘汰标志位_8_q ), .clk(CLK), .clr(and_16_out));  // open: load, D, carry, preset
  assign C7 = Set0 ? \淘汰标志位_8_q  : 16'bz;  // Controlled_Buffer controlled_buffer_24
  or or_1 (Hit, L0, L1, L2, L3, L4, L5, L6, L7);
  Register #(.width(32), .trigger("rising"), .Select("low")) \u_数据块副本  (
    .D(BlockDataIn), .en(and_1_out), .Q(\数据块副本_q ), .clk(CLK));  // open: clr
  Register #(.width(32), .trigger("rising"), .Select("low")) \u_数据块副本_2  (
    .D(BlockDataIn), .en(and_2_out), .Q(\数据块副本_2_q ), .clk(CLK));  // open: clr
  Register #(.width(32), .trigger("rising"), .Select("low")) \u_数据块副本_3  (
    .D(BlockDataIn), .en(and_3_out), .Q(\数据块副本_3_q ), .clk(CLK));  // open: clr
  Register #(.width(32), .trigger("rising"), .Select("low")) \u_数据块副本_4  (
    .D(BlockDataIn), .en(and_4_out), .Q(\数据块副本_4_q ), .clk(CLK));  // open: clr
  Register #(.width(32), .trigger("rising"), .Select("low")) \u_数据块副本_5  (
    .D(BlockDataIn), .en(and_5_out), .Q(\数据块副本_5_q ), .clk(CLK));  // open: clr
  Register #(.width(32), .trigger("rising"), .Select("low")) \u_数据块副本_6  (
    .D(BlockDataIn), .en(and_6_out), .Q(\数据块副本_6_q ), .clk(CLK));  // open: clr
  Register #(.width(32), .trigger("rising"), .Select("low")) \u_数据块副本_7  (
    .D(BlockDataIn), .en(and_7_out), .Q(\数据块副本_7_q ), .clk(CLK));  // open: clr
  Register #(.width(32), .trigger("rising"), .Select("low")) \u_数据块副本_8  (
    .D(BlockDataIn), .en(and_8_out), .Q(\数据块副本_8_q ), .clk(CLK));  // open: clr
  assign SlotData = and_9_out ? \数据块副本_q  : 32'bz;  // Controlled_Buffer controlled_buffer_25
  and and_9 (and_9_out, L0, Set0);
  assign SlotData = and_10_out ? \数据块副本_2_q  : 32'bz;  // Controlled_Buffer controlled_buffer_26
  and and_10 (and_10_out, L1, Set0);
  assign SlotData = and_11_out ? \数据块副本_3_q  : 32'bz;  // Controlled_Buffer controlled_buffer_27
  and and_11 (and_11_out, L2, Set0);
  assign SlotData = and_12_out ? \数据块副本_4_q  : 32'bz;  // Controlled_Buffer controlled_buffer_28
  and and_12 (and_12_out, L3, Set0);
  assign SlotData = and_13_out ? \数据块副本_5_q  : 32'bz;  // Controlled_Buffer controlled_buffer_29
  and and_13 (and_13_out, L4, Set0);
  assign SlotData = and_14_out ? \数据块副本_6_q  : 32'bz;  // Controlled_Buffer controlled_buffer_30
  and and_14 (and_14_out, L5, Set0);
  assign SlotData = and_15_out ? \数据块副本_7_q  : 32'bz;  // Controlled_Buffer controlled_buffer_31
  and and_15 (and_15_out, L6, Set0);
  assign SlotData = and_16_out ? \数据块副本_8_q  : 32'bz;  // Controlled_Buffer controlled_buffer_32
  and and_16 (and_16_out, L7, Set0);
  Register #(.width(1), .trigger("rising"), .Select("low")) VALID_9 (
    .D(1'b1), .en(and_17_out), .Q(VALID_9_q), .clk(CLK));  // open: clr
  assign V0 = Set1 ? VALID_9_q : 1'bz;  // Controlled_Buffer controlled_buffer_33
  Register #(.width(1), .trigger("rising"), .Select("low")) VALID_10 (
    .D(1'b1), .en(and_18_out), .Q(VALID_10_q), .clk(CLK));  // open: clr
  assign V1 = Set1 ? VALID_10_q : 1'bz;  // Controlled_Buffer controlled_buffer_34
  Register #(.width(1), .trigger("rising"), .Select("low")) VALID_11 (
    .D(1'b1), .en(and_19_out), .Q(VALID_11_q), .clk(CLK));  // open: clr
  assign V2 = Set1 ? VALID_11_q : 1'bz;  // Controlled_Buffer controlled_buffer_35
  assign V3 = Set1 ? VALID_12_q : 1'bz;  // Controlled_Buffer controlled_buffer_36
  Register #(.width(1), .trigger("rising"), .Select("low")) VALID_12 (
    .D(1'b1), .en(and_20_out), .Q(VALID_12_q), .clk(CLK));  // open: clr
  assign V4 = Set1 ? VALID_13_q : 1'bz;  // Controlled_Buffer controlled_buffer_37
  Register #(.width(1), .trigger("rising"), .Select("low")) VALID_13 (
    .D(1'b1), .en(and_21_out), .Q(VALID_13_q), .clk(CLK));  // open: clr
  Register #(.width(1), .trigger("rising"), .Select("low")) VALID_14 (
    .D(1'b1), .en(and_22_out), .Q(VALID_14_q), .clk(CLK));  // open: clr
  assign V5 = Set1 ? VALID_14_q : 1'bz;  // Controlled_Buffer controlled_buffer_38
  Register #(.width(1), .trigger("rising"), .Select("low")) VALID_15 (
    .D(1'b1), .en(and_23_out), .Q(VALID_15_q), .clk(CLK));  // open: clr
  assign V6 = Set1 ? VALID_15_q : 1'bz;  // Controlled_Buffer controlled_buffer_39
  assign V7 = Set1 ? VALID_16_q : 1'bz;  // Controlled_Buffer controlled_buffer_40
  Register #(.width(1), .trigger("rising"), .Select("low")) VALID_16 (
    .D(1'b1), .en(and_24_out), .Q(VALID_16_q), .clk(CLK));  // open: clr
  Comparator #(.width(13), .mode("twosComplement")) comparator_1 (
    .a(Addr[15:3]), .b(Tag0), .eq(comparator_1_eq));  // open: gt, lt
  Comparator #(.width(13), .mode("twosComplement")) comparator_2 (
    .a(Addr[15:3]), .b(Tag1), .eq(comparator_2_eq));  // open: gt, lt
  Comparator #(.width(13), .mode("twosComplement")) comparator_3 (
    .a(Addr[15:3]), .b(Tag2), .eq(comparator_3_eq));  // open: gt, lt
  Comparator #(.width(13), .mode("twosComplement")) comparator_4 (
    .a(Addr[15:3]), .b(Tag3), .eq(comparator_4_eq));  // open: gt, lt
  \Max3_归并比较_电路  \max3_归并比较_电路_1  (
    .Y(C1), .X(C0), .Y_num(3'b001), .X_num(3'b000), .MAX(\max3_归并比较_电路_1_max ),
    .Max_num(\max3_归并比较_电路_1_max_num ));
  \Max3_归并比较_电路  \max3_归并比较_电路_2  (
    .Y(C3), .X(C2), .Y_num(3'b011), .X_num(3'b010), .MAX(\max3_归并比较_电路_2_max ),
    .Max_num(\max3_归并比较_电路_2_max_num ));
  \Max3_归并比较_电路  \max3_归并比较_电路_3  (
    .Y(C5), .X(C4), .Y_num(3'b101), .X_num(3'b100), .MAX(\max3_归并比较_电路_3_max ),
    .Max_num(\max3_归并比较_电路_3_max_num ));
  \Max3_归并比较_电路  \max3_归并比较_电路_4  (
    .Y(C7), .X(C6), .Y_num(3'b111), .X_num(3'b110), .MAX(\max3_归并比较_电路_4_max ),
    .Max_num(\max3_归并比较_电路_4_max_num ));
  and and_17 (and_17_out, Set1, R0);
  and and_18 (and_18_out, Set1, R1);
  and and_19 (and_19_out, Set1, R2);
  and and_20 (and_20_out, Set1, R3);
  and and_21 (and_21_out, Set1, R4);
  and and_22 (and_22_out, Set1, R5);
  and and_23 (and_23_out, Set1, R6);
  and and_24 (and_24_out, Set1, R7);
  and and_25 (L0, V0, comparator_1_eq);
  and and_26 (L1, V1, comparator_2_eq);
  and and_27 (L2, V2, comparator_3_eq);
  and and_28 (L3, V3, comparator_4_eq);
  \Max3_归并比较_电路  \max3_归并比较_电路_5  (
    .Y(\max3_归并比较_电路_2_max ), .X(\max3_归并比较_电路_1_max ), .Y_num(\max3_归并比较_电路_2_max_num ),
    .X_num(\max3_归并比较_电路_1_max_num ), .MAX(\max3_归并比较_电路_5_max ), .Max_num(\max3_归并比较_电路_5_max_num ));
  \Max3_归并比较_电路  \max3_归并比较_电路_6  (
    .Y(\max3_归并比较_电路_4_max ), .X(\max3_归并比较_电路_3_max ), .Y_num(\max3_归并比较_电路_4_max_num ),
    .X_num(\max3_归并比较_电路_3_max_num ), .MAX(\max3_归并比较_电路_6_max ), .Max_num(\max3_归并比较_电路_6_max_num ));
  Register #(.width(13), .trigger("rising"), .Select("low")) \u_标记位_9  (
    .D(Addr[15:3]), .en(and_17_out), .Q(\标记位_9_q ), .clk(CLK));  // open: clr
  Register #(.width(13), .trigger("rising"), .Select("low")) \u_标记位_10  (
    .D(Addr[15:3]), .en(and_18_out), .Q(\标记位_10_q ), .clk(CLK));  // open: clr
  Register #(.width(13), .trigger("rising"), .Select("low")) \u_标记位_11  (
    .D(Addr[15:3]), .en(and_19_out), .Q(\标记位_11_q ), .clk(CLK));  // open: clr
  Register #(.width(13), .trigger("rising"), .Select("low")) \u_标记位_12  (
    .D(Addr[15:3]), .en(and_20_out), .Q(\标记位_12_q ), .clk(CLK));  // open: clr
  Register #(.width(13), .trigger("rising"), .Select("low")) \u_标记位_13  (
    .D(Addr[15:3]), .en(and_21_out), .Q(\标记位_13_q ), .clk(CLK));  // open: clr
  Register #(.width(13), .trigger("rising"), .Select("low")) \u_标记位_14  (
    .D(Addr[15:3]), .en(and_22_out), .Q(\标记位_14_q ), .clk(CLK));  // open: clr
  Register #(.width(13), .trigger("rising"), .Select("low")) \u_标记位_15  (
    .D(Addr[15:3]), .en(and_23_out), .Q(\标记位_15_q ), .clk(CLK));  // open: clr
  Register #(.width(13), .trigger("rising"), .Select("low")) \u_标记位_16  (
    .D(Addr[15:3]), .en(and_24_out), .Q(\标记位_16_q ), .clk(CLK));  // open: clr
  \Max3_归并比较_电路  \max3_归并比较_电路_7  (
    .Y(\max3_归并比较_电路_6_max ), .X(\max3_归并比较_电路_5_max ), .Y_num(\max3_归并比较_电路_6_max_num ),
    .X_num(\max3_归并比较_电路_5_max_num ), .Max_num(\max3_归并比较_电路_7_max_num ));  // open: MAX
  assign Tag0 = Set1 ? \标记位_9_q  : 13'bz;  // Controlled_Buffer controlled_buffer_41
  assign Tag1 = Set1 ? \标记位_10_q  : 13'bz;  // Controlled_Buffer controlled_buffer_42
  assign Tag2 = Set1 ? \标记位_11_q  : 13'bz;  // Controlled_Buffer controlled_buffer_43
  assign Tag3 = Set1 ? \标记位_12_q  : 13'bz;  // Controlled_Buffer controlled_buffer_44
  assign Tag4 = Set1 ? \标记位_13_q  : 13'bz;  // Controlled_Buffer controlled_buffer_45
  assign Tag5 = Set1 ? \标记位_14_q  : 13'bz;  // Controlled_Buffer controlled_buffer_46
  assign Tag6 = Set1 ? \标记位_15_q  : 13'bz;  // Controlled_Buffer controlled_buffer_47
  assign Tag7 = Set1 ? \标记位_16_q  : 13'bz;  // Controlled_Buffer controlled_buffer_48
  Multiplexer #(.select(1), .width(3), .disabled("Z"), .enable("false")) multiplexer_2 (
    .in0(\max3_归并比较_电路_7_max_num ), .in1(priority_encoder_1_out), .out(multiplexer_2_out),
    .sel(priority_encoder_1_gs));
  Decoder #(.select(3), .tristate("false"), .disabled(0), .enable("true")) decoder_2 (
    .out0(R0), .out1(R1), .out2(R2), .out3(R3), .out4(R4), .out5(R5), .out6(R6), .out7(R7),
    .sel(multiplexer_2_out), .en(BlkDataReady));
  Counter #(.width(16), .max('hffff), .ongoal("wrap"), .trigger("rising"), .behavior("old")) \u_淘汰标志位_9  (
    .count(Hit), .Q(\淘汰标志位_9_q ), .clk(CLK), .clr(and_33_out));  // open: load, D, carry, preset
  Counter #(.width(16), .max('hffff), .ongoal("wrap"), .trigger("rising"), .behavior("old")) \u_淘汰标志位_10  (
    .count(Hit), .Q(\淘汰标志位_10_q ), .clk(CLK), .clr(and_34_out));  // open: load, D, carry, preset
  Counter #(.width(16), .max('hffff), .ongoal("wrap"), .trigger("rising"), .behavior("old")) \u_淘汰标志位_11  (
    .count(Hit), .Q(\淘汰标志位_11_q ), .clk(CLK), .clr(and_35_out));  // open: load, D, carry, preset
  Counter #(.width(16), .max('hffff), .ongoal("wrap"), .trigger("rising"), .behavior("old")) \u_淘汰标志位_12  (
    .count(Hit), .Q(\淘汰标志位_12_q ), .clk(CLK), .clr(and_36_out));  // open: load, D, carry, preset
  Counter #(.width(16), .max('hffff), .ongoal("wrap"), .trigger("rising"), .behavior("old")) \u_淘汰标志位_13  (
    .count(Hit), .Q(\淘汰标志位_13_q ), .clk(CLK), .clr(and_37_out));  // open: load, D, carry, preset
  Counter #(.width(16), .max('hffff), .ongoal("wrap"), .trigger("rising"), .behavior("old")) \u_淘汰标志位_14  (
    .count(Hit), .Q(\淘汰标志位_14_q ), .clk(CLK), .clr(and_38_out));  // open: load, D, carry, preset
  Counter #(.width(16), .max('hffff), .ongoal("wrap"), .trigger("rising"), .behavior("old")) \u_淘汰标志位_15  (
    .count(Hit), .Q(\淘汰标志位_15_q ), .clk(CLK), .clr(and_39_out));  // open: load, D, carry, preset
  Counter #(.width(16), .max('hffff), .ongoal("wrap"), .trigger("rising"), .behavior("old")) \u_淘汰标志位_16  (
    .count(Hit), .Q(\淘汰标志位_16_q ), .clk(CLK), .clr(and_40_out));  // open: load, D, carry, preset
  Comparator #(.width(13), .mode("twosComplement")) comparator_5 (
    .a(Addr[15:3]), .b(Tag4), .eq(comparator_5_eq));  // open: gt, lt
  Comparator #(.width(13), .mode("twosComplement")) comparator_6 (
    .a(Addr[15:3]), .b(Tag5), .eq(comparator_6_eq));  // open: gt, lt
  Comparator #(.width(13), .mode("twosComplement")) comparator_7 (
    .a(Addr[15:3]), .b(Tag6), .eq(comparator_7_eq));  // open: gt, lt
  Comparator #(.width(13), .mode("twosComplement")) comparator_8 (
    .a(Addr[15:3]), .b(Tag7), .eq(comparator_8_eq));  // open: gt, lt
  assign C0 = Set1 ? \淘汰标志位_9_q  : 16'bz;  // Controlled_Buffer controlled_buffer_49
  assign C1 = Set1 ? \淘汰标志位_10_q  : 16'bz;  // Controlled_Buffer controlled_buffer_50
  assign C2 = Set1 ? \淘汰标志位_11_q  : 16'bz;  // Controlled_Buffer controlled_buffer_51
  assign C3 = Set1 ? \淘汰标志位_12_q  : 16'bz;  // Controlled_Buffer controlled_buffer_52
  assign C4 = Set1 ? \淘汰标志位_13_q  : 16'bz;  // Controlled_Buffer controlled_buffer_53
  assign C5 = Set1 ? \淘汰标志位_14_q  : 16'bz;  // Controlled_Buffer controlled_buffer_54
  assign C6 = Set1 ? \淘汰标志位_15_q  : 16'bz;  // Controlled_Buffer controlled_buffer_55
  assign C7 = Set1 ? \淘汰标志位_16_q  : 16'bz;  // Controlled_Buffer controlled_buffer_56
  and and_29 (L4, V4, comparator_5_eq);
  and and_30 (L5, V5, comparator_6_eq);
  and and_31 (L6, V6, comparator_7_eq);
  and and_32 (L7, V7, comparator_8_eq);
  not not_2 (not_2_out, V7);
  not not_3 (not_3_out, V6);
  not not_4 (not_4_out, V5);
  not not_5 (not_5_out, V4);
  not not_6 (not_6_out, V3);
  not not_7 (not_7_out, V2);
  not not_8 (not_8_out, V1);
  not not_9 (not_9_out, V0);
  Priority_Encoder #(.select(3), .disabled("Z")) priority_encoder_1 (
    .in0(not_9_out), .in1(not_8_out), .in2(not_7_out), .in3(not_6_out), .in4(not_5_out), .in5(not_4_out),
    .in6(not_3_out), .in7(not_2_out), .out(priority_encoder_1_out), .gs(priority_encoder_1_gs));  // open: en_out, en_in
  assign SlotData = and_33_out ? \数据块副本_9_q  : 32'bz;  // Controlled_Buffer controlled_buffer_57
  Register #(.width(32), .trigger("rising"), .Select("low")) \u_数据块副本_9  (
    .D(BlockDataIn), .en(and_17_out), .Q(\数据块副本_9_q ), .clk(CLK));  // open: clr
  and and_33 (and_33_out, L0, Set1);
  Register #(.width(32), .trigger("rising"), .Select("low")) \u_数据块副本_10  (
    .D(BlockDataIn), .en(and_18_out), .Q(\数据块副本_10_q ), .clk(CLK));  // open: clr
  assign SlotData = and_34_out ? \数据块副本_10_q  : 32'bz;  // Controlled_Buffer controlled_buffer_58
  and and_34 (and_34_out, L1, Set1);
  Register #(.width(32), .trigger("rising"), .Select("low")) \u_数据块副本_11  (
    .D(BlockDataIn), .en(and_19_out), .Q(\数据块副本_11_q ), .clk(CLK));  // open: clr
  assign SlotData = and_35_out ? \数据块副本_11_q  : 32'bz;  // Controlled_Buffer controlled_buffer_59
  and and_35 (and_35_out, L2, Set1);
  assign SlotData = and_36_out ? \数据块副本_12_q  : 32'bz;  // Controlled_Buffer controlled_buffer_60
  Register #(.width(32), .trigger("rising"), .Select("low")) \u_数据块副本_12  (
    .D(BlockDataIn), .en(and_20_out), .Q(\数据块副本_12_q ), .clk(CLK));  // open: clr
  and and_36 (and_36_out, L3, Set1);
  assign SlotData = and_37_out ? \数据块副本_13_q  : 32'bz;  // Controlled_Buffer controlled_buffer_61
  Register #(.width(32), .trigger("rising"), .Select("low")) \u_数据块副本_13  (
    .D(BlockDataIn), .en(and_21_out), .Q(\数据块副本_13_q ), .clk(CLK));  // open: clr
  and and_37 (and_37_out, L4, Set1);
  Register #(.width(32), .trigger("rising"), .Select("low")) \u_数据块副本_14  (
    .D(BlockDataIn), .en(and_22_out), .Q(\数据块副本_14_q ), .clk(CLK));  // open: clr
  assign SlotData = and_38_out ? \数据块副本_14_q  : 32'bz;  // Controlled_Buffer controlled_buffer_62
  and and_38 (and_38_out, L5, Set1);
  assign SlotData = and_39_out ? \数据块副本_15_q  : 32'bz;  // Controlled_Buffer controlled_buffer_63
  Register #(.width(32), .trigger("rising"), .Select("low")) \u_数据块副本_15  (
    .D(BlockDataIn), .en(and_23_out), .Q(\数据块副本_15_q ), .clk(CLK));  // open: clr
  and and_39 (and_39_out, L6, Set1);
  Register #(.width(32), .trigger("rising"), .Select("low")) \u_数据块副本_16  (
    .D(BlockDataIn), .en(and_24_out), .Q(\数据块副本_16_q ), .clk(CLK));  // open: clr
  assign SlotData = and_40_out ? \数据块副本_16_q  : 32'bz;  // Controlled_Buffer controlled_buffer_64
  and and_40 (and_40_out, L7, Set1);

  // Other names for the same wires on the sheet: Blk[31:0] = BlockDataIn; BlkReady = BlkDataReady;
  //   Offset[1:0] = Addr[1:0]; 字节地址[15:0] = Addr; Index = Addr[2]; Tag[12:0] = Addr[15:3]

  // Notes on the sheet:
  //   输入引脚区
  //   cache（8路组相联映射）电路(16个cache块)
  //   输出引脚区
endmodule
module \_8路相联映射_16个cache块_测试电路  (
  input  in_1
);

  wire and_2_out, Clk, comparator_1_lt, comparator_2_eq, comparator_3_eq, controlled_buffer_1_out, EN, Error,
       Go, Hit, Miss, or_1_out, RDY, Runing;
  wire [3:0] _1, _2, _3;
  wire [7:0] Dataout, \主存内容_data ;
  wire [9:0] \测试用例数 ;
  wire [15:0] adder_1_out, Addr, bit_extender_3_out, \cache块交换逻辑电路_1_byteaddrout , counter_1_q,
       subtractor_1_out, \命中次数 , \时钟周期数 , \校验和 , \缺失次数 , \访问次数 ;
  wire [31:0] bit_extender_1_out, bit_extender_2_out, BlkDataIn, divider_1_out, divider_2_out,
       multiplier_1_out;
  wire [31:4] divider_2_rem, divider_3_out, divider_3_rem;

  not not_1 (Hit, Miss);
  and and_1 (EN, Hit, Go);
  Clock #(.highDuration(1), .lowDuration(1)) clock_1 (.out(Clk));
  Counter #(.width(16), .max('hffff), .ongoal("wrap"), .trigger("rising"), .behavior("old")) counter_1 (
    .count(and_2_out), .Q(counter_1_q), .clk(Clk));  // open: load, D, carry, clr, preset
  and and_2 (and_2_out, Miss, RDY, Runing);
  Subtractor #(.width(16)) subtractor_1 (.a(\访问次数 ), .b(\缺失次数 ), .out(subtractor_1_out));  // open: bin, bout
  Comparator #(.width(16), .mode("twosComplement")) comparator_1 (
    .a(\访问次数 ), .b(\缺失次数 ), .lt(comparator_1_lt));  // open: gt, eq
  // Probe on \访问次数 
  // Probe on \测试用例数 
  Counter #(.width(10), .max('h3ff), .ongoal("wrap"), .trigger("rising"), .behavior("old")) \u_计数器  (
    .count(EN), .Q(\测试用例数 ), .clk(Clk));  // open: load, D, carry, clr, preset
  Register #(.width(16), .trigger("rising"), .Select("low")) register_1 (
    .D(counter_1_q), .en(EN), .Q(\缺失次数 ), .clk(Clk));  // open: clr
  not not_2 (Runing, comparator_2_eq);
  Comparator #(.width(10), .mode("twosComplement")) comparator_2 (
    .a(\测试用例数 ), .b(10'h100), .eq(comparator_2_eq));  // open: gt, lt
  Multiplexer #(.select(1), .width(16), .disabled(0), .enable("false")) multiplexer_1 (
    .in0(subtractor_1_out), .in1({16{1'b0}}), .out(\命中次数 ), .sel(comparator_1_lt));
  // Probe on \命中次数 
  // Probe on \时钟周期数 
  ROM #(.addrWidth(10), .dataWidth(16), .Select("high")) \u_主存地址  (.addr(\测试用例数 ), .data(Addr));
  Counter #(.width(16), .max('hffff), .ongoal("wrap"), .trigger("rising"), .behavior("old")) counter_2 (
    .count(EN), .Q(\访问次数 ), .clk(Clk));  // open: load, D, carry, clr, preset
  assign bit_extender_1_out = {{16{1'b0}}, \命中次数 };  // Bit_Extender bit_extender_1
  // Probe on Dataout
  Multiplier #(.width(32)) multiplier_1 (
    .a(bit_extender_1_out), .b(32'h64), .out(multiplier_1_out));  // open: cin, cout
  assign bit_extender_2_out = {{16{1'b0}}, \访问次数 };  // Bit_Extender bit_extender_2
  // Probe on \缺失次数 
  // Probe on \校验和 
  \cache_8路组相联映射_电路_16个cache块  \cache_8路组相联映射_电路_16个cache块_1  (
    .BlkDataReady(RDY), .BlockDataIn(BlkDataIn), .Addr(Addr), .CLK(Clk), .Miss(Miss), .DataOut(Dataout));
  assign bit_extender_3_out = {{8{1'b0}}, Dataout};  // Bit_Extender bit_extender_3
  Divider #(.width(32)) divider_1 (
    .a(multiplier_1_out), .b(bit_extender_2_out), .out(divider_1_out));  // open: upper, rem
  Adder #(.width(16)) adder_1 (.a(\校验和 ), .b(bit_extender_3_out), .out(adder_1_out));  // open: cin, cout
  LED #(.active("true")) \u_读数据出错  (.in(Error));
  Pull_Resistor #(.pull(1)) pull_resistor_1 (.node(Miss));
  LED #(.active("true")) \u_缺失  (.in(Miss));
  Register #(.width(16), .trigger("rising"), .Select("low")) \u_校验和  (
    .D(adder_1_out), .en(EN), .Q(\校验和 ), .clk(Clk));  // open: clr
  Divider #(.width(32)) divider_2 (
    .a(divider_1_out), .b(32'ha), .out(divider_2_out), .rem({divider_2_rem, _1}));  // open: upper
  \cache块交换逻辑电路  \cache块交换逻辑电路_1  (
    .Addr(Addr), .CLK(Clk), .ByteAddrOut(\cache块交换逻辑电路_1_byteaddrout ), .ByteDataIn(\主存内容_data ),
    .Miss(Miss), .BlkDataReady(RDY), .BlockDataIn(BlkDataIn), .Enable(Runing));
  // Probe on \校验和 
  Divider #(.width(32)) divider_3 (
    .a(divider_2_out), .b(32'ha), .out({divider_3_out, _3}), .rem({divider_3_rem, _2}));  // open: upper
  ROM #(.addrWidth(16), .dataWidth(8), .Select("high")) \u_主存内容  (
    .addr(\cache块交换逻辑电路_1_byteaddrout ), .data(\主存内容_data ));
  Comparator #(.width(8), .mode("twosComplement")) comparator_3 (
    .a(Addr[7:0]), .b(Dataout), .eq(comparator_3_eq));  // open: gt, lt
  assign controlled_buffer_1_out = Hit ? comparator_3_eq : 1'bz;  // Controlled_Buffer controlled_buffer_1
  Pull_Resistor #(.pull(1)) pull_resistor_2 (.node(controlled_buffer_1_out));
  Hex_Digit_Display hex_digit_display_1 (.value(_2));  // open: dp
  Hex_Digit_Display hex_digit_display_2 (.value(_3), .dp(1'b1));
  or or_1 (or_1_out, controlled_buffer_1_out, ~in_1);  // OR_Gate
  Counter #(.width(16), .max('hffff), .ongoal("wrap"), .trigger("rising"), .behavior("old")) counter_3 (
    .count(Runing), .Q(\时钟周期数 ), .clk(Clk));  // open: load, D, carry, clr, preset
  Hex_Digit_Display hex_digit_display_3 (.value(_1));  // open: dp
  // Probe on Addr
  LED #(.active("true")) led_1 (.in(RDY));
  // Probe on BlkDataIn
  // Probe on Dataout
  and and_3 (Go, Runing, or_1_out);
  not not_3 (Error, or_1_out);

  // Other names for the same wires on the sheet: 读错误暂停 = in_1

  // Notes on the sheet:
  //   contents of 主存地址 (hex, n*v repeats v):
  //   0 1 2 3 8 9 a b 10 11 12 13 20 21 22 23 8 9 a b 4 5 6 7 24 25 26 27 4 5 6 7 0 1 2 3 8 9 a b 8 9 a b
  //   20 21 22 23 28 29 2a 2b 24 25 26 27 4 5 6 7 24 25 26 27 0 1 2 3 8 9 a b 20 21 22 23 20 21 22 23 30
  //   31 32 33 4 5 6 7 24 25 26 27 4 5 6 7 0 1 2 3 8 9 a b 20 21 22 23 20 21 22 23 28 29 2a 2b 4 5 6 7 24
  //   25 26 27 24 25 26 27 0 1 2 3 8 9 a b 8 9 a b 20 21 22 23 30 31 32 33 4 5 6 7 24 25 26 27 24 25 26 27
  //   0 1 2 3 0 1 2 3 8 9 a b 20 21 22 23 28 29 2a 2b 4 5 6 7 24 25 26 27 4 5 6 7 0 1 2 3 8 9 a b 0 1 2 3
  //   20 21 22 23 30 31 32 33 24 25 26 27 4 5 6 7 24 25 26 27 0 1 2 3 8 9 a b 20 21 22 23 20 21 22 23 28
  //   29 2a 2b 4 5 6 7 24 25 26 27 4 5 6 7
  //   8路组相连映射cache测试电路
  //   命中率
  //   contents of 主存内容 (hex, n*v repeats v):
  //   0 1 2 3 4 5 6 7 8 9 a b c d e f 10 11 12 13 14 15 16 17 18 19 1a 1b 1c 1d 1e 1f 20 21 22 23 24 25 26
  //   27 28 29 2a 2b 2c 2d 2e 2f 30 31 32 33 34 35 36 37 38 39 3a 3b 3c 3d 3e 3f 40 41 42 43 44 45 46 47
  //   48 49 4a 4b 4c 4d 4e 4f 50 51 52 53 54 55 56 57 58 59 5a 5b 5c 5d 5e 5f 60 61 62 63 64 65 66 67 68
  //   69 6a 6b 6c 6d 6e 6f 70 71 72 73 74 75 76 77 78 79 7a 7b 7c 7d 7e 7f 80 81 82 83 84 85 86 87 88 89
  //   8a 8b 8c 8d 8e 8f 90 91 92 93 94 95 96 97 98 99 9a 9b 9c 9d 9e 9f a0 a1 a2 a3 a4 a5 a6 a7 a8 a9 aa
  //   ab ac ad ae af b0 b1 b2 b3 b4 b5 b6 b7 b8 b9 ba bb bc bd be bf c0 c1 c2 c3 c4 c5 c6 c7 c8 c9 ca cb
  //   cc cd ce cf d0 d1 d2 d3 d4 d5 d6 d7 d8 d9 da db dc dd de df e0 e1 e2 e3 e4 e5 e6 e7 e8 e9 ea eb ec
  //   ed ee ef f0 f1 f2 f3 f4 f5 f6 f7 f8 f9 fa fb fc fd fe ff 0 1 2 3 4 5 6 7 8 9 a b c d e f 10 11 12 13
  //   14 15 16 17 18 19 1a 1b 1c 1d 1e 1f 20 21 22 23 24 25 26 27 28 29 2a 2b 2c 2d 2e 2f 30 31 32 33 34
  //   35 36 37 38 39 3a 3b 3c 3d 3e 3f 40 41 42 43 44 45 46 47 48 49 4a 4b 4c 4d 4e 4f 50 51 52 53 54 55
  //   56 57 58 59 5a 5b 5c 5d 5e 5f 60 61 62 63 64 65 66 67 68 69 6a 6b 6c 6d 6e 6f 70 71 72 73 74 75 76
  //   77 78 79 7a 7b 7c 7d 7e 7f 80 81 82 83 84 85 86 87 88 89 8a 8b 8c 8d 8e 8f 90 91 92 93 94 95 96 97
  //   98 99 9a 9b 9c 9d 9e 9f a0 a1 a2 a3 a4 a5 a6 a7 a8 a9 aa ab ac ad ae af b0 b1 b2 b3 b4 b5 b6 b7 b8
  //   b9 ba bb bc bd be bf c0 c1 c2 c3 c4 c5 c6 c7 c8 c9 ca cb cc cd ce cf d0 d1 d2 d3 d4 d5 d6 d7 d8 d9
  //   da db dc dd de df e0 e1 e2 e3 e4 e5 e6 e7 e8 e9 ea eb ec ed ee ef f0 f1 f2 f3 f4 f5 f6 f7 f8 f9 fa
  //   fb fc fd fe ff 0 1 2 3 4 5 6 7 8 9 a b c d e f 10 11 12 13 14 15 16 17 18 19 1a 1b 1c 1d 1e 1f 20 21
  //   22 23 24 25 26 27 28 29 2a 2b 2c 2d 2e 2f 30 31 32 33 34 35 36 37 38 39 3a 3b 3c 3d 3e 3f 40 41 42
  //   43 44 45 46 47 48 49 4a 4b 4c 4d 4e 4f 50 51 52 53 54 55 56 57 58 59 5a 5b 5c 5d 5e 5f 60 61 62 63
  //   64 65 66 67 68 69 6a 6b 6c 6d 6e 6f 70 71 72 73 74 75 76 77 78 79 7a 7b 7c 7d 7e 7f 80 81 82 83 84
  //   85 86 87 88 89 8a 8b 8c 8d 8e 8f 90 91 92 93 94 95 96 97 98 99 9a 9b 9c 9d 9e 9f a0 a1 a2 a3 a4 a5
  //   a6 a7 a8 a9 aa ab ac ad ae af b0 b1 b2 b3 b4 b5 b6 b7 b8 b9 ba bb bc bd be bf c0 c1 c2 c3 c4 c5 c6
  //   c7 c8 c9 ca cb cc cd ce cf d0 d1 d2 d3 d4 d5 d6 d7 d8 d9 da db dc dd de df e0 e1 e2 e3 e4 e5 e6 e7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
  //   cache模拟器
endmodule

// Max2
module \Max2_归并比较_电路  (
  input  [15:0] Y,
  input  [15:0] X,
  input  [1:0] Y_num,
  input  [1:0] X_num,
  output [15:0] MAX,
  output [1:0] MAX_num
);

  wire comparator_1_eq, comparator_1_gt, or_1_out;

  Multiplexer #(.select(1), .width(16), .disabled("Z"), .enable("true")) multiplexer_1 (
    .in0(Y), .in1(X), .out(MAX), .sel(or_1_out), .en(1'b1));
  Comparator #(.width(16), .mode("unsigned")) comparator_1 (
    .a(X), .b(Y), .gt(comparator_1_gt), .eq(comparator_1_eq));  // open: lt
  or or_1 (or_1_out, comparator_1_gt, comparator_1_eq);
  Multiplexer #(.select(1), .width(2), .disabled("Z"), .enable("false")) multiplexer_2 (
    .in0(Y_num), .in1(X_num), .out(MAX_num), .sel(or_1_out));

  // Notes on the sheet:
  //   电路功能：输出两个输入中的较大值，并输出较大值的2位编号
  //   Max2（归并比较）电路
endmodule

// Max3
module \Max3_归并比较_电路  (
  input  [15:0] Y,
  input  [15:0] X,
  input  [2:0] Y_num,
  input  [2:0] X_num,
  output [15:0] MAX,
  output [2:0] Max_num
);

  wire comparator_1_eq, comparator_1_gt, or_1_out;

  Multiplexer #(.select(1), .width(16), .disabled("Z"), .enable("false")) multiplexer_1 (
    .in0(Y), .in1(X), .out(MAX), .sel(or_1_out));
  Comparator #(.width(16), .mode("unsigned")) comparator_1 (
    .a(X), .b(Y), .gt(comparator_1_gt), .eq(comparator_1_eq));  // open: lt
  or or_1 (or_1_out, comparator_1_gt, comparator_1_eq);
  Multiplexer #(.select(1), .width(3), .disabled("Z"), .enable("false")) multiplexer_2 (
    .in0(Y_num), .in1(X_num), .out(Max_num), .sel(or_1_out));

  // Notes on the sheet:
  //   电路功能：输出两个输入中的较大值，并输出较大值的3位编号
  //   Max3（归并比较）电路
endmodule
