// Logisim project 8位扩展海明码传输测试实验.circ as structural Verilog: 4 circuits, main circuit 8位扩展海明码传输测试实验
module \_8位扩展海明码传输测试实验  (
  input  [7:0] \原始数据 
);

  wire CLK_out, comparator_1_eq, \n8位扩展海明码解码电路_1_out_2 , \n8位扩展海明码解码电路_1_out_3 , \n8位扩展海明码解码电路_1_out_4 ;
  wire [7:0] \n8位扩展海明码解码电路_1_纠错后数据 ;
  wire [12:0] \n8位扩展海明码编码电路_1_扩展海明码 , \n13位随机干扰电路_1_加扰后数据 , \n13位随机干扰电路_1_随机加扰屏蔽字 ;

  // Probe on \原始数据 
  // Probe on \n8位扩展海明码编码电路_1_扩展海明码 
  \_8位扩展海明码编码电路  \u_8位扩展海明码编码电路_1  (.\原始数据 (\原始数据 ), .\扩展海明码 (\n8位扩展海明码编码电路_1_扩展海明码 ));
  // Probe on \n13位随机干扰电路_1_随机加扰屏蔽字 
  Clock #(.highDuration(1), .lowDuration(1)) CLK (.out(CLK_out));
  \_13位随机干扰电路  \u_13位随机干扰电路_1  (
    .CLK(CLK_out), .\随机加扰屏蔽字 (\n13位随机干扰电路_1_随机加扰屏蔽字 ), .\加扰后数据 (\n13位随机干扰电路_1_加扰后数据 ),
    .\_13位输入 (\n8位扩展海明码编码电路_1_扩展海明码 ));
  // Probe on \n13位随机干扰电路_1_加扰后数据 
  LED #(.active("true")) \_2位错  (.in(\n8位扩展海明码解码电路_1_out_4 ));
  LED #(.active("true")) \_1位错  (.in(\n8位扩展海明码解码电路_1_out_3 ));
  LED #(.active("true")) \u_无错  (.in(\n8位扩展海明码解码电路_1_out_2 ));
  \_8位扩展海明码解码电路  \u_8位扩展海明码解码电路_1  (
    .out_3(\n8位扩展海明码解码电路_1_out_3 ), .out_4(\n8位扩展海明码解码电路_1_out_4 ), .out_2(\n8位扩展海明码解码电路_1_out_2 ),
    .\扩展海明码 (\n13位随机干扰电路_1_加扰后数据 ), .\纠错后数据 (\n8位扩展海明码解码电路_1_纠错后数据 ));
  // Probe on \n8位扩展海明码解码电路_1_纠错后数据 
  Comparator #(.width(8), .mode("twosComplement")) comparator_1 (
    .a(\原始数据 ), .b(\n8位扩展海明码解码电路_1_纠错后数据 ), .eq(comparator_1_eq));  // open: gt, lt
  LED #(.active("true")) \u_数据正确  (.in(comparator_1_eq));

  // Notes on the sheet:
  //   发送方
  //   1、无错：无错指示灯红色，数据正确指示灯红色，干扰屏蔽字=0，接收数据等于发送数据
  //   电路功能：测试扩展海明编解码电路的正确性。点击“CLK”按钮2次，观看4个指示灯，有以下4种情况：
  //   2、1位错：1位错指示灯红色，数据正确指示灯红色，干扰屏蔽字中有1个1，接收数据等于发送数据（可以纠正1位错）
  //   3、2位错：2位错指示灯红色，数据正确指示灯白色，干扰屏蔽字中有2个1，接收数据不等于发送数据（不能纠正2位错）
  //   4、2位错：2位错指示灯红色，数据正确指示灯红色，干扰屏蔽字中有2个1，接收数据等于发送数据（此时可以纠正错误）
  //   扩展海明码传输测试实验
  //   接收方
endmodule

// 海明编码
module \_8位扩展海明码编码电路  (
  input  [7:0] \原始数据 ,
  output [12:0] \扩展海明码 
);

  xor xor_1 (\扩展海明码 [0], \原始数据 [0], \原始数据 [1], \原始数据 [3], \原始数据 [4], \原始数据 [6]);
  xor xor_2 (\扩展海明码 [1], \原始数据 [0], \原始数据 [2], \原始数据 [3], \原始数据 [5], \原始数据 [6]);
  xor xor_3 (\扩展海明码 [3], \原始数据 [1], \原始数据 [2], \原始数据 [3], \原始数据 [7]);
  xor xor_4 (\扩展海明码 [7], \原始数据 [4], \原始数据 [5], \原始数据 [6], \原始数据 [7]);
  xor xor_5 (\扩展海明码 [12], \原始数据 [0], \原始数据 [1], \原始数据 [2], \原始数据 [3], \原始数据 [4], \原始数据 [5], \原始数据 [6], \原始数据 [7], \扩展海明码 [0], \扩展海明码 [1], \扩展海明码 [3], \扩展海明码 [7]);

  assign {\扩展海明码 [11:8], \扩展海明码 [6:4], \扩展海明码 [2]} = \原始数据 ;

  // Other names for the same wires on the sheet: P1 = \扩展海明码 [0]; P2 = \扩展海明码 [1]; D1 = \原始数据 [0]; P3 = \扩展海明码 [3];
  //   D2 = \原始数据 [1]; D3 = \原始数据 [2]; D4 = \原始数据 [3]; P4 = \扩展海明码 [7]; D5 = \原始数据 [4]; D6 = \原始数据 [5]; D7 = \原始数据 [6];
  //   D8 = \原始数据 [7]; P5 = \扩展海明码 [12]

  // Notes on the sheet:
  //   输入引脚区
  //   电路功能：扩展海明码编码电路
  //   输入：8位原始数据                 输出：13位海明码（8位数据位+4位校验位+1位总偶校验位）
  //   输出引脚区
  //   扩展海明码编码电路
  //   总偶校验位
endmodule

// 海明解码
module \_8位扩展海明码解码电路  (
  input  [12:0] \扩展海明码 ,
  output out_2,
  output out_3,
  output out_4,
  output [7:0] \纠错后数据 
);

  wire G, G1, G2, G3, G4, xor_1_out, xor_2_out, xor_3_out, xor_4_out, xor_9_out;
  wire [3:0] subtractor_1_out;
  wire [12:0] decoder_1_out0, xor_11_out;

  LED #(.active("true")) led_1 (.in(out_2));
  LED #(.active("true")) led_2 (.in(out_3));
  xor xor_1 (xor_1_out, \扩展海明码 [2], \扩展海明码 [4], \扩展海明码 [6], \扩展海明码 [8], \扩展海明码 [10]);
  xor xor_2 (xor_2_out, \扩展海明码 [2], \扩展海明码 [5], \扩展海明码 [6], \扩展海明码 [9], \扩展海明码 [10]);
  xor xor_3 (xor_3_out, \扩展海明码 [4], \扩展海明码 [5], \扩展海明码 [6], \扩展海明码 [11]);
  xor xor_4 (xor_4_out, \扩展海明码 [8], \扩展海明码 [9], \扩展海明码 [10], \扩展海明码 [11]);
  LED #(.active("true")) led_3 (.in(out_4));
  xor xor_5 (G1, xor_1_out, \扩展海明码 [0]);
  xor xor_6 (G2, xor_2_out, \扩展海明码 [1]);
  xor xor_7 (G3, xor_3_out, \扩展海明码 [3]);
  xor xor_8 (G4, xor_4_out, \扩展海明码 [7]);
  xor xor_9 (xor_9_out, \扩展海明码 [2], \扩展海明码 [4], \扩展海明码 [5], \扩展海明码 [6], \扩展海明码 [8], \扩展海明码 [9], \扩展海明码 [10], \扩展海明码 [11], \扩展海明码 [0], \扩展海明码 [1], \扩展海明码 [3], \扩展海明码 [7]);
  Subtractor #(.width(4)) subtractor_1 (.a({G4, G3, G2, G1}), .b(4'b0001), .out(subtractor_1_out));  // open: bin, bout
  or or_1 (G, G1, G2, G3, G4);
  Decoder #(.select(4), .tristate("false"), .disabled("Z"), .enable("false")) decoder_1 (
    .out0(decoder_1_out0[0]), .out1(decoder_1_out0[1]), .out2(decoder_1_out0[2]), .out3(decoder_1_out0[3]),
    .out4(decoder_1_out0[4]), .out5(decoder_1_out0[5]), .out6(decoder_1_out0[6]), .out7(decoder_1_out0[7]),
    .out8(decoder_1_out0[8]), .out9(decoder_1_out0[9]), .out10(decoder_1_out0[10]),
    .out11(decoder_1_out0[11]), .out12(decoder_1_out0[12]), .sel(subtractor_1_out));  // open: out13, out14, out15
  xor xor_10 (out_3, xor_9_out, \扩展海明码 [12]);
  assign {xor_11_out[12], \纠错后数据 [7:4], xor_11_out[7], \纠错后数据 [3:1], xor_11_out[3], \纠错后数据 [0], xor_11_out[1:0]} = decoder_1_out0 ^ \扩展海明码 ;  // XOR_Gate xor_11, 13 bits wide
  and and_1 (out_4, ~out_3, G);  // AND_Gate
  and and_2 (out_2, ~out_3, ~G);  // AND_Gate

  // Other names for the same wires on the sheet: _2位错 = out_4; _1位错 = out_3; G5 = out_3; P1 = \扩展海明码 [0];
  //   P2 = \扩展海明码 [1]; D1 = \扩展海明码 [2]; P3 = \扩展海明码 [3]; D2 = \扩展海明码 [4]; D3 = \扩展海明码 [5]; D4 = \扩展海明码 [6];
  //   P4 = \扩展海明码 [7]; D5 = \扩展海明码 [8]; D6 = \扩展海明码 [9]; D7 = \扩展海明码 [10]; D8 = \扩展海明码 [11]; P5 = \扩展海明码 [12];
  //   无错误 = out_2

  // Notes on the sheet:
  //   输入引脚区
  //   输出引脚区
  //   总偶校验位
  //   输入：扩展海明码（13位）
  //   总偶检错位
  //   G1G2G3G4=0
  //   纠错逻辑：检错码-1，译码后，与扩展海明码异或
  //   电路功能：8位海明码的数据解码，能判断无错误、1位错、2位错，1位错能自动纠错
  //   输出：错误模式（无错误、1位错、2位错），纠错后的数据（8位）
  //   提取数据位
  //   海明码解码电路
endmodule

// 随机干扰
module \_13位随机干扰电路  (
  input  CLK,
  input  [12:0] \_13位输入 ,
  output [12:0] \随机加扰屏蔽字 ,
  output [12:0] \加扰后数据 
);

  wire comparator_1_eq, not_1_out, pull_resistor_1_node, \随机信号_5_out ;
  wire [1:0] pull_resistor_2_node, \随机信号_4_out ;
  wire [3:0] \随机信号_2_out , \随机信号_3_out , \随机信号_out ;
  wire [15:0] \_1位加扰A , decoder_3_out0;
  wire [21:0] \_1位加扰 , \_2位加扰 , \_3位加扰 , multiplexer_1_out, multiplexer_2_out, multiplexer_4_out;
  wire [21:6] \_1位加扰B ;
  wire [21:13] multiplexer_3_out;

  Random #(.width(4), .seed(0), .trigger("rising")) \u_随机信号  (.clk(CLK), .out(\随机信号_out ));  // open: next, clr
  Decoder #(.select(4), .tristate("false"), .disabled("Z"), .enable("false")) decoder_1 (
    .out0(\_1位加扰A [0]), .out1(\_1位加扰A [1]), .out2(\_1位加扰A [2]), .out3(\_1位加扰A [3]), .out4(\_1位加扰A [4]),
    .out5(\_1位加扰A [5]), .out6(\_1位加扰A [6]), .out7(\_1位加扰A [7]), .out8(\_1位加扰A [8]), .out9(\_1位加扰A [9]),
    .out10(\_1位加扰A [10]), .out11(\_1位加扰A [11]), .out12(\_1位加扰A [12]), .out13(\_1位加扰A [13]),
    .out14(\_1位加扰A [14]), .out15(\_1位加扰A [15]), .sel(\随机信号_out ));
  Decoder #(.select(4), .tristate("false"), .disabled("Z"), .enable("false")) decoder_2 (
    .out0(\_1位加扰B [6]), .out1(\_1位加扰B [7]), .out2(\_1位加扰B [8]), .out3(\_1位加扰B [9]), .out4(\_1位加扰B [10]),
    .out5(\_1位加扰B [11]), .out6(\_1位加扰B [12]), .out7(\_1位加扰B [13]), .out8(\_1位加扰B [14]), .out9(\_1位加扰B [15]),
    .out10(\_1位加扰B [16]), .out11(\_1位加扰B [17]), .out12(\_1位加扰B [18]), .out13(\_1位加扰B [19]),
    .out14(\_1位加扰B [20]), .out15(\_1位加扰B [21]), .sel(\随机信号_2_out ));
  Random #(.width(4), .seed(18), .trigger("rising")) \u_随机信号_2  (.clk(CLK), .out(\随机信号_2_out ));  // open: next, clr
  Decoder #(.select(4), .tristate("false"), .disabled("Z"), .enable("false")) decoder_3 (
    .out0(decoder_3_out0[0]), .out1(decoder_3_out0[1]), .out2(decoder_3_out0[2]), .out3(decoder_3_out0[3]),
    .out4(decoder_3_out0[4]), .out5(decoder_3_out0[5]), .out6(decoder_3_out0[6]), .out7(decoder_3_out0[7]),
    .out8(decoder_3_out0[8]), .out9(decoder_3_out0[9]), .out10(decoder_3_out0[10]),
    .out11(decoder_3_out0[11]), .out12(decoder_3_out0[12]), .out13(decoder_3_out0[13]),
    .out14(decoder_3_out0[14]), .out15(decoder_3_out0[15]), .sel(\随机信号_3_out ));
  Random #(.width(4), .seed(3), .trigger("rising")) \u_随机信号_3  (.clk(CLK), .out(\随机信号_3_out ));  // open: next, clr
  Random #(.width(2), .seed(21), .trigger("rising")) \u_随机信号_4  (.clk(CLK), .out(\随机信号_4_out ));  // open: next, clr
  Random #(.width(1), .seed(31), .trigger("rising")) \u_随机信号_5  (.clk(CLK), .out(\随机信号_5_out ));  // open: next, clr
  Pull_Resistor #(.pull(0)) pull_resistor_1 (.node(pull_resistor_1_node));
  Multiplexer #(.select(1), .width(22), .disabled("Z"), .enable("false")) multiplexer_1 (
    .in0({\_1位加扰B , {6{1'b0}}}), .in1(\_3位加扰 ), .out(multiplexer_1_out), .sel(pull_resistor_1_node));
  Pull_Resistor #(.pull(1)) pull_resistor_2 (.node(pull_resistor_2_node));
  Multiplexer #(.select(2), .width(22), .disabled("Z"), .enable("false")) multiplexer_2 (
    .in0({22{1'b0}}), .in1({{6{1'b0}}, \_1位加扰A }), .in2(\_2位加扰 ), .in3(multiplexer_1_out),
    .out(multiplexer_2_out), .sel(\随机信号_4_out ));
  Multiplexer #(.select(2), .width(22), .disabled("Z"), .enable("false")) multiplexer_3 (
    .in0({22{1'b0}}), .in1(\_1位加扰 ), .in2(\_2位加扰 ), .in3(multiplexer_2_out),
    .out({multiplexer_3_out, \随机加扰屏蔽字 }), .sel(pull_resistor_2_node));
  Comparator #(.width(22), .mode("unsigned")) comparator_1 (
    .a({{6{1'b0}}, \_1位加扰A }), .b({\_1位加扰B , {6{1'b0}}}), .eq(comparator_1_eq));  // open: gt, lt
  not not_1 (not_1_out, comparator_1_eq);
  Multiplexer #(.select(1), .width(22), .disabled("Z"), .enable("false")) multiplexer_4 (
    .in0(22'h1), .in1({{6{1'b0}}, \_1位加扰A }), .out(multiplexer_4_out), .sel(not_1_out));
  assign \_2位加扰  = multiplexer_4_out ^ {\_1位加扰B , {6{1'b0}}};  // XOR_Gate xor_1, 22 bits wide
  assign \_3位加扰  = \_2位加扰  ^ {decoder_3_out0, {6{1'b0}}};  // XOR_Gate xor_2, 22 bits wide
  Multiplexer #(.select(1), .width(22), .disabled("Z"), .enable("false")) multiplexer_5 (
    .in0(multiplexer_4_out), .in1({\_1位加扰B , {6{1'b0}}}), .out(\_1位加扰 ), .sel(\随机信号_5_out ));
  assign \加扰后数据  = \随机加扰屏蔽字  ^ \_13位输入 ;  // XOR_Gate xor_3, 13 bits wide
  // also tied to GND on the sheet: pull_resistor_1_node
  // also tied to VCC on the sheet: {pull_resistor_2_node[0], pull_resistor_2_node[1]}

  // Notes on the sheet:
  //   随机干扰电路
endmodule
