// Logisim project 循环冗余校验码（串行）实验2.circ as structural Verilog: 5 circuits, main circuit CRC串行编码电路2
module \CRC串行编解码测试实验2  (
  input  [3:0] \原始数据 ,
  input  [6:0] \干扰项 ,
  output [3:0] \接收数据 
);

  wire comparator_1_eq, \crc串行编码电路2_封装用_1_out_7 , \crc串行解码电路2_封装用_1_out_8 , \复位1_out , \复位2_out , \时钟1_out ,
       \时钟2_out , \装入1_out , \装入2_out ;
  wire [2:0] \crc串行编码电路2_封装用_1_余数 , \crc串行解码电路2_封装用_1_余数 ;
  wire [6:0] \crc串行编码电路2_封装用_1_crc码 , \crc串行解码电路2_封装用_1_纠正后的crc码 , xor_1_out;

  // Probe on \crc串行编码电路2_封装用_1_余数 
  Button \u_复位1  (.out(\复位1_out ));
  LED #(.active("true")) \u_余数生成1  (.in(\crc串行编码电路2_封装用_1_out_7 ));
  \CRC串行编码电路2_封装用  \crc串行编码电路2_封装用_1  (
    .\原始数据 (\原始数据 ), .out_7(\crc串行编码电路2_封装用_1_out_7 ), .\复位 (\复位1_out ), .\装入 (\装入1_out ), .\时钟 (\时钟1_out ),
    .\CRC码 (\crc串行编码电路2_封装用_1_crc码 ), .\余数 (\crc串行编码电路2_封装用_1_余数 ));
  Button \u_时钟1  (.out(\时钟1_out ));
  Button \u_装入1  (.out(\装入1_out ));
  // Probe on \crc串行编码电路2_封装用_1_crc码 
  assign xor_1_out = \crc串行编码电路2_封装用_1_crc码  ^ \干扰项 ;  // XOR_Gate xor_1, 7 bits wide
  // Probe on xor_1_out
  // Probe on \crc串行解码电路2_封装用_1_余数 
  LED #(.active("true")) \u_余数生成2  (.in(\crc串行解码电路2_封装用_1_out_8 ));
  \CRC串行解码电路2_封装用  \crc串行解码电路2_封装用_1  (
    .\CRC码 (xor_1_out), .\复位 (\复位2_out ), .\装入 (\装入2_out ), .\时钟 (\时钟2_out ), .\余数 (\crc串行解码电路2_封装用_1_余数 ),
    .\纠正后的CRC码 (\crc串行解码电路2_封装用_1_纠正后的crc码 ), .out_8(\crc串行解码电路2_封装用_1_out_8 ), .\纠错后的数据 (\接收数据 ));
  Button \u_装入2  (.out(\装入2_out ));
  Button \u_时钟2  (.out(\时钟2_out ));
  Button \u_复位2  (.out(\复位2_out ));
  // Probe on \crc串行解码电路2_封装用_1_纠正后的crc码 
  LED #(.active("true")) \u_数据正确  (.in(comparator_1_eq));
  Comparator #(.width(4), .mode("twosComplement")) comparator_1 (
    .a(\原始数据 ), .b(\接收数据 ), .eq(comparator_1_eq));  // open: gt, lt

  // Notes on the sheet:
  //   第二步：设置干扰项（只设置1个1）
  //   第五步：重复第二步（设置2个1）、第三步，此时“数据正确”指示灯不亮（接收数据不等于原始数据，无法纠正2位错）
  //   第一步：首先设置4位原始数据，然后按“复位1”按钮，再按“装入1”按钮，再按“时钟1”按钮多次，直到“余数生成1”指示灯变红色
  //   第三步：按“复位2”按钮，再按“装入2”按钮，再按“时钟2”按钮多次，直到“余数生成2”指示灯变红色；此时“数据正确”指示灯应为红色（可以纠正1位错）
  //   电路功能：测试CRC串行编码、解码电路的功能                       输入：4位原始数据、7位干扰项                      输出：4位接收数据（纠错后的数据）         数据正确指示灯
  //   第四步：重复第二步（设置另外位置的1，仍然为1个1）、第三步，直到干扰项的7个位置都测试过，7种情况下“数据正确”指示灯都是红色（可以纠正1位错）
  //   CRC串行编解码测试实验2
endmodule

module \CRC串行编码电路2  (
  input  [3:0] \原始数据 ,
  output [6:0] \CRC码 ,
  output [2:0] \余数 
);

  wire and_1_out, comparator_2_eq, \D触发器_3_q , \D触发器_q , LED, multiplexer_1_out, multiplexer_2_out,
       not_1_out, not_2_out, or_1_out, shift_register_1_out, \复位_out , \时钟_out , \装入_out , \计数器_2_q ;
  wire [2:0] \计数器_q ;

  Button \u_复位  (.out(\复位_out ));
  Button \u_装入  (.out(\装入_out ));
  Button \u_时钟  (.out(\时钟_out ));
  and and_1 (and_1_out, \装入_out , multiplexer_2_out);
  or or_1 (or_1_out, and_1_out, \时钟_out );
  Shift_Register #(.width(1), .length(4), .parallel("true"), .trigger("rising")) shift_register_1 (
    .in(1'b0), .clk(or_1_out), .out(shift_register_1_out), .load(multiplexer_2_out), .clr(\复位_out ),
    .d0(\原始数据 [0]), .d1(\原始数据 [1]), .d2(\原始数据 [2]), .d3(\原始数据 [3]));  // open: shift, q0, q1, q2, q3
  Counter #(.width(3), .max('h7), .ongoal("wrap"), .trigger("rising"), .behavior("old")) \u_计数器  (
    .count(multiplexer_1_out), .Q(\计数器_q ), .clk(or_1_out), .clr(multiplexer_2_out));  // open: load, D, carry, preset
  xor xor_1 (\CRC码 [0], \D触发器_3_q , shift_register_1_out);
  not not_1 (not_1_out, LED);
  Comparator #(.width(3), .mode("unsigned")) comparator_1 (.a(\计数器_q ), .b(3'b110), .eq(LED));  // open: gt, lt
  Counter #(.width(1), .max('h1), .ongoal("wrap"), .trigger("rising"), .behavior("old")) \u_计数器_2  (
    .count(multiplexer_2_out), .Q(\计数器_2_q ), .clk(and_1_out), .clr(\复位_out ));  // open: load, D, carry, preset
  D_Flip_Flop #(.trigger("rising"), .Pre_Clr_Positions("LEGACY"), .NegatePresetClear("false"), .enable("true"), .NewFFLayout("false")) \D触发器  (
    .clk(or_1_out), .D(\CRC码 [0]), .Q(\D触发器_q ), .en(multiplexer_1_out), .reset(\复位_out ));  // open: Qn, preset
  Multiplexer #(.select(1), .width(1), .disabled("Z"), .enable("false")) multiplexer_1 (
    .in0(1'b1), .in1(not_1_out), .out(multiplexer_1_out), .sel(1'b1));
  Comparator #(.width(1), .mode("unsigned")) comparator_2 (
    .a(\计数器_2_q ), .b(1'b1), .eq(comparator_2_eq));  // open: gt, lt
  LED #(.active("true")) \u_余数生成指示灯  (.in(LED));
  Multiplexer #(.select(1), .width(1), .disabled("Z"), .enable("false")) multiplexer_2 (
    .in0(1'b1), .in1(not_2_out), .out(multiplexer_2_out), .sel(1'b1));
  not not_2 (not_2_out, comparator_2_eq);
  xor xor_2 (\CRC码 [1], \D触发器_3_q , \D触发器_q );
  D_Flip_Flop #(.trigger("rising"), .Pre_Clr_Positions("LEGACY"), .NegatePresetClear("false"), .enable("true"), .NewFFLayout("false")) \D触发器_2  (
    .clk(or_1_out), .D(\CRC码 [1]), .Q(\CRC码 [2]), .en(multiplexer_1_out), .reset(\复位_out ));  // open: Qn, preset
  D_Flip_Flop #(.trigger("rising"), .Pre_Clr_Positions("LEGACY"), .NegatePresetClear("false"), .enable("true"), .NewFFLayout("false")) \D触发器_3  (
    .clk(or_1_out), .D(\CRC码 [2]), .Q(\D触发器_3_q ), .en(multiplexer_1_out), .reset(\复位_out ));  // open: Qn, preset

  assign \CRC码 [6:3] = \原始数据 ;
  assign \余数  = \CRC码 [2:0];

  // Other names for the same wires on the sheet: R0 = \CRC码 [0]; R1 = \CRC码 [1]; R2 = \CRC码 [2]; C0 = \原始数据 [0];
  //   C1 = \原始数据 [1]; C2 = \原始数据 [2]; C3 = \原始数据 [3]

  // Notes on the sheet:
  //   移位寄存器
  //   0
  //   1*
  //   x
  //   比较器
  //   比较器
  //   1*
  //   1
  //   x
  //   第二步：按“复位”按钮
  //   第三步：按“装入”按钮
  //   第一步：置左上角的原始数据（例如：1100）
  //   生成的余数=010
  //   2
  //   0*
  //   x
  //   CRC串行编码电路2（生成多项式=1011）
  //   原始数据=4位；余数=3位；CRC码=原始数据4位+余数3位
  //   第四步：按“时钟”按钮多次，直到“余数生成指示灯”变红
  //   生成的CRC码在右上角（1100010）
  //   3
  //   1*
  //   x
endmodule

module \CRC串行解码电路2  (
  input  [6:0] \CRC码 ,
  output [2:0] \余数 ,
  output [6:0] \纠正后的CRC码 
);

  wire and_1_out, and_2_out, and_3_out, and_4_out, and_5_out, and_6_out, and_7_out, and_8_out, and_9_out,
       CLK, CLR, comparator_1_eq, comparator_2_eq, comparator_3_eq, comparator_4_eq, comparator_5_eq,
       comparator_6_eq, comparator_7_eq, comparator_8_eq, comparator_9_eq, comparator_11_eq, \D触发器_3_q ,
       \D触发器_q , LED, multiplexer_1_out, multiplexer_2_out, not_1_out, not_2_out, not_3_out, or_1_out, R0,
       R1, R2, shift_register_1_out, Stop, \装入_out , \计数器_2_q ;
  wire [2:0] \计数器_q ;
  wire [3:0] \计数器_3_q ;

  Comparator #(.width(3), .mode("unsigned")) comparator_1 (.a(\余数 ), .b(3'b000), .eq(comparator_1_eq));  // open: gt, lt
  Button \u_复位  (.out(CLR));
  Button \u_装入  (.out(\装入_out ));
  Button \u_时钟  (.out(CLK));
  and and_1 (and_1_out, LED, comparator_1_eq);
  LED #(.active("true")) \u_无错  (.in(and_1_out));
  and and_2 (and_2_out, \装入_out , multiplexer_2_out);
  Comparator #(.width(3), .mode("unsigned")) comparator_2 (.a(\余数 ), .b(3'b101), .eq(comparator_2_eq));  // open: gt, lt
  or or_1 (or_1_out, and_2_out, CLK);
  and and_3 (and_3_out, LED, comparator_2_eq);
  LED #(.active("true")) \u_第7位错  (.in(and_3_out));
  xor xor_1 (\纠正后的CRC码 [6], comparator_2_eq, \CRC码 [6]);
  and and_4 (and_4_out, LED, comparator_3_eq);
  LED #(.active("true")) \u_第6位错  (.in(and_4_out));
  Comparator #(.width(3), .mode("unsigned")) comparator_3 (.a(\余数 ), .b(3'b111), .eq(comparator_3_eq));  // open: gt, lt
  Shift_Register #(.width(1), .length(7), .parallel("true"), .trigger("rising")) shift_register_1 (
    .in(1'b0), .clk(or_1_out), .out(shift_register_1_out), .load(multiplexer_2_out), .clr(CLR),
    .d0(\CRC码 [0]), .d1(\CRC码 [1]), .d2(\CRC码 [2]), .d3(\CRC码 [3]), .d4(\CRC码 [4]), .d5(\CRC码 [5]),
    .d6(\CRC码 [6]));  // open: shift, q0, q1, q2, q3, q4, q5, q6
  Counter #(.width(3), .max('h7), .ongoal("wrap"), .trigger("rising"), .behavior("old")) \u_计数器  (
    .count(multiplexer_1_out), .Q(\计数器_q ), .clk(or_1_out), .clr(multiplexer_2_out));  // open: load, D, carry, preset
  Comparator #(.width(3), .mode("unsigned")) comparator_4 (.a(\余数 ), .b(3'b110), .eq(comparator_4_eq));  // open: gt, lt
  xor xor_2 (\纠正后的CRC码 [5], comparator_3_eq, \CRC码 [5]);
  xor xor_3 (R0, \D触发器_3_q , shift_register_1_out);
  Comparator #(.width(3), .mode("unsigned")) comparator_5 (
    .a(\计数器_q ), .b(3'b110), .eq(comparator_5_eq));  // open: gt, lt
  Counter #(.width(1), .max('h1), .ongoal("wrap"), .trigger("rising"), .behavior("old")) \u_计数器_2  (
    .count(multiplexer_2_out), .Q(\计数器_2_q ), .clk(and_2_out), .clr(CLR));  // open: load, D, carry, preset
  and and_5 (and_5_out, LED, comparator_4_eq);
  LED #(.active("true")) \u_第5位错  (.in(and_5_out));
  xor xor_4 (\纠正后的CRC码 [4], comparator_4_eq, \CRC码 [4]);
  Register #(.width(3), .trigger("rising"), .Select("low")) \u_寄存器  (
    .D({R2, R1, R0}), .en(Stop), .Q(\余数 ), .clk(CLK), .clr(CLR));
  Multiplexer #(.select(1), .width(1), .disabled("Z"), .enable("false")) multiplexer_1 (
    .in0(1'b1), .in1(not_1_out), .out(multiplexer_1_out), .sel(1'b1));
  not not_1 (not_1_out, comparator_5_eq);
  Comparator #(.width(1), .mode("unsigned")) comparator_6 (
    .a(\计数器_2_q ), .b(1'b1), .eq(comparator_6_eq));  // open: gt, lt
  Comparator #(.width(3), .mode("unsigned")) comparator_7 (.a(\余数 ), .b(3'b011), .eq(comparator_7_eq));  // open: gt, lt
  D_Flip_Flop #(.trigger("rising"), .Pre_Clr_Positions("LEGACY"), .NegatePresetClear("false"), .enable("true"), .NewFFLayout("false")) \D触发器  (
    .clk(or_1_out), .D(R0), .Q(\D触发器_q ), .en(multiplexer_1_out), .reset(CLR));  // open: Qn, preset
  Multiplexer #(.select(1), .width(1), .disabled("Z"), .enable("false")) multiplexer_2 (
    .in0(1'b1), .in1(not_2_out), .out(multiplexer_2_out), .sel(1'b1));
  not not_2 (not_2_out, comparator_6_eq);
  and and_6 (and_6_out, LED, comparator_7_eq);
  LED #(.active("true")) \u_第4位错  (.in(and_6_out));
  xor xor_5 (\纠正后的CRC码 [3], comparator_7_eq, \CRC码 [3]);
  Comparator #(.width(3), .mode("unsigned")) comparator_8 (.a(\余数 ), .b(3'b100), .eq(comparator_8_eq));  // open: gt, lt
  LED #(.active("true")) \u_余数生成指示灯  (.in(LED));
  xor xor_6 (R1, \D触发器_3_q , \D触发器_q );
  and and_7 (and_7_out, LED, comparator_8_eq);
  LED #(.active("true")) \u_第3位错  (.in(and_7_out));
  xor xor_7 (\纠正后的CRC码 [2], comparator_8_eq, \CRC码 [2]);
  Counter #(.width(4), .max('hf), .ongoal("wrap"), .trigger("rising"), .behavior("old")) \u_计数器_3  (
    .count(Stop), .Q(\计数器_3_q ), .clk(or_1_out), .clr(CLR));  // open: load, D, carry, preset
  and and_8 (and_8_out, LED, comparator_9_eq);
  Comparator #(.width(3), .mode("unsigned")) comparator_9 (.a(\余数 ), .b(3'b010), .eq(comparator_9_eq));  // open: gt, lt
  D_Flip_Flop #(.trigger("rising"), .Pre_Clr_Positions("LEGACY"), .NegatePresetClear("false"), .enable("true"), .NewFFLayout("false")) \D触发器_2  (
    .clk(or_1_out), .D(R1), .Q(R2), .en(multiplexer_1_out), .reset(CLR));  // open: Qn, preset
  not not_3 (not_3_out, LED);
  Comparator #(.width(4), .mode("unsigned")) comparator_10 (.a(\计数器_3_q ), .b(4'b1000), .eq(LED));  // open: gt, lt
  LED #(.active("true")) \u_第2位错  (.in(and_8_out));
  xor xor_8 (\纠正后的CRC码 [1], comparator_9_eq, \CRC码 [1]);
  Multiplexer #(.select(1), .width(1), .disabled("Z"), .enable("false")) multiplexer_3 (
    .in0(1'b1), .in1(not_3_out), .out(Stop), .sel(1'b1));
  and and_9 (and_9_out, LED, comparator_11_eq);
  LED #(.active("true")) \u_第1位错  (.in(and_9_out));
  Comparator #(.width(3), .mode("unsigned")) comparator_11 (
    .a(\余数 ), .b(3'b001), .eq(comparator_11_eq));  // open: gt, lt
  D_Flip_Flop #(.trigger("rising"), .Pre_Clr_Positions("LEGACY"), .NegatePresetClear("false"), .enable("true"), .NewFFLayout("false")) \D触发器_3  (
    .clk(or_1_out), .D(R2), .Q(\D触发器_3_q ), .en(multiplexer_1_out), .reset(CLR));  // open: Qn, preset
  xor xor_9 (\纠正后的CRC码 [0], comparator_11_eq, \CRC码 [0]);

  // Other names for the same wires on the sheet: C0 = \CRC码 [0]; C1 = \CRC码 [1]; C2 = \CRC码 [2]; C3 = \CRC码 [3];
  //   C4 = \CRC码 [4]; C5 = \CRC码 [5]; C6 = \CRC码 [6]; R[2:0] = \余数 ; C0_prime = \纠正后的CRC码 [0];
  //   C1_prime = \纠正后的CRC码 [1]; C2_prime = \纠正后的CRC码 [2]; C3_prime = \纠正后的CRC码 [3]; C4_prime = \纠正后的CRC码 [4];
  //   C5_prime = \纠正后的CRC码 [5]; C6_prime = \纠正后的CRC码 [6]

  // Notes on the sheet:
  //   第二步：按“复位”按钮
  //   第三步：按“装入”按钮
  //   第一步：置左上角的CRC码（如：1100010）
  //   第四步：按“时钟”按钮多次，直到“余数生成指示灯”变红
  //   第五步：置有一位错的CRC码（如：0100010）
  //   重复第二、三、四步
  //   此时，余数=101，下面的“第7位错”指示灯变红
  //   纠正后的CRC码见右上角
  //   此时，余数=000，下面的“无错”指示灯变红，表示无错
  //   比较器
  //   比较器
  //   比较器
  //   移位寄存器
  //   比较器
  //   0
  //   x
  //   1*
  //   比较器
  //   比较器
  //   比较器
  //   比较器
  //   1
  //   x
  //   1*
  //   比较器
  //   比较器
  //   2
  //   0*
  //   x
  //   CRC串行解码电路2（生成多项式=1011）
  //   原始数据=4位；余数=3位；CRC码=原始数据4位+余数3位
  //   比较器
  //   3
  //   x
  //   1*
endmodule

// CRC编码
module \CRC串行编码电路2_封装用  (
  input  [3:0] \原始数据 ,
  input  \复位 ,
  input  \装入 ,
  input  \时钟 ,
  output [6:0] \CRC码 ,
  output [2:0] \余数 ,
  output out_7
);

  wire and_1_out, comparator_2_eq, \D触发器_3_q , \D触发器_q , multiplexer_1_out, multiplexer_2_out, not_1_out,
       not_2_out, or_1_out, shift_register_1_out, \计数器_2_q ;
  wire [2:0] \计数器_q ;

  and and_1 (and_1_out, \装入 , multiplexer_2_out);
  or or_1 (or_1_out, and_1_out, \时钟 );
  Shift_Register #(.width(1), .length(4), .parallel("true"), .trigger("rising")) shift_register_1 (
    .in(1'b0), .clk(or_1_out), .out(shift_register_1_out), .load(multiplexer_2_out), .clr(\复位 ),
    .d0(\原始数据 [0]), .d1(\原始数据 [1]), .d2(\原始数据 [2]), .d3(\原始数据 [3]));  // open: shift, q0, q1, q2, q3
  Counter #(.width(3), .max('h7), .ongoal("wrap"), .trigger("rising"), .behavior("old")) \u_计数器  (
    .count(multiplexer_1_out), .Q(\计数器_q ), .clk(or_1_out), .clr(multiplexer_2_out));  // open: load, D, carry, preset
  xor xor_1 (\CRC码 [0], \D触发器_3_q , shift_register_1_out);
  Comparator #(.width(3), .mode("unsigned")) comparator_1 (.a(\计数器_q ), .b(3'b110), .eq(out_7));  // open: gt, lt
  not not_1 (not_1_out, out_7);
  Counter #(.width(1), .max('h1), .ongoal("wrap"), .trigger("rising"), .behavior("old")) \u_计数器_2  (
    .count(multiplexer_2_out), .Q(\计数器_2_q ), .clk(and_1_out), .clr(\复位 ));  // open: load, D, carry, preset
  D_Flip_Flop #(.trigger("rising"), .Pre_Clr_Positions("LEGACY"), .NegatePresetClear("false"), .enable("true"), .NewFFLayout("false")) \D触发器  (
    .clk(or_1_out), .D(\CRC码 [0]), .Q(\D触发器_q ), .en(multiplexer_1_out), .reset(\复位 ));  // open: Qn, preset
  Multiplexer #(.select(1), .width(1), .disabled("Z"), .enable("false")) multiplexer_1 (
    .in0(1'b1), .in1(not_1_out), .out(multiplexer_1_out), .sel(1'b1));
  Comparator #(.width(1), .mode("unsigned")) comparator_2 (
    .a(\计数器_2_q ), .b(1'b1), .eq(comparator_2_eq));  // open: gt, lt
  LED #(.active("true")) \u_余数生成指示灯  (.in(out_7));
  Multiplexer #(.select(1), .width(1), .disabled("Z"), .enable("false")) multiplexer_2 (
    .in0(1'b1), .in1(not_2_out), .out(multiplexer_2_out), .sel(1'b1));
  not not_2 (not_2_out, comparator_2_eq);
  xor xor_2 (\CRC码 [1], \D触发器_3_q , \D触发器_q );
  D_Flip_Flop #(.trigger("rising"), .Pre_Clr_Positions("LEGACY"), .NegatePresetClear("false"), .enable("true"), .NewFFLayout("false")) \D触发器_2  (
    .clk(or_1_out), .D(\CRC码 [1]), .Q(\CRC码 [2]), .en(multiplexer_1_out), .reset(\复位 ));  // open: Qn, preset
  D_Flip_Flop #(.trigger("rising"), .Pre_Clr_Positions("LEGACY"), .NegatePresetClear("false"), .enable("true"), .NewFFLayout("false")) \D触发器_3  (
    .clk(or_1_out), .D(\CRC码 [2]), .Q(\D触发器_3_q ), .en(multiplexer_1_out), .reset(\复位 ));  // open: Qn, preset

  assign \CRC码 [6:3] = \原始数据 ;
  assign \余数  = \CRC码 [2:0];

  // Other names for the same wires on the sheet: R0 = \CRC码 [0]; R1 = \CRC码 [1]; R2 = \CRC码 [2]; C0 = \原始数据 [0];
  //   C1 = \原始数据 [1]; C2 = \原始数据 [2]; C3 = \原始数据 [3]; LED = out_7

  // Notes on the sheet:
  //   移位寄存器
  //   0
  //   1*
  //   x
  //   比较器
  //   比较器
  //   1*
  //   1
  //   x
  //   第二步：按“复位”按钮
  //   第三步：按“装入”按钮
  //   第一步：置左上角的原始数据（例如：1100）
  //   生成的余数=010
  //   2
  //   x
  //   0*
  //   CRC串行编码电路2（生成多项式=1011）
  //   原始数据=4位；余数=3位；CRC码=原始数据4位+余数3位
  //   第四步：按“时钟”按钮多次，直到“余数生成指示灯”变红
  //   生成的CRC码在右上角（1100010）
  //   3
  //   1*
  //   x
endmodule

// CRC解码
module \CRC串行解码电路2_封装用  (
  input  [6:0] \CRC码 ,
  input  \复位 ,
  input  \装入 ,
  input  \时钟 ,
  output [3:0] \纠错后的数据 ,
  output [2:0] \余数 ,
  output [6:0] \纠正后的CRC码 ,
  output out_8
);

  wire and_1_out, and_2_out, and_3_out, and_4_out, and_5_out, and_6_out, and_7_out, and_8_out, and_9_out,
       comparator_1_eq, comparator_2_eq, comparator_3_eq, comparator_4_eq, comparator_5_eq, comparator_6_eq,
       comparator_7_eq, comparator_8_eq, comparator_9_eq, comparator_11_eq, \D触发器_3_q , \D触发器_q ,
       multiplexer_1_out, multiplexer_2_out, not_1_out, not_2_out, not_3_out, or_1_out, R0, R1, R2,
       shift_register_1_out, Stop, \计数器_2_q ;
  wire [2:0] \计数器_q ;
  wire [3:0] \计数器_3_q ;

  Comparator #(.width(3), .mode("unsigned")) comparator_1 (.a(\余数 ), .b(3'b000), .eq(comparator_1_eq));  // open: gt, lt
  and and_1 (and_1_out, out_8, comparator_1_eq);
  LED #(.active("true")) \u_无错  (.in(and_1_out));
  and and_2 (and_2_out, \装入 , multiplexer_2_out);
  Comparator #(.width(3), .mode("unsigned")) comparator_2 (.a(\余数 ), .b(3'b101), .eq(comparator_2_eq));  // open: gt, lt
  or or_1 (or_1_out, and_2_out, \时钟 );
  and and_3 (and_3_out, out_8, comparator_2_eq);
  LED #(.active("true")) \u_第7位错  (.in(and_3_out));
  xor xor_1 (\纠正后的CRC码 [6], comparator_2_eq, \CRC码 [6]);
  and and_4 (and_4_out, out_8, comparator_3_eq);
  LED #(.active("true")) \u_第6位错  (.in(and_4_out));
  Comparator #(.width(3), .mode("unsigned")) comparator_3 (.a(\余数 ), .b(3'b111), .eq(comparator_3_eq));  // open: gt, lt
  Shift_Register #(.width(1), .length(7), .parallel("true"), .trigger("rising")) shift_register_1 (
    .in(1'b0), .clk(or_1_out), .out(shift_register_1_out), .load(multiplexer_2_out), .clr(\复位 ),
    .d0(\CRC码 [0]), .d1(\CRC码 [1]), .d2(\CRC码 [2]), .d3(\CRC码 [3]), .d4(\CRC码 [4]), .d5(\CRC码 [5]),
    .d6(\CRC码 [6]));  // open: shift, q0, q1, q2, q3, q4, q5, q6
  Counter #(.width(3), .max('h7), .ongoal("wrap"), .trigger("rising"), .behavior("old")) \u_计数器  (
    .count(multiplexer_1_out), .Q(\计数器_q ), .clk(or_1_out), .clr(multiplexer_2_out));  // open: load, D, carry, preset
  Comparator #(.width(3), .mode("unsigned")) comparator_4 (.a(\余数 ), .b(3'b110), .eq(comparator_4_eq));  // open: gt, lt
  xor xor_2 (\纠正后的CRC码 [5], comparator_3_eq, \CRC码 [5]);
  xor xor_3 (R0, \D触发器_3_q , shift_register_1_out);
  Comparator #(.width(3), .mode("unsigned")) comparator_5 (
    .a(\计数器_q ), .b(3'b110), .eq(comparator_5_eq));  // open: gt, lt
  Counter #(.width(1), .max('h1), .ongoal("wrap"), .trigger("rising"), .behavior("old")) \u_计数器_2  (
    .count(multiplexer_2_out), .Q(\计数器_2_q ), .clk(and_2_out), .clr(\复位 ));  // open: load, D, carry, preset
  and and_5 (and_5_out, out_8, comparator_4_eq);
  LED #(.active("true")) \u_第5位错  (.in(and_5_out));
  xor xor_4 (\纠正后的CRC码 [4], comparator_4_eq, \CRC码 [4]);
  Register #(.width(3), .trigger("rising"), .Select("low")) \u_寄存器  (
    .D({R2, R1, R0}), .en(Stop), .Q(\余数 ), .clk(\时钟 ), .clr(\复位 ));
  Multiplexer #(.select(1), .width(1), .disabled("Z"), .enable("false")) multiplexer_1 (
    .in0(1'b1), .in1(not_1_out), .out(multiplexer_1_out), .sel(1'b1));
  not not_1 (not_1_out, comparator_5_eq);
  Comparator #(.width(1), .mode("unsigned")) comparator_6 (
    .a(\计数器_2_q ), .b(1'b1), .eq(comparator_6_eq));  // open: gt, lt
  Comparator #(.width(3), .mode("unsigned")) comparator_7 (.a(\余数 ), .b(3'b011), .eq(comparator_7_eq));  // open: gt, lt
  D_Flip_Flop #(.trigger("rising"), .Pre_Clr_Positions("LEGACY"), .NegatePresetClear("false"), .enable("true"), .NewFFLayout("false")) \D触发器  (
    .clk(or_1_out), .D(R0), .Q(\D触发器_q ), .en(multiplexer_1_out), .reset(\复位 ));  // open: Qn, preset
  Multiplexer #(.select(1), .width(1), .disabled("Z"), .enable("false")) multiplexer_2 (
    .in0(1'b1), .in1(not_2_out), .out(multiplexer_2_out), .sel(1'b1));
  not not_2 (not_2_out, comparator_6_eq);
  and and_6 (and_6_out, out_8, comparator_7_eq);
  LED #(.active("true")) \u_第4位错  (.in(and_6_out));
  xor xor_5 (\纠正后的CRC码 [3], comparator_7_eq, \CRC码 [3]);
  Comparator #(.width(3), .mode("unsigned")) comparator_8 (.a(\余数 ), .b(3'b100), .eq(comparator_8_eq));  // open: gt, lt
  LED #(.active("true")) \u_余数生成指示灯  (.in(out_8));
  xor xor_6 (R1, \D触发器_3_q , \D触发器_q );
  and and_7 (and_7_out, out_8, comparator_8_eq);
  LED #(.active("true")) \u_第3位错  (.in(and_7_out));
  xor xor_7 (\纠正后的CRC码 [2], comparator_8_eq, \CRC码 [2]);
  Counter #(.width(4), .max('hf), .ongoal("wrap"), .trigger("rising"), .behavior("old")) \u_计数器_3  (
    .count(Stop), .Q(\计数器_3_q ), .clk(or_1_out), .clr(\复位 ));  // open: load, D, carry, preset
  and and_8 (and_8_out, out_8, comparator_9_eq);
  Comparator #(.width(3), .mode("unsigned")) comparator_9 (.a(\余数 ), .b(3'b010), .eq(comparator_9_eq));  // open: gt, lt
  D_Flip_Flop #(.trigger("rising"), .Pre_Clr_Positions("LEGACY"), .NegatePresetClear("false"), .enable("true"), .NewFFLayout("false")) \D触发器_2  (
    .clk(or_1_out), .D(R1), .Q(R2), .en(multiplexer_1_out), .reset(\复位 ));  // open: Qn, preset
  Comparator #(.width(4), .mode("unsigned")) comparator_10 (.a(\计数器_3_q ), .b(4'b1000), .eq(out_8));  // open: gt, lt
  not not_3 (not_3_out, out_8);
  LED #(.active("true")) \u_第2位错  (.in(and_8_out));
  xor xor_8 (\纠正后的CRC码 [1], comparator_9_eq, \CRC码 [1]);
  Multiplexer #(.select(1), .width(1), .disabled("Z"), .enable("false")) multiplexer_3 (
    .in0(1'b1), .in1(not_3_out), .out(Stop), .sel(1'b1));
  and and_9 (and_9_out, out_8, comparator_11_eq);
  LED #(.active("true")) \u_第1位错  (.in(and_9_out));
  Comparator #(.width(3), .mode("unsigned")) comparator_11 (
    .a(\余数 ), .b(3'b001), .eq(comparator_11_eq));  // open: gt, lt
  D_Flip_Flop #(.trigger("rising"), .Pre_Clr_Positions("LEGACY"), .NegatePresetClear("false"), .enable("true"), .NewFFLayout("false")) \D触发器_3  (
    .clk(or_1_out), .D(R2), .Q(\D触发器_3_q ), .en(multiplexer_1_out), .reset(\复位 ));  // open: Qn, preset
  xor xor_9 (\纠正后的CRC码 [0], comparator_11_eq, \CRC码 [0]);

  assign \纠错后的数据  = \纠正后的CRC码 [3:0];

  // Other names for the same wires on the sheet: CLK = \时钟 ; CLR = \复位 ; C0 = \CRC码 [0]; C1 = \CRC码 [1];
  //   C2 = \CRC码 [2]; C3 = \CRC码 [3]; C4 = \CRC码 [4]; C5 = \CRC码 [5]; C6 = \CRC码 [6]; LED = out_8; R[2:0] = \余数 ;
  //   C0_prime = \纠正后的CRC码 [0]; C1_prime = \纠正后的CRC码 [1]; C2_prime = \纠正后的CRC码 [2]; C3_prime = \纠正后的CRC码 [3];
  //   C4_prime = \纠正后的CRC码 [4]; C5_prime = \纠正后的CRC码 [5]; C6_prime = \纠正后的CRC码 [6]

  // Notes on the sheet:
  //   第二步：按“复位”按钮
  //   第三步：按“装入”按钮
  //   第一步：置左上角的CRC码（如：1100010）
  //   第四步：按“时钟”按钮多次，直到“余数生成指示灯”变红
  //   第五步：置有一位错的CRC码（如：0100010）
  //   重复第二、三、四步
  //   此时，余数=101，下面的“第7位错”指示灯变红
  //   纠正后的CRC码见右上角
  //   此时，余数=000，下面的“无错”指示灯变红，表示无错
  //   比较器
  //   比较器
  //   比较器
  //   移位寄存器
  //   比较器
  //   0
  //   x
  //   1*
  //   比较器
  //   比较器
  //   比较器
  //   比较器
  //   1
  //   1*
  //   x
  //   比较器
  //   比较器
  //   2
  //   x
  //   0*
  //   CRC串行解码电路2（生成多项式=1011）
  //   原始数据=4位；余数=3位；CRC码=原始数据4位+余数3位
  //   比较器
  //   3
  //   x
  //   1*
endmodule
