// Logisim project 循环冗余校验码（并行）实验.circ as structural Verilog: 7 circuits, main circuit 国标码转区位码电路
module \CRC码传输测试实验1  (
  input  [15:0] \原始数据 
);

  wire CLK_out, comparator_1_eq, \crc并行解码电路_1__1位错 , \crc并行解码电路_1__2位错 , \crc并行解码电路_1_无错误 ;
  wire [15:0] \crc并行解码电路_1_纠错后数据 ;
  wire [21:0] \crc并行编码电路_1_crc校验码 , \随机干扰电路_1_加扰后数据 , \随机干扰电路_1_随机加扰屏蔽字 ;

  // Probe on \原始数据 
  // Probe on \crc并行编码电路_1_crc校验码 
  \CRC并行编码电路  \crc并行编码电路_1  (.\原始数据 (\原始数据 ), .\CRC校验码 (\crc并行编码电路_1_crc校验码 ));
  // Probe on \随机干扰电路_1_随机加扰屏蔽字 
  Clock #(.highDuration(1), .lowDuration(1)) CLK (.out(CLK_out));
  \随机干扰电路  \u_随机干扰电路_1  (
    .\随机加扰屏蔽字 (\随机干扰电路_1_随机加扰屏蔽字 ), .\_22位输入 (\crc并行编码电路_1_crc校验码 ), .\加扰后数据 (\随机干扰电路_1_加扰后数据 ), .CLK(CLK_out));
  // Probe on \随机干扰电路_1_加扰后数据 
  LED #(.active("true")) \u_无错  (.in(\crc并行解码电路_1_无错误 ));
  LED #(.active("true")) \_1位错  (.in(\crc并行解码电路_1__1位错 ));
  LED #(.active("true")) \_2位错  (.in(\crc并行解码电路_1__2位错 ));
  \CRC并行解码电路  \crc并行解码电路_1  (
    .\CRC编码 (\随机干扰电路_1_加扰后数据 ), .\无错误 (\crc并行解码电路_1_无错误 ), .\_1位错 (\crc并行解码电路_1__1位错 ),
    .\_2位错 (\crc并行解码电路_1__2位错 ), .\纠错后数据 (\crc并行解码电路_1_纠错后数据 ));
  // Probe on \crc并行解码电路_1_纠错后数据 
  Comparator #(.width(16), .mode("twosComplement")) comparator_1 (
    .a(\原始数据 ), .b(\crc并行解码电路_1_纠错后数据 ), .eq(comparator_1_eq));  // open: gt, lt
  LED #(.active("true")) \u_数据正确  (.in(comparator_1_eq));

  // Notes on the sheet:
  //   发送方
  //   电路功能：测试CRC编解码电路正确性
  //   1、无错：无错灯红色，数据正确灯红色，接收数据等于发送数据
  //   先设置原始数据，然后每按“CLK”按钮2次，产生1个随机干扰，观看4个指示灯，有4种情况：
  //   2、1位错：1位错灯红色，数据正确灯红色，接收数据等于发送数据（可以纠正1位错）
  //   3、2位错：2位错灯红色，数据正确灯白色，接收数据不等于发送数据（不能纠正1位错）
  //   4、2位错：2位错灯红色，数据正确灯红色，接收数据等于发送数据（可以纠正某些情况的2位错误）
  //   输入：16位原始数据             输出：16位解码后的数据，4个指示灯（无错、1位错、2位错、数据正确）
  //   CRC码传输测试实验1
  //   接收方
endmodule

module \CRC码传输测试实验2  (
);

  wire CLK, CLR_out, comparator_1_eq, \crc并行解码电路_1__1位错 , \crc并行解码电路_1__2位错 , \crc并行解码电路_1_无错误 ;
  wire [6:0] \国标码转区位码电路_1_位号 , \国标码转区位码电路_1_区号 , \国标码转区位码电路_2_位号 , \国标码转区位码电路_2_区号 ;
  wire [7:0] counter_1_q;
  wire [15:0] \发送 , \接收 ;
  wire [21:0] \crc并行编码电路_1_crc校验码 , \随机干扰电路_1_加扰后数据 , \随机干扰电路_1_随机加扰屏蔽字 ;
  wire [31:0] \字库电路_1_out_3 , \字库电路_1_out_4 , \字库电路_1_out_5 , \字库电路_1_out_6 , \字库电路_1_out_7 , \字库电路_1_out_8 ,
       \字库电路_1_out_9 , \字库电路_1_out_10 , \字库电路_1_out_11 , \字库电路_1_out_12 , \字库电路_1_out_13 , \字库电路_1_out_14 ,
       \字库电路_1_out_15 , \字库电路_1_out_16 , \字库电路_1_out_17 , \字库电路_1_out_18 , \字库电路_1_out_19 , \字库电路_1_out_20 ,
       \字库电路_1_out_21 , \字库电路_1_out_22 , \字库电路_1_out_23 , \字库电路_1_out_24 , \字库电路_1_out_25 , \字库电路_1_out_26 ,
       \字库电路_1_out_27 , \字库电路_1_out_28 , \字库电路_1_out_29 , \字库电路_1_out_30 , \字库电路_1_out_31 , \字库电路_1_out_32 ,
       \字库电路_1_out_33 , \字库电路_1_out_34 , \字库电路_2_out_3 , \字库电路_2_out_4 , \字库电路_2_out_5 , \字库电路_2_out_6 ,
       \字库电路_2_out_7 , \字库电路_2_out_8 , \字库电路_2_out_9 , \字库电路_2_out_10 , \字库电路_2_out_11 , \字库电路_2_out_12 ,
       \字库电路_2_out_13 , \字库电路_2_out_14 , \字库电路_2_out_15 , \字库电路_2_out_16 , \字库电路_2_out_17 , \字库电路_2_out_18 ,
       \字库电路_2_out_19 , \字库电路_2_out_20 , \字库电路_2_out_21 , \字库电路_2_out_22 , \字库电路_2_out_23 , \字库电路_2_out_24 ,
       \字库电路_2_out_25 , \字库电路_2_out_26 , \字库电路_2_out_27 , \字库电路_2_out_28 , \字库电路_2_out_29 , \字库电路_2_out_30 ,
       \字库电路_2_out_31 , \字库电路_2_out_32 , \字库电路_2_out_33 , \字库电路_2_out_34 ;

  Counter #(.width(8), .max('hff), .ongoal("wrap"), .trigger("rising"), .behavior("old")) counter_1 (
    .Q(counter_1_q), .clk(CLK), .clr(CLR_out));  // open: load, D, count, carry, preset
  Button CLR (.out(CLR_out));
  Clock #(.highDuration(1), .lowDuration(1)) \u_时钟  (.out(CLK));
  \国标码转区位码电路  \u_国标码转区位码电路_1  (.\位号 (\国标码转区位码电路_1_位号 ), .\区号 (\国标码转区位码电路_1_区号 ), .GB2312(\发送 ));
  \字库电路  \u_字库电路_1  (
    .out_3(\字库电路_1_out_3 ), .out_4(\字库电路_1_out_4 ), .out_5(\字库电路_1_out_5 ), .out_6(\字库电路_1_out_6 ),
    .out_7(\字库电路_1_out_7 ), .out_8(\字库电路_1_out_8 ), .out_9(\字库电路_1_out_9 ), .out_10(\字库电路_1_out_10 ),
    .out_11(\字库电路_1_out_11 ), .out_12(\字库电路_1_out_12 ), .out_13(\字库电路_1_out_13 ), .out_14(\字库电路_1_out_14 ),
    .out_15(\字库电路_1_out_15 ), .out_16(\字库电路_1_out_16 ), .out_17(\字库电路_1_out_17 ), .out_18(\字库电路_1_out_18 ),
    .out_19(\字库电路_1_out_19 ), .out_20(\字库电路_1_out_20 ), .out_21(\字库电路_1_out_21 ), .out_22(\字库电路_1_out_22 ),
    .out_23(\字库电路_1_out_23 ), .out_24(\字库电路_1_out_24 ), .out_25(\字库电路_1_out_25 ), .out_26(\字库电路_1_out_26 ),
    .out_27(\字库电路_1_out_27 ), .out_28(\字库电路_1_out_28 ), .out_29(\字库电路_1_out_29 ), .out_30(\字库电路_1_out_30 ),
    .out_31(\字库电路_1_out_31 ), .out_32(\字库电路_1_out_32 ), .out_33(\字库电路_1_out_33 ), .out_34(\字库电路_1_out_34 ),
    .\区号 (\国标码转区位码电路_1_区号 ), .\位号 (\国标码转区位码电路_1_位号 ));
  DotMatrix #(.inputtype("row"), .matrixcols(32), .matrixrows(32), .persist(0), .dotshape("circle")) dotmatrix_1 (
    .row0(\字库电路_1_out_3 ), .row1(\字库电路_1_out_4 ), .row2(\字库电路_1_out_5 ), .row3(\字库电路_1_out_6 ),
    .row4(\字库电路_1_out_7 ), .row5(\字库电路_1_out_8 ), .row6(\字库电路_1_out_9 ), .row7(\字库电路_1_out_10 ),
    .row8(\字库电路_1_out_11 ), .row9(\字库电路_1_out_12 ), .row10(\字库电路_1_out_13 ), .row11(\字库电路_1_out_14 ),
    .row12(\字库电路_1_out_15 ), .row13(\字库电路_1_out_16 ), .row14(\字库电路_1_out_17 ), .row15(\字库电路_1_out_18 ),
    .row16(\字库电路_1_out_19 ), .row17(\字库电路_1_out_20 ), .row18(\字库电路_1_out_21 ), .row19(\字库电路_1_out_22 ),
    .row20(\字库电路_1_out_23 ), .row21(\字库电路_1_out_24 ), .row22(\字库电路_1_out_25 ), .row23(\字库电路_1_out_26 ),
    .row24(\字库电路_1_out_27 ), .row25(\字库电路_1_out_28 ), .row26(\字库电路_1_out_29 ), .row27(\字库电路_1_out_30 ),
    .row28(\字库电路_1_out_31 ), .row29(\字库电路_1_out_32 ), .row30(\字库电路_1_out_33 ), .row31(\字库电路_1_out_34 ));
  ROM #(.addrWidth(8), .dataWidth(16), .Select("high")) rom_1 (.addr(counter_1_q), .data(\发送 ));
  // Probe on \发送 
  \CRC并行编码电路  \crc并行编码电路_1  (.\原始数据 (\发送 ), .\CRC校验码 (\crc并行编码电路_1_crc校验码 ));
  // Probe on \crc并行编码电路_1_crc校验码 
  // Probe on \随机干扰电路_1_随机加扰屏蔽字 
  \随机干扰电路  \u_随机干扰电路_1  (
    .\随机加扰屏蔽字 (\随机干扰电路_1_随机加扰屏蔽字 ), .\_22位输入 (\crc并行编码电路_1_crc校验码 ), .\加扰后数据 (\随机干扰电路_1_加扰后数据 ), .CLK(CLK));
  // Probe on \随机干扰电路_1_加扰后数据 
  \字库电路  \u_字库电路_2  (
    .out_3(\字库电路_2_out_3 ), .out_4(\字库电路_2_out_4 ), .out_5(\字库电路_2_out_5 ), .out_6(\字库电路_2_out_6 ),
    .out_7(\字库电路_2_out_7 ), .out_8(\字库电路_2_out_8 ), .out_9(\字库电路_2_out_9 ), .out_10(\字库电路_2_out_10 ),
    .out_11(\字库电路_2_out_11 ), .out_12(\字库电路_2_out_12 ), .out_13(\字库电路_2_out_13 ), .out_14(\字库电路_2_out_14 ),
    .out_15(\字库电路_2_out_15 ), .out_16(\字库电路_2_out_16 ), .out_17(\字库电路_2_out_17 ), .out_18(\字库电路_2_out_18 ),
    .out_19(\字库电路_2_out_19 ), .out_20(\字库电路_2_out_20 ), .out_21(\字库电路_2_out_21 ), .out_22(\字库电路_2_out_22 ),
    .out_23(\字库电路_2_out_23 ), .out_24(\字库电路_2_out_24 ), .out_25(\字库电路_2_out_25 ), .out_26(\字库电路_2_out_26 ),
    .out_27(\字库电路_2_out_27 ), .out_28(\字库电路_2_out_28 ), .out_29(\字库电路_2_out_29 ), .out_30(\字库电路_2_out_30 ),
    .out_31(\字库电路_2_out_31 ), .out_32(\字库电路_2_out_32 ), .out_33(\字库电路_2_out_33 ), .out_34(\字库电路_2_out_34 ),
    .\区号 (\国标码转区位码电路_2_区号 ), .\位号 (\国标码转区位码电路_2_位号 ));
  \国标码转区位码电路  \u_国标码转区位码电路_2  (.\位号 (\国标码转区位码电路_2_位号 ), .\区号 (\国标码转区位码电路_2_区号 ), .GB2312(\接收 ));
  LED #(.active("true")) \u_无错  (.in(\crc并行解码电路_1_无错误 ));
  LED #(.active("true")) \_1位错  (.in(\crc并行解码电路_1__1位错 ));
  DotMatrix #(.inputtype("row"), .matrixcols(32), .matrixrows(32), .persist(0), .dotshape("circle")) dotmatrix_2 (
    .row0(\字库电路_2_out_3 ), .row1(\字库电路_2_out_4 ), .row2(\字库电路_2_out_5 ), .row3(\字库电路_2_out_6 ),
    .row4(\字库电路_2_out_7 ), .row5(\字库电路_2_out_8 ), .row6(\字库电路_2_out_9 ), .row7(\字库电路_2_out_10 ),
    .row8(\字库电路_2_out_11 ), .row9(\字库电路_2_out_12 ), .row10(\字库电路_2_out_13 ), .row11(\字库电路_2_out_14 ),
    .row12(\字库电路_2_out_15 ), .row13(\字库电路_2_out_16 ), .row14(\字库电路_2_out_17 ), .row15(\字库电路_2_out_18 ),
    .row16(\字库电路_2_out_19 ), .row17(\字库电路_2_out_20 ), .row18(\字库电路_2_out_21 ), .row19(\字库电路_2_out_22 ),
    .row20(\字库电路_2_out_23 ), .row21(\字库电路_2_out_24 ), .row22(\字库电路_2_out_25 ), .row23(\字库电路_2_out_26 ),
    .row24(\字库电路_2_out_27 ), .row25(\字库电路_2_out_28 ), .row26(\字库电路_2_out_29 ), .row27(\字库电路_2_out_30 ),
    .row28(\字库电路_2_out_31 ), .row29(\字库电路_2_out_32 ), .row30(\字库电路_2_out_33 ), .row31(\字库电路_2_out_34 ));
  LED #(.active("true")) \_2位错  (.in(\crc并行解码电路_1__2位错 ));
  \CRC并行解码电路  \crc并行解码电路_1  (
    .\CRC编码 (\随机干扰电路_1_加扰后数据 ), .\无错误 (\crc并行解码电路_1_无错误 ), .\_1位错 (\crc并行解码电路_1__1位错 ),
    .\_2位错 (\crc并行解码电路_1__2位错 ), .\纠错后数据 (\接收 ));
  // Probe on \接收 
  Comparator #(.width(16), .mode("twosComplement")) comparator_1 (
    .a(\发送 ), .b(\接收 ), .eq(comparator_1_eq));  // open: gt, lt
  LED #(.active("true")) \u_数据正确  (.in(comparator_1_eq));

  // Notes on the sheet:
  //   发送方
  //   计数器
  //   发送方
  //   汉字显示
  //   ROM存储器
  //   电路功能：测试CRC编解码电路正确性
  //   contents of rom_1 (hex, n*v repeats v):
  //   bbaa d6d0 bfc6 bcbc b4f3 d1a7 cac7 b9fa bcd2 bdcc d3fd b2bf d6b1 caf4 b5c4 c8ab b9fa d6d8 b5e3 b4f3
  //   d1a7 a3ac d3c9 d4ad bbaa d6d0 c0ed b9a4 b4f3 d1a7 a1a2 cdac bcc3 d2bd bfc6 b4f3 d1a7 a1a2 cee4 baba
  //   b3c7 cad0 bda8 c9e8 d1a7 d4ba d3da a3b2 a3b0 a3b0 a3b0 c4ea a3b5 d4c2 a3b2 a3b6 c8d5 bacf b2a2 b3c9
  //   c1a2 a3ac cac7 cad7 c5fa c1d0 c8eb b9fa bcd2 a1b0 a3b2 a3b1 a3b1 b9a4 b3cc a1b1 d6d8 b5e3 bda8 c9e8
  //   bacd b9fa bcd2 a1b0 a3b9 a3b8 a3b5 b9a4 b3cc a1b1 bda8 c9e8 b8df d0a3 d6ae d2bb a1a3 d1a7 d0a3 d0a3
  //   d4b0 d5bc b5d8 c6df c7a7 d3e0 c4b6 a3ac d4b0 c4da caf7 c4be b4d0 dcd7 a3ac b1cc b2dd c8e7 d2f0 a3ac
  //   bbb7 beb3 d3c5 d1c5 a3ac beb0 c9ab d0e3 c0f6 a3ac c2cc bbaf b8b2 b8c7 c2ca 3732 25a3 acb1 bbd3 fece
  //   aaa1 b0c9 adc1 d6ca bdb4 f3d1 a7a1 b1a1
  //   1、无错：无错灯红色，数据正确灯红色，接收数据等于发送数据
  //   2、1位错：1位错灯红色，数据正确灯红色，接收数据等于发送数据（可以纠正1位错）
  //   3、2位错：2位错灯红色，数据正确灯白色，接收数据不等于发送数据（不能纠正1位错）
  //   4、2位错：2位错灯红色，数据正确灯红色，接收数据等于发送数据（可以纠正某些情况的2位错误）
  //   输入：16位汉字国标码（存放在ROM存储器中）             输出：16位解码后的数据（汉字国标码），4个指示灯（无错、1位错、2位错、数据正确），接收方与发送方显示的汉字
  //   先按“CLR”按钮，使计数器清零；然后每按“时钟”按钮2次，输出1个汉字的国标码，并产生1个随机干扰；观看4个指示灯和发送方与接收方显示的汉字，有4种情况：
  //   CRC码传输测试实验2
  //   接收方
  //   汉字显示
  //   接收方
endmodule

// CRC编码
module \CRC并行编码电路  (
  input  [15:0] \原始数据 ,
  output [21:0] \CRC校验码 
);

  wire [4:0] multiplexer_1_out, multiplexer_2_out, multiplexer_3_out, multiplexer_4_out, multiplexer_5_out,
       multiplexer_6_out, multiplexer_7_out, multiplexer_8_out, multiplexer_9_out, multiplexer_10_out,
       multiplexer_11_out, multiplexer_12_out, multiplexer_13_out, multiplexer_14_out, multiplexer_15_out,
       multiplexer_16_out;

  Multiplexer #(.select(1), .width(5), .disabled("Z"), .enable("true")) multiplexer_1 (
    .in0({5{1'b0}}), .in1(5'b01100), .out(multiplexer_1_out), .sel(\原始数据 [15]));  // open: en
  Multiplexer #(.select(1), .width(5), .disabled("Z"), .enable("true")) multiplexer_2 (
    .in0({5{1'b0}}), .in1(5'b00110), .out(multiplexer_2_out), .sel(\原始数据 [14]));  // open: en
  Multiplexer #(.select(1), .width(5), .disabled("Z"), .enable("true")) multiplexer_3 (
    .in0({5{1'b0}}), .in1(5'b00011), .out(multiplexer_3_out), .sel(\原始数据 [13]));  // open: en
  Multiplexer #(.select(1), .width(5), .disabled("Z"), .enable("true")) multiplexer_4 (
    .in0({5{1'b0}}), .in1(5'b10011), .out(multiplexer_4_out), .sel(\原始数据 [12]));  // open: en
  Multiplexer #(.select(1), .width(5), .disabled("Z"), .enable("true")) multiplexer_5 (
    .in0({5{1'b0}}), .in1(5'b11011), .out(multiplexer_5_out), .sel(\原始数据 [11]));  // open: en
  assign \CRC校验码 [4:0] = multiplexer_1_out ^ multiplexer_2_out ^ multiplexer_3_out ^ multiplexer_4_out ^ multiplexer_5_out ^ multiplexer_6_out ^ multiplexer_7_out ^ multiplexer_8_out ^ multiplexer_9_out ^ multiplexer_11_out ^ multiplexer_10_out ^ multiplexer_12_out ^ multiplexer_13_out ^ multiplexer_14_out ^ multiplexer_15_out ^ multiplexer_16_out;  // XOR_Gate xor_1, 5 bits wide
  Multiplexer #(.select(1), .width(5), .disabled("Z"), .enable("true")) multiplexer_6 (
    .in0({5{1'b0}}), .in1({5{1'b1}}), .out(multiplexer_6_out), .sel(\原始数据 [10]));  // open: en
  Multiplexer #(.select(1), .width(5), .disabled("Z"), .enable("true")) multiplexer_7 (
    .in0({5{1'b0}}), .in1(5'b11101), .out(multiplexer_7_out), .sel(\原始数据 [9]));  // open: en
  Multiplexer #(.select(1), .width(5), .disabled("Z"), .enable("true")) multiplexer_8 (
    .in0({5{1'b0}}), .in1(5'b11100), .out(multiplexer_8_out), .sel(\原始数据 [8]));  // open: en
  Multiplexer #(.select(1), .width(5), .disabled("Z"), .enable("true")) multiplexer_9 (
    .in0({5{1'b0}}), .in1(5'b01110), .out(multiplexer_9_out), .sel(\原始数据 [7]));  // open: en
  Multiplexer #(.select(1), .width(5), .disabled("Z"), .enable("true")) multiplexer_10 (
    .in0({5{1'b0}}), .in1(5'b10001), .out(multiplexer_10_out), .sel(\原始数据 [5]));  // open: en
  Multiplexer #(.select(1), .width(5), .disabled("Z"), .enable("true")) multiplexer_11 (
    .in0({5{1'b0}}), .in1(5'b00111), .out(multiplexer_11_out), .sel(\原始数据 [6]));  // open: en
  Multiplexer #(.select(1), .width(5), .disabled("Z"), .enable("true")) multiplexer_12 (
    .in0({5{1'b0}}), .in1(5'b11010), .out(multiplexer_12_out), .sel(\原始数据 [4]));  // open: en
  Multiplexer #(.select(1), .width(5), .disabled("Z"), .enable("true")) multiplexer_13 (
    .in0({5{1'b0}}), .in1(5'b01101), .out(multiplexer_13_out), .sel(\原始数据 [3]));  // open: en
  Multiplexer #(.select(1), .width(5), .disabled("Z"), .enable("true")) multiplexer_14 (
    .in0({5{1'b0}}), .in1(5'b10100), .out(multiplexer_14_out), .sel(\原始数据 [2]));  // open: en
  Multiplexer #(.select(1), .width(5), .disabled("Z"), .enable("true")) multiplexer_15 (
    .in0({5{1'b0}}), .in1(5'b01010), .out(multiplexer_15_out), .sel(\原始数据 [1]));  // open: en
  Multiplexer #(.select(1), .width(5), .disabled("Z"), .enable("true")) multiplexer_16 (
    .in0({5{1'b0}}), .in1(5'b00101), .out(multiplexer_16_out), .sel(\原始数据 [0]));  // open: en
  xor xor_2 (\CRC校验码 [21], \CRC校验码 [0], \CRC校验码 [1], \原始数据 [0], \原始数据 [1], \原始数据 [2], \原始数据 [3], \原始数据 [4], \原始数据 [5], \原始数据 [6], \原始数据 [7], \CRC校验码 [2], \原始数据 [8], \原始数据 [9], \原始数据 [10], \原始数据 [11], \原始数据 [12], \原始数据 [13], \原始数据 [14], \原始数据 [15], \CRC校验码 [3], \CRC校验码 [4]);

  assign \CRC校验码 [20:5] = \原始数据 ;

  // Other names for the same wires on the sheet: CRC编码[21:0] = {\CRC校验码 [21], \原始数据 , \CRC校验码 [4:0]};
  //   P1 = \CRC校验码 [0]; P2 = \CRC校验码 [1]; P3 = \CRC校验码 [2]; P4 = \CRC校验码 [3]; P5 = \CRC校验码 [4]; D1 = \原始数据 [0];
  //   D2 = \原始数据 [1]; D3 = \原始数据 [2]; D4 = \原始数据 [3]; D5 = \原始数据 [4]; D6 = \原始数据 [5]; D7 = \原始数据 [6]; D8 = \原始数据 [7];
  //   D9 = \原始数据 [8]; D10 = \原始数据 [9]; D11 = \原始数据 [10]; D12 = \原始数据 [11]; D13 = \原始数据 [12]; D14 = \原始数据 [13];
  //   D15 = \原始数据 [14]; D16 = \原始数据 [15]; P6 = \CRC校验码 [21]

  // Notes on the sheet:
  //   电路功能：循环冗余校验编码电路
  //   输入引脚区
  //   CRC并行编码电路
  //   输出引脚区
  //   输入：16位原始数据                             输出：22位循环冗余校验码（16位数据位+6位校验位）
endmodule

// CRC解码
module \CRC并行解码电路  (
  input  [21:0] \CRC编码 ,
  output \无错误 ,
  output \_1位错 ,
  output \_2位错 ,
  output [15:0] \纠错后数据 
);

  wire and_2_out, nor_1_out, xor_1_out, xor_2_out;
  wire [4:0] multiplexer_1_out, multiplexer_2_out, multiplexer_3_out, multiplexer_4_out, multiplexer_5_out,
       multiplexer_6_out, multiplexer_8_out, multiplexer_9_out, multiplexer_10_out, multiplexer_11_out,
       multiplexer_12_out, multiplexer_13_out, multiplexer_15_out, multiplexer_16_out, multiplexer_17_out,
       multiplexer_18_out, xor_3_out;
  wire [15:0] and_4_out, multiplexer_7_out, multiplexer_14_out;

  and and_1 (\_2位错 , ~xor_1_out, ~nor_1_out);  // AND_Gate
  xor xor_1 (xor_1_out, xor_2_out, \CRC编码 [21]);
  xor xor_2 (xor_2_out, \CRC编码 [0], \CRC编码 [1], \CRC编码 [5], \CRC编码 [6], \CRC编码 [7], \CRC编码 [8], \CRC编码 [9], \CRC编码 [10], \CRC编码 [11], \CRC编码 [12], \CRC编码 [2], \CRC编码 [13], \CRC编码 [14], \CRC编码 [15], \CRC编码 [16], \CRC编码 [17], \CRC编码 [18], \CRC编码 [19], \CRC编码 [20], \CRC编码 [3], \CRC编码 [4]);
  or or_1 (\_1位错 , xor_1_out, and_2_out);
  and and_2 (and_2_out, xor_1_out, ~nor_1_out);  // AND_Gate
  and and_3 (\无错误 , ~xor_1_out, nor_1_out);  // AND_Gate
  nor nor_1 (nor_1_out, xor_3_out[4], xor_3_out[3], xor_3_out[2], xor_3_out[1], xor_3_out[0]);
  Multiplexer #(.select(1), .width(5), .disabled("Z"), .enable("true")) multiplexer_1 (
    .in0({5{1'b0}}), .in1(5'b01100), .out(multiplexer_1_out), .sel(\CRC编码 [20]));  // open: en
  Multiplexer #(.select(1), .width(5), .disabled("Z"), .enable("true")) multiplexer_2 (
    .in0({5{1'b0}}), .in1(5'b00110), .out(multiplexer_2_out), .sel(\CRC编码 [19]));  // open: en
  Multiplexer #(.select(1), .width(5), .disabled("Z"), .enable("true")) multiplexer_3 (
    .in0({5{1'b0}}), .in1(5'b00011), .out(multiplexer_3_out), .sel(\CRC编码 [18]));  // open: en
  Multiplexer #(.select(1), .width(5), .disabled("Z"), .enable("true")) multiplexer_4 (
    .in0({5{1'b0}}), .in1(5'b10011), .out(multiplexer_4_out), .sel(\CRC编码 [17]));  // open: en
  Multiplexer #(.select(1), .width(5), .disabled("Z"), .enable("true")) multiplexer_5 (
    .in0({5{1'b0}}), .in1({5{1'b1}}), .out(multiplexer_5_out), .sel(\CRC编码 [15]));  // open: en
  Multiplexer #(.select(1), .width(5), .disabled("Z"), .enable("true")) multiplexer_6 (
    .in0({5{1'b0}}), .in1(5'b11011), .out(multiplexer_6_out), .sel(\CRC编码 [16]));  // open: en
  Multiplexer #(.select(5), .width(16), .disabled("Z"), .enable("true")) multiplexer_7 (
    .in0({16{1'b0}}), .in1({16{1'b0}}), .in2({16{1'b0}}), .in3(16'h2000), .in4({16{1'b0}}), .in5(16'h1),
    .in6(16'h4000), .in7(16'h40), .in8({16{1'b0}}), .in9({16{1'b0}}), .in10(16'h2), .in11({16{1'b0}}),
    .in12(16'h8000), .in13(16'h8), .in14(16'h80), .in15({16{1'b0}}), .in16({16{1'b0}}), .in17(16'h20),
    .in18({16{1'b0}}), .in19(16'h1000), .in20(16'h4), .in21({16{1'b0}}), .in22({16{1'b0}}),
    .in23({16{1'b0}}), .in24({16{1'b0}}), .in25({16{1'b0}}), .in26(16'h10), .in27(16'h800), .in28(16'h100),
    .in29(16'h200), .in30({16{1'b0}}), .in31(16'h400), .out(multiplexer_7_out), .sel(xor_3_out), .en(1'b1));
  assign xor_3_out = multiplexer_1_out ^ multiplexer_2_out ^ multiplexer_3_out ^ multiplexer_4_out ^ multiplexer_6_out ^ multiplexer_5_out ^ multiplexer_8_out ^ multiplexer_9_out ^ \CRC编码 [4:0] ^ multiplexer_10_out ^ multiplexer_12_out ^ multiplexer_11_out ^ multiplexer_13_out ^ multiplexer_16_out ^ multiplexer_15_out ^ multiplexer_17_out ^ multiplexer_18_out;  // XOR_Gate xor_3, 5 bits wide
  Multiplexer #(.select(1), .width(5), .disabled("Z"), .enable("true")) multiplexer_8 (
    .in0({5{1'b0}}), .in1(5'b11101), .out(multiplexer_8_out), .sel(\CRC编码 [14]));  // open: en
  Multiplexer #(.select(1), .width(5), .disabled("Z"), .enable("true")) multiplexer_9 (
    .in0({5{1'b0}}), .in1(5'b11100), .out(multiplexer_9_out), .sel(\CRC编码 [13]));  // open: en
  Multiplexer #(.select(1), .width(5), .disabled("Z"), .enable("true")) multiplexer_10 (
    .in0({5{1'b0}}), .in1(5'b01110), .out(multiplexer_10_out), .sel(\CRC编码 [12]));  // open: en
  Multiplexer #(.select(1), .width(5), .disabled("Z"), .enable("true")) multiplexer_11 (
    .in0({5{1'b0}}), .in1(5'b10001), .out(multiplexer_11_out), .sel(\CRC编码 [10]));  // open: en
  Multiplexer #(.select(1), .width(5), .disabled("Z"), .enable("true")) multiplexer_12 (
    .in0({5{1'b0}}), .in1(5'b00111), .out(multiplexer_12_out), .sel(\CRC编码 [11]));  // open: en
  Multiplexer #(.select(1), .width(5), .disabled("Z"), .enable("true")) multiplexer_13 (
    .in0({5{1'b0}}), .in1(5'b11010), .out(multiplexer_13_out), .sel(\CRC编码 [9]));  // open: en
  Multiplexer #(.select(1), .width(16), .disabled("Z"), .enable("true")) multiplexer_14 (
    .in0({16{1'b0}}), .in1({16{1'b1}}), .out(multiplexer_14_out), .sel(\_1位错 ));  // open: en
  Multiplexer #(.select(1), .width(5), .disabled("Z"), .enable("true")) multiplexer_15 (
    .in0({5{1'b0}}), .in1(5'b10100), .out(multiplexer_15_out), .sel(\CRC编码 [7]));  // open: en
  Multiplexer #(.select(1), .width(5), .disabled("Z"), .enable("true")) multiplexer_16 (
    .in0({5{1'b0}}), .in1(5'b01101), .out(multiplexer_16_out), .sel(\CRC编码 [8]));  // open: en
  assign and_4_out = multiplexer_14_out & multiplexer_7_out;  // AND_Gate and_4, 16 bits wide
  Multiplexer #(.select(1), .width(5), .disabled("Z"), .enable("true")) multiplexer_17 (
    .in0({5{1'b0}}), .in1(5'b01010), .out(multiplexer_17_out), .sel(\CRC编码 [6]));  // open: en
  Multiplexer #(.select(1), .width(5), .disabled("Z"), .enable("true")) multiplexer_18 (
    .in0({5{1'b0}}), .in1(5'b00101), .out(multiplexer_18_out), .sel(\CRC编码 [5]));  // open: en
  assign \纠错后数据  = \CRC编码 [20:5] ^ and_4_out;  // XOR_Gate xor_4, 16 bits wide

  // Other names for the same wires on the sheet: CRC[21:0] = \CRC编码 ; P1 = \CRC编码 [0]; P2 = \CRC编码 [1];
  //   P3 = \CRC编码 [2]; P4 = \CRC编码 [3]; P5 = \CRC编码 [4]; D1 = \CRC编码 [5]; D2 = \CRC编码 [6]; D3 = \CRC编码 [7];
  //   D4 = \CRC编码 [8]; D5 = \CRC编码 [9]; D6 = \CRC编码 [10]; D7 = \CRC编码 [11]; D8 = \CRC编码 [12]; D9 = \CRC编码 [13];
  //   D10 = \CRC编码 [14]; D11 = \CRC编码 [15]; D12 = \CRC编码 [16]; D13 = \CRC编码 [17]; D14 = \CRC编码 [18];
  //   D15 = \CRC编码 [19]; D16 = \CRC编码 [20]; P6 = \CRC编码 [21]

  // Notes on the sheet:
  //   电路功能：实现22位CRC编码的数据解码，能判断无错误、1位错、2位错，1位错具有自动纠错功能
  //   输入引脚区
  //   CRC并行解码电路
  //   输出引脚区
  //   输入：22位CRC编码                   输出：16位纠错后的数据，错误标志（无错误、1位错、2位错）
endmodule

// 随机干扰
module \随机干扰电路  (
  input  CLK,
  input  [21:0] \_22位输入 ,
  output [21:0] \随机加扰屏蔽字 ,
  output [21:0] \加扰后数据 
);

  wire comparator_1_eq, not_1_out, pull_resistor_1_node, \随机信号_5_out ;
  wire [1:0] pull_resistor_2_node, \随机信号_4_out ;
  wire [3:0] \随机信号_2_out , \随机信号_3_out , \随机信号_out ;
  wire [15:0] \_1位加扰A , decoder_3_out0;
  wire [21:0] \_1位加扰 , \_2位加扰 , \_3位加扰 , multiplexer_1_out, multiplexer_2_out, multiplexer_4_out;
  wire [21:6] \_1位加扰B ;

  Decoder #(.select(4), .tristate("false"), .disabled("Z"), .enable("false")) decoder_1 (
    .out0(\_1位加扰A [0]), .out1(\_1位加扰A [1]), .out2(\_1位加扰A [2]), .out3(\_1位加扰A [3]), .out4(\_1位加扰A [4]),
    .out5(\_1位加扰A [5]), .out6(\_1位加扰A [6]), .out7(\_1位加扰A [7]), .out8(\_1位加扰A [8]), .out9(\_1位加扰A [9]),
    .out10(\_1位加扰A [10]), .out11(\_1位加扰A [11]), .out12(\_1位加扰A [12]), .out13(\_1位加扰A [13]),
    .out14(\_1位加扰A [14]), .out15(\_1位加扰A [15]), .sel(\随机信号_out ));
  Random #(.width(4), .seed(0), .trigger("rising")) \u_随机信号  (.clk(CLK), .out(\随机信号_out ));  // open: next, clr
  Decoder #(.select(4), .tristate("false"), .disabled("Z"), .enable("false")) decoder_2 (
    .out0(\_1位加扰B [6]), .out1(\_1位加扰B [7]), .out2(\_1位加扰B [8]), .out3(\_1位加扰B [9]), .out4(\_1位加扰B [10]),
    .out5(\_1位加扰B [11]), .out6(\_1位加扰B [12]), .out7(\_1位加扰B [13]), .out8(\_1位加扰B [14]), .out9(\_1位加扰B [15]),
    .out10(\_1位加扰B [16]), .out11(\_1位加扰B [17]), .out12(\_1位加扰B [18]), .out13(\_1位加扰B [19]),
    .out14(\_1位加扰B [20]), .out15(\_1位加扰B [21]), .sel(\随机信号_2_out ));
  Random #(.width(4), .seed(18), .trigger("rising")) \u_随机信号_2  (.clk(CLK), .out(\随机信号_2_out ));  // open: next, clr
  Random #(.width(4), .seed(3), .trigger("rising")) \u_随机信号_3  (.clk(CLK), .out(\随机信号_3_out ));  // open: next, clr
  Decoder #(.select(4), .tristate("false"), .disabled("Z"), .enable("false")) decoder_3 (
    .out0(decoder_3_out0[0]), .out1(decoder_3_out0[1]), .out2(decoder_3_out0[2]), .out3(decoder_3_out0[3]),
    .out4(decoder_3_out0[4]), .out5(decoder_3_out0[5]), .out6(decoder_3_out0[6]), .out7(decoder_3_out0[7]),
    .out8(decoder_3_out0[8]), .out9(decoder_3_out0[9]), .out10(decoder_3_out0[10]),
    .out11(decoder_3_out0[11]), .out12(decoder_3_out0[12]), .out13(decoder_3_out0[13]),
    .out14(decoder_3_out0[14]), .out15(decoder_3_out0[15]), .sel(\随机信号_3_out ));
  Random #(.width(2), .seed(21), .trigger("rising")) \u_随机信号_4  (.clk(CLK), .out(\随机信号_4_out ));  // open: next, clr
  Random #(.width(1), .seed(31), .trigger("rising")) \u_随机信号_5  (.clk(CLK), .out(\随机信号_5_out ));  // open: next, clr
  Pull_Resistor #(.pull(0)) pull_resistor_1 (.node(pull_resistor_1_node));
  Multiplexer #(.select(1), .width(22), .disabled("Z"), .enable("false")) multiplexer_1 (
    .in0({\_1位加扰B , {6{1'b0}}}), .in1(\_3位加扰 ), .out(multiplexer_1_out), .sel(pull_resistor_1_node));
  Pull_Resistor #(.pull(1)) pull_resistor_2 (.node(pull_resistor_2_node));
  Multiplexer #(.select(2), .width(22), .disabled("Z"), .enable("false")) multiplexer_2 (
    .in0({22{1'b0}}), .in1({{6{1'b0}}, \_1位加扰A }), .in2(\_2位加扰 ), .in3(multiplexer_1_out),
    .out(multiplexer_2_out), .sel(\随机信号_4_out ));
  Multiplexer #(.select(2), .width(22), .disabled("Z"), .enable("false")) multiplexer_3 (
    .in0({22{1'b0}}), .in1(\_1位加扰 ), .in2(\_2位加扰 ), .in3(multiplexer_2_out), .out(\随机加扰屏蔽字 ),
    .sel(pull_resistor_2_node));
  Comparator #(.width(22), .mode("unsigned")) comparator_1 (
    .a({{6{1'b0}}, \_1位加扰A }), .b({\_1位加扰B , {6{1'b0}}}), .eq(comparator_1_eq));  // open: gt, lt
  not not_1 (not_1_out, comparator_1_eq);
  Multiplexer #(.select(1), .width(22), .disabled("Z"), .enable("false")) multiplexer_4 (
    .in0(22'h1), .in1({{6{1'b0}}, \_1位加扰A }), .out(multiplexer_4_out), .sel(not_1_out));
  assign \_2位加扰  = multiplexer_4_out ^ {\_1位加扰B , {6{1'b0}}};  // XOR_Gate xor_1, 22 bits wide
  assign \_3位加扰  = \_2位加扰  ^ {decoder_3_out0, {6{1'b0}}};  // XOR_Gate xor_2, 22 bits wide
  Multiplexer #(.select(1), .width(22), .disabled("Z"), .enable("false")) multiplexer_5 (
    .in0(multiplexer_4_out), .in1({\_1位加扰B , {6{1'b0}}}), .out(\_1位加扰 ), .sel(\随机信号_5_out ));
  assign \加扰后数据  = \随机加扰屏蔽字  ^ \_22位输入 ;  // XOR_Gate xor_3, 22 bits wide
  // also tied to GND on the sheet: pull_resistor_1_node
  // also tied to VCC on the sheet: {pull_resistor_2_node[0], pull_resistor_2_node[1]}

  // Notes on the sheet:
  //   随机干扰电路
endmodule

module \国标码转区位码电路  (
  input  [15:0] GB2312,
  output [6:0] \区号 ,
  output [6:0] \位号 
);

  wire [15:7] adder_1_out;

  // Probe on GB2312
  // Probe on \区号 
  Adder #(.width(16)) adder_1 (
    .a(GB2312), .b(16'h5f60), .out({adder_1_out[15], \区号 , adder_1_out[7], \位号 }));  // open: cin, cout
  // Probe on \位号 

  // Notes on the sheet:
  //   输入引脚区
  //   国标码转区位码电路
  //   输出引脚区
  //   探测区
endmodule

// 字库
module \字库电路  (
  input  [6:0] \区号 ,
  input  [6:0] \位号 ,
  output [31:0] out_3,
  output [31:0] out_4,
  output [31:0] out_5,
  output [31:0] out_6,
  output [31:0] out_7,
  output [31:0] out_8,
  output [31:0] out_9,
  output [31:0] out_10,
  output [31:0] out_11,
  output [31:0] out_12,
  output [31:0] out_13,
  output [31:0] out_14,
  output [31:0] out_15,
  output [31:0] out_16,
  output [31:0] out_17,
  output [31:0] out_18,
  output [31:0] out_19,
  output [31:0] out_20,
  output [31:0] out_21,
  output [31:0] out_22,
  output [31:0] out_23,
  output [31:0] out_24,
  output [31:0] out_25,
  output [31:0] out_26,
  output [31:0] out_27,
  output [31:0] out_28,
  output [31:0] out_29,
  output [31:0] out_30,
  output [31:0] out_31,
  output [31:0] out_32,
  output [31:0] out_33,
  output [31:0] out_34
);

  wire [6:0] multiplier_1_cout, multiplier_1_out, subtractor_1_out;
  wire [13:0] adder_1_out, bit_extender_1_out, subtractor_2_out;

  ROM #(.addrWidth(14), .dataWidth(32), .Select("high")) rom_1 (.addr(subtractor_2_out), .data(out_3));
  ROM #(.addrWidth(14), .dataWidth(32), .Select("high")) rom_2 (.addr(subtractor_2_out), .data(out_4));
  ROM #(.addrWidth(14), .dataWidth(32), .Select("high")) rom_3 (.addr(subtractor_2_out), .data(out_5));
  ROM #(.addrWidth(14), .dataWidth(32), .Select("high")) rom_4 (.addr(subtractor_2_out), .data(out_6));
  ROM #(.addrWidth(14), .dataWidth(32), .Select("high")) rom_5 (.addr(subtractor_2_out), .data(out_7));
  ROM #(.addrWidth(14), .dataWidth(32), .Select("high")) rom_6 (.addr(subtractor_2_out), .data(out_8));
  ROM #(.addrWidth(14), .dataWidth(32), .Select("high")) rom_7 (.addr(subtractor_2_out), .data(out_9));
  ROM #(.addrWidth(14), .dataWidth(32), .Select("high")) rom_8 (.addr(subtractor_2_out), .data(out_10));
  Subtractor #(.width(7)) subtractor_1 (.a(\区号 ), .b(7'b0000001), .out(subtractor_1_out));  // open: bin, bout
  Multiplier #(.width(7)) multiplier_1 (
    .a(subtractor_1_out), .b(7'b1011110), .out(multiplier_1_out), .cout(multiplier_1_cout));  // open: cin
  ROM #(.addrWidth(14), .dataWidth(32), .Select("high")) rom_9 (.addr(subtractor_2_out), .data(out_11));
  ROM #(.addrWidth(14), .dataWidth(32), .Select("high")) rom_10 (.addr(subtractor_2_out), .data(out_12));
  ROM #(.addrWidth(14), .dataWidth(32), .Select("high")) rom_11 (.addr(subtractor_2_out), .data(out_13));
  ROM #(.addrWidth(14), .dataWidth(32), .Select("high")) rom_12 (.addr(subtractor_2_out), .data(out_14));
  ROM #(.addrWidth(14), .dataWidth(32), .Select("high")) rom_13 (.addr(subtractor_2_out), .data(out_15));
  ROM #(.addrWidth(14), .dataWidth(32), .Select("high")) rom_14 (.addr(subtractor_2_out), .data(out_16));
  ROM #(.addrWidth(14), .dataWidth(32), .Select("high")) rom_15 (.addr(subtractor_2_out), .data(out_17));
  ROM #(.addrWidth(14), .dataWidth(32), .Select("high")) rom_16 (.addr(subtractor_2_out), .data(out_18));
  assign bit_extender_1_out = {{7{1'b0}}, \位号 };  // Bit_Extender bit_extender_1
  Adder #(.width(14)) adder_1 (
    .a({multiplier_1_cout, multiplier_1_out}), .b(bit_extender_1_out), .out(adder_1_out));  // open: cin, cout
  ROM #(.addrWidth(14), .dataWidth(32), .Select("high")) rom_17 (.addr(subtractor_2_out), .data(out_19));
  ROM #(.addrWidth(14), .dataWidth(32), .Select("high")) rom_18 (.addr(subtractor_2_out), .data(out_20));
  ROM #(.addrWidth(14), .dataWidth(32), .Select("high")) rom_19 (.addr(subtractor_2_out), .data(out_21));
  ROM #(.addrWidth(14), .dataWidth(32), .Select("high")) rom_20 (.addr(subtractor_2_out), .data(out_22));
  ROM #(.addrWidth(14), .dataWidth(32), .Select("high")) rom_21 (.addr(subtractor_2_out), .data(out_23));
  ROM #(.addrWidth(14), .dataWidth(32), .Select("high")) rom_22 (.addr(subtractor_2_out), .data(out_24));
  ROM #(.addrWidth(14), .dataWidth(32), .Select("high")) rom_23 (.addr(subtractor_2_out), .data(out_25));
  ROM #(.addrWidth(14), .dataWidth(32), .Select("high")) rom_24 (.addr(subtractor_2_out), .data(out_26));
  Subtractor #(.width(14)) subtractor_2 (.a(adder_1_out), .b(14'h1), .out(subtractor_2_out));  // open: bin, bout
  ROM #(.addrWidth(14), .dataWidth(32), .Select("high")) rom_25 (.addr(subtractor_2_out), .data(out_27));
  ROM #(.addrWidth(14), .dataWidth(32), .Select("high")) rom_26 (.addr(subtractor_2_out), .data(out_28));
  ROM #(.addrWidth(14), .dataWidth(32), .Select("high")) rom_27 (.addr(subtractor_2_out), .data(out_29));
  ROM #(.addrWidth(14), .dataWidth(32), .Select("high")) rom_28 (.addr(subtractor_2_out), .data(out_30));
  ROM #(.addrWidth(14), .dataWidth(32), .Select("high")) rom_29 (.addr(subtractor_2_out), .data(out_31));
  ROM #(.addrWidth(14), .dataWidth(32), .Select("high")) rom_30 (.addr(subtractor_2_out), .data(out_32));
  ROM #(.addrWidth(14), .dataWidth(32), .Select("high")) rom_31 (.addr(subtractor_2_out), .data(out_33));
  ROM #(.addrWidth(14), .dataWidth(32), .Select("high")) rom_32 (.addr(subtractor_2_out), .data(out_34));
  DotMatrix #(.inputtype("row"), .matrixcols(32), .matrixrows(32), .persist(0), .dotshape("circle")) dotmatrix_1 (
    .row0(out_3), .row1(out_4), .row2(out_5), .row3(out_6), .row4(out_7), .row5(out_8), .row6(out_9),
    .row7(out_10), .row8(out_11), .row9(out_12), .row10(out_13), .row11(out_14), .row12(out_15),
    .row13(out_16), .row14(out_17), .row15(out_18), .row16(out_19), .row17(out_20), .row18(out_21),
    .row19(out_22), .row20(out_23), .row21(out_24), .row22(out_25), .row23(out_26), .row24(out_27),
    .row25(out_28), .row26(out_29), .row27(out_30), .row28(out_31), .row29(out_32), .row30(out_33),
    .row31(out_34));

  // Other names for the same wires on the sheet: D0[31:0] = out_3; D1[31:0] = out_4; D2[31:0] = out_5;
  //   D3[31:0] = out_6; D4[31:0] = out_7; D5[31:0] = out_8; D6[31:0] = out_9; D7[31:0] = out_10; D8[31:0] = out_11;
  //   D9[31:0] = out_12; D10[31:0] = out_13; D11[31:0] = out_14; D12[31:0] = out_15; D13[31:0] = out_16;
  //   D14[31:0] = out_17; D15[31:0] = out_18; D16[31:0] = out_19; D17[31:0] = out_20; D18[31:0] = out_21;
  //   D19[31:0] = out_22; D20[31:0] = out_23; D21[31:0] = out_24; D22[31:0] = out_25; D23[31:0] = out_26;
  //   D24[31:0] = out_27; D25[31:0] = out_28; D26[31:0] = out_29; D27[31:0] = out_30; D28[31:0] = out_31;
  //   D29[31:0] = out_32; D30[31:0] = out_33; D31[31:0] = out_34

  // Notes on the sheet:
  //   contents of rom_1 (hex, n*v repeats v):
  //   281*0 ffffffff 272*0 60000000 202*0 18000 3c000 0 0 18000 3c000 0 0 18000 3c000 8*0 18000 18000
  //   3c000 3c000 18000 18000 3c000 3c000 18000 18000 3c000 18000 3c000 3c000 18000 3c000 18000 18000
  //   3c000 18000 3c000 3c000 18000 3c000 8*0 4*18000 4*3c000 4*18000 3c000 18000 3c000 3c000 3c000 18000
  //   18000 3c000 18000 3c000 3c000 3c000
  //   contents of rom_2 (hex, n*v repeats v):
  //   150*0 1c000 9*18000 121*0 ffffffff 269*0 10000 0 60000000 60000000 202*0 3c000 3c000 0 0 3c000 3c000
  //   0 0 3c000 3c000 8*0 24*3c000 8*0 24*3c000 587*0 8000 11*0 2000 124*0 8000 28*0 8000 291*0 400000
  //   742*0 1000 189*0 80 822*0 10000 654*0 40000 50*0 20000 64*0 4000 252*0 20000 56*0 40000 51*0 2000
  //   74*0 1000000 18*0 8000 74*0 2000 8*0 800000 400*0 40000 676*0 20 393*0 20000 31*0 2000 547*0 100
  //   58*0 800000 200 1000000 200200 387*0 1000000 5*0 800000 26*0 800000 22*0 8000 22*0 10000 0 8000 10*0
  //   10000 241*0 800000 0 0 1000000 7*0 1000000 1000000 10*0 1000000 9*0 20000 41*0 1000 301*0 20000 18*0
  //   800000 800000
  //   contents of rom_3 (hex, n*v repeats v):
  //   150*0 1ffc00 9*3ffc00 59*0 ff000 26*0 7ff0 0 ffe0000 30*0 10000 109*0 1c0000 144*0 60000006 0
  //   60000006 13*0 40000002 38000 0 60000000 e0000000 15*0 181800 0 0 0 e6000 182*0 3c000 3c000 0 0 3c000
  //   3c000 0 0 3c000 3c000 8*0 24*3c000 8*0 24*3c000 581*0 1800 1801800 8100 3000 60000 c00 c000 383800
  //   7000020 181800 0 e0 0 c200c00 1800000 30000 c06000 1003000 3000 1c000 1000 70000 2000 0 18000 0
  //   600c00 e00800 e00000 3000020 1040300 60000 6007000 6000 181800 3000018 1800000 0 0 3801800 0 8000 0
  //   3006000 2000 6100000 1800000 1800000 3000000 80 0 100800 20000 1800c00 0 3000000 800000 1800 80000
  //   301800 0 8000 30000 1800020 c00000 8 3800040 e00020 1000400 1801800 603000 c000100 30000 60000 1c00
  //   700000 300000 3818000 3803800 1800 18000 3803800 1800 1000c00 6003800 c06000 3000 181000 4000 200000
  //   30000 10 181c00 80 e00000 0 300c000 60000 3006000 1000000 100 181800 3001800 6040020 c00000 1c00
  //   1c3800 60000 102000 c3000 182000 0 2000000 602000 0 180000 c0000 2002000 6000c00 30000 380c00 18000
  //   1003000 1c000 0 8 0 c00 40180 0 70000 4000 0 1801000 1001c00 600 383000 381800 600c000 6004000
  //   c00c000 c0 18000 e000 1800000 400600 600c00 0 1800 c00 c00 200 400 c606000 3000 3000 30 18000 800000
  //   70000 40000 600c200 6000300 4018200 3000 3800000 300000 0 30000 c00800 400800 20 e000 180c000 200
  //   70000 3000 30000 3001000 0 2000 3000000 0 380 60000c0 2000000 c000 400400 c00 101000 10000c0 1001800
  //   3001800 1c00 4003300 e00e00 3801b80 3000c00 1800c00 c03000 30000 c00600 c00 1900 30100 0 0 3001000
  //   60000 3000 1000800 1c00 0 30000 1c000 3803000 c00000 2000000 3003000 1c00 603800 1c001c0 3000 1c0 20
  //   0 1e0 1c000 183000 1c1c00 300000 20000 c0 3000 6020000 6006000 1000c00 301800 800800 18000 6000
  //   183000 2000000 3000300 3806300 c3000 181800 0 c01800 1800000 0 0 0 c0 3000000 0 101800 301c00 1c000
  //   1800 1018300 38000 6000 800400 2000 3000020 202000 100180 380c000 3803000 30080c0 2004000 8000 1800
  //   3001800 30000 6000000 c00000 100 0 3000000 18000 18200 800000 1803000 0 0 600700 1800000 0 400000
  //   c00000 1800800 2000600 600000 30000 40000 60c080 1c00 3000800 60000 1000800 2020080 1380030 1040000
  //   40100 2010000 0 0 18000 1000080 6001800 0 3000 c00c00 2000180 3000c00 3000 600 3000000 8000 0 380
  //   100000 400000 0 c00 0 0 c00 100000 6000 c000 3001800 0 8000000 0 0 c00 300 1c000 403000 0 1c000
  //   3000000 180 3800000 60000 1800 18000 1c000 70000 3000800 10 1c00 c00 100000 1c00 1c00c00 0 800000 0
  //   0 60000 3000000 10000 7000000 10 c180 180 3000400 8000400 1800 600e00 400 800 18000 3006000 1800200
  //   0 3800c00 0 30000 3006000 601000 c00000 1800 18000 c000 38000 2003000 18000 0 400000 6000 1002000
  //   3000000 2000040 100 70000 3807000 800 0 6000 1800 70000 600 1800 c000 101000 c0 3200 1800 200c00
  //   18000 0 3800 300010 0 c000 80 181800 30000 200000 401000 201800 4000 1c00000 30c0 1c00800 c00000
  //   1800 1801800 30000 1000800 18000 c01c00 6000 c000 1803000 6000 60 1c001c0 70000 1800 8080 2000000
  //   1000080 300c300 3001000 200e100 1008100 4003000 1801800 6000 800000 38000 0 0 806000 300c00 418400
  //   c00 600000 e1ee00 408000 c03800 3000 30000 1800 1000000 800100 600c00 60000 3810180 0 0 1800000 0
  //   2020180 0 0 10180 20 10000 1000800 18000 181800 3801800 0 3003000 30 1800000 e0000 3000c00 100 10
  //   100010 2001800 8060180 c000 1001800 400000 c01800 0 1000000 0 1800c00 0 4100 0 2000000 c00000 e000
  //   1000 1800 800800 1000 8000 20020 3003000 1000000 30000 1800 381c00 1801800 30000 400c00 20100 3000
  //   e00000 1001000 1000 6600 38000 c6000 1800800 c03000 30000 400000 600000 18000 6001800 300c00 6000 0
  //   0 0 100 0 0 3001800 0 1000 0 c00 181800 1880 3001840 1000 3180 200 0 0 0 2000000 8 200 3001800 20000
  //   0 100 30000 80000 183800 300c700 800 3801000 1800000 6000000 2000 8000000 10000 1800100 1000 1c00 0
  //   0 c000 600000 600000 38000 1801c00 800 3000 3000 3000 1800 1800000 3001800 800 18000 2000 1800800
  //   c00 3000000 6002000 40000 300000 1000000 2000c00 400c00 1000 0 20300c0 1000 8080 c00e00 1800008 0
  //   3000c00 180 c0 3000000 1000 18000 30000 2000000 e00000 0 0 c00 0 3007000 3000 600 200 200600 1800c00
  //   1800008 8600 3000700 0 0 1000000 0 0 6000200 4*0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
  //   contents of rom_4 (hex, n*v repeats v):
  //   11*0 c3000 5*0 40 2000000 10 8000000 80 0 1ff0 100000 1ff0 f80000 1fff0 fff8000 1ffe0 7ff0000 18*0
  //   800 3800 13*0 10000 18000 0 c00000 c20000 0 18000 0 0 0 400 3e000 0 10000 10000 13*0 18000 57*0
  //   10*f00f00 34*0 c00000 24*0 3ffe00 26*0 7ff0 1800000 ffe0000 0 0 300 26*0 1c0 18000 3c00000 49*0 1c0
  //   57*0 80000 1e0380 0 0 0 180 11*0 70 11*0 20000 0 0 18000 0 0 80 0 0 0 3c0 0 0 1e0 5*0 c0 18*0 6000 0
  //   0 0 e0000 74*0 3800001c 0 7000000e 13*0 60000006 38000 0 60000000 e0000000 15*0 1c1c00 0 0 0 e7000
  //   104*0 200000 18180000 6000000 13*0 60000 0 0 300000 0 0 6000 6*0 30000 3000 0 0 0 20000 0 300 0
  //   38000 3000 0 0 30000 0 0 2000000 60000 31*0 3c000 3c000 0 0 3c000 3c000 0 0 3c000 3c000 8*0 24*3c000
  //   8*0 24*3c000 579*0 218008 30600008 3801c00 1c01c00 e380 3800 38000 1800e00 6000 383010 78001f0
  //   1c1c00 18030 1ff0 2301c0 e380600 3c00000 18000 e07000 3c01800 1800 301e000 1800 38000 8103000
  //   3ffff80 1c000 0 700e00 e00e00 e00000 18000f0 1ce0700 70000 7007000 800e000 1c1c00 380001c 1c00700
  //   600 0 3803c00 2000 e000 0 3807200 3800 7180000 1c00000 1c00000 3800000 3ffffc0 6000060 380f00 38000
  //   1c00e00 10 3840010 1e00000 83c00 3c0000 f83800 60000 e000 3038000 1c000e0 c04080 41fffc 38001e0
  //   e00070 1c00600 1c01c00 703800 6000180 38000 70000 1801c00 601008 300010 3818000 3801c00 8200c00
  //   3018000 3803800 e00 1c00e00 7001c00 e03800 8003800 1c3800 7000 780000 18000 1001c 1c1c00 3ffffc0
  //   e40040 e40080 780f000 38000 380f000 1c30060 1ffff80 3c3800 3801c00 70ffff0 e00000 1c00 1c3800 70000
  //   3c3800 c3810 1c3800 800080 3800000 f03000 180000 1c0000 1e0200 3803800 3000c00 38000 380e00 1c000
  //   3c03800 381c060 1800008 18 18 10230c30 c0301c0 8000030 60200 6007000 c018808 1c01c00 1801c00 600
  //   383800 381c00 700e000 700e000 e00e000 fe0 c000 7000 1c00000 700700 8710e00 c0000 e00 e00 8040600
  //   8000380 10270700 e706000 6003800 1801c00 800f0 1c000 e00008 38000 70000 300e380 3000380 701c380
  //   c003800 3800000 380000 8 38000 8e60c00 8720c00 4010038 7000 1c0e000 4000380 18060008 c001800 18000
  //   3801c00 700 10003800 3800000 10 1f80 70180e0 3800000 e000 300e00 c00 1c1c00 18007e0 1c01c00 7801c00
  //   c001c00 70039c0 e00e00 3801dc0 3800e00 1c01e00 f03c00 30000 e00700 8000e00 c201cc0 18030180 4001c00
  //   180070 3801d00 70000 3b00 1801c00 3801c00 18 38000 1c000 3803800 600000 7807000 3801800 301c00
  //   703c00 1e001e0 3800 100c01c0 1f0 f0 7ff0 fe030 183800 181c00 380000 70000 7ffffe0 3800 7070008
  //   7007000 1c00e00 381c00 e01e00 3c000 c007000 1c3000 7020100 3000380 3007380 c3800 1c1c00 4000008
  //   e01c00 1c00018 2040040 c202038 6000060 c0e0 38000e0 80 381c00 381c00 1c000 1c00 381c380 1c000 c2000
  //   600f00 8003800 38000e0 303800 3801c0 380e000 3807000 38060e0 700e000 601c000 1000c00 3800e00 38000
  //   3000000 e00018 ffff80 180000 3800180 1c100 c18300 e00300 1e03800 c1000c0 18 700700 1c00040 20020
  //   700000 e00000 1c00e00 3800700 700000 30400 18060000 70e1c0 1e00 3800e00 f0000 1c00e00 30301c0
  //   1b80038 3870000 8060180 3018000 4000030 20 1c000 1ffffc0 7001c00 c000000 10203800 e00e00 18001c0
  //   3800e00 383800 3800680 3004840 e600 1800100 7fc0 790010 e00020 c004840 6000ec0 300 c0600c0 e00
  //   380000 7000 e000 3801c00 6061000 e003800 4000000 1c00 e00 380 1c000 603800 0 1c000 3800000 7c0
  //   3c00000 30000 1c00 1c000 301c060 38000 3800e00 301c 1e00 18180e00 7a0008 381e00 1c01e00 71c000
  //   1e00008 6180 0 70000 1c00000 1c000 7000000 6000038 e180 60001c0 7806700 c000700 10203800 700e00 700
  //   1c01c00 38030 3803800 1c00380 c00c00 3c00e00 1c00070 1c000 3806000 701c00 e06040 1c00 18000 e000
  //   1c000 3801800 1c000 1800000 f00018 7800 1c07800 38000e0 38001e0 1f80 78000 3007800 e00 30 8007000
  //   3801c00 70040 c0c700 3801c00 6000 1c1c00 80e0 3303b00 180c00 380e00 c01c000 c000010 383c00 300038
  //   10118030 1800f000 880e0 1c1c00 38000 380000 701c00 701c00 f000 1c00000 38c0 1c01c00 e00040 10300c00
  //   1c03c00 18000 3800e00 301c040 1ec1c00 7000 e000 1c01800 3000 ffe7ff0 1e001c0 78000 1c00 c1c0 383ffe0
  //   38081c0 380e380 3801c00 380e380 381c380 6003800 1c01c00 7000 1c00000 38000 1ffff80 10 e07000 380e80
  //   71c700 e00 706000 f0c780 e0ee00 1e03800 c003800 78000 41c00 1c00000 ffff00 300e00 3070000 381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
  //   contents of rom_5 (hex, n*v repeats v):
  //   8*0 40000 0 0 c3000 0 20 3c00000 1820 3c70000 e0 6000000 30 18000000 198 19800000 1800 100000 1830
  //   d80000 1ffe0 7ff8000 1ffc0 7ff0000 18000 0 0 0 18000 12*0 7e000 3c00 7c00 6*0 30000 c000 10 4000000
  //   0 0 0 18000 ff000 800000 1c00000 1c70000 2000000 18000 18000018 0 c000 7000c00 ff800 0 18000 18000
  //   3c000 7e000 7e000 18000 18000 0 0 18000 18000 0 0 0 18000 18000 3ffffff8 18000 301c00 4008060
  //   3000000 0 180 820 8000 2000000 7*0 4000 1c000 c000 0 c0e00 0 0 8000 0 1000 0 1000 0 0 10300 0 1ff00
  //   3000 0 1c01000 7*1000080 1000180 12*1000080 1c00180 9*1c00380 0 0 10*1000080 0 0 1ff800 1fe7fc0
  //   7fdffbfe 1fffc0fc 7f81fe0 7fc1fffc 7f07fffe 7e0ffffe 3fffc1fc 7fc1fc0 1fe0fffc 7f83fffe 7*0 1f8000
  //   1c00000 20 4000000 5*0 c00 16*0 f80700 26*0 7000 c00000 e0000 18000 0 700 9*0 38000 16*0 780 18000
  //   e00000 0 30000 70000 0 0 0 80000 18*0 1c000 30000 0 0 0 e000 0 0 c0000 180000 0 0 180 0 0 0 80000 0
  //   0 0 300000 0 0 180 260 12*0 30000 19*0 10000 14*0 c000 3000 0 20000 4*0 c000 0 e0000 e0980 70000
  //   601c0 40000 1800c0 0 c0 7000 6040 0 0 0 180 0 300 600 38 38000 100 7000 6000 0 e0400 30 c00 30 e0000
  //   0 38000 0 0 1e000 2000 0 60 0 300000 0 240 0 60 120 0 100 200 18000 40180 1e0 0 f0000 30000 3000 c00
  //   0 780000 6*0 18000 0 0 0 c00 7000 0 c00 3c0000 700c0 18000 e0000 41*0 10000 0 7f000 28*0 1e000078 0
  //   3000000c 13*0 3000000c 38000 0 60000000 60000000 15*0 181c00 0 0 0 7e000 104*0 600000 c300000
  //   7000000 12*0 300000 70000 0 0 380000 60000 3000 7000 100400 0 0 3800 10000 0 38000 3000 400 0 200
  //   38000 18000 300 0 1c000 c03c00 7f0 0 38000 0 7c00 3800000 78000 60000 c000 70000 300 27*0 3c000
  //   3c000 0 0 3c000 3c000 0 0 3c000 3c000 8*0 24*3c000 8*0 24*3c000 579*0 3ffffc 3ff3fffc 3803800
  //   1803800 c380 7000 1c000 3800c00 7010 383038 7003ff0 181c00 dfff8 7ffff0 1ff181c0 c300700 3800020
  //   1c000 c0e000 3801c00 1c00 381c070 1fe00c00 18000 ff81c00 3ffffc0 18000 10 600e00 e10c00 c00000
  //   1c007f0 38e0700 40000 7006000 600c000 181800 38c1018 1c08600 8600 60 3023810 103000 6000 0 3806380
  //   8183300 6184010 1800010 1818030 383fff0 18000 7fffff0 7003c0 78000 1800c00 1ffffff8 387fff8 1c00018
  //   1ffc3800 1fc0018 7f83000 330018 30c008 3030420 18003f0 1807fc0 221fffc 3800ff0 18c003f0 1804600
  //   1801800 e03000 70030c0 38000 60000 1c01c20 601ffc 309ff8 3018618 3000c00 1ff00e08 3818010 3803000
  //   100e10 1800c00 7000c00 1c01800 6001c10 1c3800 c10e000 700000 1c018 fff8018 181c08 3ffffc0 c7ffe0
  //   e7ffc0 700e000 38000 300e000 183fff0 1c00180 703800 3003800 70e0060 c00018 181800 1c3000 c0000
  //   383800 c3ff8 1c3070 ffffc0 383fff0 e01800 101d0018 380200 1fff00 3801800 3800c00 30000 380c00 18000
  //   3803800 381c070 38ff7fc 1ffffffc 3ffffffc 1ff30c38 7018380 c1ffff8 ffff00 7007000 fffcffc 3803808
  //   3c01800 60c00 383818 381808 700e000 600e060 e00e060 1ffe0 e000 3008 e00030 10620e00 e638c00 60300
  //   c040600 c040600 ffe0610 e10c180 1ff60600 c60e008 3003000 3800c00 1ffc0ff8 c000 1e0001c 1c008 38000
  //   380c180 3860180 3018180 6001800 3800070 304030 1feffffc 38000 ee71c00 c671c00 7ff8038 3008 180c030
  //   6000340 c06001c 6081800 1c000 3000c00 7f80 18003000 3000018 3ffffff8 fffc0 700c0c0 380001c 7000
  //   380e00 c00 181800 180ffe0 1831d80 7001800 7001800 60038c0 e00e00 38018e0 3800c00 3801c00 e03800
  //   60000 c00600 ff00c00 ff01ce0 c030180 7001c00 1ffc00f0 30019c0 70000 31c0 c01c00 3801800 3ffffffc
  //   78000 1c000 7027010 700808 7007000 3001c00 30781808 703900 1c001c0 3000 1ffe01c0 10203ff8 1ff01ff0
  //   3ffffc0 3ffc038 183808 181c38 3f8030 f0000 7ffffe0 c3900 607001c 700e000 1800e00 381c00 1c01c00
  //   78000 6007000 183018 703ff80 30c1380 3006300 c3000 181810 7fffffc 1c01800 3a00018 3fc7fc0 63ff038
  //   7fffff0 183060c0 3000ff0 7ffffc0 381800 301c08 18000 301c00 3818300 400c008 1e3000 300e00 6001800
  //   38007f0 303020 f001c0 381c100 380e000 30070c0 700e100 301c200 3c00600 7000600 1c000 187fff0 617ffc
  //   ffff80 303b0030 387ffc0 1818380 e18700 e00780 1c03860 ffbffe0 3fffffc 8718700 181ffe0 3fff0 720060
  //   c0fff8 1800c00 3800600 601818 307f8 1c060ff8 c18380 1c00 3800c00 e0000 1800e00 30181c0 3b88630
  //   3c60000 6030380 3018408 ffffff8 3000030 18000 18001c0 7001c00 6040008 1ff07000 c01c00 1c0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
  //   contents of rom_6 (hex, n*v repeats v):
  //   4*0 1ff800 300c00 181800 0 70000 0 0 c3000 0 c0 3c00000 20c0 3cf8000 1c0 3000000 30 c000000 1b0
  //   18c00000 1800 100000 1bf0 d80000 180c0 3018000 1ffc0 3ff0000 18000 0 0 0 18000 c000030 7ffff80
  //   1ffffff8 4*0 180 18000 8060 0 0 3ffc00 6e00 ce00 5*0 300 30000 c000 70 7800000 0 0 0 18000 1e7800
  //   7e00000 1c00000 1c70000 f80fc00 ff000 c1ff830 800 7f800 1f801800 c3800 0 18000 18000 3ffc00 3ffc00
  //   3ffc00 3c000 3c000 ffffff0 ffffff0 18000 18000 c018030 0 0 18000 18000 3ffffffc 3c000 781c00 e03c0f0
  //   7800000 0 1c0 1c70 1ce38 f000000 7*0 1c000 7f800 7f800 1800 1ffe00 1f800 1fff00 7f000 7f000 c07c00
  //   c01800 c0fe00 c0fc00 c00300 1c1ff00 c07e00 c1ff00 c0fc00 c0fc00 7f07c00 30080c0 301c0c0 30180c0
  //   30000c0 30c38c0 301c0c0 31ff8c0 30180c0 301c0c0 31000c0 31004c0 3103ec0 3183cc0 31806c0 3187ec0
  //   3181ec0 310ffc0 3183cc0 3183cc0 33c1cc0 10*30000c0 0 0 10*30000c0 0 0 ff000 1fe3f80 7fcff3f8 fcf0078
  //   7f00fe0 3f81fffc 3f03def8 7c0ffbfc 1fcfc0f8 3fc0fc0 1fc07bf8 3f01cffc 5*0 ff807f0 1e00030 39e000
  //   1c00000 c0 3000000 0 18000 0 0 0 c00 5*0 180400 0 0 18000 6*0 1f80000 1e001c0 0 1ffe000 1e100
  //   1ff8000 1ffff00 1ffff00 7c000 3f81fc0 ff000 ff800 3fc3f80 1fe0000 f0000f0 7800fe0 38000 1fff000
  //   18000 1fff000 78000 ffff00 0 3f80fc0 f87e1f0 1fc1fc0 3f80fc0 7fff00 7000 e00000 e0000 3c000 0 380 0
  //   180000 0 1800 0 fc00 0 180000 18000 3c000 7c0000 78000 14*0 600 18000 700000 0 30000 70000 0 0 0
  //   60000 0 e0000 0 300000 0 1c0 80000 380 c000 30000 c03800 e1c0 0 100 3c0000 380000 380000 300000 e000
  //   38080 6000 7000 f000 3f000 e0000 c0000 e0000 c0000 0 0 c0 0 0 e0000 e0000 c0000 800000 60000 380000
  //   0 0 e0 260 0 c0 1c0 0 180 80700 0 0 0 600 0 19c0 38000 38000 300000 1c000 18000 0 0 0 8000 0 20000
  //   80000 300000 6000 1c0000 3000 0 80000 0 4000 30000 c0000 13*0 7000 3800 38000 38000 0 0 c000 c000
  //   e000 c0 e0000 e0e80 70000 700c0 60000 1c0640 0 60 303800 207270 f0000 0 1000 c0 70000 180 700 1d8
  //   38000 601c0 7800 f070 60800 70700 198 1fe00 7c18 f0000 401c0 38000 3800 1800 e000 3800 0 230 1c0
  //   1c0000 300 640 1c00 330 320 0 1c0 780 1e000 78cc0 78320 0 3e000 38000 1c00 1fe00 380000 380000 0 0
  //   3000 1800 fc00 7800 e000 380000 0 0 807e00 7000 0 dffe00 1e0000 70760 1e000 70000 22*0 18000 4*0
  //   101e00 7e000 0 0 3c000 9*0 fe000 0 e3800 0 7e000 0 3e000 0 0 3c0000 0 0 1fe000 6*0 1c000 11*0
  //   7c001e0 0 38000018 13*0 1ffc7ffc 38000 0 60000000 60000000 10*0 fffe00 1ffe000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
  //   contents of rom_7 (hex, n*v repeats v):
  //   4*0 3ffc00 1c3800 3c3c00 0 60000 0 0 c3000 0 180 3c00000 6180 3cf8000 180 1800000 60 c000000 330
  //   cc00000 1800 100000 1be0 d80000 18180 1818000 1ff80 1ff0000 18000 80 38000 18000 3c000 c000030
  //   3ffff80 ffffff0 0 3c000 0 1800180 180 18000 c060 18 0 780e00 ce00 cc00 5*0 300 30000 c000 3e0
  //   3e00000 0 1c00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
  //   contents of rom_8 (hex, n*v repeats v):
  //   5*0 77000 3c3c00 0 60000 0 0 c3000 0 180 3c00000 c180 3c78000 300 c00000 60 6000000 320 c600000 1800
  //   100000 1a00 d80000 18180 1c18000 1ff00 ff0000 18000 30001c0 7c000 3c000 3c000 6000060 3800380
  //   1c00380 1800180 1ff800 0 3c003c0 180 18000 180c0 70 0 1c00300 c000 c000 5*0 600 30000 c000 1f00
  //   7c0000 0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
  //   contents of rom_9 (hex, n*v repeats v):
  //   5*0 3c000 181800 0 c0000 0 0 c3000 0 300 c00000 1c300 c30000 600 600000 c0 6000000 660 6600000 1800
  //   100000 1a00 d80000 18300 c18000 1ff00 ff0000 18000 1800380 7c000 7e000 66000 6000060 1c00080 1c00380
  //   1800180 7ffe00 3fffc0 3e007c0 300 18000 380c0 e0 7e000 3800180 c000 c000 0 1800f80 0 0 0 c00 30038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
  //   contents of rom_10 (hex, n*v repeats v):
  //   5*0 18000 0 0 c0300 0 0 c3000 0 3c0 1800000 1e3c0 1830000 400 600000 c0 3000000 660 6300000 1800
  //   100000 1a00 d80000 18600 618000 1fe00 7f0000 18000 c00700 7c000 3c000 66000 30000c0 e000c0 1c00380
  //   1800180 e00700 7fffc0 3e007c0 300 18000 30180 1c0 3ffc00 30000c0 18000 1c000 0 7803fe0 0 0 0 c00
  //   301f0 f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
  //   contents of rom_11 (hex, n*v repeats v):
  //   8*0 187f80 0 0 c3000 0 7c0 1000000 1f7c0 1060000 400 600000 180 3000000 cc0 3300000 1800 100000 1a00
  //   d80000 18600 618000 1fc00 7f0000 18000 600e00 38000 3c000 63000 30000c0 e00040 1c00380 1800180
  //   c00300 e00000 3c003c0 300 18000 60180 380 f00f00 6000060 18000 1c000 ffffff0 e007070 f00000 0 0 1800
  //   30f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
  //   contents of rom_12 (hex, n*v repeats v):
  //   7*0 31c00 1ff700 0 0 c3000 0 3c0 2000000 1f3c0 20c0000 400 600000 180 1800000 cc0 3180000 1800
  //   100000 1a00 d80000 18c00 318000 1fc00 3f0000 18000 301c00 0 0 c3000 1800180 700000 1c00380 1800180
  //   1c00380 1800000 800100 600 18000 60300 700 1c00380 e000060 18000 1c000 1ffffff8 c00c030 3fc0000
  //   800700 f00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
  //   contents of rom_13 (hex, n*v repeats v):
  //   7*0 71c00 360600 0 0 c3000 0 3c0 4000000 1e3c0 4180000 400 600000 300 1800000 1980 1980000 1800
  //   100000 1a00 d80000 18c00 318000 1fc00 3f0000 18000 183800 0 0 c1800 1800180 780000 1c00380 1800180
  //   1800180 3800000 0 600 18000 c0300 e00 38001c0 c000030 18000 7f000 0 1c018038 70f0018 7803fc0 3fc07f0
  //   1fff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
  //   contents of rom_14 (hex, n*v repeats v):
  //   0 0 0 3c000 0 0 0 73800 200600 0 1e00000 c3000 0 80 0 4080 0 400 600000 300 c00000 1980 18c0000 1800
  //   100000 1a00 d80000 18800 318000 1f800 3f0000 18000 c7000 0 0 181800 c00300 380000 1c00380 1800180
  //   1800180 3000000 0 600 18000 c0600 1c00 60000e0 c000030 18000 fb800 0 1c030038 c03c030 e0070e0
  //   70f1e00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
  //   contents of rom_15 (hex, n*v repeats v):
  //   0 0 0 7e000 0 0 0 63800 400c00 0 7f80008 c3000 e03c070 4*0 400 600000 600 c00000 3300 cc0000 1800
  //   100000 1a00 d80000 19800 118000 1f800 3f0000 7ffffe0 6e000 0 0 181800 c00300 1c0000 1c00380 1800180
  //   1800180 3000000 0 c00 18000 180600 3800 e000070 1c038030 18000 198c00 0 c070030 1800f0e0 c00c030
  //   c03b0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
  //   contents of rom_16 (hex, n*v repeats v):
  //   0 0 0 ff000 0 0 0 e3000 800c00 0 e1f0018 c3000 1f07c0f8 4*0 400 600000 600 600000 3300 c60000 1800
  //   100000 1a00 d80000 19800 198000 1f800 3f0000 7ffffe0 3c000 0 0 300c00 600600 1e0000 1c00380 1800180
  //   1800180 3ffff80 0 c00 18000 180c00 6000 c000030 1807c030 18000 198c00 0 e0e0070 3fc0 1801c030
  //   1801e00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
  //   contents of rom_17 (hex, n*v repeats v):
  //   0 0 0 ff000 0 0 0 c7000 1800 ffffffff 1803e030 c3000 1f07e1f8 4*0 400 600000 c00 600000 6600 460000
  //   1800 100000 1a00 d80000 19800 198000 1f800 3f0000 18000 38000 ffffff0 0 300c00 600600 e0000 1c00380
  //   1800180 1800180 3ffffc0 0 c00 18000 301c00 c000 18000018 1807e038 18000 198c00 1ffffff8 7fc01e0 f00f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
  //   contents of rom_18 (hex, n*v repeats v):
  //   0 0 0 ff000 0 0 0 c6000 1000 0 10007fe0 c3000 1f07c0f8 4*0 400 600000 600 600000 3300 c60000 1800
  //   100000 1a00 d80000 19800 198000 1f800 3f0000 18000 3c000 7ffffe0 0 600600 300c00 70000 1c00380
  //   1800180 1800180 3ffff80 0 1800 18000 301800 18000 18000018 1807c030 18000 198c00 0 1f00180 3fc0000
  //   1c030030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
  //   contents of rom_19 (hex, n*v repeats v):
  //   0 0 0 fe000 0 0 0 186000 3000 0 20000fc0 c3000 e03c0f0 4*0 400 600000 600 c00000 3300 cc0000 1800
  //   100000 1a00 d80000 19800 118000 1f800 3f0000 18000 6e000 0 0 600600 300c00 60000 1c00380 1800180
  //   1800180 3000000 0 181800 18000 603800 30000 10000008 1c03c030 18000 199c00 0 0 70f0018 c0e0070
  //   e03b800 30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
  //   contents of rom_20 (hex, n*v repeats v):
  //   0 0 0 7e000 0 0 0 18c000 42000 0 100 c3000 5*0 400 600000 300 c00000 3180 18c0000 1800 100000 1a00
  //   d80000 18800 318000 1f800 3f0000 18000 c7000 0 0 c00300 181c00 c0000 1c00380 1800180 1800180 3000000
  //   0 3c1800 18000 603000 60000 0 c000030 18000 db800 0 0 c03c030 7bc01e0 7ff1ff0 1ffffff0 3f0000 f800 1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
  //   contents of rom_21 (hex, n*v repeats v):
  //   7*0 10c000 36000 0 0 c3000 5*0 400 600000 300 1800000 1980 1980000 1800 100000 1a00 d80000 18c00
  //   318000 1fc00 3f0000 18000 183800 0 0 c00300 181800 180000 1c00380 1800180 1800180 3800000 0 6e3000
  //   18000 c06000 c0000 0 c000030 18000 7f000 0 1ffffff8 1800f0e0 3f803c0 3fc07e0 1ffffff0 7e000 7c000
  //   f8001f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
  //   contents of rom_22 (hex, n*v repeats v):
  //   0 1c000000 3c00000 4*0 308000 1c000 0 0 c3000 5*0 400 600000 180 1800000 18c0 3180000 1800 100000
  //   1a00 d80000 18c00 218000 1fc00 7f0000 18000 301c00 0 0 1800180 c3800 380000 1c00380 1800300 1800180
  //   1800000 0 73000 18000 c06000 180000 0 c000070 18000 3c000 1ffffff8 ffffff0 3fc0 0 0 c0000 3fc00
  //   3ec000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
  //   contents of rom_23 (hex, n*v repeats v):
  //   0 f000000 7e00000 4*0 200000 e000 0 0 c3000 5*0 400 600000 180 3000000 cc0 3300000 1800 100000 1a00
  //   d80000 18600 618000 1fc00 7f0000 18000 600e00 38000 38000 1800180 c3000 300000 1c00380 c00300
  //   1800180 e00000 3c003c0 73000 18000 180c000 300000 0 6000060 18000 18000 ffffff0 0 f00 0 0 180000
  //   31f80 1f0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
  //   contents of rom_24 (hex, n*v repeats v):
  //   0 3c00000 c200000 5*0 7000 0 0 c3000 5*0 400 600000 c0 3000000 c60 6300000 1800 100000 1a00 d80000
  //   18600 e18000 1fe00 7f0000 18000 c00700 7c000 7c000 1000180 67000 600040 1c00380 e00600 1800180
  //   7fff80 3c007c0 3f000 18000 180c000 600000 0 70000e0 38000 18000 5*0 300000 303f0 f80c000 fc000 3f000
  //   0 7e0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
  //   contents of rom_25 (hex, n*v repeats v):
  //   0 1e00000 c300000 5*0 7800 0 0 c3000 5*0 400 600000 c0 6000000 660 6600000 1800 100000 1a00 d80000
  //   18300 c18000 1fe00 ff0000 18000 1800380 7c000 7c000 30000c0 66000 c000c0 1c00380 7c3c00 1800180
  //   3fffc0 7e007c0 1e000 18000 3018000 c00000 0 38001c0 30000 18000 5*0 300000 30078 1e00c000 1f800
  //   f8000 0 7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
  //   contents of rom_26 (hex, n*v repeats v):
  //   0 e00000 c300000 5*0 3800 0 0 c3000 5*0 600 c00000 60 6000000 660 c600000 1800 100000 1a00 d80000
  //   18300 1818000 1ff00 1ff0000 0 30001c0 7c000 3c000 30000c0 3e000 1c00180 1c00380 1ff800 1800180 0
  //   3c007c0 e000 18000 7018000 3800000 0 1c00380 30000 30000 0 ffffff0 0 0 0 600000 30000 c000 3f00
  //   7c0000 0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
  //   contents of rom_27 (hex, n*v repeats v):
  //   0 e00000 6600000 5*0 1000 0 0 c3000 5*0 300 1800000 60 c000000 330 cc00000 1800 100000 1a00 fd80000
  //   18180 3818000 1ff80 1ff0000 0 80 38000 38000 6000060 3c000 1ffff80 1c00380 7c000 1800180 0 1800380
  //   e000 18000 6030000 7000000 0 f00f00 330000 3b0000 0 ffffff0 0 0 0 c00000 30000 c000 7e0 3e00000 0
  //   3c0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
  //   contents of rom_28 (hex, n*v repeats v):
  //   0 600000 3c00000 8*0 c3000 5*0 180 3000000 60 c000000 330 18c00000 1800 100000 1a00 fd80000 180c0
  //   3018000 1ff80 3ff0000 7ffffe0 0 0 0 6000060 1c000 3ffff80 ff01ff0 4*0 4000 ffffff0 6030000 fffffe0 0
  //   3ffc00 330000 3f0000 5*0 400000 30000 c000 f0 7000000 0 0 0 1ff800 18000 0 0 0 1fc00 dff800 c1ff830
  //   1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
  //   contents of rom_29 (hex, n*v repeats v):
  //   0 600000 1000000 8*0 c3000 5*0 c0 6000000 30 18000000 198 19800000 1800 100000 1a00 c180000 18060
  //   7ff8000 1ffc0 7ff0000 7ffffe0 0 0 0 c000030 18000 7ffff80 ff01ff0 9*0 ff000 3e0000 3e0000 6*0 30000
  //   c000 10 4*0 fe000 18000 4*0 7e000 18018010 0 0 3c0f0 1c7000 0 1800180 1800180 7e000 3c000 3c000
  //   18000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
  //   contents of rom_30 (hex, n*v repeats v):
  //   11*0 c3000 5*0 40 0 10 8000000 108 10800000 1800 ff00000 1e00 ff80000 1fff0 fff8000 1ffe0 7ff0000
  //   4*0 20 8000 12*0 80000 14*0 18000 5*0 18000 4*0 fe000 0 1000080 1000080 12*0 18000 58*0 f00700
  //   9*e00f00 39*0 8000000 0 0 200000 11*0 3000000 4*0 1ffc00 16*0 700 9*0 7ff0 380 7fe0000 9*0 3ff800 0
  //   0 ff000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
  //   contents of rom_31 (hex, n*v repeats v):
  //   24*0 7f00000 e00 7f00000 0 0 ffe0 7fe0000 119*0 10*3ffc00 54*0 6000000 4*0 3c000 26*0 7ff0 0 ffe0000
  //   9*0 1fe000 0 0 7e0000 5*0 7e0000 7f00 7*0 3c0000 0 0 10000 271*0 38000 0 60000000 70000000 77*0
  //   300000 56*0 38700000 22*0 80000 44*0 3c000 3c000 0 0 3c000 3c000 0 0 10*3c000 8*0 24*3c000 8*0
  //   16*3c000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
  //   contents of rom_32 (hex, n*v repeats v):
  //   150*0 10*7e000 88*0 7fc0000 0 ffffffff 16*0 7e0000 3e00 282*0 10000 0 60000000 70000000 134*0
  //   1fe00000 67*0 3c000 3c000 0 0 3c000 3c000 0 0 10*3c000 8*0 24*3c000 8*0 16*3c000 25*0 3c00 fc0ffff
  //   556*0 1000000 11*0 4 17*0 800000 800000 10*0 80000 4*0 400000 29*0 200000 20*0 20000 0 0 2000 19*0
  //   40000 22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
  //   字库电路
endmodule
