// Logisim project 算术逻辑单元.circ as structural Verilog: 4 circuits, main circuit 1位全加器FA
// ALU
module \_32位ALU_算术逻辑单元  (
  input  [31:0] X,
  input  [31:0] Y,
  input  [3:0] AluOP,
  output OF,
  output UOF,
  output Equal,
  output [31:0] Result1,
  output [31:0] Result2
);

  wire \n32位加法器_1_c31 , \n32位加法器_1_c32 , \n32位加法器_2_c31 , \n32位加法器_2_c32 , not_2_out, xor_2_out, xor_3_out;
  wire [0:0] comparator_1_lt, comparator_2_lt;
  wire [31:0] AND_out, divider_1_out, divider_1_rem, multiplier_1_cout, multiplier_1_out, \n32位加法器_1_s ,
       \n32位加法器_2_s , NOR_out, not_1_out, OR_out, shifter_1_out, shifter_2_out, shifter_3_out, XOR_out;

  // Probe on X
  assign not_1_out = ~Y;  // NOT_Gate not_1, 32 bits wide
  // Probe on Y
  Shifter #(.width(32), .shift("ll")) shifter_1 (.in(X), .\dist (Y[4:0]), .out(shifter_1_out));
  Shifter #(.width(32), .shift("ar")) shifter_2 (.in(X), .\dist (Y[4:0]), .out(shifter_2_out));
  Shifter #(.width(32), .shift("lr")) shifter_3 (.in(X), .\dist (Y[4:0]), .out(shifter_3_out));
  Multiplier #(.width(32)) multiplier_1 (.a(X), .b(Y), .out(multiplier_1_out), .cout(multiplier_1_cout));  // open: cin
  Divider #(.width(32)) divider_1 (.a(X), .b(Y), .out(divider_1_out), .rem(divider_1_rem));  // open: upper
  \_32位加法器  \u_32位加法器_1  (
    .X(X), .Y(Y), .C0(1'b0), .S(\n32位加法器_1_s ), .C31(\n32位加法器_1_c31 ), .C32(\n32位加法器_1_c32 ));  // open: OF
  \_32位加法器  \u_32位加法器_2  (
    .X(X), .Y(not_1_out), .C0(1'b1), .S(\n32位加法器_2_s ), .C31(\n32位加法器_2_c31 ), .C32(\n32位加法器_2_c32 ));  // open: OF
  assign AND_out = X & Y;  // AND_Gate AND, 32 bits wide
  assign OR_out = X | Y;  // OR_Gate OR, 32 bits wide
  assign XOR_out = X ^ Y;  // XOR_Gate XOR, 32 bits wide
  assign NOR_out = ~(X | Y);  // NOR_Gate NOR, 32 bits wide
  Comparator #(.width(32), .mode("twosComplement")) comparator_1 (
    .a(X), .b(Y), .eq(Equal), .lt(comparator_1_lt[0]));  // open: gt
  Comparator #(.width(32), .mode("unsigned")) comparator_2 (.a(X), .b(Y), .lt(comparator_2_lt[0]));  // open: gt, eq
  xor xor_2 (xor_2_out, \n32位加法器_1_c31 , \n32位加法器_1_c32 );
  xor xor_3 (xor_3_out, \n32位加法器_2_c31 , \n32位加法器_2_c32 );
  not not_2 (not_2_out, \n32位加法器_2_c32 );
  // Probe on AluOP
  // Probe on Result1
  Multiplexer #(.select(4), .width(32), .disabled("Z"), .enable("false")) multiplexer_1 (
    .in0(shifter_1_out), .in1(shifter_2_out), .in2(shifter_3_out), .in3(multiplier_1_out),
    .in4(divider_1_out), .in5(\n32位加法器_1_s ), .in6(\n32位加法器_2_s ), .in7(AND_out), .in8(OR_out),
    .in9(XOR_out), .in10(NOR_out), .in11({{31{1'b0}}, comparator_1_lt[0]}),
    .in12({{31{1'b0}}, comparator_2_lt[0]}), .in13({32{1'b0}}), .in14({32{1'b0}}), .in15({32{1'b0}}),
    .out(Result1), .sel(AluOP));
  Multiplexer #(.select(4), .width(32), .disabled("Z"), .enable("false")) multiplexer_2 (
    .in0({32{1'b0}}), .in1({32{1'b0}}), .in2({32{1'b0}}), .in3(multiplier_1_cout), .in4(divider_1_rem),
    .in5({32{1'b0}}), .in6({32{1'b0}}), .in7({32{1'b0}}), .in8({32{1'b0}}), .in9({32{1'b0}}),
    .in10({32{1'b0}}), .in11({32{1'b0}}), .in12({32{1'b0}}), .in13({32{1'b0}}), .in14({32{1'b0}}),
    .in15({32{1'b0}}), .out(Result2), .sel(AluOP));
  Multiplexer #(.select(4), .width(1), .disabled("Z"), .enable("false")) multiplexer_3 (
    .in0(1'b0), .in1(1'b0), .in2(1'b0), .in3(1'b0), .in4(1'b0), .in5(\n32位加法器_1_c32 ), .in6(not_2_out),
    .in7(1'b0), .in8(1'b0), .in9(1'b0), .in10(1'b0), .in11(1'b0), .in12(1'b0), .in13(1'b0), .in14(1'b0),
    .in15(1'b0), .out(UOF), .sel(AluOP));
  Multiplexer #(.select(4), .width(1), .disabled("Z"), .enable("false")) multiplexer_4 (
    .in0(1'b0), .in1(1'b0), .in2(1'b0), .in3(1'b0), .in4(1'b0), .in5(xor_2_out), .in6(xor_3_out), .in7(1'b0),
    .in8(1'b0), .in9(1'b0), .in10(1'b0), .in11(1'b0), .in12(1'b0), .in13(1'b0), .in14(1'b0), .in15(1'b0),
    .out(OF), .sel(AluOP));
  // Probe on Result2

  // Notes on the sheet:
  //   X: pull=down
  //   Y: pull=down
  //   AluOP: pull=down
  //   输入引脚
  //   输入：X、Y、AluOP（运算功能）            输出：Result1、Result2（乘法运算乘积的高32位、除法运算的余数）               
  //   32位ALU（算术逻辑单元）
  //   OF：有符号数加减法的溢出标志      UOF：无符号数加减法的溢出标志       Equal：有符号数比较相等标志          
  //   输出引脚
  //   AluOP    运算功能
  //   0000      逻辑左移
  //   0001      算术右移
  //   0010      逻辑右移
  //   0011      乘法运算
  //   0100      除法运算
  //   0101      加法运算
  //   0110      减法运算
  //   0111      逻辑与运算
  //   1000      逻辑或运算
  //   1001      逻辑异或运算
  //   1010      逻辑或非运算
  //   1011      有符号数比较
  //   1100      无符号数比较
endmodule

module \_32位加法器  (
  input  C0,
  input  [31:0] X,
  input  [31:0] Y,
  output C32,
  output C31,
  output OF,
  output [31:0] S
);

  wire \n8位加法器_2_c8 , \n8位加法器_3_c8 , \n8位加法器_4_c8 ;

  xor xor_1 (OF, C31, C32);
  \_8位加法器  \u_8位加法器_1  (.X(X[31:24]), .Y(Y[31:24]), .C0(\n8位加法器_2_c8 ), .S(S[31:24]), .C8(C32), .C7(C31));  // open: OF
  \_8位加法器  \u_8位加法器_2  (
    .X(X[23:16]), .Y(Y[23:16]), .C0(\n8位加法器_3_c8 ), .S(S[23:16]), .C8(\n8位加法器_2_c8 ));  // open: C7, OF
  // Probe on X
  // Probe on Y
  // Probe on S
  \_8位加法器  \u_8位加法器_3  (.X(X[15:8]), .Y(Y[15:8]), .C0(\n8位加法器_4_c8 ), .S(S[15:8]), .C8(\n8位加法器_3_c8 ));  // open: C7, OF
  \_8位加法器  \u_8位加法器_4  (.X(X[7:0]), .Y(Y[7:0]), .C0(C0), .S(S[7:0]), .C8(\n8位加法器_4_c8 ));  // open: C7, OF
  // Probe on X
  // Probe on Y
  // Probe on S

  // Other names for the same wires on the sheet: S0[7:0] = S[7:0]; S1[7:0] = S[15:8]; S2[7:0] = S[23:16];
  //   S3[7:0] = S[31:24]; X0[7:0] = X[7:0]; X1[7:0] = X[15:8]; X2[7:0] = X[23:16]; X3[7:0] = X[31:24];
  //   Y0[7:0] = Y[7:0]; Y1[7:0] = Y[15:8]; Y2[7:0] = Y[23:16]; Y3[7:0] = Y[31:24]

  // Notes on the sheet:
  //   C0: pull=down
  //   Y: pull=down
  //   X: pull=down
  //   输入引脚区
  //   输出引脚区
  //   +
  //   =
  //   输入：X、Y、C0                             输出：S、C32、C31、OF
  //   有符号加法
  //   32位加法器
  //   +
  //   =
  //   无符号加法
endmodule

module \_8位加法器  (
  input  [7:0] X,
  input  [7:0] Y,
  input  C0,
  output [7:0] S,
  output C8,
  output C7,
  output OF
);

  wire \n1位全加器fa_3_cout , \n1位全加器fa_4_cout , \n1位全加器fa_5_cout , \n1位全加器fa_6_cout , \n1位全加器fa_7_cout ,
       \n1位全加器fa_8_cout ;

  xor xor_1 (OF, C8, C7);
  \_1位全加器FA  \u_1位全加器fa_1  (.Cout(C8), .Si(S[7]), .Cin(C7), .Xi(X[7]), .Yi(Y[7]));
  \_1位全加器FA  \u_1位全加器fa_2  (.Cout(C7), .Si(S[6]), .Cin(\n1位全加器fa_3_cout ), .Xi(X[6]), .Yi(Y[6]));
  \_1位全加器FA  \u_1位全加器fa_3  (.Cout(\n1位全加器fa_3_cout ), .Si(S[5]), .Cin(\n1位全加器fa_4_cout ), .Xi(X[5]), .Yi(Y[5]));
  \_1位全加器FA  \u_1位全加器fa_4  (.Cout(\n1位全加器fa_4_cout ), .Si(S[4]), .Cin(\n1位全加器fa_5_cout ), .Xi(X[4]), .Yi(Y[4]));
  \_1位全加器FA  \u_1位全加器fa_5  (.Cout(\n1位全加器fa_5_cout ), .Si(S[3]), .Cin(\n1位全加器fa_6_cout ), .Xi(X[3]), .Yi(Y[3]));
  \_1位全加器FA  \u_1位全加器fa_6  (.Cout(\n1位全加器fa_6_cout ), .Si(S[2]), .Cin(\n1位全加器fa_7_cout ), .Xi(X[2]), .Yi(Y[2]));
  \_1位全加器FA  \u_1位全加器fa_7  (.Cout(\n1位全加器fa_7_cout ), .Si(S[1]), .Cin(\n1位全加器fa_8_cout ), .Xi(X[1]), .Yi(Y[1]));
  // Probe on X
  // Probe on Y
  // Probe on S
  \_1位全加器FA  \u_1位全加器fa_8  (.Cout(\n1位全加器fa_8_cout ), .Si(S[0]), .Cin(C0), .Xi(X[0]), .Yi(Y[0]));
  // Probe on X
  // Probe on Y
  // Probe on S

  // Notes on the sheet:
  //   Y: pull=down
  //   C0: pull=down
  //   X: pull=down
  //   输入引脚区
  //   符号位
  //   输出引脚区
  //   8位串行加法器
  //   +
  //   =
  //   有符号加法
  //   +
  //   =
  //   无符号加法
endmodule

// FA
module \_1位全加器FA  (
  input  Cin,
  input  Xi,
  input  Yi,
  output Cout,
  output Si
);

  wire AND_2_out, AND_out, XOR_2_out;

  or OR (Cout, AND_out, AND_2_out);
  and AND (AND_out, Xi, Yi);
  and AND_2 (AND_2_out, Cin, XOR_2_out);
  xor XOR (Si, Cin, XOR_2_out);
  xor XOR_2 (XOR_2_out, Xi, Yi);

  // Notes on the sheet:
  //   Xi: pull=down
  //   Cin: pull=down
  //   Yi: pull=down
  //   Si = Xi ^ Yi ^ Cin
  //   Cout = Xi Yi + Cin (Xi ^ Yi)
  //   1位全加器（FA）
endmodule
