// Logisim project 原码和补码一位乘法器（答案）.circ as structural Verilog: 6 circuits, main circuit 1位全加器（FA）
// 8位无符号一位乘法器
module \_8位无符号数一位乘法器  (
  input  [7:0] X,
  input  [7:0] Y,
  output [15:0] \乘积 
);

  wire CLK, comparator_1_eq, d_ff_1_q, END, not_1_out, RST;
  wire [0:0] \n8位串行加法器_1_s ;
  wire [3:0] counter_1_q;
  wire [7:0] multiplexer_1_out, multiplexer_2_out, \n8位串行加法器_1_cout ;

  Button \u_复位  (.out(RST));
  // Probe on \乘积 [15:8]
  Register #(.width(8), .trigger("rising"), .Select("low")) register_1 (
    .D(\n8位串行加法器_1_cout ), .en(not_1_out), .Q(\乘积 [15:8]), .clk(CLK), .clr(RST));
  \_8位串行加法器  \u_8位串行加法器_1  (
    .X(\乘积 [15:8]), .Y(multiplexer_1_out), .Cin(1'b0), .S({\n8位串行加法器_1_cout [6:0], \n8位串行加法器_1_s [0]}),
    .Cout(\n8位串行加法器_1_cout [7]));  // open: out_6
  Multiplexer #(.select(1), .width(8), .disabled("Z"), .enable("false")) multiplexer_1 (
    .in0({8{1'b0}}), .in1(X), .out(multiplexer_1_out), .sel(\乘积 [0]));
  Button u_CLK (.out(CLK));
  Multiplexer #(.select(1), .width(8), .disabled("Z"), .enable("false")) multiplexer_2 (
    .in0(Y), .in1({\n8位串行加法器_1_s [0], \乘积 [7:1]}), .out(multiplexer_2_out), .sel(d_ff_1_q));
  // Probe on \乘积 [7:0]
  Register #(.width(8), .trigger("rising"), .Select("low")) Y_2 (
    .D(multiplexer_2_out), .en(not_1_out), .Q(\乘积 [7:0]), .clk(CLK), .clr(RST));
  Counter #(.width(4), .max('hf), .ongoal("wrap"), .trigger("rising"), .behavior("old")) counter_1 (
    .count(not_1_out), .Q(counter_1_q), .clk(CLK), .clr(RST));  // open: load, D, carry, preset
  D_Flip_Flop #(.trigger("rising"), .Pre_Clr_Positions("LEGACY"), .NegatePresetClear("false"), .enable("true"), .NewFFLayout("false")) d_ff_1 (
    .clk(CLK), .D(1'b1), .Q(d_ff_1_q), .reset(RST));  // open: Qn, preset, en
  Comparator #(.width(4), .mode("unsigned")) comparator_1 (
    .a(counter_1_q), .b(4'b1001), .eq(comparator_1_eq));  // open: gt, lt
  not not_1 (not_1_out, comparator_1_eq);
  LED #(.active("true")) led_1 (.in(END));
  not not_2 (END, not_1_out);
  // Probe on X
  // Probe on Y
  // Probe on \乘积 

  // Other names for the same wires on the sheet: P[15:0] = \乘积 

  // Notes on the sheet:
  //   输入引脚区
  //   ∑
  //   功能说明: 8位无符号数一位乘法器                输入：X、Y 为8位无符号数               输出：乘积=X*Y 为16位无符号数
  //   首先设置X、Y值，然后按“复位”按钮，接下去按“CLK”按钮多次，直到“END”指示灯变红，此时观看乘积是不是正确？
  //   8位无符号数一位乘法器
  //   输出引脚区
  //   ×
  //   =
endmodule

// 8位无符号数一位乘法器
module \_8位无符号数一位乘法器_封装用  (
  input  [7:0] X,
  input  [7:0] Y,
  input  in_3,
  input  in_4,
  output [15:0] \乘积 ,
  output out_6
);

  wire comparator_1_eq, d_ff_1_q, not_1_out;
  wire [0:0] \n8位串行加法器_1_s ;
  wire [3:0] counter_1_q;
  wire [7:0] multiplexer_1_out, multiplexer_2_out, \n8位串行加法器_1_cout ;

  // Probe on \乘积 [15:8]
  Register #(.width(8), .trigger("rising"), .Select("low")) register_1 (
    .D(\n8位串行加法器_1_cout ), .en(not_1_out), .Q(\乘积 [15:8]), .clk(in_4), .clr(in_3));
  \_8位串行加法器  \u_8位串行加法器_1  (
    .X(\乘积 [15:8]), .Y(multiplexer_1_out), .Cin(1'b0), .S({\n8位串行加法器_1_cout [6:0], \n8位串行加法器_1_s [0]}),
    .Cout(\n8位串行加法器_1_cout [7]));  // open: out_6
  Multiplexer #(.select(1), .width(8), .disabled("Z"), .enable("false")) multiplexer_1 (
    .in0({8{1'b0}}), .in1(X), .out(multiplexer_1_out), .sel(\乘积 [0]));
  Multiplexer #(.select(1), .width(8), .disabled("Z"), .enable("false")) multiplexer_2 (
    .in0(Y), .in1({\n8位串行加法器_1_s [0], \乘积 [7:1]}), .out(multiplexer_2_out), .sel(d_ff_1_q));
  // Probe on \乘积 [7:0]
  Register #(.width(8), .trigger("rising"), .Select("low")) Y_2 (
    .D(multiplexer_2_out), .en(not_1_out), .Q(\乘积 [7:0]), .clk(in_4), .clr(in_3));
  Counter #(.width(4), .max('hf), .ongoal("wrap"), .trigger("rising"), .behavior("old")) counter_1 (
    .count(not_1_out), .Q(counter_1_q), .clk(in_4), .clr(in_3));  // open: load, D, carry, preset
  D_Flip_Flop #(.trigger("rising"), .Pre_Clr_Positions("LEGACY"), .NegatePresetClear("false"), .enable("true"), .NewFFLayout("false")) d_ff_1 (
    .clk(in_4), .D(1'b1), .Q(d_ff_1_q), .reset(in_3));  // open: Qn, preset, en
  Comparator #(.width(4), .mode("unsigned")) comparator_1 (
    .a(counter_1_q), .b(4'b1001), .eq(comparator_1_eq));  // open: gt, lt
  not not_1 (not_1_out, comparator_1_eq);
  LED #(.active("true")) led_1 (.in(out_6));
  not not_2 (out_6, not_1_out);
  // Probe on X
  // Probe on Y
  // Probe on \乘积 

  // Other names for the same wires on the sheet: CLK = in_4; END = out_6; P[15:0] = \乘积 ; RST = in_3

  // Notes on the sheet:
  //   输入引脚区
  //   ∑
  //   功能说明: 8位无符号数一位乘法器                输入：X、Y为8位无符号数               输出：乘积=X*Y，为16位无符号数
  //   首先设置X、Y值，然后按“复位”按钮，接下去按“CLK”按钮多次，直到“END”指示灯变红，此时观看乘积是不是正确？
  //   8位无符号数一位乘法器（封装用）
  //   输出引脚区
  //   =
endmodule

module \_8位原码一位乘法器_答案  (
  input  [7:0] X,
  input  [7:0] Y,
  output [15:0] \乘积 
);

  wire CLK, END, RST;
  wire [7:0] adder_1_out, adder_2_out, X_prime, \X真值 , Y_prime, \Y真值 ;
  wire [15:0] adder_3_out, P_prime, \P真值 ;
  wire [15:15] P_t;

  Adder #(.width(8)) adder_1 (.a(X), .b(8'h80), .out(adder_1_out));  // open: cin, cout
  Adder #(.width(8)) adder_2 (.a(Y), .b(8'h80), .out(adder_2_out));  // open: cin, cout
  Adder #(.width(16)) adder_3 (.a(\乘积 ), .b(16'h8000), .out(adder_3_out));  // open: cin, cout
  Button \u_复位  (.out(RST));
  Subtractor #(.width(8)) subtractor_1 (.a({8{1'b0}}), .b(adder_1_out), .out(X_prime));  // open: bin, bout
  Subtractor #(.width(8)) subtractor_2 (.a({8{1'b0}}), .b(adder_2_out), .out(Y_prime));  // open: bin, bout
  Subtractor #(.width(16)) subtractor_3 (.a({16{1'b0}}), .b(adder_3_out), .out(P_prime));  // open: bin, bout
  Button u_CLK (.out(CLK));
  \_8位无符号数一位乘法器_封装用  \u_8位无符号数一位乘法器_封装用_1  (
    .X({1'b0, X[6:0]}), .Y({1'b0, Y[6:0]}), .in_3(RST), .in_4(CLK), .out_6(END), .\乘积 ({P_t[15], \乘积 [14:0]}));
  LED #(.active("true")) led_1 (.in(END));
  Multiplexer #(.select(1), .width(8), .disabled("Z"), .enable("false")) multiplexer_1 (
    .in0(X), .in1(X_prime), .out(\X真值 ), .sel(X[7]));
  Multiplexer #(.select(1), .width(8), .disabled("Z"), .enable("false")) multiplexer_2 (
    .in0(Y), .in1(Y_prime), .out(\Y真值 ), .sel(Y[7]));
  Multiplexer #(.select(1), .width(16), .disabled("Z"), .enable("false")) multiplexer_3 (
    .in0(\乘积 ), .in1(P_prime), .out(\P真值 ), .sel(\乘积 [15]));
  xor xor_1 (\乘积 [15], X[7], Y[7]);
  // Probe on \P真值 
  // Probe on \X真值 
  // Probe on \Y真值 

  // Other names for the same wires on the sheet: P[15:0] = \乘积 ; P15 = \乘积 [15]; P_t[14:0] = \乘积 [14:0];
  //   X_t[6:0] = X[6:0]; Y_t[6:0] = Y[6:0]

  // Notes on the sheet:
  //   输入引脚区
  //   功能说明: 8位原码一位乘法器                输入：X、Y 为8位原码               输出：乘积=X*Y 为16位原码
  //   首先设置X、Y值，然后按“复位”按钮，接下去按“CLK”按钮多次，直到“END”指示灯变红，此时观看乘积是不是正确？
  //   8位原码一位乘法器（答案）
  //   输出引脚区
  //   ×
  //   =
endmodule

module \_8位补码一位乘法器_用8位无符号数一位乘法器实现__答案  (
  input  [7:0] X,
  input  [7:0] Y,
  output [15:0] \乘积 
);

  wire CLK, END, or_1_out, or_2_out, P14A, P14B, PSS, RST;
  wire [1:0] PS;
  wire [7:0] negator_1_out, negator_3_out;
  wire [13:0] negator_2_out, PA;
  wire [13:7] PX, PY;
  wire [15:0] P_prime;

  Negator #(.width(8)) negator_1 (.in(X), .out(negator_1_out));
  xor xor_1 (P14A, X[7], Y[7]);
  Multiplexer #(.select(1), .width(7), .disabled("Z"), .enable("false")) multiplexer_1 (
    .in0(X[6:0]), .in1(negator_1_out[6:0]), .out(PX), .sel(X[7]));
  Negator #(.width(14)) negator_2 (.in(PA), .out(negator_2_out));
  Button \u_复位  (.out(RST));
  Multiplexer #(.select(1), .width(1), .disabled("Z"), .enable("false")) multiplexer_2 (
    .in0(P14B), .in1(1'b1), .out(\乘积 [14]), .sel(PSS));
  Negator #(.width(8)) negator_3 (.in(Y), .out(negator_3_out));
  Multiplexer #(.select(1), .width(14), .disabled("Z"), .enable("false")) multiplexer_3 (
    .in0(PA), .in1(negator_2_out), .out(\乘积 [13:0]), .sel(P14A));
  Button \u_时钟  (.out(CLK));
  Comparator #(.width(8), .mode("twosComplement")) comparator_1 (.a(X), .b(8'h80), .eq(PS[0]));  // open: gt, lt
  and and_1 (PSS, PS[0], PS[1]);
  Comparator #(.width(8), .mode("twosComplement")) comparator_2 (.a(8'h80), .b(Y), .eq(PS[1]));  // open: gt, lt
  Multiplexer #(.select(1), .width(7), .disabled("Z"), .enable("false")) multiplexer_4 (
    .in0(Y[6:0]), .in1(negator_3_out[6:0]), .out(PY), .sel(Y[7]));
  Multiplexer #(.select(1), .width(1), .disabled("Z"), .enable("false")) multiplexer_5 (
    .in0(\乘积 [14]), .in1(1'b0), .out(\乘积 [15]), .sel(PSS));
  LED #(.active("true")) led_1 (.in(END));
  \_8位无符号数一位乘法器_封装用  \u_8位无符号数一位乘法器_封装用_1  (
    .X({1'b0, PX}), .Y({1'b0, PY}), .in_3(RST), .in_4(CLK), .out_6(END), .\乘积 (P_prime));
  Multiplexer #(.select(2), .width(14), .disabled("Z"), .enable("false")) multiplexer_6 (
    .in0(P_prime[13:0]), .in1({PY, {7{1'b0}}}), .in2({PX, {7{1'b0}}}), .in3({14{1'b0}}), .out(PA), .sel(PS));
  or or_1 (or_1_out, X[0], X[1], X[2], X[3], X[4], X[5], X[6], X[7]);
  or or_2 (or_2_out, Y[0], Y[1], Y[2], Y[3], Y[4], Y[5], Y[6], Y[7]);
  // Probe on X
  // Probe on Y
  // Probe on \乘积 
  and and_2 (P14B, or_1_out, P14A, or_2_out);

  // Other names for the same wires on the sheet: P[15:0] = \乘积 ; PB[13:0] = \乘积 [13:0]; P14 = \乘积 [14];
  //   P15 = \乘积 [15]; P_t[13:0] = P_prime[13:0]; X_prime[6:0] = PX; X_t[6:0] = PX; Y_prime[6:0] = PY; Y_t[6:0] = PY

  // Notes on the sheet:
  //   输入引脚区
  //   首先设置X、Y值，然后按“复位”按钮，接下去按“CLK”按钮多次，直到“END”指示灯变红，此时观看乘积是不是正确？
  //   功能说明: 8位补码一位乘法器（用8位无符号数一位乘法器实现）                输入：X、Y 为8位补码               输出：乘积=X*Y 为16位补码
  //   8位补码一位乘法器（用8位无符号数一位乘法器实现）（答案）
  //   输出引脚区
  //   ×
  //   =
endmodule

module \_8位串行加法器  (
  input  [7:0] X,
  input  [7:0] Y,
  input  Cin,
  output [7:0] S,
  output Cout,
  output out_6
);

  wire \n1位全加器_fa_2_cout , \n1位全加器_fa_3_cout , \n1位全加器_fa_4_cout , \n1位全加器_fa_5_cout , \n1位全加器_fa_6_cout ,
       \n1位全加器_fa_7_cout , \n1位全加器_fa_8_cout ;

  xor xor_1 (out_6, Cout, \n1位全加器_fa_2_cout );
  \_1位全加器_FA  \u_1位全加器_fa_1  (.Cout(Cout), .Si(S[7]), .Cin(\n1位全加器_fa_2_cout ), .Xi(X[7]), .Yi(Y[7]));
  \_1位全加器_FA  \u_1位全加器_fa_2  (.Cout(\n1位全加器_fa_2_cout ), .Si(S[6]), .Cin(\n1位全加器_fa_3_cout ), .Xi(X[6]), .Yi(Y[6]));
  \_1位全加器_FA  \u_1位全加器_fa_3  (.Cout(\n1位全加器_fa_3_cout ), .Si(S[5]), .Cin(\n1位全加器_fa_4_cout ), .Xi(X[5]), .Yi(Y[5]));
  \_1位全加器_FA  \u_1位全加器_fa_4  (.Cout(\n1位全加器_fa_4_cout ), .Si(S[4]), .Cin(\n1位全加器_fa_5_cout ), .Xi(X[4]), .Yi(Y[4]));
  \_1位全加器_FA  \u_1位全加器_fa_5  (.Cout(\n1位全加器_fa_5_cout ), .Si(S[3]), .Cin(\n1位全加器_fa_6_cout ), .Xi(X[3]), .Yi(Y[3]));
  \_1位全加器_FA  \u_1位全加器_fa_6  (.Cout(\n1位全加器_fa_6_cout ), .Si(S[2]), .Cin(\n1位全加器_fa_7_cout ), .Xi(X[2]), .Yi(Y[2]));
  // Probe on X
  // Probe on Y
  // Probe on S
  \_1位全加器_FA  \u_1位全加器_fa_7  (.Cout(\n1位全加器_fa_7_cout ), .Si(S[1]), .Cin(\n1位全加器_fa_8_cout ), .Xi(X[1]), .Yi(Y[1]));
  // Probe on X
  // Probe on Y
  // Probe on S
  \_1位全加器_FA  \u_1位全加器_fa_8  (.Cout(\n1位全加器_fa_8_cout ), .Si(S[0]), .Cin(Cin), .Xi(X[0]), .Yi(Y[0]));

  // Other names for the same wires on the sheet: OF = out_6

  // Notes on the sheet:
  //   Cin: pull=down
  //   X: pull=down
  //   Y: pull=down
  //   输入引脚区
  //   符号位
  //   输出引脚区
  //   8位串行加法器
  //   OF
  //   +
  //   有符号加法
  //   +
  //   =
  //   无符号加法
endmodule

// FA
module \_1位全加器_FA  (
  input  Cin,
  input  Xi,
  input  Yi,
  output Cout,
  output Si
);

  wire AND_2_out, AND_out, XOR_2_out;

  and AND (AND_out, Xi, Yi);
  or OR (Cout, AND_out, AND_2_out);
  and AND_2 (AND_2_out, Cin, XOR_2_out);
  xor XOR (Si, Cin, XOR_2_out);
  xor XOR_2 (XOR_2_out, Xi, Yi);

  // Notes on the sheet:
  //   Yi: pull=down
  //   Xi: pull=down
  //   Cin: pull=down
  //   Cout = Xi Yi + Cin (Xi ^ Yi)
  //   Si = Xi ^ Yi ^ Cin
  //   1位全加器（FA）
endmodule
