// Logisim project MIPS RAM 存储器验证实验.circ as structural Verilog: 3 circuits, main circuit 复杂的MIPS RAM存储器测试电路
module \MIPS_RAM存储器电路  (
  input  [11:0] \字节地址 ,
  input  [31:0] Din,
  input  CLK,
  input  WE,
  input  [1:0] Mode,
  output [31:0] DataOut
);

  wire and_1_out, and_2_out, CS0, CS1, CS2, CS3, decoder_2_out0, decoder_2_out1, decoder_2_out2,
       decoder_2_out3, or_1_out, or_2_out, or_3_out, or_4_out, \半字访问 , \字节访问 , \字访问 , \无效访问 ;
  wire [7:0] D0, D1, D2, D3, multiplexer_1_out;
  wire [15:0] multiplexer_2_out;
  wire [31:0] \数据 ;

  RAM #(.addrWidth(10), .dataWidth(8), .bus("separate"), .Select("high")) ram_1 (
    .addr(\字节地址 [11:2]), .din(\数据 [31:24]), .data(D3), .str(WE), .sel(CS3), .clk(CLK));  // open: ld, clr
  RAM #(.addrWidth(10), .dataWidth(8), .bus("separate"), .Select("high")) ram_2 (
    .addr(\字节地址 [11:2]), .din(\数据 [23:16]), .data(D2), .str(WE), .sel(CS2), .clk(CLK));  // open: ld, clr
  RAM #(.addrWidth(10), .dataWidth(8), .bus("separate"), .Select("high")) ram_3 (
    .addr(\字节地址 [11:2]), .din(\数据 [15:8]), .data(D1), .str(WE), .sel(CS1), .clk(CLK));  // open: ld, clr
  RAM #(.addrWidth(10), .dataWidth(8), .bus("separate"), .Select("high")) ram_4 (
    .addr(\字节地址 [11:2]), .din(\数据 [7:0]), .data(D0), .str(WE), .sel(CS0), .clk(CLK));  // open: ld, clr
  // Probe on Din
  Decoder #(.select(2), .tristate("false"), .disabled("Z"), .enable("false")) decoder_1 (
    .out0(\字访问 ), .out1(\字节访问 ), .out2(\半字访问 ), .out3(\无效访问 ), .sel(Mode));
  Multiplexer #(.select(2), .width(8), .disabled("Z"), .enable("false")) multiplexer_1 (
    .in0(D0), .in1(D1), .in2(D2), .in3(D3), .out(multiplexer_1_out), .sel(\字节地址 [1:0]));
  Multiplexer #(.select(1), .width(16), .disabled("Z"), .enable("false")) multiplexer_2 (
    .in0({D1, D0}), .in1({D3, D2}), .out(multiplexer_2_out), .sel(\字节地址 [1]));
  Multiplexer #(.select(2), .width(32), .disabled("Z"), .enable("false")) multiplexer_3 (
    .in0({D3, D2, D1, D0}), .in1({{24{1'b0}}, multiplexer_1_out}), .in2({{16{1'b0}}, multiplexer_2_out}),
    .out(DataOut), .sel(Mode));  // open: in3
  and and_1 (and_1_out, \半字访问 , \字节地址 [1]);
  Decoder #(.select(2), .tristate("false"), .disabled("Z"), .enable("false")) decoder_2 (
    .out0(decoder_2_out0), .out1(decoder_2_out1), .out2(decoder_2_out2), .out3(decoder_2_out3),
    .sel(\字节地址 [1:0]));
  and and_2 (and_2_out, \半字访问 , ~\字节地址 [1]);  // AND_Gate
  // Probe on DataOut
  or or_1 (or_1_out, \字访问 , and_1_out, decoder_2_out3);
  or or_2 (or_2_out, \字访问 , and_1_out, decoder_2_out2);
  or or_3 (or_3_out, \字访问 , and_2_out, decoder_2_out1);
  or or_4 (or_4_out, \字访问 , and_2_out, decoder_2_out0);
  Multiplexer #(.select(2), .width(32), .disabled("Z"), .enable("false")) multiplexer_4 (
    .in0(Din), .in1({Din[7:0], Din[7:0], Din[7:0], Din[7:0]}), .in2({Din[15:0], Din[15:0]}), .out(\数据 ),
    .sel(Mode));  // open: in3
  and and_3 (CS3, ~\无效访问 , or_1_out);  // AND_Gate
  and and_4 (CS2, ~\无效访问 , or_2_out);  // AND_Gate
  and and_5 (CS1, ~\无效访问 , or_3_out);  // AND_Gate
  and and_6 (CS0, ~\无效访问 , or_4_out);  // AND_Gate

  // Other names for the same wires on the sheet: Din2[7:0] = Din[23:16]; Din3[7:0] = Din[31:24]; Din0[7:0] = Din[7:0];
  //   Din1[7:0] = Din[15:8]; A[11:0] = \字节地址 ; 字节选择[1:0] = \字节地址 [1:0]; 半字选择 = \字节地址 [1]; 字地址[9:0] = \字节地址 [11:2];
  //   Dout[31:0] = DataOut

  // Notes on the sheet:
  //   输入引脚区
  //   MIPS RAM存储器电路
  //   输出引脚区
endmodule

module \简单的MIPS_RAM存储器测试电路  (
  input  [11:0] A,
  input  [31:0] Din,
  input  WE,
  input  [1:0] Mode,
  output [31:0] Dout
);

  wire CLK_out;

  // Probe on A
  // Probe on Din
  \MIPS_RAM存储器电路  \mips_ram存储器电路_1  (.\字节地址 (A), .Din(Din), .DataOut(Dout), .CLK(CLK_out), .WE(WE), .Mode(Mode));
  Clock #(.highDuration(1), .lowDuration(1)) CLK (.out(CLK_out));
  // Probe on Dout

  // Notes on the sheet:
  //   简单的MIPS  RAM存储器测试电路
endmodule

module \复杂的MIPS_RAM存储器测试电路  (
);

  wire CLK_out, comparator_1_eq, comparator_2_eq, comparator_3_eq, err, not_1_out, not_3_out, or_1_out,
       rom_3_data, Testing, \计数器_2_q ;
  wire [1:0] rom_4_data, rom_5_data;
  wire [7:0] \计数器_q ;
  wire [8:0] \计数器_3_q ;
  wire [11:0] rom_1_data;
  wire [15:0] multiplexer_1_out, multiplexer_1_out_2;
  wire [31:0] adder_1_out, Din, Dout, \Dout上拉 , \Dout期望值 , \寄存器_q ;

  // Probe on \计数器_q 
  Clock #(.highDuration(1), .lowDuration(1)) CLK (.out(CLK_out));
  // Probe on \计数器_q 
  Counter #(.width(8), .max('hff), .ongoal("wrap"), .trigger("rising"), .behavior("old")) \u_计数器  (
    .count(Testing), .Q(\计数器_q ), .clk(not_1_out));  // open: load, D, carry, clr, preset
  not not_1 (not_1_out, \计数器_2_q );
  Counter #(.width(1), .max('h1), .ongoal("wrap"), .trigger("rising"), .behavior("old")) \u_计数器_2  (
    .count(Testing), .Q(\计数器_2_q ), .clk(CLK_out));  // open: load, D, carry, clr, preset
  Counter #(.width(9), .max('h1ff), .ongoal("wrap"), .trigger("rising"), .behavior("old")) \u_计数器_3  (
    .count(Testing), .Q(\计数器_3_q ), .clk(CLK_out));  // open: load, D, carry, clr, preset
  // Probe on \计数器_3_q 
  ROM #(.addrWidth(8), .dataWidth(12), .Select("high")) rom_1 (.addr(\计数器_q ), .data(rom_1_data));
  ROM #(.addrWidth(8), .dataWidth(32), .Select("high")) rom_2 (.addr(\计数器_q ), .data(Din));
  ROM #(.addrWidth(8), .dataWidth(1), .Select("high")) rom_3 (.addr(\计数器_q ), .data(rom_3_data));
  ROM #(.addrWidth(8), .dataWidth(2), .Select("high")) rom_4 (.addr(\计数器_q ), .data(rom_4_data));
  ROM #(.addrWidth(8), .dataWidth(2), .Select("high")) rom_5 (.addr(\计数器_q ), .data(rom_5_data));
  ROM #(.addrWidth(9), .dataWidth(32), .Select("high")) rom_6 (.addr(\计数器_3_q ), .data(\Dout期望值 ));
  // Probe on rom_1_data
  // Probe on Din
  // Probe on rom_4_data
  // Probe on rom_5_data
  // Probe on \Dout期望值 
  // Probe on rom_3_data
  Comparator #(.width(2), .mode("twosComplement")) comparator_1 (
    .a(rom_5_data), .b(2'b11), .eq(comparator_1_eq));  // open: gt, lt
  Comparator #(.width(32), .mode("twosComplement")) comparator_2 (
    .a(\Dout上拉 ), .b(\Dout期望值 ), .eq(comparator_2_eq));  // open: gt, lt
  \MIPS_RAM存储器电路  \mips_ram存储器电路_1  (
    .\字节地址 (rom_1_data), .Din(Din), .DataOut(Dout), .CLK(\计数器_2_q ), .WE(rom_3_data), .Mode(rom_4_data));
  // Probe on Dout
  _7_Segment_Display #(.active("true")) u_7_segment_display_1 (
    .g(multiplexer_1_out[15]), .f(multiplexer_1_out[14]), .a(multiplexer_1_out[13]),
    .b(multiplexer_1_out[12]), .e(multiplexer_1_out_2[15]), .d(multiplexer_1_out_2[14]),
    .c(multiplexer_1_out_2[13]), .dp(multiplexer_1_out_2[12]));
  _7_Segment_Display #(.active("true")) u_7_segment_display_2 (
    .g(multiplexer_1_out[11]), .f(multiplexer_1_out[10]), .a(multiplexer_1_out[9]), .b(multiplexer_1_out[8]),
    .e(multiplexer_1_out_2[11]), .d(multiplexer_1_out_2[10]), .c(multiplexer_1_out_2[9]),
    .dp(multiplexer_1_out_2[8]));
  not not_2 (err, comparator_2_eq);
  and and_1 (Testing, ~comparator_1_eq, comparator_2_eq);  // AND_Gate
  assign \Dout上拉  = Dout;  // Buffer buffer_1, 32 bits wide
  Pull_Resistor #(.pull(1)) pull_resistor_1 (.node(\Dout上拉 ));
  // Probe on \Dout上拉 
  _7_Segment_Display #(.active("true")) u_7_segment_display_3 (
    .g(multiplexer_1_out[7]), .f(multiplexer_1_out[6]), .a(multiplexer_1_out[5]), .b(multiplexer_1_out[4]),
    .e(multiplexer_1_out_2[7]), .d(multiplexer_1_out_2[6]), .c(multiplexer_1_out_2[5]),
    .dp(multiplexer_1_out_2[4]));
  _7_Segment_Display #(.active("true")) u_7_segment_display_4 (
    .g(multiplexer_1_out[3]), .f(multiplexer_1_out[2]), .a(multiplexer_1_out[1]), .b(multiplexer_1_out[0]),
    .e(multiplexer_1_out_2[3]), .d(multiplexer_1_out_2[2]), .c(multiplexer_1_out_2[1]),
    .dp(multiplexer_1_out_2[0]));
  Adder #(.width(32)) adder_1 (.a(\寄存器_q ), .b(\Dout上拉 ), .out(adder_1_out));  // open: cin, cout
  not not_3 (not_3_out, comparator_1_eq);
  // Probe on Din
  // Probe on \寄存器_q 
  Register #(.width(32), .trigger("rising"), .Select("low")) \u_寄存器  (
    .D(adder_1_out), .en(not_3_out), .Q(\寄存器_q ), .clk(\计数器_2_q ));  // open: clr
  // Probe on Dout
  Multiplexer #(.select(1), .width(32), .disabled(0), .enable("true")) multiplexer_1 (
    .in0(32'h8a8cef44), .in1(32'h8a66ffee), .out({multiplexer_1_out_2, multiplexer_1_out}),
    .sel(comparator_3_eq), .en(or_1_out));
  or or_1 (or_1_out, err, comparator_1_eq);
  // Probe on \Dout上拉 
  Comparator #(.width(32), .mode("twosComplement")) comparator_3 (
    .a(\寄存器_q ), .b(32'he1f5edf0), .eq(comparator_3_eq));  // open: gt, lt
  // Probe on \Dout期望值 

  // Notes on the sheet:
  //   电路功能：测试MIPS RAM存储器
  //   测试用例存储器
  //   contents of rom_1 (hex, n*v repeats v):
  //   0 4 8 c 10 14 18 1c 20 24 28 2c 30 34 38 3c 2 6 a e 31 35 39 3d 13 17 1b 1f 12 16 1a 1e 11 15 19 1d
  //   10 14 18 1c 0 4 8 c 10 14 18 1c 20 24 28 2c 30 34 38 3c 0 2 4 6 8 a c e 10 12 14 16 18 1a 1c 1e 20
  //   22 24 26 28 2a 2c 2e 30 32 34 36 38 3a 3c 3e 0 1 2 3 4 5 6 7 8 9 a b c d e f 10 11 12 13 14 15 16 17
  //   18 19 1a 1b 1c 1d 1e 1f 20 21 22 23 24 25 26 27 28 29 2a 2b 2c 2d 2e 2f 30 31 32 33 34 35 36 37 38
  //   39 3a 3b 3c 3d 3e 3f 3f
  //   contents of rom_2 (hex, n*v repeats v):
  //   203 607 a0b e0f 4*0 20212223 24252627 28292a2b 2c2d2e2f 30310000 34350000 38390000 3c3d0000 1 405
  //   809 c0d 3233 3637 3a3b 3e3f 10 14 18 1c 11 15 19 1d 12 16 1a 1e 13 17 1b 1f
  //   contents of rom_3 (hex, n*v repeats v):
  //   40*1
  //   contents of rom_4 (hex, n*v repeats v):
  //   16*0 8*2 16*1 16*0 32*2 65*1
  //   contents of rom_5 (hex, n*v repeats v):
  //   16*0 8*2 16*1 16*0 32*2 64*1 3
  //   contents of rom_6 (hex, n*v repeats v):
  //   0 203 0 607 0 a0b 0 e0f 9*0 20212223 0 24252627 0 28292a2b 0 2c2d2e2f 0 30310000 0 34350000 0
  //   38390000 0 3c3d0000 0 1 0 405 0 809 0 c0d 0 3233 0 3637 0 3a3b 0 3e3f 0 10 0 14 0 18 0 1c 0 11 0 15
  //   0 19 0 1d 0 12 0 16 0 1a 0 1e 0 13 0 17 0 1b 0 1f 10203 10203 4050607 4050607 8090a0b 8090a0b
  //   c0d0e0f c0d0e0f 10111213 10111213 14151617 14151617 18191a1b 18191a1b 1c1d1e1f 1c1d1e1f 20212223
  //   20212223 24252627 24252627 28292a2b 28292a2b 2c2d2e2f 2c2d2e2f 30313233 30313233 34353637 34353637
  //   38393a3b 38393a3b 3c3d3e3f 3c3d3e3f 203 203 1 1 607 607 405 405 a0b a0b 809 809 e0f e0f c0d c0d 1213
  //   1213 1011 1011 1617 1617 1415 1415 1a1b 1a1b 1819 1819 1e1f 1e1f 1c1d 1c1d 2223 2223 2021 2021 2627
  //   2627 2425 2425 2a2b 2a2b 2829 2829 2e2f 2e2f 2c2d 2c2d 3233 3233 3031 3031 3637 3637 3435 3435 3a3b
  //   3a3b 3839 3839 3e3f 3e3f 3c3d 3c3d 3 3 2 2 1 1 0 0 7 7 6 6 5 5 4 4 b b a a 9 9 8 8 f f e e d d c c
  //   13 13 12 12 11 11 10 10 17 17 16 16 15 15 14 14 1b 1b 1a 1a 19 19 18 18 1f 1f 1e 1e 1d 1d 1c 1c 23
  //   23 22 22 21 21 20 20 27 27 26 26 25 25 24 24 2b 2b 2a 2a 29 29 28 28 2f 2f 2e 2e 2d 2d 2c 2c 33 33
  //   32 32 31 31 30 30 37 37 36 36 35 35 34 34 3b 3b 3a 3a 39 39 38 38 3f 3f 3e 3e 3d 3d 3c 3c 3c
  //   测试结束时，如果显示“PASS”，则表示测试通过；如果显示“FAIL”，则表示测试失败
  //   首先设置运行频率=1KHz；然后按 Ctrl+R，使电路复位（清零） ；再按Ctrl+K，启动时钟（CLK）
  //   也可以修改写入数据存储器的内容（第2个存储器）；之后，再按Ctrl+R，启动时钟；测试结束时，观察是不是显示“FAIL”？
  //   也可以修改期望值存储器的内容（第6个存储器）；之后，再按Ctrl+R，启动时钟；测试结束时，观察是不是显示“FAIL”？
  //   复杂的MIPS RAM存储器测试电路
endmodule
