// Logisim project 存储器扩展设计实验.circ as structural Verilog: 3 circuits, main circuit 存储器扩展电路
module \存储器扩展电路  (
  input  [6:0] \区号 ,
  input  [6:0] \位号 ,
  output [31:0] D0,
  output [31:0] D1,
  output [31:0] D6,
  output [31:0] D3,
  output [31:0] D4,
  output [31:0] D5,
  output [31:0] D6_2,
  output [31:0] D7
);

  wire decoder_1_out0, decoder_1_out1, decoder_1_out2, decoder_1_out3;
  wire [6:0] multiplier_1_cout, multiplier_1_out, subtractor_1_out;
  wire [13:0] adder_1_out, Addr, bit_extender_1_out;

  Decoder #(.select(2), .tristate("false"), .disabled("Z"), .enable("false")) decoder_1 (
    .out0(decoder_1_out0), .out1(decoder_1_out1), .out2(decoder_1_out2), .out3(decoder_1_out3),
    .sel(Addr[13:12]));
  ROM #(.addrWidth(14), .dataWidth(32), .Select("high")) rom_1 (.addr(Addr), .data(D0));
  ROM #(.addrWidth(12), .dataWidth(32), .Select("high")) rom_2 (.addr(Addr[11:0]), .data(D1), .sel(decoder_1_out0));
  Subtractor #(.width(7)) subtractor_1 (.a(\区号 ), .b(7'b0000001), .out(subtractor_1_out));  // open: bin, bout
  Multiplier #(.width(7)) multiplier_1 (
    .a(subtractor_1_out), .b(7'b1011110), .out(multiplier_1_out), .cout(multiplier_1_cout));  // open: cin
  ROM #(.addrWidth(14), .dataWidth(32), .Select("high")) rom_3 (.addr(Addr), .data(D6));
  ROM #(.addrWidth(14), .dataWidth(32), .Select("high")) rom_4 (.addr(Addr), .data(D3));
  ROM #(.addrWidth(12), .dataWidth(32), .Select("high")) rom_5 (.addr(Addr[11:0]), .data(D1), .sel(decoder_1_out1));
  assign bit_extender_1_out = {{7{1'b0}}, \位号 };  // Bit_Extender bit_extender_1
  Adder #(.width(14)) adder_1 (
    .a({multiplier_1_cout, multiplier_1_out}), .b(bit_extender_1_out), .out(adder_1_out));  // open: cin, cout
  Subtractor #(.width(14)) subtractor_2 (.a(adder_1_out), .b(14'h1), .out(Addr));  // open: bin, bout
  ROM #(.addrWidth(14), .dataWidth(32), .Select("high")) rom_6 (.addr(Addr), .data(D4));
  ROM #(.addrWidth(14), .dataWidth(32), .Select("high")) rom_7 (.addr(Addr), .data(D5));
  ROM #(.addrWidth(12), .dataWidth(32), .Select("high")) rom_8 (.addr(Addr[11:0]), .data(D1), .sel(decoder_1_out2));
  ROM #(.addrWidth(14), .dataWidth(32), .Select("high")) rom_9 (.addr(Addr), .data(D6_2));
  ROM #(.addrWidth(14), .dataWidth(32), .Select("high")) rom_10 (.addr(Addr), .data(D7));
  ROM #(.addrWidth(12), .dataWidth(32), .Select("high")) rom_11 (.addr(Addr[11:0]), .data(D1), .sel(decoder_1_out3));

  // Other names for the same wires on the sheet: D2[31:0] = D6; D6_t[31:0] = D6_2

  // Notes on the sheet:
  //   输入引脚区
  //   contents of rom_1 (hex, n*v repeats v):
  //   8*0 1000000 0 0 2400000 5*0 c0000 18000000 16*0 800000 0 0 0 10040000 7f00000 0 0 80000 800000 0 0 0
  //   c1803e0 0 600000 5*0 200000 0 18200000 180006 c003000 0 0 0 800000 1c00000 1c00000 200000 900000
  //   48003000 0 0 500000 0 40000 1c00000 38300000 800080 800080 3c00000 3c00000 c1803e0 1400080 1c00080 0
  //   0 800000 800000 0 0 0 800000 800000 3ffc0000 16*0 1000000 0 0 800000 5*0 8e00000 4200000 9*0 8080000
  //   8080000 8080000 8480000 5*8080000 11*10080000 10*c1803e0 0 0 5*10080000 11080000 4*10080000 16*0
  //   1800000 6*0 40000 20000000 5*0 20000 4*0 400000 38*0 7f80000 60000000 ff00000 0 0 1000100 26*0
  //   10000c0 800080 400180 0 0 800000 9*0 80000 2000000 2060008 0 60008 200000 30004 0 60008 2000000
  //   2060008 0 100000 800000 860008 0 60008 0 60008 0 30004 800000 830004 0 0 60008 0 30004 0 80000 0 0 0
  //   8000000 0 200000 230004 250002 0 30004 20000 0 100000 0 0 100000 0 f80000 fb0004 fa0000 800000 0
  //   4000000 800000 1000000 0 0 0 200000 0 800000 0 0 0 8000000 5*0 1000000 13*0 1ffe0000 0 3c0000 0
  //   400000 0 0 0 100000 1000000 1060008 2000000 2060008 2000000 2060008 1000000 1060008 0 60008 200000
  //   260008 0 60008 0 60008 0 60008 0 60008 2000000 2060008 0 60008 0 0 60008 0 60008 2000000 2060008 0 0
  //   0 2000000 0 0 60008 40000 0 60008 40000 0 60008 20000 0 60008 40000 0 60008 20000 12*0 400000 400000
  //   4*0 800000 0 0 0 30004 10*0 800000 0 0 800000 6*0 800000 8*0 380000 0 0 0 3e00000 21*0 400000 48*0
  //   800000 5*0 2200000 0 3c00000 0 6300000 38*0 300000 19*0 800000 25*0 800000 4400000 2000000 0 800000
  //   4400000 2000000 0 1000000 4400000 2000000 0 800000 4400000 2000000 0 800000 8800000 2000000 7c00000
  //   1000080 2800440 1000200 0 1000000 0 800000 800000 4400000 2000000 5*0 8000000 4000000 0 0 4000000
  //   1000000 0 1000000 0 0 0 200000 800000 0 1000000 400000 0 0 0 2000000 1000000 10080000 0 1000000 0 0
  //   0 2000000 0 3fe00000 8000000 2000000 0 0 1000000 100000 27*0 1000100 1800180 16*0 1000100 1000100
  //   1800180 1800180 1000100 1000100 1800180 1800180 1000100 1000100 1800180 1000100 1800180 1800180
  //   1000100 1800180 1000100 1000100 1800180 1000100 1800180 1800180 1000100 1800180 8*0 4*1000100
  //   4*1800180 4*1000100 1800180 1000100 1800180 1800180 1800180 1000100 1000100 1800180 1000100 1800180
  //   1800180 1800180 15*0 600000 6*0 80000 10000000 5*0 20000 4*0 200000 38*0 7f80000 60000000 ff00000 0
  //   0 1000100 26*0 400030 800080 1000600 0 600000 6*0 80000 10000000 5*0 20000 4*0 200000 38*0 7f80000
  //   60000000 ff00000 0 0 1000100 26*0 400030 800080 1000600 0 4*300c0ff0 381c0ff0 381c0ff0 300c0ff0
  //   3bdc0ff0 3ffc0ff0 3dfc0ff0 3ffc0ff0 3e7c0ff0 3f7c0ff0 3cfc0ff0 c423c423 2a543bdc 3bdc3bdc d5abc423
  //   294030c 39c030c fd6bfcf3 fce3fdf3 fc3ffe7f 3c00180 3c00180 fc3ffe7f e700420 f18ffbdf 7e00180
  //   f81ffe7f 66003c0 f99ffc3f 7e003c0 f81ffc3f 0 ffffffff 3c00180 1c380000 7e003c0 1800000 381c0ff0
  //   3ffc0ff0 4400000 400000 4000000 1800180 1800180 1800180 c000c0 1800180 1800180 1800180 4*0 1ff80000
  //   8001ffff 0 60002 600060 60004000 6000600 7e0000 700070 7e000000 e000e00 c000c c000c0 0 7000380 0
  //   300c300c 1800000 c000c00 c000c000 30003 0 80008000 10001 0 24001800 10081ff8 1c00000 3800000 4800000
  //   fb7fffff 1000100 38000000 6*0 1c00040 0 1e00060 0 3c001e0 3c000c0 0 0 1b00110 0 7000200 0 3e00120
  //   1e00180 0 0 1800180 0 1800180 0 1800180 1800180 0 0 7e00180 0 1800180 0 7e003c0 5a00180 0 0 3e001e00
  //   0 fc0078 0 1a001e00 ec0078 0 3cb0301 f800e0 0 7d00fe00 40004000 1ff00f0 3ec07580 10000 0 1d781900 0
  //   1800080 0 1df00900 f80098 0 0 2400040 0 2400200 0 4e00200 7700040 0 77fc01f8 12e00c0 0 7000300 0
  //   c8008c0 3c00180 0 1cde0000 1f80078 0 78000800 0 3cc01838 7801c00 0 0 2000200 0 400040 0 2000200
  //   600040 0 0 2000180 0 2000180 0 3000180 0 0 7ff80000 4000000 1000000 1bfe2004 1000000 0 0 1000100 0 0
  //   8000000 0 0 0 10000000 0 800000 0 0 0 800000 7ffc0000 0 1000000 80000 0 ff00020 20*0 7ffc3ffc 7f0000
  //   ff000000 3010301 80c080c0 5*0 ffffffff c000c000 ffffffff 30003 c000c000 30003 ffffffff 0 ffffffff 0
  //   8000ffff 80008000 1ffff 10001 80008000 10001 ffff 112*0 2f7e0004 7ffe0004 10401040 10401040 900090
  //   400040 1040200 10201020 440080 fffe0824 21e02018 4440440 5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
  //   contents of rom_2 (hex, n*v repeats v):
  //   7*0 1100000 3000380 0 0 2400240 0 100008 c000c00 440022 33003300 600038 3000e00 400000 1000200
  //   2400000 2400000 10001f0 800080 20803f8 500070 8200ff0 20807f8 7e007f0 3f007f0 800080 0 0 0 2200140
  //   20020000 18041ffc 18183ffc 10041004 180c0c18 30000c0 18180000 100008 800080 1200120 100008 63001c0
  //   20021004 900060 1000090 0 10480830 0 0 0 200020 230020c 1a00620 1800060 c00300 0 3c3c1818 3c00180
  //   2a001c0 2200220 2200220 600020 1b00090 33e84800 3f00090 163421c2 6b003f0 f80070 24101808 2000220
  //   1c401870 1400140 1c001c0 10080c30 1ff80ff0 263211c4 4100220 7f003e0 20043ffc 3ffc3ffc 14001c0
  //   1c001c0 11880000 0 0 1c001c0 800080 3ffc3ffc 16*0 3000700 cc00780 cc00780 3800180 18001fe0 cc00780
  //   1fe01fe0 cc00780 cc00780 1b1839b0 c601ce0 71e010c0 736011c0 70601020 730013f8 71b010e0 73f813f8
  //   71b010e0 71b010e0 799830f0 13841084 136411c4 136411c4 11c410c4 17f41004 133411e4 17f41004 136411c4
  //   11c41004 2c942464 2c642424 2c942464 2c942464 2c642424 2c8424f4 2c942464 2c9424f4 2c942464 2c942464
  //   29542624 21c21044 236211c4 236211c4 20c21044 27f21004 233211e4 27f21004 236211c4 21c21004 2eda1274 0
  //   0 20042004 20242004 2ff42024 28142004 2ff42024 21142104 21042104 22442044 22042204 20842084 0 0
  //   8001c0 2200770 8881ddc 8881ddc 4100e38 8881ddc 11143bbe 11543bfe 8881ddc 4100e38 8881ddc 11283bfc
  //   c300000 0 3c003c0 4200000 2200220 380c7c1e 12080c04 19000e0 700000 100008 8001000 0 800000 0 0 0
  //   80004 63003e0 3800080 66003c0 66003c0 1c000c0 c000ff0 66003c0 ff00ff0 66003c0 66003c0 0 0 30000c 0
  //   c003000 181807f0 41003e0 1c00080 c381fe0 63803e0 c701fc0 c181ff8 c181ff8 61c03f0 c181e3c 18003c0
  //   c001e0 c301e7c c001e00 180c380e e101c38 63003e0 c301fe0 e3803e0 c301fe0 c1807e8 318c3ffc c081e1c
  //   18083c1c 18c43dee c081e1c 380c7c1e 20183ff8 6000600 18003000 300030 800000 0 800180 0 6000e00 0
  //   6000e0 0 19800f0 0 6000e00 1800000 c00000 6000e00 1800380 7*0 800000 6*0 1000100 800080 400040 0
  //   1000100 1000080 8000000 10001000 7c00000 6007c0 1800300 8003c0 4600800 40c0818 1000200 1000206
  //   1f00200 1f60208 c00040 c60048 10101030 10131024 fc00000 fc60008 1000200 1060208 4000400 410040c
  //   800080 860088 2200020 2260028 24007c0 24607c8 4380400 43b0404 c9000a0 c9300a4 0 0 60008 3c0000
  //   3b0004 1000100 1080106 4300400 8080800 2700400 8600800 c600380 9240820 9230824 9240822 6180010
  //   61b0014 61a0015 3000000 310000c 3140008 0 10000c 140008 8200820 8230824 8220825 800080 f000000
  //   1f000400 13c01080 7000100 3400000 6000000 700020 10ec1050 800080 e00080 6000c0 4000400 64009c0
  //   8600800 64009c0 4000800 4000800 3e000000 8003c0 7c00100 1000100 11*0 ff80000 980004 600000 f8001e0
  //   800080 ffe0040 0 ff80000 200000 100010 1000100 1060108 1000200 1060208 4000200 4060208 4000200
  //   4060200 0 60008 2200220 2260228 6000c00 6060c08 ff80000 ff60008 2000200 2060208 100010 160008
  //   4000200 4060208 f0000f0 f0600e8 0 11080000 110e0008 ff0 60fe8 2000200 2060208 800080 ff80000 ff80000
  //   800100 300010 1000000 1060008 104000a 2000200 2060208 204020a 1ff80000 1ff60008 1ffa0004 0 60008
  //   40008 800080 860088 820085 0 1e00e00 c00040 180008 7f00000 2000000 4000400 0 0 7f00000 41ffc 7f0
  //   4400040 4400440 4000400 ffc0000 0 ffe0000 800080 ff80000 81ff8 c000000 430044 800080 1000000 8*0
  //   14001c0 e381ff0 e181ff8 1c001c0 e181ff8 20183ff8 c181e3c 63003e0 18003c0 c301e78 14001c0 380e0000
  //   e081c1c ff80ff8 63003e0 c181ffc e301fe0 8080ff8 11881ff8 1bc80e6c 18003c0 c081e1c 118823c4 c180630
  //   8*0 7200000 36000c0 80000 67003c0 3c00000 2600120 5b000e0 36001c0 7000100 e100200 a000400 c300000 0
  //   2200180 1c00000 0 33001e0 1f80000 fe00000 0 1000100 a100408 11000100 2200000 38*0 14001c0 e181ff8
  //   e381ff0 e181ff8 2300ff8 e181ff8 1ff80000 399c73ce 18381470 c181e3c 1e3c03e0 c341e18 2300ff8 380e0000
  //   c181e3c 63003e0 c181ffc e301fe0 63803e0 11881ff8 c081e1c 18003c0 c081e1c c181e3c c181e3c 318c7bde
  //   318c7bde 16001f00 18183c3c 6000f00 e300be0 198c3cf8 61803fc 15*0 3800000 38000e0 fe00000 ff00000
  //   ff80000 0 1200000 0 5c00000 f780000 2200000 f100000 ff80000 0 f780000 1c00000 ff80000 6e00000
  //   1e00000 ff00000 f380000 1800380 f380000 f780000 f780000 1ddc0000 1ddc0000 1f000000 1e3c0000 f000000
  //   3c00000 1e7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
  //   contents of rom_3 (hex, n*v repeats v):
  //   5*0 10041004 0 3300110 ffc0608 0 0 2400240 0 300030 10000800 cc00cc 44002200 400040 1000100 1000080
  //   400080 4800240 1200240 1000100 800080 28002f8 500050 8800840 880108 78007c0 f001f0 800080 4100808
  //   1800180 1800180 4100220 10042002 6000c04 18181818 10041004 10041004 4000400 1818 200010 800080
  //   1200120 400020 8080c18 40812002 1000100 3800100 1ffc0000 21042084 11040e00 10240c18 12200c1c
  //   1ffc0040 30002c0 380060 18000600 c0030 12240c18 18183c3c 18003c0 800490 1c00220 1c00220 c00040
  //   3600120 c180638 c800c90 10040808 18800c90 1900098 24402420 800100 16401440 7c1f0220 7fff03e0
  //   20041008 3ffc1ff8 4809280a 10040808 1ffc0ff8 20042004 3ffc3ffc 2200220 3e003e0 4200990 300040
  //   6000100 3e003e0 800080 3ffc 16*0 3000300 18601860 601860 5800780 18001800 18001860 c01060 18601860
  //   18601860 1b181b18 c600c60 33303330 30303630 30e030e0 33003300 33003318 30303218 33183318 33183318
  //   cd98cd98 21822182 24322632 20322632 22c222c2 26022602 26022612 243227f2 26322632 26322362 44924492
  //   44224422 44924492 44124492 44e24462 44824482 44824492 44124412 44924492 44924492 41524952 40c120c2
  //   44312632 40312632 42c121c2 46012602 46012612 443127f2 46312632 46312362 46d926da 0 0 40024002
  //   40024ff2 40024002 4a524ff6 42024202 40025ffa 413a4102 42424242 42424fc2 40824082 0 0 800080 2200220
  //   8880888 8880888 4100410 8880888 11141114 11541154 8880888 2200410 8880888 11281128 0 0 18003c0
  //   e700e70 ff80ff8 e301c18 c201210 3200310 c00060 200020 4000400 4100808 800080 0 0 0 200010 c180c18
  //   1800180 c300c30 300c30 2c003c0 c000c00 c000c30 600830 c300c30 c300c30 0 0 30000c0 0 c00300 380c300c
  //   11c40808 2600140 c180c18 18000c18 c0c0c18 c000c08 c000c08 18040c0c c180c18 1800180 c000c0 cc00c60
  //   c000c00 162c1c1c b100b10 180c0c18 c180c18 180c180c c180c18 18001808 21842184 c080c08 18101808
  //   18c418c4 7300618 e301c18 600030 6000600 6000c00 300030 2200140 0 4000c0 0 6000600 0 600060 0 1800180
  //   0 6000600 180 c0 6000600 1800180 7*0 1800180 6*0 1000100 800080 400040 0 ff00100 1001ff8 8100820
  //   10101020 1800060 10000c0 200 100 e000430 1f300400 f881110 f881116 800f00 800f00 3000180 3000180
  //   1010107c 107c1010 18000e0 18000e0 e8001f0 e8001f0 4000400 400040c 1ffc0080 1ffc0080 1ffc0220
  //   1ffc0220 1000080 1000080 4081f0c 4081f0c 8007e0 8007e0 8e00000 23880070 23880070 1d0003c0 1d0003c0
  //   1000100 1000106 4081f18 80008f0 17040188 9083c90 21081110 82008f8 82008f8 82008f8 8141c18 8141c18
  //   8141c18 1000180 100018c 1000188 0 c 8 82009fc 82009fc 82009fc 8003e0 2100100 412040c 8901ca0 18001c0
  //   2100480 8340908 96408a8 11221124 8000e0 800080 2000180 5800400 800080 9103c90 800080 e000400
  //   1f000400 4602400 3900160 2180100 2000200 11*0 1600018 8000e0 7000180 803080 8080ff8 8040802 8007f0
  //   800080 ff80020 301ffe 1083ff8 1083ff8 f8001f8 f8001f8 41007f0 41007f0 10400bf8 10400bf8 81ff8 81ff8
  //   3ffe0220 3ffe0220 40000 40000 200010 200010 3f0402fc 3f0402fc c100810 c100810 41007f0 41007f0 800080
  //   800080 5200020 8901988 8901988 0 0 3000200 3000200 800080 0 100010 800fc0 400060 2200300 2200300
  //   2200300 2c00230 2c00230 2c00230 100008 100008 100008 2000000 2000000 2000000 1c03ffe 3ffe0080
  //   3ffe0080 81ffc 0 1000080 4200010 800080 ff80200 2081ffc 2007e0 101ff0 100010 40004 1ffc0000 4400440
  //   4400440 4040400 8040804 8080ff8 8040802 8800ff0 200010 101ff8 40600 8040ffe 8807f8 3f00200 8*0
  //   2600360 c380c18 c000c08 2600360 c000c08 600030 c180c18 180c0c18 1800180 cc00c60 2600360 162c1c1c
  //   b080b08 808 180c0c18 c180c18 c180c18 c000800 1800180 1800180 19980ff0 7300618 11881188 180c180c 8*0
  //   cc00fc0 6300630 a100408 6000c20 c200670 8001c0 6180f18 6300630 3000300 6400638 800100 c300c30
  //   6080e18 8001c0 6300360 ff807f8 4180618 6300360 3001300 6100e30 d600380 c00120 9603900 c180410 38*0
  //   2600360 c000c08 c380c18 c000c08 2300230 c000c08 c080c18 9900990 38101c c580c38 c380c18 c800c60
  //   2300230 162c1c1c c180c18 180c0c18 c180c18 c180c18 18080c18 1800180 e080c08 19980ff0 7300618 c180c18
  //   c180c18 318c318c 318c318c 6000600 18181818 6000600 80c0c18 1b061906 c180c18 15*0 c6006c0 5c00400
  //   6300630 6100630 2600260 33001e0 1e00000 19980bd0 4300760 6300630 f780000 6400638 1300130 c38181c
  //   6300630 6300360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
  //   contents of rom_4 (hex, n*v repeats v):
  //   0 0 0 1800000 7f00000 8080808 c300000 6600330 10300c18 7ffe0000 3f800e00 2400240 318c0000 4*0 400040
  //   1000100 4000200 100020 9000480 900120 1000100 800080 2800280 500050 9000880 480088 7000780 7000f0
  //   800ff8 1400220 0 0 8080410 8081004 3000300 18181818 10041004 10041004 8000800 0 400020 800080
  //   2400240 1000080 10041004 43e141c1 1000100 5400540 1ffc0000 c101208 e702088 20822042 20802140 800040
  //   32000e00 230026 18003000 c0006 20822142 0 0 800080 800080 0 1800080 6c00240 c000c08 1c00680 20021004
  //   19001880 ff00180 1001880 2200140 16401640 10042002 1ffc3ffe 20042004 3ffc3ffc 50055005 40012002
  //   7fff3ffe 20042004 3ffc3ffc 4100410 7f007f0 19980240 3ffe003c 3ffe1e00 800490 800080 17*0 3000300
  //   600060 38000c0 19800d80 1cc01f80 1cc01b80 1800180 7800cc0 18601860 1b181b18 c600c60 30303030
  //   30c03060 336031e0 33b033e0 33b03360 30603060 30e031b0 33183318 d980d98 21822182 20622032 20c22062
  //   24c224c2 276227c2 276226c2 20622022 21c22362 23722632 44924492 44224422 44224412 44224412 45a244a2
  //   441244e2 44e24482 44224412 44624492 44724492 42524352 40c140c1 40614031 40c14061 44c142c1 476147c1
  //   476146c1 40614021 41c14361 46314631 46d946d9 0 0 5ffa4012 40024002 47e24042 4a524a52 42224fe2
  //   44424442 5d0243e2 42224262 42424242 4ffa4092 0 0 800080 2200220 8880888 8880888 2200610 8880888
  //   11141114 11541154 8500850 800140 5080508 a280a28 c301c70 0 1800180 4200420 2200220 3c00760 800040
  //   3800140 1000080 400040 2000200 1400220 ff80080 0 ff80000 0 800040 c180c18 1800180 300030 1c00060
  //   cc006c0 e600fc0 e600dc0 c000c0 3c00660 c300c30 0 18000000 30000c00 1ff8 c0030 e00038 12241224
  //   4300260 ff00c30 18001800 c0c0c0c fe00c20 fe00c20 18001800 ff80c18 1800180 c000c0 f800d80 c000c00
  //   136c162c 9900990 180c180c c300c18 180c180c c300c18 3e00e00 1800180 c080c08 c200c10 cc80cc4 1c00360
  //   3c00760 18000c0 6000600 1800300 300030 8080410 0 40 c6007c0 61807e0 c3003e0 c6007e0 c3003e0 18007e0
  //   cc007f0 73006e0 1800380 c001c0 6300678 1800180 18c66f7c c3037e0 63003e0 61819f0 63003e8 6180df0
  //   63003e0 18007e0 c301c70 18083c1c 18c43dee c303c3c e081f1c 43007f0 4000200 0 100020 3f800e00 3800100
  //   3600180 8080818 1808101c fe00200 300fe0 400fe0 400fe0 5900460 4840448 2440148 2440148 f4000f0
  //   f4000f0 4000200 4000200 18101010 18101010 0 0 4000c0 4000c0 4000400 4000400 1800080 1800080 2200220
  //   2200220 4700200 4700200 4000410 4000410 800080 800080 80710 41c04 41c04 1000100 1000100 1800140
  //   1800140 4200410 10000800 a041504 2a040904 21042108 8200820 8200820 8200820 8120814 8120814 8120814
  //   1000200 1000200 1000200 a000400 a000400 a000400 8200820 8200820 8200820 7f00080 4100210 c100410
  //   13040d88 5100320 b840268 370204c4 9240924 11221122 400080 400080 2000200 64006c0 1700100 2a200910
  //   1700100 53004c0 4c80430 6080590 a00410 f480424 52004c0 11*0 1000180 800080 1000900 800080 100808
  //   80004 800080 800080 a00060 900050 1080108 1080108 800080 800080 10200820 10200820 800040 800040
  //   80008 80008 2200220 2200220 6100c08 6100c08 800040 800040 2100208 2100208 200420 200420 12200820
  //   12200820 3ffc0080 3ffc0080 400520 400020 400020 803ffc 803ffc 2400280 2400280 803ffe 0 2200420
  //   2a00100 1000080 4080410 4080410 4080410 2000300 2000300 2000300 400020 400020 400020 8800500 8800500
  //   8800500 49002a0 49002a0 49002a0 200010 1e00e00 2000100 1c00220 800080 1100108 2000210 200020 100010
  //   7f00010 1ffc0004 100008 4400440 4400440 4100408 8040804 100808 80004 8800880 8000c0 400020 100008
  //   80004 880088 8400440 8*0 4300260 fc00c70 c000c00 4300260 fe00c20 18000c0 ff80c18 1bec1a2c 1800180
  //   f800d80 4300260 132c162c 9880988 7f00410 180c180c c180c18 e300c18 3000600 1800180 1800180 318c318c
  //   1c00360 db01998 180c180c 8*0 18c018c0 78006e0 1200210 3c00300 3c00600 4000300 6180618 7b00630
  //   3000300 7800680 1400080 c300c30 2100610 1800060 6300630 2401240 c300c18 6300630 3000300 6080618
  //   31181930 1400080 11101130 188c1888 38*0 4300260 fe00c00 fc00c70 c000c00 4300430 fe00c20 c200c00
  //   db005a0 1c00070 c980c58 c580c58 f800d00 4300430 132c162c ff80c18 180c180c c180c18 e300c18 18001800
  //   1800180 7100610 318c318c 1c00360 c180c18 c380c18 318c318c 318c318c 7e00600 1f181818 7e00600 7c000c
  //   1f061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
  //   contents of rom_5 (hex, n*v repeats v):
  //   280fffe 53fc5048 420fffe 4bfc4950 11001ffe 2007ffc 13f810a0 21242124 45084508 43f838a0 11081108
  //   3e442220 448845fc 48887dfc 20881080 8207efc 57fe7840 11081108 17f830a0 7f241424 20082008 1000100
  //   841080 104817fe 21082108 888f888 104017c0 10441040 4bfe4894 10a010a0 24401820 11083108 48a048a0
  //   44a044a0 54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
  //   输出引脚区
  //   contents of rom_6 (hex, n*v repeats v):
  //   0 0 0 180 0 4100410 c30 4400440 2600030 0 fe61c3 2400240 318c 4*0 400040 1000100 4000800 400020
  //   4800900 1200090 1000100 800080 2800280 500050 8800900 880048 7800700 f00070 800080 1400080 1ff8 0
  //   10040808 4100808 4000200 18181818 10041004 10041004 8000fc0 0 800040 800080 2400240 4000200 20022002
  //   40814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
  //   contents of rom_7 (hex, n*v repeats v):
  //   0 18002000 30000000 0 0 2200220 0 8800880 c001c0 0 38 2400240 5*0 400040 1000100 1000200 1000080
  //   2400480 2400120 1000100 800080 2800280 500050 8400880 1080088 7c00780 1f000f0 80 4100220 1800000
  //   1800000 20021004 2200410 8040400 18181818 10041004 10041004 4000800 18180000 3b001080 800080 4800480
  //   1ff80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
  //   contents of rom_8 (hex, n*v repeats v):
  //   18c618c6 4cc03fe 7fcc00ce 7ff800ac 2cff7f8e e1affff 7ffe0cc2 7ffe4862 19987f98 7ffe0186 fffc03ff
  //   7fff0238 3a781830 1bfe1ede ffc0c0c 7fff0332 19ff0982 183018fe ffc0c0c ffc0c0c 198c1d8e d180c18
  //   1b7e13de 14781fff 14701fff 1818181f 359919f9 7f7f7f60 1f8c1fee 189408d8 3d8831fc e6d0c6c 1830194e
  //   7fff0032 6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
  //   存储器扩展电路
  //   存储器地址A（14位）
  //   contents of rom_9 (hex, n*v repeats v):
  //   0 c000c00 48004800 0 0 1c00140 0 11001100 4000e0 0 0 2400240 5*0 380060 e000300 400080 200 240 240
  //   1000100 f800080 3800280 10101fd0 ff00820 7f80208 7f007e0 7f003f0 ff8 808 180 180 2002 1400220
  //   1ffc1ffc 3c3c1818 c18180c 10041004 3000400 1818 c002e00 1ffc0080 4800480 0 0 c181004 c001200 c001200
  //   5*0 20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
  //   contents of rom_10 (hex, n*v repeats v):
  //   0 0 3000 0 0 80 5*0 240 5*0 c 1800 7*0 1ff0 9*0 80 0 0 7f0 1004 c0 0 400 4*0 3e0 7*0 200 20c 0 60018
  //   30000c00 10*0 21c2 400 430 0 1c0 605e 2002 2002 0 0 3e0 80 80 7*0 80 80 3ffc 16*0 7b0 8*0 3ce6 1ef6
  //   9*0 9*808 11*1008 10*3e0 0 0 10*1008 23*0 4 2000 17*0 2000 c 0 3000 180 17*0 300048 9*0 7f8 2 ff0 9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
endmodule

module \存储器扩展测试电路  (
  input  CLR
);

  wire CLK_out;
  wire [7:0] counter_1_q;
  wire [15:0] adder_1_out, rom_1_data;
  wire [31:0] \存储器扩展电路_1_d0 , \存储器扩展电路_1_d1 , \存储器扩展电路_1_d3 , \存储器扩展电路_1_d4 , \存储器扩展电路_1_d5 , \存储器扩展电路_1_d6 ,
       \存储器扩展电路_1_d6_2 , \存储器扩展电路_1_d7 , \汉字字库电路_1_d0 , \汉字字库电路_1_d1 , \汉字字库电路_1_d3 , \汉字字库电路_1_d4 ,
       \汉字字库电路_1_d5 , \汉字字库电路_1_d6 , \汉字字库电路_1_d6_2 , \汉字字库电路_1_d7 ;

  Counter #(.width(8), .max('hff), .ongoal("wrap"), .trigger("rising"), .behavior("old")) counter_1 (
    .Q(counter_1_q), .clk(CLK_out), .clr(CLR));  // open: load, D, count, carry, preset
  Clock #(.highDuration(1), .lowDuration(1)) CLK (.out(CLK_out));
  ROM #(.addrWidth(8), .dataWidth(16), .Select("high")) rom_1 (.addr(counter_1_q), .data(rom_1_data));
  Adder #(.width(16)) adder_1 (.a(rom_1_data), .b(16'h5f60), .out(adder_1_out));  // open: cin, cout
  \存储器扩展电路  \u_存储器扩展电路_1  (
    .D0(\存储器扩展电路_1_d0 ), .D1(\存储器扩展电路_1_d1 ), .D6(\存储器扩展电路_1_d6 ), .D3(\存储器扩展电路_1_d3 ),
    .\区号 (adder_1_out[14:8]), .\位号 (adder_1_out[6:0]), .D4(\存储器扩展电路_1_d4 ), .D5(\存储器扩展电路_1_d5 ),
    .D6_2(\存储器扩展电路_1_d6_2 ), .D7(\存储器扩展电路_1_d7 ));
  \汉字字库电路  \u_汉字字库电路_1  (
    .D0(\汉字字库电路_1_d0 ), .D1(\汉字字库电路_1_d1 ), .D6(\汉字字库电路_1_d6 ), .D3(\汉字字库电路_1_d3 ), .\区号 (adder_1_out[14:8]),
    .\位号 (adder_1_out[6:0]), .D4(\汉字字库电路_1_d4 ), .D5(\汉字字库电路_1_d5 ), .D6_2(\汉字字库电路_1_d6_2 ),
    .D7(\汉字字库电路_1_d7 ));
  DotMatrix #(.inputtype("row"), .matrixcols(16), .matrixrows(16), .persist(0), .dotshape("circle")) dotmatrix_1 (
    .row0(\存储器扩展电路_1_d0 [15:0]), .row1(\存储器扩展电路_1_d0 [31:16]), .row2(\存储器扩展电路_1_d1 [15:0]),
    .row3(\存储器扩展电路_1_d1 [31:16]), .row4(\存储器扩展电路_1_d6 [15:0]), .row5(\存储器扩展电路_1_d6 [31:16]),
    .row6(\存储器扩展电路_1_d3 [15:0]), .row7(\存储器扩展电路_1_d3 [31:16]), .row8(\存储器扩展电路_1_d4 [15:0]),
    .row9(\存储器扩展电路_1_d4 [31:16]), .row10(\存储器扩展电路_1_d5 [15:0]), .row11(\存储器扩展电路_1_d5 [31:16]),
    .row12(\存储器扩展电路_1_d6_2 [15:0]), .row13(\存储器扩展电路_1_d6_2 [31:16]), .row14(\存储器扩展电路_1_d7 [15:0]),
    .row15(\存储器扩展电路_1_d7 [31:16]));
  DotMatrix #(.inputtype("row"), .matrixcols(16), .matrixrows(16), .persist(0), .dotshape("circle")) dotmatrix_2 (
    .row0(\汉字字库电路_1_d0 [15:0]), .row1(\汉字字库电路_1_d0 [31:16]), .row2(\汉字字库电路_1_d1 [15:0]),
    .row3(\汉字字库电路_1_d1 [31:16]), .row4(\汉字字库电路_1_d6 [15:0]), .row5(\汉字字库电路_1_d6 [31:16]),
    .row6(\汉字字库电路_1_d3 [15:0]), .row7(\汉字字库电路_1_d3 [31:16]), .row8(\汉字字库电路_1_d4 [15:0]),
    .row9(\汉字字库电路_1_d4 [31:16]), .row10(\汉字字库电路_1_d5 [15:0]), .row11(\汉字字库电路_1_d5 [31:16]),
    .row12(\汉字字库电路_1_d6_2 [15:0]), .row13(\汉字字库电路_1_d6_2 [31:16]), .row14(\汉字字库电路_1_d7 [15:0]),
    .row15(\汉字字库电路_1_d7 [31:16]));

  // Notes on the sheet:
  //   GB2312
  //   contents of rom_1 (hex, n*v repeats v):
  //   bbaa d6d0 bfc6 bcbc b4f3 d1a7 cac7 b9fa bcd2 bdcc d3fd b2bf d6b1 caf4 b5c4 c8ab b9fa d6d8 b5e3 b4f3
  //   d1a7 a3ac d3c9 d4ad bbaa d6d0 c0ed b9a4 b4f3 d1a7 a1a2 cdac bcc3 d2bd bfc6 b4f3 d1a7 a1a2 cee4 baba
  //   b3c7 cad0 bda8 c9e8 d1a7 d4ba d3da a3b2 a3b0 a3b0 a3b0 c4ea a3b5 d4c2 a3b2 a3b6 c8d5 bacf b2a2 b3c9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
  //   存储器扩展测试电路
  //   标准库
endmodule

module \汉字字库电路  (
  input  [6:0] \区号 ,
  input  [6:0] \位号 ,
  output [31:0] D0,
  output [31:0] D1,
  output [31:0] D6,
  output [31:0] D3,
  output [31:0] D4,
  output [31:0] D5,
  output [31:0] D6_2,
  output [31:0] D7
);

  wire [6:0] multiplier_1_cout, multiplier_1_out, subtractor_1_out;
  wire [13:0] adder_1_out, bit_extender_1_out, subtractor_2_out;

  ROM #(.addrWidth(14), .dataWidth(32), .Select("high")) rom_1 (.addr(subtractor_2_out), .data(D0));
  ROM #(.addrWidth(14), .dataWidth(32), .Select("high")) rom_2 (.addr(subtractor_2_out), .data(D4));
  Subtractor #(.width(7)) subtractor_1 (.a(\区号 ), .b(7'b0000001), .out(subtractor_1_out));  // open: bin, bout
  Multiplier #(.width(7)) multiplier_1 (
    .a(subtractor_1_out), .b(7'b1011110), .out(multiplier_1_out), .cout(multiplier_1_cout));  // open: cin
  ROM #(.addrWidth(14), .dataWidth(32), .Select("high")) rom_3 (.addr(subtractor_2_out), .data(D1));
  ROM #(.addrWidth(14), .dataWidth(32), .Select("high")) rom_4 (.addr(subtractor_2_out), .data(D5));
  Adder #(.width(14)) adder_1 (
    .a({multiplier_1_cout, multiplier_1_out}), .b(bit_extender_1_out), .out(adder_1_out));  // open: cin, cout
  assign bit_extender_1_out = {{7{1'b0}}, \位号 };  // Bit_Extender bit_extender_1
  ROM #(.addrWidth(14), .dataWidth(32), .Select("high")) rom_5 (.addr(subtractor_2_out), .data(D6));
  ROM #(.addrWidth(14), .dataWidth(32), .Select("high")) rom_6 (.addr(subtractor_2_out), .data(D6_2));
  Subtractor #(.width(14)) subtractor_2 (.a(adder_1_out), .b(14'h1), .out(subtractor_2_out));  // open: bin, bout
  DotMatrix #(.inputtype("row"), .matrixcols(16), .matrixrows(16), .persist(0), .dotshape("circle")) dotmatrix_1 (
    .row0(D0[15:0]), .row1(D0[31:16]), .row2(D1[15:0]), .row3(D1[31:16]), .row4(D6[15:0]), .row5(D6[31:16]),
    .row6(D3[15:0]), .row7(D3[31:16]), .row8(D4[15:0]), .row9(D4[31:16]), .row10(D5[15:0]),
    .row11(D5[31:16]), .row12(D6_2[15:0]), .row13(D6_2[31:16]), .row14(D7[15:0]), .row15(D7[31:16]));
  ROM #(.addrWidth(14), .dataWidth(32), .Select("high")) rom_7 (.addr(subtractor_2_out), .data(D3));
  ROM #(.addrWidth(14), .dataWidth(32), .Select("high")) rom_8 (.addr(subtractor_2_out), .data(D7));

  // Other names for the same wires on the sheet: D2[31:0] = D6; D6_t[31:0] = D6_2

  // Notes on the sheet:
  //   输入引脚区
  //   输入引脚区
  //   contents of rom_1 (hex, n*v repeats v):
  //   8*0 1000000 0 0 2400000 5*0 c0000 18000000 16*0 800000 0 0 0 10040000 7f00000 0 0 80000 800000 0 0 0
  //   c1803e0 0 600000 5*0 200000 0 18200000 180006 c003000 0 0 0 800000 1c00000 1c00000 200000 900000
  //   48003000 0 0 500000 0 40000 1c00000 38300000 800080 800080 3c00000 3c00000 c1803e0 1400080 1c00080 0
  //   0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
  //   contents of rom_2 (hex, n*v repeats v):
  //   0 0 0 180 0 4100410 c30 4400440 2600030 0 fe61c3 2400240 318c 4*0 400040 1000100 4000800 400020
  //   4800900 1200090 1000100 800080 2800280 500050 8800900 880048 7800700 f00070 800080 1400080 1ff8 0
  //   10040808 4100808 4000200 18181818 10041004 10041004 8000fc0 0 800040 800080 2400240 4000200 20022002
  //   40814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
  //   输出引脚区
  //   contents of rom_3 (hex, n*v repeats v):
  //   7*0 1100000 3000380 0 0 2400240 0 100008 c000c00 440022 33003300 600038 3000e00 400000 1000200
  //   2400000 2400000 10001f0 800080 20803f8 500070 8200ff0 20807f8 7e007f0 3f007f0 800080 0 0 0 2200140
  //   20020000 18041ffc 18183ffc 10041004 180c0c18 30000c0 18180000 100008 800080 1200120 100008 63001c0
  //   2002100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
  //   contents of rom_4 (hex, n*v repeats v):
  //   0 18002000 30000000 0 0 2200220 0 8800880 c001c0 0 38 2400240 5*0 400040 1000100 1000200 1000080
  //   2400480 2400120 1000100 800080 2800280 500050 8400880 1080088 7c00780 1f000f0 80 4100220 1800000
  //   1800000 20021004 2200410 8040400 18181818 10041004 10041004 4000800 18180000 3b001080 800080 4800480
  //   1ff80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
  //   汉字字库电路
  //   contents of rom_5 (hex, n*v repeats v):
  //   5*0 10041004 0 3300110 ffc0608 0 0 2400240 0 300030 10000800 cc00cc 44002200 400040 1000100 1000080
  //   400080 4800240 1200240 1000100 800080 28002f8 500050 8800840 880108 78007c0 f001f0 800080 4100808
  //   1800180 1800180 4100220 10042002 6000c04 18181818 10041004 10041004 4000400 1818 200010 800080
  //   1200120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
  //   contents of rom_6 (hex, n*v repeats v):
  //   0 c000c00 48004800 0 0 1c00140 0 11001100 4000e0 0 0 2400240 5*0 380060 e000300 400080 200 240 240
  //   1000100 f800080 3800280 10101fd0 ff00820 7f80208 7f007e0 7f003f0 ff8 808 180 180 2002 1400220
  //   1ffc1ffc 3c3c1818 c18180c 10041004 3000400 1818 c002e00 1ffc0080 4800480 0 0 c181004 c001200 c001200
  //   5*0 20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
  //   汉字显示验证区
  //   contents of rom_7 (hex, n*v repeats v):
  //   0 0 0 1800000 7f00000 8080808 c300000 6600330 10300c18 7ffe0000 3f800e00 2400240 318c0000 4*0 400040
  //   1000100 4000200 100020 9000480 900120 1000100 800080 2800280 500050 9000880 480088 7000780 7000f0
  //   800ff8 1400220 0 0 8080410 8081004 3000300 18181818 10041004 10041004 8000800 0 400020 800080
  //   2400240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
  //   contents of rom_8 (hex, n*v repeats v):
  //   0 0 3000 0 0 80 5*0 240 5*0 c 1800 7*0 1ff0 9*0 80 0 0 7f0 1004 c0 0 400 4*0 3e0 7*0 200 20c 0 60018
  //   30000c00 10*0 21c2 400 430 0 1c0 605e 2002 2002 0 0 3e0 80 80 7*0 80 80 3ffc 16*0 7b0 8*0 3ce6 1ef6
  //   9*0 9*808 11*1008 10*3e0 0 0 10*1008 23*0 4 2000 17*0 2000 c 0 3000 180 17*0 300048 9*0 7f8 2 ff0 9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
endmodule
