// Logisim project 寄存器文件设计实验.circ as structural Verilog: 4 circuits, main circuit 寄存器文件电路（4个寄存器）
// 寄存器
module \寄存器文件电路_4个寄存器  (
  input  [1:0] in_1,
  input  [1:0] in_2,
  input  [31:0] in_3,
  input  [1:0] in_4,
  input  in_5,
  input  in_6,
  output [31:0] out_7,
  output [31:0] out_8
);

  wire and_1_out, and_2_out, and_3_out, and_4_out, decoder_1_out0, decoder_1_out1, decoder_1_out2,
       decoder_1_out3;
  wire [31:0] Reg0, Reg1, Reg2, Reg3;

  Decoder #(.select(2), .tristate("false"), .disabled("Z"), .enable("false")) decoder_1 (
    .out0(decoder_1_out0), .out1(decoder_1_out1), .out2(decoder_1_out2), .out3(decoder_1_out3), .sel(in_4));
  and and_1 (and_1_out, in_5, decoder_1_out0);
  and and_2 (and_2_out, in_5, decoder_1_out1);
  and and_3 (and_3_out, in_5, decoder_1_out2);
  and and_4 (and_4_out, in_5, decoder_1_out3);
  Register #(.width(32), .trigger("rising"), .Select("low")) register_1 (
    .D(in_3), .en(and_1_out), .Q(Reg0), .clk(in_6));  // open: clr
  Register #(.width(32), .trigger("rising"), .Select("low")) register_2 (
    .D(in_3), .en(and_2_out), .Q(Reg1), .clk(in_6));  // open: clr
  Register #(.width(32), .trigger("rising"), .Select("low")) register_3 (
    .D(in_3), .en(and_3_out), .Q(Reg2), .clk(in_6));  // open: clr
  Register #(.width(32), .trigger("rising"), .Select("low")) register_4 (
    .D(in_3), .en(and_4_out), .Q(Reg3), .clk(in_6));  // open: clr
  Multiplexer #(.select(2), .width(32), .disabled("Z"), .enable("false")) multiplexer_1 (
    .in0(Reg0), .in1(Reg1), .in2(Reg2), .in3(Reg3), .out(out_7), .sel(in_1));
  Multiplexer #(.select(2), .width(32), .disabled("Z"), .enable("false")) multiplexer_2 (
    .in0(Reg0), .in1(Reg1), .in2(Reg2), .in3(Reg3), .out(out_8), .sel(in_2));

  // Other names for the same wires on the sheet: CLK = in_6; Din[31:0] = in_3; R1_num[1:0] = in_1; R2_num[1:0] = in_2;
  //   RD1[31:0] = out_7; RD2[31:0] = out_8; W_num[1:0] = in_4; WE = in_5

  // Notes on the sheet:
  //   输入引脚
  //   寄存器文件电路（4个寄存器）
  //   输出引脚
endmodule

// 寄存器
module \寄存器文件电路_4个寄存器_R0_0  (
  input  [1:0] in_1,
  input  [1:0] in_2,
  input  [31:0] in_3,
  input  [1:0] in_4,
  input  in_5,
  input  in_6,
  output [31:0] out_7,
  output [31:0] out_8
);

  wire and_1_out, and_2_out, and_3_out, and_4_out, decoder_1_out0, decoder_1_out1, decoder_1_out2,
       decoder_1_out3;
  wire [31:0] Reg0, Reg1, Reg2, Reg3;

  Decoder #(.select(2), .tristate("false"), .disabled("Z"), .enable("false")) decoder_1 (
    .out0(decoder_1_out0), .out1(decoder_1_out1), .out2(decoder_1_out2), .out3(decoder_1_out3), .sel(in_4));
  and and_1 (and_1_out, in_5, decoder_1_out0);
  and and_2 (and_2_out, in_5, decoder_1_out1);
  and and_3 (and_3_out, in_5, decoder_1_out2);
  and and_4 (and_4_out, in_5, decoder_1_out3);
  Register #(.width(32), .trigger("rising"), .Select("low")) register_1 (
    .D({32{1'b0}}), .en(and_1_out), .Q(Reg0), .clk(in_6));  // open: clr
  Register #(.width(32), .trigger("rising"), .Select("low")) register_2 (
    .D(in_3), .en(and_2_out), .Q(Reg1), .clk(in_6));  // open: clr
  Register #(.width(32), .trigger("rising"), .Select("low")) register_3 (
    .D(in_3), .en(and_3_out), .Q(Reg2), .clk(in_6));  // open: clr
  Register #(.width(32), .trigger("rising"), .Select("low")) register_4 (
    .D(in_3), .en(and_4_out), .Q(Reg3), .clk(in_6));  // open: clr
  Multiplexer #(.select(2), .width(32), .disabled("Z"), .enable("false")) multiplexer_1 (
    .in0(Reg0), .in1(Reg1), .in2(Reg2), .in3(Reg3), .out(out_7), .sel(in_1));
  Multiplexer #(.select(2), .width(32), .disabled("Z"), .enable("false")) multiplexer_2 (
    .in0(Reg0), .in1(Reg1), .in2(Reg2), .in3(Reg3), .out(out_8), .sel(in_2));

  // Other names for the same wires on the sheet: CLK = in_6; Din[31:0] = in_3; R1_num[1:0] = in_1; R2_num[1:0] = in_2;
  //   RD1[31:0] = out_7; RD2[31:0] = out_8; W_num[1:0] = in_4; WE = in_5

  // Notes on the sheet:
  //   输入引脚
  //   寄存器文件电路（4个寄存器，R0=0）
  //   输出引脚
endmodule

module \寄存器文件测试电路_4个寄存器__R0_0  (
  input  [1:0] R1_num,
  input  [1:0] R2_num,
  input  [31:0] Din,
  input  WE,
  input  [1:0] W_num,
  output [31:0] RD1,
  output [31:0] RD2
);

  wire clock_1_out;

  Clock #(.highDuration(1), .lowDuration(1)) clock_1 (.out(clock_1_out));
  \寄存器文件电路_4个寄存器_R0_0  \u_寄存器文件电路_4个寄存器_r0_0_1  (
    .in_1(R1_num), .in_2(R2_num), .in_3(Din), .in_4(W_num), .in_5(WE), .in_6(clock_1_out), .out_7(RD1),
    .out_8(RD2));

  // Notes on the sheet:
  //   寄存器文件测试电路（四个寄存器）（R0=0）
endmodule

module \寄存器文件测试电路_4个寄存器  (
  input  [1:0] R1_num,
  input  [1:0] R2_num,
  input  [31:0] Din,
  input  WE,
  input  [1:0] W_num,
  output [31:0] RD1,
  output [31:0] RD2
);

  wire clock_1_out;

  Clock #(.highDuration(1), .lowDuration(1)) clock_1 (.out(clock_1_out));
  \寄存器文件电路_4个寄存器  \u_寄存器文件电路_4个寄存器_1  (
    .in_1(R1_num), .in_2(R2_num), .in_3(Din), .in_4(W_num), .in_5(WE), .in_6(clock_1_out), .out_7(RD1),
    .out_8(RD2));

  // Notes on the sheet:
  //   寄存器文件测试电路（四个寄存器）
endmodule
