// Logisim project 多周期MIPS处理器（硬布线控制器）（8条指令）.circ as structural Verilog: 7 circuits, main circuit 多周期MIPS处理器（硬布线控制器）数据通路
module \多周期MIPS处理器_硬布线控制器_数据通路  (
);

  wire alu_1_equal, and_1_out, and_2_out, CLK, comparator_1_eq, MemRead, MemWrite, not_1_out, or_1_out, RST,
       \硬布线控制器_1_alusrca , \硬布线控制器_1_beq , \硬布线控制器_1_bne , \硬布线控制器_1_iord , \硬布线控制器_1_irwrite ,
       \硬布线控制器_1_memtoreg , \硬布线控制器_1_pcsrc , \硬布线控制器_1_pcwrite , \硬布线控制器_1_regdst , \硬布线控制器_1_regwrite ;
  wire [1:0] \硬布线控制器_1_alusrcb ;
  wire [3:0] \现态 , \硬布线控制器_1_alu_op ;
  wire [4:0] multiplexer_2_out;
  wire [15:0] \总周期数 ;
  wire [31:0] A_q, alu_1_result, B_q, bit_extender_1_out, C_q, DR_q, IR_q, multiplexer_1_out,
       multiplexer_3_out, multiplexer_4_out, multiplexer_5_out, multiplexer_6_out, PC_q, ram_1_data,
       regifile_1_r1, regifile_1_r2, shifter_1_out;

  Button \u_总复位  (.out(RST));
  Register #(.width(32), .trigger("rising"), .Select("low")) PC (
    .D(multiplexer_6_out), .en(or_1_out), .Q(PC_q), .clk(CLK), .clr(RST));
  Multiplexer #(.select(1), .width(32), .disabled("Z"), .enable("false")) multiplexer_1 (
    .in0(PC_q), .in1(C_q), .out(multiplexer_1_out), .sel(\硬布线控制器_1_iord ));
  Clock #(.highDuration(1), .lowDuration(1)) u_CLK (.out(CLK));
  RAM #(.addrWidth(10), .dataWidth(32), .bus("separate"), .Select("high")) ram_1 (
    .addr(multiplexer_1_out[11:2]), .din(B_q), .data(ram_1_data), .str(MemWrite), .clk(CLK), .ld(MemRead));  // open: sel, clr
  Register #(.width(32), .trigger("rising"), .Select("low")) IR (
    .D(ram_1_data), .en(\硬布线控制器_1_irwrite ), .Q(IR_q), .clk(CLK));  // open: clr
  Register #(.width(32), .trigger("rising"), .Select("low")) DR (.D(ram_1_data), .Q(DR_q), .clk(CLK));  // open: en, clr
  // Probe on \现态 
  \硬布线控制器  \u_硬布线控制器_1  (
    .AluSrcB(\硬布线控制器_1_alusrcb ), .OP(IR_q[31:26]), .CLK(CLK), .\现态 (\现态 ), .IorD(\硬布线控制器_1_iord ),
    .PCsrc(\硬布线控制器_1_pcsrc ), .AluSrcA(\硬布线控制器_1_alusrca ), .MemToReg(\硬布线控制器_1_memtoreg ),
    .RegDst(\硬布线控制器_1_regdst ), .IrWrite(\硬布线控制器_1_irwrite ), .PcWrite(\硬布线控制器_1_pcwrite ),
    .RegWrite(\硬布线控制器_1_regwrite ), .MemWrite(MemWrite), .MemRead(MemRead), .Beq(\硬布线控制器_1_beq ),
    .Bne(\硬布线控制器_1_bne ), .Func(IR_q[5:0]), .ALU_OP(\硬布线控制器_1_alu_op ), .RST(RST));
  Multiplexer #(.select(1), .width(5), .disabled("Z"), .enable("false")) multiplexer_2 (
    .in0(IR_q[20:16]), .in1(IR_q[15:11]), .out(multiplexer_2_out), .sel(\硬布线控制器_1_regdst ));
  // Probe on \总周期数 
  Multiplexer #(.select(1), .width(32), .disabled("Z"), .enable("false")) multiplexer_3 (
    .in0(C_q), .in1(DR_q), .out(multiplexer_3_out), .sel(\硬布线控制器_1_memtoreg ));
  Regifile regifile_1 (
    .Din(multiplexer_3_out), .Clk(CLK), .R1(regifile_1_r1), .R2(regifile_1_r2), .WE(\硬布线控制器_1_regwrite ),
    .W_num(multiplexer_2_out), .R1_num(IR_q[25:21]), .R2_num(IR_q[20:16]));
  assign bit_extender_1_out = {{16{IR_q[15]}}, IR_q[15:0]};  // Bit_Extender bit_extender_1
  Register #(.width(32), .trigger("rising"), .Select("low")) A (
    .D(regifile_1_r1), .Q(A_q), .clk(CLK));  // open: en, clr
  Register #(.width(32), .trigger("rising"), .Select("low")) B (
    .D(regifile_1_r2), .Q(B_q), .clk(CLK));  // open: en, clr
  Comparator #(.width(4), .mode("twosComplement")) comparator_1 (
    .a(\现态 ), .b(4'b1101), .eq(comparator_1_eq));  // open: gt, lt
  Multiplexer #(.select(1), .width(32), .disabled("Z"), .enable("false")) multiplexer_4 (
    .in0(PC_q), .in1(A_q), .out(multiplexer_4_out), .sel(\硬布线控制器_1_alusrca ));
  Shifter #(.width(32), .shift("ll")) shifter_1 (.in(bit_extender_1_out), .\dist (5'b00010), .out(shifter_1_out));
  not not_1 (not_1_out, comparator_1_eq);
  Multiplexer #(.select(2), .width(32), .disabled("Z"), .enable("false")) multiplexer_5 (
    .in0(B_q), .in1(32'h4), .in2(bit_extender_1_out), .in3(shifter_1_out), .out(multiplexer_5_out),
    .sel(\硬布线控制器_1_alusrcb ));
  Counter #(.width(16), .max('hffff), .ongoal("wrap"), .trigger("rising"), .behavior("old")) counter_1 (
    .count(not_1_out), .Q(\总周期数 ), .clk(CLK), .clr(RST));  // open: load, D, carry, preset
  and and_1 (and_1_out, \硬布线控制器_1_bne , ~alu_1_equal);  // AND_Gate
  ALU alu_1 (
    .X(multiplexer_4_out), .Y(multiplexer_5_out), .AluOP(\硬布线控制器_1_alu_op ), .Equal(alu_1_equal),
    .Result(alu_1_result));  // open: Result_2
  and and_2 (and_2_out, \硬布线控制器_1_beq , alu_1_equal);
  Multiplexer #(.select(1), .width(32), .disabled("Z"), .enable("false")) multiplexer_6 (
    .in0(alu_1_result), .in1(C_q), .out(multiplexer_6_out), .sel(\硬布线控制器_1_pcsrc ));
  Register #(.width(32), .trigger("rising"), .Select("low")) C (.D(alu_1_result), .Q(C_q), .clk(CLK));  // open: en, clr
  or or_1 (or_1_out, \硬布线控制器_1_pcwrite , and_2_out, and_1_out);

  // Notes on the sheet:
  //   IorD
  //   存储器
  //   IRWrite
  //   MemWrite
  //   MemRead
  //   IRWrite
  //   指令字
  //   rs
  //   rt
  //   rd
  //   Imm16
  //   支持LW、SW、BEQ、BNE、SLT、ADDI、ADD、SYSCALL等8条指令
  //   IorD
  //   OP
  //   Func
  //   RegDst
  //   PcWrite
  //   Beq
  //   Bne
  //   PcSrc
  //   AluOP
  //   AluSrcB
  //   AluSrcA
  //   RegWrite
  //   MemToReg
  //   多周期 MIPS 处理器（硬布线控制器）数据通路                
  //   PcEnable
endmodule

module \硬布线控制器  (
  input  [5:0] OP,
  input  [5:0] Func,
  input  CLK,
  input  RST,
  output Bne,
  output Beq,
  output MemRead,
  output MemWrite,
  output RegWrite,
  output PcWrite,
  output IrWrite,
  output RegDst,
  output MemToReg,
  output [3:0] \现态 ,
  output [1:0] AluSrcB,
  output AluSrcA,
  output PCsrc,
  output IorD,
  output [3:0] ALU_OP
);

  wire ADD, ADDI, BEQ_t, BNE_t, comparator_6_eq, comparator_7_eq, comparator_8_eq, comparator_9_eq,
       comparator_10_eq, LW, R_TYPE, SLT, SW, SysCall;
  wire [1:0] ALU_Control;
  wire [3:0] multiplexer_1_out, \控制器状态机_1_n0 ;

  Comparator #(.width(6), .mode("twosComplement")) comparator_1 (.a(OP), .b(6'b100011), .eq(LW));  // open: gt, lt
  Comparator #(.width(6), .mode("twosComplement")) comparator_2 (.a(OP), .b(6'b101011), .eq(SW));  // open: gt, lt
  Comparator #(.width(6), .mode("twosComplement")) comparator_3 (.a(OP), .b(6'b000100), .eq(BEQ_t));  // open: gt, lt
  Comparator #(.width(6), .mode("twosComplement")) comparator_4 (.a(OP), .b(6'b000101), .eq(BNE_t));  // open: gt, lt
  Comparator #(.width(6), .mode("twosComplement")) comparator_5 (.a(OP), .b(6'b001000), .eq(ADDI));  // open: gt, lt
  Comparator #(.width(6), .mode("twosComplement")) comparator_6 (
    .a(OP), .b({6{1'b0}}), .eq(comparator_6_eq));  // open: gt, lt
  \控制器状态机  \u_控制器状态机_1  (
    .S3(\现态 [3]), .S2(\现态 [2]), .S1(\现态 [1]), .S0(\现态 [0]), .LW(LW), .SW(SW), .BEQ(BEQ_t),
    .N3(\控制器状态机_1_n0 [3]), .BNE(BNE_t), .RTYPE(R_TYPE), .ADDI(ADDI), .SYSCALL(SysCall),
    .N2(\控制器状态机_1_n0 [2]), .N1(\控制器状态机_1_n0 [1]), .N0(\控制器状态机_1_n0 [0]));
  or or_1 (R_TYPE, ADD, SLT);
  Comparator #(.width(6), .mode("twosComplement")) comparator_7 (
    .a(Func), .b(6'b100000), .eq(comparator_7_eq));  // open: gt, lt
  Comparator #(.width(6), .mode("twosComplement")) comparator_8 (
    .a(Func), .b(6'b101010), .eq(comparator_8_eq));  // open: gt, lt
  Comparator #(.width(6), .mode("twosComplement")) comparator_9 (
    .a(Func), .b(6'b001100), .eq(comparator_9_eq));  // open: gt, lt
  Register #(.width(4), .trigger("rising"), .Select("low")) register_1 (
    .D(\控制器状态机_1_n0 ), .Q(\现态 ), .clk(CLK), .clr(RST));  // open: en
  and and_1 (ADD, comparator_7_eq, comparator_6_eq);
  and and_2 (SLT, comparator_8_eq, comparator_6_eq);
  and and_3 (SysCall, comparator_9_eq, comparator_6_eq);
  \输出函数  \u_输出函数_1  (
    .N3(\现态 [3]), .N2(\现态 [2]), .IorD(IorD), .N1(\现态 [1]), .N0(\现态 [0]), .PCSrc(PCsrc), .AluSrcA(AluSrcA),
    .AluSrcB1(AluSrcB[1]), .AluSrcB0(AluSrcB[0]), .MemToReg(MemToReg), .RegDst(RegDst), .IRWrite(IrWrite),
    .PCWrite(PcWrite), .RegWrite(RegWrite), .MemWrite(MemWrite), .MemRead(MemRead), .Beq(Beq), .Bne(Bne),
    .AluCtrl1(ALU_Control[1]), .AluCtrl0(ALU_Control[0]));
  Comparator #(.width(6), .mode("twosComplement")) comparator_10 (
    .a(Func), .b(6'b101010), .eq(comparator_10_eq));  // open: gt, lt
  Multiplexer #(.select(1), .width(4), .disabled("Z"), .enable("false")) multiplexer_1 (
    .in0(4'b0101), .in1(4'b1100), .out(multiplexer_1_out), .sel(comparator_10_eq));
  Multiplexer #(.select(2), .width(4), .disabled("Z"), .enable("false")) multiplexer_2 (
    .in0(4'b0101), .in1(4'b0101), .in2(multiplexer_1_out), .in3(4'b0101), .out(ALU_OP), .sel(ALU_Control));

  // Notes on the sheet:
  //   输入信号
  //   指令译码信号
  //   现态
  //   指令译码逻辑
  //   次态
  //   状态寄存器
  //   硬布线控制器
  //   输出信号
  //   加法
  //   比较
  //   比较
  //   现态（4位）            14个控制信号
  //   ALU控制器逻辑
  //   ALU_Control = 10：运算方式由Func决定 
  //   ALU_Control = 00、01、11：运算器做加法
endmodule

module \控制器状态机  (
  input  S3,
  input  S2,
  input  S1,
  input  S0,
  input  LW,
  input  SW,
  input  BEQ,
  input  BNE,
  input  RTYPE,
  input  ADDI,
  input  SYSCALL,
  output N3,
  output N2,
  output N1,
  output N0
);

  wire and_1_out, and_2_out, and_3_out, and_4_out, and_5_out, and_6_out, and_7_out, and_8_out, and_9_out,
       and_10_out, and_11_out, and_12_out, and_13_out, and_14_out, and_15_out, and_16_out, and_17_out,
       and_18_out, and_19_out, and_20_out, and_21_out, and_22_out, and_23_out, and_24_out, and_25_out,
       and_26_out, and_27_out, and_28_out, not_1_out, not_2_out, not_3_out, not_4_out, not_5_out, not_6_out,
       not_7_out, not_8_out, not_9_out, not_10_out, not_11_out, not_12_out, not_13_out, not_14_out,
       not_15_out, not_16_out, not_17_out, not_18_out, not_19_out, not_20_out, not_21_out, not_22_out,
       not_23_out, not_24_out, not_25_out, not_26_out, not_27_out, not_28_out, not_29_out, not_30_out,
       not_31_out, not_32_out, not_33_out, not_34_out, not_35_out, not_36_out, not_37_out, not_38_out,
       not_39_out, not_40_out, not_41_out, not_42_out, not_43_out, not_44_out, not_45_out, not_46_out,
       not_47_out, not_48_out, not_49_out, not_50_out, not_51_out, not_52_out, not_53_out, not_54_out,
       not_55_out, not_56_out, not_57_out, not_58_out, not_59_out, not_60_out, not_61_out, not_62_out,
       not_63_out, not_64_out, not_65_out, not_66_out, not_67_out, not_68_out, not_69_out, not_70_out;

  not not_1 (not_1_out, S3);
  not not_2 (not_2_out, S2);
  not not_3 (not_3_out, S1);
  not not_4 (not_4_out, S3);
  not not_5 (not_5_out, S2);
  not not_6 (not_6_out, S1);
  not not_7 (not_7_out, S3);
  not not_8 (not_8_out, S2);
  not not_9 (not_9_out, S1);
  not not_10 (not_10_out, S3);
  not not_11 (not_11_out, S2);
  not not_12 (not_12_out, S1);
  not not_13 (not_13_out, S2);
  not not_14 (not_14_out, S1);
  not not_15 (not_15_out, S2);
  not not_16 (not_16_out, S1);
  not not_17 (not_17_out, S3);
  not not_18 (not_18_out, S2);
  not not_19 (not_19_out, S1);
  not not_20 (not_20_out, S3);
  not not_21 (not_21_out, S2);
  not not_22 (not_22_out, S1);
  not not_23 (not_23_out, S3);
  not not_24 (not_24_out, S2);
  not not_25 (not_25_out, S1);
  not not_26 (not_26_out, S3);
  not not_27 (not_27_out, S2);
  not not_28 (not_28_out, S3);
  not not_29 (not_29_out, S1);
  not not_30 (not_30_out, S2);
  not not_31 (not_31_out, S1);
  not not_32 (not_32_out, S3);
  not not_33 (not_33_out, S2);
  not not_34 (not_34_out, S1);
  not not_35 (not_35_out, S3);
  not not_36 (not_36_out, S2);
  not not_37 (not_37_out, S1);
  not not_38 (not_38_out, S3);
  not not_39 (not_39_out, S2);
  not not_40 (not_40_out, S1);
  not not_41 (not_41_out, S3);
  not not_42 (not_42_out, S2);
  not not_43 (not_43_out, S0);
  not not_44 (not_44_out, S3);
  not not_45 (not_45_out, S1);
  not not_46 (not_46_out, S2);
  not not_47 (not_47_out, S1);
  not not_48 (not_48_out, S3);
  not not_49 (not_49_out, S2);
  not not_50 (not_50_out, S1);
  not not_51 (not_51_out, S0);
  not not_52 (not_52_out, S3);
  not not_53 (not_53_out, S2);
  not not_54 (not_54_out, S1);
  not not_55 (not_55_out, S3);
  not not_56 (not_56_out, S2);
  not not_57 (not_57_out, S1);
  not not_58 (not_58_out, S3);
  not not_59 (not_59_out, S2);
  not not_60 (not_60_out, S1);
  not not_61 (not_61_out, S3);
  not not_62 (not_62_out, S2);
  not not_63 (not_63_out, S1);
  not not_64 (not_64_out, S3);
  not not_65 (not_65_out, S2);
  not not_66 (not_66_out, S1);
  not not_67 (not_67_out, S3);
  not not_68 (not_68_out, S2);
  not not_69 (not_69_out, S0);
  not not_70 (not_70_out, S1);
  and and_1 (and_1_out, not_1_out, not_2_out, not_3_out, S0, BNE);
  and and_2 (and_2_out, not_4_out, not_5_out, not_6_out, S0, RTYPE);
  and and_3 (and_3_out, not_7_out, not_8_out, not_9_out, S0, ADDI);
  and and_4 (and_4_out, not_10_out, not_11_out, not_12_out, S0, SYSCALL);
  and and_5 (and_5_out, S3, not_13_out, not_14_out, S0);
  and and_6 (and_6_out, S3, not_15_out, S1, S0);
  and and_7 (and_7_out, S3, S2, not_16_out, S0);
  and and_8 (and_8_out, not_17_out, not_18_out, not_19_out, S0, SW);
  and and_9 (and_9_out, not_20_out, not_21_out, not_22_out, S0, BEQ);
  and and_10 (and_10_out, not_23_out, not_24_out, not_25_out, S0, SYSCALL);
  and and_11 (and_11_out, not_26_out, not_27_out, S1, S0);
  and and_12 (and_12_out, not_28_out, S2, not_29_out, S0);
  and and_13 (and_13_out, S3, not_30_out, S1, S0);
  and and_14 (and_14_out, S3, S2, not_31_out, S0);
  and and_15 (and_15_out, not_32_out, not_33_out, not_34_out, S0, LW);
  and and_16 (and_16_out, not_35_out, not_36_out, not_37_out, S0, BEQ);
  and and_17 (and_17_out, not_38_out, not_39_out, not_40_out, S0, ADDI);
  and and_18 (and_18_out, not_41_out, not_42_out, S1, not_43_out);
  and and_19 (and_19_out, not_44_out, S2, not_45_out, S0);
  and and_20 (and_20_out, S3, not_46_out, not_47_out, S0);
  and and_21 (and_21_out, not_48_out, not_49_out, not_50_out, not_51_out);
  and and_22 (and_22_out, not_52_out, not_53_out, not_54_out, S0, SW);
  and and_23 (and_23_out, not_55_out, not_56_out, not_57_out, S0, BEQ);
  and and_24 (and_24_out, not_58_out, not_59_out, not_60_out, S0, RTYPE);
  and and_25 (and_25_out, not_61_out, not_62_out, not_63_out, S0, ADDI);
  and and_26 (and_26_out, not_64_out, not_65_out, not_66_out, S0, SYSCALL);
  and and_27 (and_27_out, not_67_out, not_68_out, S1, not_69_out);
  and and_28 (and_28_out, S3, S2, not_70_out, S0);
  or or_1 (N3, and_1_out, and_2_out, and_3_out, and_4_out, and_5_out, and_6_out, and_7_out);
  or or_2 (N2, and_8_out, and_9_out, and_10_out, and_11_out, and_12_out, and_13_out, and_14_out);
  or or_3 (N1, and_15_out, and_16_out, and_17_out, and_18_out, and_19_out, and_20_out);
  or or_4 (N0, and_21_out, and_22_out, and_23_out, and_24_out, and_25_out, and_26_out, and_27_out, and_28_out);
endmodule

module \输出函数  (
  input  N3,
  input  N2,
  input  N1,
  input  N0,
  output IorD,
  output PCSrc,
  output AluSrcA,
  output AluSrcB1,
  output AluSrcB0,
  output MemToReg,
  output RegDst,
  output IRWrite,
  output PCWrite,
  output RegWrite,
  output MemWrite,
  output MemRead,
  output Beq,
  output Bne,
  output AluCtrl1,
  output AluCtrl0
);

  wire and_1_out, and_2_out, and_3_out, and_4_out, and_5_out, and_6_out, and_7_out, and_8_out, and_9_out,
       and_10_out, and_11_out, and_12_out, and_13_out, and_14_out, and_15_out, and_16_out, and_21_out,
       and_22_out, and_23_out, and_25_out, and_26_out, and_30_out, and_31_out, not_1_out, not_2_out,
       not_3_out, not_4_out, not_5_out, not_6_out, not_7_out, not_8_out, not_9_out, not_10_out, not_11_out,
       not_12_out, not_13_out, not_14_out, not_15_out, not_16_out, not_17_out, not_18_out, not_19_out,
       not_20_out, not_21_out, not_22_out, not_23_out, not_24_out, not_25_out, not_26_out, not_27_out,
       not_28_out, not_29_out, not_30_out, not_31_out, not_32_out, not_33_out, not_34_out, not_35_out,
       not_36_out, not_37_out, not_38_out, not_39_out, not_40_out, not_41_out, not_42_out, not_43_out,
       not_44_out, not_45_out, not_46_out, not_47_out, not_48_out, not_49_out, not_50_out, not_51_out,
       not_52_out, not_53_out, not_54_out, not_55_out, not_56_out, not_57_out, not_58_out, not_59_out,
       not_60_out, not_61_out, not_62_out, not_63_out, not_64_out, not_65_out, not_66_out, not_67_out,
       not_68_out, not_69_out, not_70_out, not_71_out, not_72_out, not_73_out, not_74_out;

  not not_1 (not_1_out, N3);
  not not_2 (not_2_out, N2);
  not not_3 (not_3_out, N3);
  not not_4 (not_4_out, N0);
  not not_5 (not_5_out, N3);
  not not_6 (not_6_out, N2);
  not not_7 (not_7_out, N1);
  not not_8 (not_8_out, N0);
  not not_9 (not_9_out, N3);
  not not_10 (not_10_out, N2);
  not not_11 (not_11_out, N0);
  not not_12 (not_12_out, N3);
  not not_13 (not_13_out, N1);
  not not_14 (not_14_out, N3);
  not not_15 (not_15_out, N2);
  not not_16 (not_16_out, N1);
  not not_17 (not_17_out, N0);
  not not_18 (not_18_out, N2);
  not not_19 (not_19_out, N1);
  not not_20 (not_20_out, N2);
  not not_21 (not_21_out, N3);
  not not_22 (not_22_out, N2);
  not not_23 (not_23_out, N1);
  not not_24 (not_24_out, N3);
  not not_25 (not_25_out, N2);
  not not_26 (not_26_out, N0);
  not not_27 (not_27_out, N3);
  not not_28 (not_28_out, N1);
  not not_29 (not_29_out, N2);
  not not_30 (not_30_out, N3);
  not not_31 (not_31_out, N2);
  not not_32 (not_32_out, N1);
  not not_33 (not_33_out, N0);
  not not_34 (not_34_out, N3);
  not not_35 (not_35_out, N2);
  not not_36 (not_36_out, N1);
  not not_37 (not_37_out, N3);
  not not_38 (not_38_out, N1);
  not not_39 (not_39_out, N0);
  not not_40 (not_40_out, N2);
  not not_41 (not_41_out, N0);
  not not_42 (not_42_out, N3);
  not not_43 (not_43_out, N2);
  not not_44 (not_44_out, N1);
  not not_45 (not_45_out, N0);
  not not_46 (not_46_out, N3);
  not not_47 (not_47_out, N2);
  not not_48 (not_48_out, N1);
  not not_49 (not_49_out, N0);
  not not_50 (not_50_out, N3);
  not not_51 (not_51_out, N1);
  not not_52 (not_52_out, N0);
  not not_53 (not_53_out, N2);
  not not_54 (not_54_out, N0);
  not not_55 (not_55_out, N1);
  not not_56 (not_56_out, N0);
  not not_57 (not_57_out, N3);
  not not_58 (not_58_out, N0);
  not not_59 (not_59_out, N3);
  not not_60 (not_60_out, N2);
  not not_61 (not_61_out, N1);
  not not_62 (not_62_out, N0);
  not not_63 (not_63_out, N3);
  not not_64 (not_64_out, N2);
  not not_65 (not_65_out, N3);
  not not_66 (not_66_out, N2);
  not not_67 (not_67_out, N1);
  not not_68 (not_68_out, N0);
  not not_69 (not_69_out, N2);
  not not_70 (not_70_out, N1);
  not not_71 (not_71_out, N3);
  not not_72 (not_72_out, N2);
  not not_73 (not_73_out, N1);
  not not_74 (not_74_out, N0);
  and and_1 (and_1_out, not_1_out, not_2_out, N1, N0);
  or or_1 (IorD, and_1_out, and_2_out);
  and and_2 (and_2_out, not_3_out, N2, N1, not_4_out);
  and and_3 (and_3_out, not_5_out, N2, N1, N0);
  or or_2 (PCSrc, and_3_out, and_4_out);
  and and_4 (and_4_out, N3, not_6_out, not_7_out, not_8_out);
  and and_5 (and_5_out, not_9_out, not_10_out, N1, not_11_out);
  and and_6 (and_6_out, not_12_out, N2, not_13_out, N0);
  and and_7 (and_7_out, not_14_out, N2, N1, N0);
  and and_8 (and_8_out, N3, not_15_out, not_16_out, not_17_out);
  and and_9 (and_9_out, N3, not_18_out, not_19_out, N0);
  and and_10 (and_10_out, N3, not_20_out, N1, N0);
  and and_11 (and_11_out, not_21_out, not_22_out, not_23_out, N0);
  and and_12 (and_12_out, not_24_out, not_25_out, N1, not_26_out);
  and and_13 (and_13_out, not_27_out, N2, not_28_out, N0);
  and and_14 (and_14_out, N3, not_29_out, N1, N0);
  and and_15 (and_15_out, not_30_out, not_31_out, not_32_out, not_33_out);
  or or_3 (AluSrcB0, and_15_out, and_16_out);
  and and_16 (and_16_out, not_34_out, not_35_out, not_36_out, N0);
  and and_17 (MemToReg, not_37_out, N2, not_38_out, not_39_out);
  and and_18 (RegDst, N3, not_40_out, N1, not_41_out);
  and and_19 (IRWrite, not_42_out, not_43_out, not_44_out, not_45_out);
  and and_20 (PCWrite, not_46_out, not_47_out, not_48_out, not_49_out);
  and and_21 (and_21_out, not_50_out, N2, not_51_out, not_52_out);
  or or_4 (RegWrite, and_21_out, and_22_out, and_23_out);
  and and_22 (and_22_out, N3, not_53_out, N1, not_54_out);
  and and_23 (and_23_out, N3, N2, not_55_out, not_56_out);
  and and_24 (MemWrite, not_57_out, N2, N1, not_58_out);
  and and_25 (and_25_out, not_59_out, not_60_out, not_61_out, not_62_out);
  or or_5 (MemRead, and_25_out, and_26_out);
  and and_26 (and_26_out, not_63_out, not_64_out, N1, N0);
  and and_27 (Beq, not_65_out, N2, N1, N0);
  and and_28 (Bne, N3, not_66_out, not_67_out, not_68_out);
  and and_29 (AluCtrl1, N3, not_69_out, not_70_out, N0);
  and and_30 (and_30_out, not_71_out, N2, N1, N0);
  or or_6 (AluCtrl0, and_30_out, and_31_out);
  and and_31 (and_31_out, N3, not_72_out, not_73_out, not_74_out);
  or or_7 (AluSrcA, and_5_out, and_6_out, and_7_out, and_8_out, and_9_out, and_10_out);
  or or_8 (AluSrcB1, and_11_out, and_12_out, and_13_out, and_14_out);
endmodule

module ALU (
  input  [31:0] X,
  input  [31:0] Y,
  input  [3:0] AluOP,
  output Equal,
  output [31:0] Result,
  output [31:0] Result_2
);

  wire [0:0] comparator_1_lt, comparator_2_lt;
  wire [31:0] adder_1_out, AND_out, divider_1_out, divider_1_rem, multiplier_1_cout, multiplier_1_out,
       NOR_out, OR_out, shifter_1_out, shifter_2_out, shifter_3_out, subtractor_1_out, XOR_out;

  Shifter #(.width(32), .shift("ll")) shifter_1 (.in(X), .\dist (Y[4:0]), .out(shifter_1_out));
  Shifter #(.width(32), .shift("ar")) shifter_2 (.in(X), .\dist (Y[4:0]), .out(shifter_2_out));
  Shifter #(.width(32), .shift("lr")) shifter_3 (.in(X), .\dist (Y[4:0]), .out(shifter_3_out));
  Multiplier #(.width(32)) multiplier_1 (.a(X), .b(Y), .out(multiplier_1_out), .cout(multiplier_1_cout));  // open: cin
  Divider #(.width(32)) divider_1 (.a(X), .b(Y), .out(divider_1_out), .rem(divider_1_rem));  // open: upper
  Adder #(.width(32)) adder_1 (.a(X), .b(Y), .out(adder_1_out));  // open: cin, cout
  Subtractor #(.width(32)) subtractor_1 (.a(X), .b(Y), .out(subtractor_1_out));  // open: bin, bout
  assign AND_out = X & Y;  // AND_Gate AND, 32 bits wide
  assign OR_out = X | Y;  // OR_Gate OR, 32 bits wide
  assign XOR_out = X ^ Y;  // XOR_Gate XOR, 32 bits wide
  assign NOR_out = ~(X | Y);  // NOR_Gate NOR, 32 bits wide
  Comparator #(.width(32), .mode("twosComplement")) comparator_1 (
    .a(X), .b(Y), .eq(Equal), .lt(comparator_1_lt[0]));  // open: gt
  Comparator #(.width(32), .mode("twosComplement")) comparator_2 (
    .a(X), .b(Y), .lt(comparator_2_lt[0]));  // open: gt, eq
  Multiplexer #(.select(4), .width(32), .disabled("Z"), .enable("false")) multiplexer_1 (
    .in0(shifter_1_out), .in1(shifter_2_out), .in2(shifter_3_out), .in3(multiplier_1_out),
    .in4(divider_1_out), .in5(adder_1_out), .in6(subtractor_1_out), .in7(AND_out), .in8(OR_out),
    .in9(XOR_out), .in10(NOR_out), .in11({{31{1'b0}}, comparator_1_lt[0]}),
    .in12({{31{1'b0}}, comparator_2_lt[0]}), .in13({32{1'b0}}), .in14({32{1'b0}}), .in15({32{1'b0}}),
    .out(Result), .sel(AluOP));
  Multiplexer #(.select(4), .width(32), .disabled("Z"), .enable("false")) multiplexer_2 (
    .in0({32{1'b0}}), .in1({32{1'b0}}), .in2({32{1'b0}}), .in3(multiplier_1_cout), .in4(divider_1_rem),
    .in5({32{1'b0}}), .in6({32{1'b0}}), .in7({32{1'b0}}), .in8({32{1'b0}}), .in9({32{1'b0}}),
    .in10({32{1'b0}}), .in11({32{1'b0}}), .in12({32{1'b0}}), .in13({32{1'b0}}), .in14({32{1'b0}}),
    .in15({32{1'b0}}), .out(Result_2), .sel(AluOP));

  // Other names for the same wires on the sheet: Result2[31:0] = Result_2; S[3:0] = AluOP

  // Notes on the sheet:
  //   输入引脚
  //   算术逻辑单元ALU
  //   输出引脚
endmodule

module Regifile (
  input  [31:0] Din,
  input  Clk,
  input  WE,
  input  [4:0] W_num,
  input  [4:0] R1_num,
  input  [4:0] R2_num,
  output [31:0] R1,
  output [31:0] R2
);

  // RegisterFile registerfile_1: pin names not known; wires that end beside it: Din, Clk, WE, W_num, R1_num, R2_num, R1, R2

  // Notes on the sheet:
  //   寄存器堆Regfile
endmodule

module \测试  (
  input  [3:0] \现态 ,
  input  LW,
  input  SW,
  input  BEQ,
  input  BNE,
  input  R_TYPE,
  input  ADDI,
  input  SYSCALL,
  output [3:0] \次态 
);

  // Probe on \现态 
  \控制器状态机  \u_控制器状态机_1  (
    .S3(\现态 [3]), .S2(\现态 [2]), .S1(\现态 [1]), .S0(\现态 [0]), .LW(LW), .SW(SW), .BEQ(BEQ), .N3(\次态 [3]),
    .BNE(BNE), .RTYPE(R_TYPE), .ADDI(ADDI), .SYSCALL(SYSCALL), .N2(\次态 [2]), .N1(\次态 [1]), .N0(\次态 [0]));
  // Probe on \次态 
endmodule
