// Logisim project 多周期MIPS处理器（微程序控制器）（8条指令）.circ as structural Verilog: 6 circuits, main circuit 多周期MIPS处理器（微程序控制器）数据通路
module \多周期MIPS处理器_微程序控制器_数据通路  (
);

  wire alu_1_equal, and_1_out, and_2_out, CLK, comparator_1_eq, MemRead, MemWrite, not_1_out, or_1_out, RST,
       \微程序控制器_1_alusrca , \微程序控制器_1_beq , \微程序控制器_1_bne , \微程序控制器_1_iord , \微程序控制器_1_irwrite ,
       \微程序控制器_1_memtoreg , \微程序控制器_1_pcsrc , \微程序控制器_1_pcwrite , \微程序控制器_1_regdst , \微程序控制器_1_regwrite ;
  wire [1:0] \微程序控制器_1_alusrcb ;
  wire [3:0] \微地址 , \微程序控制器_1_alu_op ;
  wire [4:0] multiplexer_2_out;
  wire [15:0] \总周期数 ;
  wire [31:0] A_q, alu_1_result, B_q, bit_extender_1_out, C_q, DR_q, IR_q, multiplexer_1_out,
       multiplexer_3_out, multiplexer_4_out, multiplexer_5_out, multiplexer_6_out, PC_q, ram_1_data,
       regifile_1_r1, regifile_1_r2, shifter_1_out;

  Button \u_总复位  (.out(RST));
  Register #(.width(32), .trigger("rising"), .Select("low")) PC (
    .D(multiplexer_6_out), .en(or_1_out), .Q(PC_q), .clk(CLK), .clr(RST));
  Multiplexer #(.select(1), .width(32), .disabled("Z"), .enable("false")) multiplexer_1 (
    .in0(PC_q), .in1(C_q), .out(multiplexer_1_out), .sel(\微程序控制器_1_iord ));
  Clock #(.highDuration(1), .lowDuration(1)) u_CLK (.out(CLK));
  RAM #(.addrWidth(10), .dataWidth(32), .bus("separate"), .Select("high")) ram_1 (
    .addr(multiplexer_1_out[11:2]), .din(B_q), .data(ram_1_data), .str(MemWrite), .clk(CLK), .ld(MemRead));  // open: sel, clr
  // Probe on \微地址 
  Register #(.width(32), .trigger("rising"), .Select("low")) IR (
    .D(ram_1_data), .en(\微程序控制器_1_irwrite ), .Q(IR_q), .clk(CLK));  // open: clr
  Register #(.width(32), .trigger("rising"), .Select("low")) DR (.D(ram_1_data), .Q(DR_q), .clk(CLK));  // open: en, clr
  \微程序控制器  \u_微程序控制器_1  (
    .PcWrite(\微程序控制器_1_pcwrite ), .Beq(\微程序控制器_1_beq ), .PCsrc(\微程序控制器_1_pcsrc ),
    .AluSrcB(\微程序控制器_1_alusrcb ), .AluSrcA(\微程序控制器_1_alusrca ), .RegWrite(\微程序控制器_1_regwrite ),
    .MemToReg(\微程序控制器_1_memtoreg ), .RegDst(\微程序控制器_1_regdst ), .IorD(\微程序控制器_1_iord ), .MemWrite(MemWrite),
    .MemRead(MemRead), .IrWrite(\微程序控制器_1_irwrite ), .Bne(\微程序控制器_1_bne ), .CLK(CLK), .\当前微指令地址 (\微地址 ),
    .RST(RST), .OP(IR_q[31:26]), .ALU_OP(\微程序控制器_1_alu_op ), .Func(IR_q[5:0]));
  Multiplexer #(.select(1), .width(5), .disabled("Z"), .enable("false")) multiplexer_2 (
    .in0(IR_q[20:16]), .in1(IR_q[15:11]), .out(multiplexer_2_out), .sel(\微程序控制器_1_regdst ));
  Multiplexer #(.select(1), .width(32), .disabled("Z"), .enable("false")) multiplexer_3 (
    .in0(C_q), .in1(DR_q), .out(multiplexer_3_out), .sel(\微程序控制器_1_memtoreg ));
  // Probe on \总周期数 
  assign bit_extender_1_out = {{16{IR_q[15]}}, IR_q[15:0]};  // Bit_Extender bit_extender_1
  Register #(.width(32), .trigger("rising"), .Select("low")) A (
    .D(regifile_1_r1), .Q(A_q), .clk(CLK));  // open: en, clr
  Regifile regifile_1 (
    .Din(multiplexer_3_out), .Clk(CLK), .R1(regifile_1_r1), .R2(regifile_1_r2), .WE(\微程序控制器_1_regwrite ),
    .W_num(multiplexer_2_out), .R1_num(IR_q[25:21]), .R2_num(IR_q[20:16]));
  Register #(.width(32), .trigger("rising"), .Select("low")) B (
    .D(regifile_1_r2), .Q(B_q), .clk(CLK));  // open: en, clr
  Multiplexer #(.select(1), .width(32), .disabled("Z"), .enable("false")) multiplexer_4 (
    .in0(PC_q), .in1(A_q), .out(multiplexer_4_out), .sel(\微程序控制器_1_alusrca ));
  Shifter #(.width(32), .shift("ll")) shifter_1 (.in(bit_extender_1_out), .\dist (5'b00010), .out(shifter_1_out));
  Comparator #(.width(4), .mode("twosComplement")) comparator_1 (
    .a(\微地址 ), .b(4'b1101), .eq(comparator_1_eq));  // open: gt, lt
  not not_1 (not_1_out, comparator_1_eq);
  Multiplexer #(.select(2), .width(32), .disabled("Z"), .enable("false")) multiplexer_5 (
    .in0(B_q), .in1(32'h4), .in2(bit_extender_1_out), .in3(shifter_1_out), .out(multiplexer_5_out),
    .sel(\微程序控制器_1_alusrcb ));
  Counter #(.width(16), .max('hffff), .ongoal("wrap"), .trigger("rising"), .behavior("old")) counter_1 (
    .count(not_1_out), .Q(\总周期数 ), .clk(CLK), .clr(RST));  // open: load, D, carry, preset
  ALU alu_1 (
    .X(multiplexer_4_out), .Y(multiplexer_5_out), .AluOP(\微程序控制器_1_alu_op ), .Equal(alu_1_equal),
    .Result(alu_1_result));  // open: Result_2
  and and_1 (and_1_out, \微程序控制器_1_beq , alu_1_equal);
  and and_2 (and_2_out, \微程序控制器_1_bne , ~alu_1_equal);  // AND_Gate
  Register #(.width(32), .trigger("rising"), .Select("low")) C (.D(alu_1_result), .Q(C_q), .clk(CLK));  // open: en, clr
  or or_1 (or_1_out, \微程序控制器_1_pcwrite , and_1_out, and_2_out);
  Multiplexer #(.select(1), .width(32), .disabled("Z"), .enable("false")) multiplexer_6 (
    .in0(alu_1_result), .in1(C_q), .out(multiplexer_6_out), .sel(\微程序控制器_1_pcsrc ));

  // Notes on the sheet:
  //   存储器
  //   IorD
  //   MemWrite
  //   MemRead
  //   IRWrite
  //   OP
  //   Func
  //   RegDst
  //   rs
  //   rt
  //   rd
  //   Imm16
  //   多周期 MIPS 处理器（微程序控制器）数据通路
  //   支持LW、SW、BEQ、BNE、SLT、ADDI、ADD、SYSCALL等8条指令
  //   PCWrite
  //   Beq
  //   Bne
  //   PCSrc
  //   AluOP
  //   AluSrcB
  //   AluSrcA
  //   RegWrite
  //   MemToReg
  //   AluOP
  //   Equal
  //   PCEnable
  //   PCSrc
endmodule

module \微程序控制器  (
  input  [5:0] OP,
  input  [5:0] Func,
  input  CLK,
  input  RST,
  output Bne,
  output Beq,
  output MemRead,
  output [3:0] \当前微指令地址 ,
  output MemWrite,
  output RegWrite,
  output PcWrite,
  output IrWrite,
  output RegDst,
  output MemToReg,
  output [1:0] AluSrcB,
  output AluSrcA,
  output PCsrc,
  output IorD,
  output [3:0] ALU_OP
);

  wire ADD, ADDI, BEQ_t, BNE_t, comparator_6_eq, comparator_7_eq, comparator_8_eq, comparator_9_eq,
       comparator_10_eq, LW, P, RTYPE, SLT, SW, SysCall;
  wire [1:0] ALU_Control;
  wire [3:0] multiplexer_1_out, multiplexer_2_out, rom_1_data_2, \微程序入口查找_1_s0 ;
  wire [4:4] rom_1_data;

  Comparator #(.width(6), .mode("twosComplement")) comparator_1 (.a(OP), .b(6'b100011), .eq(LW));  // open: gt, lt
  Comparator #(.width(6), .mode("twosComplement")) comparator_2 (.a(OP), .b(6'b101011), .eq(SW));  // open: gt, lt
  Comparator #(.width(6), .mode("twosComplement")) comparator_3 (.a(OP), .b(6'b000100), .eq(BEQ_t));  // open: gt, lt
  Comparator #(.width(6), .mode("twosComplement")) comparator_4 (.a(OP), .b(6'b000101), .eq(BNE_t));  // open: gt, lt
  Comparator #(.width(6), .mode("twosComplement")) comparator_5 (.a(OP), .b(6'b001000), .eq(ADDI));  // open: gt, lt
  Comparator #(.width(6), .mode("twosComplement")) comparator_6 (
    .a(OP), .b({6{1'b0}}), .eq(comparator_6_eq));  // open: gt, lt
  \微程序入口查找  \u_微程序入口查找_1  (
    .LW(LW), .S3(\微程序入口查找_1_s0 [3]), .SW(SW), .S2(\微程序入口查找_1_s0 [2]), .BEQ(BEQ_t), .S1(\微程序入口查找_1_s0 [1]),
    .BNE(BNE_t), .S0(\微程序入口查找_1_s0 [0]), .RTYPE(RTYPE), .ADDI(ADDI), .SYSCALL(SysCall));
  or or_1 (RTYPE, ADD, SLT);
  Comparator #(.width(6), .mode("twosComplement")) comparator_7 (
    .a(Func), .b(6'b100000), .eq(comparator_7_eq));  // open: gt, lt
  Comparator #(.width(6), .mode("twosComplement")) comparator_8 (
    .a(Func), .b(6'b101010), .eq(comparator_8_eq));  // open: gt, lt
  Comparator #(.width(6), .mode("twosComplement")) comparator_9 (
    .a(Func), .b(6'b001100), .eq(comparator_9_eq));  // open: gt, lt
  Multiplexer #(.select(1), .width(4), .disabled("Z"), .enable("false")) multiplexer_1 (
    .in0(rom_1_data_2), .in1(\微程序入口查找_1_s0 ), .out(multiplexer_1_out), .sel(P));
  and and_1 (ADD, comparator_7_eq, comparator_6_eq);
  and and_2 (SLT, comparator_8_eq, comparator_6_eq);
  and and_3 (SysCall, comparator_9_eq, comparator_6_eq);
  Register #(.width(4), .trigger("rising"), .Select("low")) register_1 (
    .D(multiplexer_1_out), .Q(\当前微指令地址 ), .clk(CLK), .clr(RST));  // open: en
  ROM #(.addrWidth(4), .dataWidth(22), .Select("high")) rom_1 (
    .addr(\当前微指令地址 ),
    .data({IorD, PCsrc, AluSrcA, AluSrcB, MemToReg, RegDst, IrWrite, PcWrite, RegWrite, MemWrite, MemRead, Beq, Bne, ALU_Control, P, rom_1_data[4], rom_1_data_2}));
  Comparator #(.width(6), .mode("twosComplement")) comparator_10 (
    .a(Func), .b(6'b101010), .eq(comparator_10_eq));  // open: gt, lt
  Multiplexer #(.select(1), .width(4), .disabled("Z"), .enable("false")) multiplexer_2 (
    .in0(4'b0101), .in1(4'b1100), .out(multiplexer_2_out), .sel(comparator_10_eq));
  Multiplexer #(.select(2), .width(4), .disabled("Z"), .enable("false")) multiplexer_3 (
    .in0(4'b0101), .in1(4'b0101), .in2(multiplexer_2_out), .in3(4'b0101), .out(ALU_OP), .sel(ALU_Control));

  // Notes on the sheet:
  //   指令译码信号
  //   微程序入口查找逻辑
  //       输入：OP             输出：LW、SW、BEQ、BNE、ADDI、R_TYPE、SysCall
  //   指令译码逻辑
  //   微程序入口地址
  //   输入引脚
  //   下址字段
  //   判断逻辑
  //   微程序控制器
  //   μAR
  //   控制存储器
  //   contents of rom_1 (hex, n*v repeats v):
  //   26401 60020 c0003 200404 11000 c0006 200800 180240 180140 8008a 9000 c000c 1000 d
  //   加法
  //   比较
  //   比较
  //   输出引脚                       14个控制信号、当前微指令地址
  //   输入：FUNC、ALU_Control                                    输出：ALU_OP
  //   ALU_Control= 00、01、11：     运算器做加法
  //   微指令
  //   微命令
  //   ALU控制器逻辑
  //     ALU_Control= 10：                     运算方式由Func决定 
  //   下址字段
  //   判断逻辑
endmodule

module \微程序入口查找  (
  input  LW,
  input  SW,
  input  BEQ,
  input  BNE,
  input  RTYPE,
  input  ADDI,
  input  SYSCALL,
  output S3,
  output S2,
  output S1,
  output S0
);

  or or_1 (S3, BNE, RTYPE, ADDI, SYSCALL);
  or or_2 (S2, SW, BEQ, SYSCALL);
  or or_3 (S1, LW, BEQ, ADDI);
  or or_4 (S0, SW, BEQ, RTYPE, ADDI, SYSCALL);
endmodule

module ALU (
  input  [31:0] X,
  input  [31:0] Y,
  input  [3:0] AluOP,
  output Equal,
  output [31:0] Result,
  output [31:0] Result_2
);

  wire [0:0] comparator_1_lt, comparator_2_lt;
  wire [31:0] adder_1_out, AND_out, divider_1_out, divider_1_rem, multiplier_1_cout, multiplier_1_out,
       NOR_out, OR_out, shifter_1_out, shifter_2_out, shifter_3_out, subtractor_1_out, XOR_out;

  Shifter #(.width(32), .shift("ll")) shifter_1 (.in(X), .\dist (Y[4:0]), .out(shifter_1_out));
  Shifter #(.width(32), .shift("ar")) shifter_2 (.in(X), .\dist (Y[4:0]), .out(shifter_2_out));
  Shifter #(.width(32), .shift("lr")) shifter_3 (.in(X), .\dist (Y[4:0]), .out(shifter_3_out));
  Multiplier #(.width(32)) multiplier_1 (.a(X), .b(Y), .out(multiplier_1_out), .cout(multiplier_1_cout));  // open: cin
  Divider #(.width(32)) divider_1 (.a(X), .b(Y), .out(divider_1_out), .rem(divider_1_rem));  // open: upper
  Adder #(.width(32)) adder_1 (.a(X), .b(Y), .out(adder_1_out));  // open: cin, cout
  Subtractor #(.width(32)) subtractor_1 (.a(X), .b(Y), .out(subtractor_1_out));  // open: bin, bout
  assign AND_out = X & Y;  // AND_Gate AND, 32 bits wide
  assign OR_out = X | Y;  // OR_Gate OR, 32 bits wide
  assign XOR_out = X ^ Y;  // XOR_Gate XOR, 32 bits wide
  assign NOR_out = ~(X | Y);  // NOR_Gate NOR, 32 bits wide
  Comparator #(.width(32), .mode("twosComplement")) comparator_1 (
    .a(X), .b(Y), .eq(Equal), .lt(comparator_1_lt[0]));  // open: gt
  Comparator #(.width(32), .mode("twosComplement")) comparator_2 (
    .a(X), .b(Y), .lt(comparator_2_lt[0]));  // open: gt, eq
  Multiplexer #(.select(4), .width(32), .disabled("Z"), .enable("false")) multiplexer_1 (
    .in0(shifter_1_out), .in1(shifter_2_out), .in2(shifter_3_out), .in3(multiplier_1_out),
    .in4(divider_1_out), .in5(adder_1_out), .in6(subtractor_1_out), .in7(AND_out), .in8(OR_out),
    .in9(XOR_out), .in10(NOR_out), .in11({{31{1'b0}}, comparator_1_lt[0]}),
    .in12({{31{1'b0}}, comparator_2_lt[0]}), .in13({32{1'b0}}), .in14({32{1'b0}}), .in15({32{1'b0}}),
    .out(Result), .sel(AluOP));
  Multiplexer #(.select(4), .width(32), .disabled("Z"), .enable("false")) multiplexer_2 (
    .in0({32{1'b0}}), .in1({32{1'b0}}), .in2({32{1'b0}}), .in3(multiplier_1_cout), .in4(divider_1_rem),
    .in5({32{1'b0}}), .in6({32{1'b0}}), .in7({32{1'b0}}), .in8({32{1'b0}}), .in9({32{1'b0}}),
    .in10({32{1'b0}}), .in11({32{1'b0}}), .in12({32{1'b0}}), .in13({32{1'b0}}), .in14({32{1'b0}}),
    .in15({32{1'b0}}), .out(Result_2), .sel(AluOP));

  // Other names for the same wires on the sheet: Result2[31:0] = Result_2; S[3:0] = AluOP

  // Notes on the sheet:
  //   输入引脚
  //   算术逻辑单元ALU
  //   输出引脚
endmodule

module Regifile (
  input  [31:0] Din,
  input  Clk,
  input  WE,
  input  [4:0] W_num,
  input  [4:0] R1_num,
  input  [4:0] R2_num,
  output [31:0] R1,
  output [31:0] R2
);

  // RegisterFile registerfile_1: pin names not known; wires that end beside it: Din, Clk, WE, W_num, R1_num, R2_num, R1, R2

  // Notes on the sheet:
  //   寄存器堆Regfile
endmodule

module \测试  (
  input  LW,
  input  SW,
  input  BEQ,
  input  BNE,
  input  RTYPE,
  input  ADDI,
  input  SYSCALL,
  output [3:0] \微程序入口地址 
);

  \微程序入口查找  \u_微程序入口查找_1  (
    .LW(LW), .S3(\微程序入口地址 [3]), .SW(SW), .S2(\微程序入口地址 [2]), .BEQ(BEQ), .S1(\微程序入口地址 [1]), .BNE(BNE),
    .S0(\微程序入口地址 [0]), .RTYPE(RTYPE), .ADDI(ADDI), .SYSCALL(SYSCALL));
  // Probe on \微程序入口地址 
endmodule
