// Logisim project 单总线结构MIPS处理器（硬布线控制器）（5条指令）.circ as structural Verilog: 11 circuits, main circuit 硬布线控制器
module \单总线结构MIPS处理器_硬布线控制器_数据通路  (
);

  wire Add, Add4, alu_1_equal, and_1_out, ARin, CLK, comparator_1_eq, DREin, DREout, DRin, DRout, equal,
       IR_A_out, IR_I_out, IRin, Mcal, Mex, Mif, not_1_out, PCin, PCout, PSWin, READ, RegDst, RegTgt, Rin,
       Rout, RST, Slt, T1, T2, T3, T4, Write, Xin, Zout;
  wire [4:0] registerfile_1_p4, registerfile_1_p5;
  wire [11:0] Clks, \指令数 ;
  wire [31:0] alu_1_result, AR_q, bit_extender_1_out, controlled_buffer_1_out, controlled_buffer_3_out, DR_q,
       IR, PC_q, ram_1_data, registerfile_1_p6, shifter_1_out, X_q, Z_q, \内部总线 ;

  // Probe on \指令数 
  LED #(.active("true")) led_1 (.in(Mif));
  Button u_RST (.out(RST));
  // Digital_Oscilloscope #(.nState(35), .frontlines("rising"), .showclock("true")) digital_oscilloscope_1: pin names not known; wires that end beside it: CLK, Mif, Mcal, Mex, T1, T2, T3, T4
  LED #(.active("true")) led_2 (.in(Mex));
  LED #(.active("true")) led_3 (.in(Mcal));
  Register #(.width(32), .trigger("rising"), .Select("low")) AR (.D(\内部总线 ), .en(ARin), .Q(AR_q), .clk(CLK), .clr(RST));
  Register #(.width(32), .trigger("rising"), .Select("low")) X (.D(\内部总线 ), .en(Xin), .Q(X_q), .clk(CLK), .clr(RST));
  // Probe on Clks
  LED #(.active("true")) led_4 (.in(T3));
  LED #(.active("true")) led_5 (.in(T1));
  LED #(.active("true")) led_6 (.in(T2));
  Clock #(.highDuration(1), .lowDuration(1)) u_CLK (.out(CLK));
  LED #(.active("true")) led_7 (.in(T4));
  RAM #(.addrWidth(10), .dataWidth(32), .bus("separate"), .Select("high")) ram_1 (
    .addr(AR_q[11:2]), .din(controlled_buffer_3_out), .data(ram_1_data), .str(Write), .clk(CLK), .ld(READ));  // open: sel, clr
  ALU alu_1 (
    .X(X_q), .Y(\内部总线 ), .Equal(alu_1_equal), .Result(alu_1_result), .ADD(Add), .ADD4(Add4), .SLT(Slt));  // open: SUB
  assign controlled_buffer_1_out = DRin ? \内部总线  : 32'bz;  // Controlled_Buffer controlled_buffer_1
  assign controlled_buffer_1_out = DREin ? ram_1_data : 32'bz;  // Controlled_Buffer controlled_buffer_2
  assign controlled_buffer_3_out = DREout ? DR_q : 32'bz;  // Controlled_Buffer controlled_buffer_3
  Register #(.width(32), .trigger("rising"), .Select("low")) PC (.D(\内部总线 ), .en(PCin), .Q(PC_q), .clk(CLK), .clr(RST));
  Register #(.width(32), .trigger("rising"), .Select("low")) DR (
    .D(controlled_buffer_1_out), .Q(DR_q), .clk(CLK), .clr(RST));  // open: en
  Register #(.width(1), .trigger("rising"), .Select("low")) PSW (
    .D(alu_1_equal), .en(PSWin), .Q(equal), .clk(CLK), .clr(RST));
  Register #(.width(32), .trigger("rising"), .Select("low")) Z (
    .D(alu_1_result), .Q(Z_q), .clk(CLK), .clr(RST));  // open: en
  assign \内部总线  = PCout ? PC_q : 32'bz;  // Controlled_Buffer controlled_buffer_4
  assign \内部总线  = DRout ? DR_q : 32'bz;  // Controlled_Buffer controlled_buffer_5
  assign \内部总线  = Zout ? Z_q : 32'bz;  // Controlled_Buffer controlled_buffer_6
  Register #(.width(32), .trigger("rising"), .Select("low")) u_IR (.D(\内部总线 ), .en(IRin), .Q(IR), .clk(CLK), .clr(RST));
  assign \内部总线  = IR_I_out ? bit_extender_1_out : 32'bz;  // Controlled_Buffer controlled_buffer_7
  assign \内部总线  = IR_A_out ? shifter_1_out : 32'bz;  // Controlled_Buffer controlled_buffer_8
  \硬布线控制器  \u_硬布线控制器_1  (
    .\状态节拍信号 ({T4, T3, T2, T1, Mex, Mcal, Mif}), .CLK(CLK), .IR(IR),
    .ControlBus({PCout, DRout, Zout, Rout, IR_I_out, IR_A_out, DREout, PCin, ARin, DREin, DRin, Xin, Rin, IRin, PSWin, RegTgt, RegDst, Add, Add4, Slt, READ, Write}),
    .EQUAL(equal), .RST(RST));
  // RegisterFile registerfile_1: pin names not known; wires that end beside it: \内部总线 , CLK, Rin, registerfile_1_p4, registerfile_1_p5, registerfile_1_p6
  assign bit_extender_1_out = {{16{IR[15]}}, IR[15:0]};  // Bit_Extender bit_extender_1
  assign \内部总线  = Rout ? registerfile_1_p6 : 32'bz;  // Controlled_Buffer controlled_buffer_9
  Multiplexer #(.select(1), .width(5), .disabled("Z"), .enable("false")) multiplexer_1 (
    .in0(IR[25:21]), .in1(IR[20:16]), .out(registerfile_1_p5), .sel(RegTgt));
  Multiplexer #(.select(1), .width(5), .disabled("Z"), .enable("false")) multiplexer_2 (
    .in0(IR[20:16]), .in1(IR[15:11]), .out(registerfile_1_p4), .sel(RegDst));
  Comparator #(.width(32), .mode("twosComplement")) comparator_1 (
    .a(IR), .b(32'h1000ffff), .eq(comparator_1_eq));  // open: gt, lt
  Counter #(.width(12), .max('hfff), .ongoal("wrap"), .trigger("falling"), .behavior("new")) counter_1 (
    .count(not_1_out), .Q(Clks), .clk(CLK), .clr(RST));  // open: load, D, carry, preset, down
  not not_1 (not_1_out, comparator_1_eq);
  Shifter #(.width(32), .shift("ll")) shifter_1 (.in(bit_extender_1_out), .\dist (5'b00010), .out(shifter_1_out));
  Counter #(.width(12), .max('hfff), .ongoal("wrap"), .trigger("falling"), .behavior("old")) counter_2 (
    .count(and_1_out), .Q(\指令数 ), .clk(CLK), .clr(RST));  // open: load, D, carry, preset
  and and_1 (and_1_out, not_1_out, Mif, T1);

  // Other names for the same wires on the sheet: rd[4:0] = IR[15:11]; rt[4:0] = IR[20:16]; rs[4:0] = IR[25:21];
  //   控制信号[21:0] = {PCout, DRout, Zout, Rout, IR_I_out, IR_A_out, DREout, PCin, ARin, DREin, DRin, Xin, Rin, IRin, PSWin, RegTgt, RegDst, Add, Add4, Slt, READ, Write};
  //   状态节拍信号[6:0] = {T4, T3, T2, T1, Mex, Mcal, Mif}

  // Notes on the sheet:
  //   指令数
  //   RAM
  //   外部总线
  //   时钟周期数
  //   内部总线
  //   支持LW、SW、BEQ、SLT、ADDI等5条指令
  //   单总线结构 MIPS 处理器（硬布线控制器）数据通路
  //   Immidate32
  //   BranchAddress32
endmodule

module \硬布线控制器  (
  input  CLK,
  input  [31:0] IR,
  input  EQUAL,
  input  RST,
  output [6:0] \状态节拍信号 ,
  output [21:0] ControlBus
);

  wire ADDI, BEQ, LW, not_1_out, Other;
  wire [3:0] \状态寄存器_q , \状态机_1_n0 ;
  wire [12:9] OCInput;

  Register #(.width(4), .trigger("rising"), .Select("low")) \u_状态寄存器  (
    .D(\状态机_1_n0 ), .Q(\状态寄存器_q ), .clk(not_1_out), .clr(RST));  // open: en
  not not_1 (not_1_out, CLK);
  \状态机  \u_状态机_1  (
    .LW(LW), .SW(OCInput[9]), .BEQ(BEQ), .SLT(OCInput[12]), .ADDI(ADDI), .S3(\状态寄存器_q [3]),
    .S2(\状态寄存器_q [2]), .S1(\状态寄存器_q [1]), .S0(\状态寄存器_q [0]), .N3(\状态机_1_n0 [3]), .N2(\状态机_1_n0 [2]),
    .N1(\状态机_1_n0 [1]), .N0(\状态机_1_n0 [0]));
  \输出函数  \u_输出函数_1  (
    .S3(\状态寄存器_q [3]), .S2(\状态寄存器_q [2]), .S1(\状态寄存器_q [1]), .S0(\状态寄存器_q [0]), .Mif(\状态节拍信号 [0]),
    .Mcal(\状态节拍信号 [1]), .Mex(\状态节拍信号 [2]), .T1(\状态节拍信号 [3]), .T2(\状态节拍信号 [4]), .T3(\状态节拍信号 [5]),
    .T4(\状态节拍信号 [6]));
  \指令译码器  \u_指令译码器_1  (
    .IR(IR), .LW(LW), .SW(OCInput[9]), .BEQ(BEQ), .ADDI(ADDI), .SLT(OCInput[12]), .OtherInstr(Other));
  \硬布线控制器组合逻辑单元  \u_硬布线控制器组合逻辑单元_1  (
    .SLT(OCInput[12]), .ADDI(ADDI), .LW(LW), .SW(OCInput[9]), .BEQ(BEQ), .Mif(\状态节拍信号 [0]),
    .Mcal(\状态节拍信号 [1]), .Mex(\状态节拍信号 [2]), .T1(\状态节拍信号 [3]), .T2(\状态节拍信号 [4]), .T3(\状态节拍信号 [5]),
    .T4(\状态节拍信号 [6]), .EQUAL(EQUAL), .Pcout(ControlBus[21]), .DRout(ControlBus[20]), .Zout(ControlBus[19]),
    .Rout(ControlBus[18]), .IRiout(ControlBus[17]), .IRaout(ControlBus[16]), .DREout(ControlBus[15]),
    .Pcin(ControlBus[14]), .ARin(ControlBus[13]), .DREin(ControlBus[12]), .DRin(ControlBus[11]),
    .Xin(ControlBus[10]), .Rin(ControlBus[9]), .IRin(ControlBus[8]), .PSWin(ControlBus[7]),
    .RegTgt(ControlBus[6]), .RegDst(ControlBus[5]), .Add(ControlBus[4]), .Add4(ControlBus[3]),
    .Slt_2(ControlBus[2]), .READ(ControlBus[1]), .WRITE(ControlBus[0]));

  // Other names for the same wires on the sheet: Write = ControlBus[0]; READ = ControlBus[1]; Slt_t = ControlBus[2];
  //   Add4 = ControlBus[3]; Add = ControlBus[4]; RegDst = ControlBus[5]; RegTgt = ControlBus[6];
  //   PSWin = ControlBus[7]; IRin = ControlBus[8]; Rin = ControlBus[9]; Xin = ControlBus[10]; DRin = ControlBus[11];
  //   DREin = ControlBus[12]; ARin = ControlBus[13]; PCin = ControlBus[14]; DREout = ControlBus[15];
  //   IR_A_out = ControlBus[16]; IR_I_out = ControlBus[17]; Rout = ControlBus[18]; Zout = ControlBus[19];
  //   DRout = ControlBus[20]; PCout = ControlBus[21];
  //   OCInput (some bits) = {ADDI, LW, BEQ, \状态节拍信号 [0], \状态节拍信号 [1], \状态节拍信号 [2], \状态节拍信号 [3], \状态节拍信号 [4], \状态节拍信号 [5], \状态节拍信号 [6], EQUAL};
  //   T4 = \状态节拍信号 [6]; T3 = \状态节拍信号 [5]; T2 = \状态节拍信号 [4]; T1 = \状态节拍信号 [3]; Mex = \状态节拍信号 [2]; Mcal = \状态节拍信号 [1];
  //   Mif = \状态节拍信号 [0]; SW = OCInput[9]; SLT = OCInput[12]; 指令字[31:0] = IR

  // Notes on the sheet:
  //   指令译码信号
  //   次态
  //   输入引脚
  //   现态
  //   现态
  //   次态
  //   输出引脚
  //   时序发生器
  //   硬布线控制器
  //   指令译码信号
  //   硬布线控制器组合逻辑单元
  //   指令译码
endmodule

module \指令译码器  (
  input  [31:0] IR,
  output LW,
  output SW,
  output BEQ,
  output ADDI,
  output SLT,
  output OtherInstr
);

  wire comparator_5_eq, comparator_6_eq;

  Comparator #(.width(6), .mode("twosComplement")) comparator_1 (
    .a(IR[31:26]), .b(6'b100011), .eq(LW));  // open: gt, lt
  Comparator #(.width(6), .mode("twosComplement")) comparator_2 (
    .a(IR[31:26]), .b(6'b101011), .eq(SW));  // open: gt, lt
  Comparator #(.width(6), .mode("twosComplement")) comparator_3 (
    .a(IR[31:26]), .b(6'b000100), .eq(BEQ));  // open: gt, lt
  Comparator #(.width(6), .mode("twosComplement")) comparator_4 (
    .a(IR[31:26]), .b(6'b001000), .eq(ADDI));  // open: gt, lt
  Comparator #(.width(6), .mode("twosComplement")) comparator_5 (
    .a(IR[31:26]), .b({6{1'b0}}), .eq(comparator_5_eq));  // open: gt, lt
  Comparator #(.width(6), .mode("twosComplement")) comparator_6 (
    .a(IR[5:0]), .b(6'b101010), .eq(comparator_6_eq));  // open: gt, lt
  and and_1 (SLT, comparator_6_eq, comparator_5_eq);
  nor nor_1 (OtherInstr, BEQ, SW, LW, ADDI, SLT);

  // Other names for the same wires on the sheet: FUNCT[5:0] = IR[5:0]; OP[5:0] = IR[31:26]

  // Notes on the sheet:
  //   输入引脚
  //   指令译码器（ID）
  //   输出引脚
endmodule

module \状态机  (
  input  LW,
  input  SW,
  input  BEQ,
  input  SLT,
  input  ADDI,
  input  S3,
  input  S2,
  input  S1,
  input  S0,
  output N3,
  output N2,
  output N1,
  output N0
);

  wire and_2_out, and_3_out, and_4_out, and_5_out, and_6_out, and_7_out, and_8_out, and_9_out, and_10_out,
       and_11_out, and_12_out, and_13_out, and_14_out, and_15_out, and_16_out, and_17_out, and_18_out,
       and_19_out, not_1_out, not_2_out, not_3_out, not_4_out, not_5_out, not_6_out, not_7_out, not_8_out,
       not_9_out, not_10_out, not_11_out, not_12_out, not_13_out, not_14_out, not_15_out, not_16_out,
       not_17_out, not_18_out, not_19_out, not_20_out, not_21_out, not_22_out, not_23_out, not_24_out,
       not_25_out, not_26_out, not_27_out, not_28_out, not_29_out, not_30_out, not_31_out, not_32_out,
       not_33_out, not_34_out, not_35_out, not_36_out, not_37_out, not_38_out, not_39_out, not_40_out,
       not_41_out, not_42_out, not_43_out, not_44_out;

  not not_1 (not_1_out, S3);
  not not_2 (not_2_out, S3);
  not not_3 (not_3_out, S2);
  not not_4 (not_4_out, S3);
  not not_5 (not_5_out, S2);
  not not_6 (not_6_out, S3);
  not not_7 (not_7_out, S2);
  not not_8 (not_8_out, S3);
  not not_9 (not_9_out, S2);
  not not_10 (not_10_out, S3);
  not not_11 (not_11_out, S2);
  not not_12 (not_12_out, S3);
  not not_13 (not_13_out, S1);
  not not_14 (not_14_out, S0);
  not not_15 (not_15_out, S3);
  not not_16 (not_16_out, S1);
  not not_17 (not_17_out, S3);
  not not_18 (not_18_out, S0);
  not not_19 (not_19_out, S3);
  not not_20 (not_20_out, S2);
  not not_21 (not_21_out, S1);
  not not_22 (not_22_out, S3);
  not not_23 (not_23_out, S2);
  not not_24 (not_24_out, S0);
  not not_25 (not_25_out, S3);
  not not_26 (not_26_out, S2);
  not not_27 (not_27_out, S3);
  not not_28 (not_28_out, S2);
  not not_29 (not_29_out, S3);
  not not_30 (not_30_out, S1);
  not not_31 (not_31_out, S3);
  not not_32 (not_32_out, S0);
  not not_33 (not_33_out, S3);
  not not_34 (not_34_out, S2);
  not not_35 (not_35_out, S1);
  not not_36 (not_36_out, S0);
  not not_37 (not_37_out, S3);
  not not_38 (not_38_out, S2);
  not not_39 (not_39_out, S0);
  not not_40 (not_40_out, S3);
  not not_41 (not_41_out, S1);
  not not_42 (not_42_out, S0);
  not not_43 (not_43_out, S3);
  not not_44 (not_44_out, S0);
  and and_1 (N3, not_1_out, S2, S1, S0);
  and and_2 (and_2_out, not_2_out, not_3_out, S1, S0, LW);
  and and_3 (and_3_out, not_4_out, not_5_out, S1, S0, SW);
  and and_4 (and_4_out, not_6_out, not_7_out, S1, S0, BEQ);
  and and_5 (and_5_out, not_8_out, not_9_out, S1, S0, SLT);
  and and_6 (and_6_out, not_10_out, not_11_out, S1, S0, ADDI);
  and and_7 (and_7_out, not_12_out, S2, not_13_out, not_14_out);
  and and_8 (and_8_out, not_15_out, S2, not_16_out, S0);
  and and_9 (and_9_out, not_17_out, S2, S1, not_18_out);
  and and_10 (and_10_out, not_19_out, not_20_out, not_21_out, S0);
  and and_11 (and_11_out, not_22_out, not_23_out, S1, not_24_out);
  and and_12 (and_12_out, not_25_out, not_26_out, S1, S0, SLT);
  and and_13 (and_13_out, not_27_out, not_28_out, S1, S0, ADDI);
  and and_14 (and_14_out, not_29_out, S2, not_30_out, S0);
  and and_15 (and_15_out, not_31_out, S2, S1, not_32_out);
  and and_16 (and_16_out, not_33_out, not_34_out, not_35_out, not_36_out);
  and and_17 (and_17_out, not_37_out, not_38_out, S1, not_39_out);
  and and_18 (and_18_out, not_40_out, S2, not_41_out, not_42_out);
  and and_19 (and_19_out, not_43_out, S2, S1, not_44_out);
  or or_1 (N2, and_2_out, and_3_out, and_4_out, and_5_out, and_6_out, and_7_out, and_8_out, and_9_out);
  or or_2 (N1, and_10_out, and_11_out, and_12_out, and_13_out, and_14_out, and_15_out);
  or or_3 (N0, and_16_out, and_17_out, and_18_out, and_19_out);

  // Notes on the sheet:
  //   状态机
endmodule

module \输出函数  (
  input  S3,
  input  S2,
  input  S1,
  input  S0,
  output Mif,
  output Mcal,
  output Mex,
  output T1,
  output T2,
  output T3,
  output T4
);

  wire and_3_out, and_4_out, and_5_out, and_6_out, and_7_out, and_8_out, and_9_out, and_10_out, and_11_out,
       and_12_out, not_1_out, not_2_out, not_3_out, not_4_out, not_5_out, not_6_out, not_7_out, not_8_out,
       not_9_out, not_10_out, not_11_out, not_12_out, not_13_out, not_14_out, not_15_out, not_16_out,
       not_17_out, not_18_out, not_19_out, not_20_out, not_21_out, not_22_out, not_23_out, not_24_out,
       not_25_out, not_26_out, not_27_out, not_28_out;

  not not_1 (not_1_out, S3);
  and and_1 (Mif, not_1_out, not_2_out);
  not not_2 (not_2_out, S2);
  not not_3 (not_3_out, S3);
  and and_2 (Mcal, not_3_out, S2, not_4_out);
  not not_4 (not_4_out, S1);
  not not_5 (not_5_out, S3);
  not not_6 (not_6_out, S2);
  not not_7 (not_7_out, S1);
  not not_8 (not_8_out, S0);
  not not_9 (not_9_out, S3);
  not not_10 (not_10_out, S1);
  not not_11 (not_11_out, S0);
  not not_12 (not_12_out, S3);
  not not_13 (not_13_out, S0);
  not not_14 (not_14_out, S2);
  not not_15 (not_15_out, S1);
  not not_16 (not_16_out, S3);
  not not_17 (not_17_out, S1);
  not not_18 (not_18_out, S3);
  not not_19 (not_19_out, S2);
  not not_20 (not_20_out, S0);
  not not_21 (not_21_out, S3);
  not not_22 (not_22_out, S2);
  not not_23 (not_23_out, S0);
  not not_24 (not_24_out, S2);
  not not_25 (not_25_out, S1);
  not not_26 (not_26_out, S0);
  not not_27 (not_27_out, S3);
  not not_28 (not_28_out, S2);
  and and_3 (and_3_out, not_5_out, S2, S1);
  or or_1 (Mex, and_3_out, and_4_out);
  and and_4 (and_4_out, S3, not_6_out, not_7_out, not_8_out);
  and and_5 (and_5_out, not_9_out, not_10_out, not_11_out);
  and and_6 (and_6_out, not_12_out, S2, not_13_out);
  or or_2 (T1, and_5_out, and_6_out, and_7_out);
  and and_7 (and_7_out, S3, not_14_out, not_15_out, S0);
  and and_8 (and_8_out, not_16_out, not_17_out, S0);
  or or_3 (T2, and_8_out, and_9_out, and_10_out);
  and and_9 (and_9_out, not_18_out, S2, S0);
  and and_10 (and_10_out, S3, not_19_out, S1, not_20_out);
  and and_11 (and_11_out, not_21_out, not_22_out, S1, not_23_out);
  or or_4 (T3, and_11_out, and_12_out);
  and and_12 (and_12_out, S3, not_24_out, not_25_out, not_26_out);
  and and_13 (T4, not_27_out, not_28_out, S1, S0);

  // Notes on the sheet:
  //   输出函数
endmodule

module \硬布线控制器组合逻辑单元  (
  input  SLT,
  input  ADDI,
  input  LW,
  input  SW,
  input  BEQ,
  input  Mif,
  input  Mcal,
  input  Mex,
  input  T1,
  input  T2,
  input  T3,
  input  T4,
  input  EQUAL,
  output Pcout,
  output DRout,
  output Zout,
  output Rout,
  output IRiout,
  output IRaout,
  output DREout,
  output Pcin,
  output ARin,
  output DREin,
  output DRin,
  output Xin,
  output Rin,
  output IRin,
  output PSWin,
  output RegTgt,
  output RegDst,
  output Add,
  output Add4,
  output Slt_2,
  output READ,
  output WRITE
);

  wire and_1_out, and_2_out, and_3_out, and_4_out, and_5_out, and_6_out, and_7_out, and_8_out, and_9_out,
       and_10_out, and_11_out, and_12_out, and_13_out, and_14_out, and_15_out, and_16_out, and_17_out,
       and_18_out, and_19_out, and_20_out, and_21_out, and_24_out, and_25_out, and_26_out, and_27_out,
       and_28_out, and_29_out, and_30_out, and_32_out, and_33_out, and_34_out, and_35_out, and_36_out,
       and_37_out, and_38_out, and_39_out, and_40_out, and_41_out, and_44_out, and_45_out, and_46_out,
       and_48_out, and_49_out, and_50_out, and_51_out, and_54_out, and_55_out;

  and and_1 (and_1_out, Mif, T1);
  and and_2 (and_2_out, BEQ, Mex, T1);
  and and_3 (and_3_out, Mif, T4);
  and and_4 (and_4_out, LW, Mex, T3);
  and and_5 (and_5_out, Mif, T3);
  and and_6 (and_6_out, BEQ, Mex, T3, EQUAL);
  and and_7 (and_7_out, SW, Mex, T1);
  and and_8 (and_8_out, LW, Mex, T1);
  and and_9 (and_9_out, ADDI, Mex, T3);
  and and_10 (and_10_out, SLT, Mex, T3);
  and and_11 (and_11_out, BEQ, Mcal, T2);
  and and_12 (and_12_out, BEQ, Mcal, T1);
  and and_13 (and_13_out, SW, Mex, T2);
  and and_14 (and_14_out, SW, Mcal, T1);
  and and_15 (and_15_out, LW, Mcal, T1);
  and and_16 (and_16_out, ADDI, Mex, T1);
  and and_17 (and_17_out, SLT, Mex, T2);
  and and_18 (and_18_out, SLT, Mex, T1);
  and and_19 (and_19_out, SW, Mcal, T2);
  and and_20 (and_20_out, LW, Mcal, T2);
  and and_21 (and_21_out, ADDI, Mex, T2);
  and and_22 (IRaout, BEQ, Mex, T2);
  and and_23 (DREout, SW, Mex, T3);
  and and_24 (and_24_out, Mif, T3);
  and and_25 (and_25_out, BEQ, Mex, T3, EQUAL);
  and and_26 (and_26_out, Mif, T1);
  and and_27 (and_27_out, SW, Mex, T1);
  and and_28 (and_28_out, LW, Mex, T1);
  and and_29 (and_29_out, Mif, T3);
  and and_30 (and_30_out, LW, Mex, T2);
  and and_31 (DRin, SW, Mex, T2);
  and and_32 (and_32_out, Mif, T1);
  and and_33 (and_33_out, Mcal, T1, LW);
  and and_34 (and_34_out, Mcal, T1, SW);
  and and_35 (and_35_out, Mcal, T1, BEQ);
  and and_36 (and_36_out, Mex, T1, BEQ);
  and and_37 (and_37_out, Mex, T1, SLT);
  and and_38 (and_38_out, Mex, T1, ADDI);
  and and_39 (and_39_out, LW, Mex, T3);
  and and_40 (and_40_out, ADDI, Mex, T3);
  and and_41 (and_41_out, SLT, Mex, T3);
  and and_42 (IRin, Mif, T4);
  and and_43 (PSWin, BEQ, Mcal, T2);
  and and_44 (and_44_out, BEQ, Mcal, T2);
  and and_45 (and_45_out, SW, Mex, T2);
  and and_46 (and_46_out, SLT, Mex, T2);
  and and_47 (RegDst, SLT, Mex, T3);
  and and_48 (and_48_out, BEQ, Mex, T2);
  and and_49 (and_49_out, SW, Mcal, T2);
  and and_50 (and_50_out, LW, Mcal, T2);
  and and_51 (and_51_out, ADDI, Mex, T2);
  and and_52 (Add4, Mif, T2);
  and and_53 (Slt_2, SLT, Mex, T2);
  and and_54 (and_54_out, Mif, T3);
  and and_55 (and_55_out, LW, Mex, T2);
  and and_56 (WRITE, SW, Mex, T3);
  or or_1 (Pcout, and_1_out, and_2_out);
  or or_2 (DRout, and_3_out, and_4_out);
  or or_3 (Zout, and_5_out, and_6_out, and_7_out, and_8_out, and_9_out, and_10_out);
  or or_4 (Rout, and_11_out, and_12_out, and_13_out, and_14_out, and_15_out, and_16_out, and_17_out, and_18_out);
  or or_5 (IRiout, and_19_out, and_20_out, and_21_out);
  or or_6 (Pcin, and_24_out, and_25_out);
  or or_7 (ARin, and_26_out, and_27_out, and_28_out);
  or or_8 (DREin, and_29_out, and_30_out);
  or or_9 (Xin, and_32_out, and_33_out, and_34_out, and_35_out, and_36_out, and_37_out, and_38_out);
  or or_10 (Rin, and_39_out, and_40_out, and_41_out);
  or or_11 (RegTgt, and_44_out, and_45_out, and_46_out);
  or or_12 (Add, and_48_out, and_49_out, and_50_out, and_51_out);
  or or_13 (READ, and_54_out, and_55_out);

  // Notes on the sheet:
  //   硬布线控制器组合逻辑单元
endmodule

module ALU (
  input  ADD,
  input  ADD4,
  input  [31:0] X,
  input  [31:0] Y,
  input  SUB,
  input  SLT,
  output Equal,
  output [31:0] Result
);

  wire [0:0] comparator_1_lt;
  wire [1:0] priority_encoder_1_out;
  wire [31:0] adder_1_out, adder_2_out, subtractor_1_out;

  Pull_Resistor #(.pull(0)) pull_resistor_1 (.node(Y));
  Adder #(.width(32)) adder_1 (.a(X), .b(Y), .out(adder_1_out));  // open: cin, cout
  Adder #(.width(32)) adder_2 (.a(X), .b(32'h4), .out(adder_2_out));  // open: cin, cout
  Subtractor #(.width(32)) subtractor_1 (.a(X), .b(Y), .out(subtractor_1_out));  // open: bin, bout
  Comparator #(.width(32), .mode("twosComplement")) comparator_1 (
    .a(X), .b(Y), .eq(Equal), .lt(comparator_1_lt[0]));  // open: gt
  Priority_Encoder #(.select(2), .disabled("Z")) priority_encoder_1 (
    .in0(ADD), .in1(ADD4), .in2(SUB), .in3(SLT), .out(priority_encoder_1_out));  // open: gs, en_out, en_in
  Pull_Resistor #(.pull(0)) pull_resistor_2 (.node(priority_encoder_1_out));
  Multiplexer #(.select(2), .width(32), .disabled("Z"), .enable("false")) multiplexer_1 (
    .in0(adder_1_out), .in1(adder_2_out), .in2(subtractor_1_out), .in3({{31{1'b0}}, comparator_1_lt[0]}),
    .out(Result), .sel(priority_encoder_1_out));

  // Notes on the sheet:
  //   输入引脚
  //   算术逻辑单元（ALU）
  //   输出引脚
endmodule

module \测试电路  (
  input  LW,
  input  SW,
  input  BEQ,
  input  SLT,
  input  ADDI,
  input  [3:0] \现态 ,
  input  SLT_2,
  input  ADDI_2,
  input  LW_2,
  input  SW_2,
  input  BEQ_2,
  input  [3:0] \现态_2 ,
  input  EQUAL,
  output [3:0] \次态 ,
  output [3:0] out_15
);

  wire comparator_1_eq, \输出函数_1_mcal , \输出函数_1_mex , \输出函数_1_mif , \输出函数_1_t1 , \输出函数_1_t2 , \输出函数_1_t3 ,
       \输出函数_1_t4 , \输出函数_测试_1_mcal , \输出函数_测试_1_mex , \输出函数_测试_1_mif , \输出函数_测试_1_t1 , \输出函数_测试_1_t2 ,
       \输出函数_测试_1_t3 , \输出函数_测试_1_t4 ;
  wire [21:0] \硬布线控制器组合逻辑单元_1_pcout , \硬布线控制器组合逻辑单元_测试_1_pcout ;

  LED #(.active("true")) Mif (.in(\输出函数_1_mif ));
  \输出函数  \u_输出函数_1  (
    .S3(\现态_2 [3]), .S2(\现态_2 [2]), .S1(\现态_2 [1]), .S0(\现态_2 [0]), .Mif(\输出函数_1_mif ), .Mcal(\输出函数_1_mcal ),
    .Mex(\输出函数_1_mex ), .T1(\输出函数_1_t1 ), .T2(\输出函数_1_t2 ), .T3(\输出函数_1_t3 ), .T4(\输出函数_1_t4 ));
  LED #(.active("true")) Mcal (.in(\输出函数_1_mcal ));
  \输出函数_测试  \u_输出函数_测试_1  (
    .S3(\现态_2 [3]), .S2(\现态_2 [2]), .S1(\现态_2 [1]), .S0(\现态_2 [0]), .Mif(\输出函数_测试_1_mif ),
    .Mcal(\输出函数_测试_1_mcal ), .Mex(\输出函数_测试_1_mex ), .T1(\输出函数_测试_1_t1 ), .T2(\输出函数_测试_1_t2 ),
    .T3(\输出函数_测试_1_t3 ), .T4(\输出函数_测试_1_t4 ));
  LED #(.active("true")) Mif_2 (.in(\输出函数_测试_1_mif ));
  LED #(.active("true")) Mex (.in(\输出函数_1_mex ));
  LED #(.active("true")) Mcal_2 (.in(\输出函数_测试_1_mcal ));
  LED #(.active("true")) Mex_2 (.in(\输出函数_测试_1_mex ));
  \状态机  \u_状态机_1  (
    .LW(LW), .SW(SW), .BEQ(BEQ), .SLT(SLT), .ADDI(ADDI), .S3(\现态 [3]), .S2(\现态 [2]), .S1(\现态 [1]),
    .S0(\现态 [0]), .N3(\次态 [3]), .N2(\次态 [2]), .N1(\次态 [1]), .N0(\次态 [0]));
  \状态机_测试  \u_状态机_测试_1  (
    .LW(LW), .SW(SW), .BEQ(BEQ), .SLT(SLT), .ADDI(ADDI), .S3(\现态 [3]), .S2(\现态 [2]), .S1(\现态 [1]),
    .S0(\现态 [0]), .N3(out_15[3]), .N2(out_15[2]), .N1(out_15[1]), .N0(out_15[0]));
  LED #(.active("true")) T1 (.in(\输出函数_1_t1 ));
  LED #(.active("true")) T1_2 (.in(\输出函数_测试_1_t1 ));
  LED #(.active("true")) T2 (.in(\输出函数_1_t2 ));
  LED #(.active("true")) T3 (.in(\输出函数_1_t3 ));
  LED #(.active("true")) T2_2 (.in(\输出函数_测试_1_t2 ));
  LED #(.active("true")) T3_2 (.in(\输出函数_测试_1_t3 ));
  LED #(.active("true")) T4 (.in(\输出函数_1_t4 ));
  LED #(.active("true")) T4_2 (.in(\输出函数_测试_1_t4 ));
  \硬布线控制器组合逻辑单元  \u_硬布线控制器组合逻辑单元_1  (
    .SLT(SLT_2), .ADDI(ADDI_2), .LW(LW_2), .SW(SW_2), .BEQ(BEQ_2), .Mif(\输出函数_1_mif ), .Mcal(\输出函数_1_mcal ),
    .Mex(\输出函数_1_mex ), .T1(\输出函数_1_t1 ), .T2(\输出函数_1_t2 ), .T3(\输出函数_1_t3 ), .T4(\输出函数_1_t4 ),
    .EQUAL(EQUAL), .Pcout(\硬布线控制器组合逻辑单元_1_pcout [0]), .DRout(\硬布线控制器组合逻辑单元_1_pcout [1]),
    .Zout(\硬布线控制器组合逻辑单元_1_pcout [2]), .Rout(\硬布线控制器组合逻辑单元_1_pcout [3]), .IRiout(\硬布线控制器组合逻辑单元_1_pcout [4]),
    .IRaout(\硬布线控制器组合逻辑单元_1_pcout [5]), .DREout(\硬布线控制器组合逻辑单元_1_pcout [6]), .Pcin(\硬布线控制器组合逻辑单元_1_pcout [7]),
    .ARin(\硬布线控制器组合逻辑单元_1_pcout [8]), .DREin(\硬布线控制器组合逻辑单元_1_pcout [9]), .DRin(\硬布线控制器组合逻辑单元_1_pcout [10]),
    .Xin(\硬布线控制器组合逻辑单元_1_pcout [11]), .Rin(\硬布线控制器组合逻辑单元_1_pcout [12]), .IRin(\硬布线控制器组合逻辑单元_1_pcout [13]),
    .PSWin(\硬布线控制器组合逻辑单元_1_pcout [14]), .RegTgt(\硬布线控制器组合逻辑单元_1_pcout [15]),
    .RegDst(\硬布线控制器组合逻辑单元_1_pcout [16]), .Add(\硬布线控制器组合逻辑单元_1_pcout [17]), .Add4(\硬布线控制器组合逻辑单元_1_pcout [18]),
    .Slt_2(\硬布线控制器组合逻辑单元_1_pcout [19]), .READ(\硬布线控制器组合逻辑单元_1_pcout [20]), .WRITE(\硬布线控制器组合逻辑单元_1_pcout [21]));
  \硬布线控制器组合逻辑单元_测试  \u_硬布线控制器组合逻辑单元_测试_1  (
    .SLT(SLT_2), .ADDI(ADDI_2), .LW(LW_2), .SW(SW_2), .BEQ(BEQ_2), .Mif(\输出函数_测试_1_mif ),
    .Mcal(\输出函数_测试_1_mcal ), .Mex(\输出函数_测试_1_mex ), .T1(\输出函数_测试_1_t1 ), .T2(\输出函数_测试_1_t2 ),
    .T3(\输出函数_测试_1_t3 ), .T4(\输出函数_测试_1_t4 ), .EQUAL(EQUAL), .Pcout(\硬布线控制器组合逻辑单元_测试_1_pcout [0]),
    .DRout(\硬布线控制器组合逻辑单元_测试_1_pcout [1]), .Zout(\硬布线控制器组合逻辑单元_测试_1_pcout [2]),
    .Rout(\硬布线控制器组合逻辑单元_测试_1_pcout [3]), .IRiout(\硬布线控制器组合逻辑单元_测试_1_pcout [4]),
    .IRaout(\硬布线控制器组合逻辑单元_测试_1_pcout [5]), .DREout(\硬布线控制器组合逻辑单元_测试_1_pcout [6]),
    .Pcin(\硬布线控制器组合逻辑单元_测试_1_pcout [7]), .ARin(\硬布线控制器组合逻辑单元_测试_1_pcout [8]),
    .DREin(\硬布线控制器组合逻辑单元_测试_1_pcout [9]), .DRin(\硬布线控制器组合逻辑单元_测试_1_pcout [10]),
    .Xin(\硬布线控制器组合逻辑单元_测试_1_pcout [11]), .Rin(\硬布线控制器组合逻辑单元_测试_1_pcout [12]),
    .IRin(\硬布线控制器组合逻辑单元_测试_1_pcout [13]), .PSWin(\硬布线控制器组合逻辑单元_测试_1_pcout [14]),
    .RegTgt(\硬布线控制器组合逻辑单元_测试_1_pcout [15]), .RegDst(\硬布线控制器组合逻辑单元_测试_1_pcout [16]),
    .Add(\硬布线控制器组合逻辑单元_测试_1_pcout [17]), .Add4(\硬布线控制器组合逻辑单元_测试_1_pcout [18]),
    .Slt_2(\硬布线控制器组合逻辑单元_测试_1_pcout [19]), .READ(\硬布线控制器组合逻辑单元_测试_1_pcout [20]),
    .WRITE(\硬布线控制器组合逻辑单元_测试_1_pcout [21]));
  // Probe on \硬布线控制器组合逻辑单元_1_pcout 
  // Probe on \硬布线控制器组合逻辑单元_测试_1_pcout 
  LED #(.active("true")) led_1 (.in(comparator_1_eq));
  Comparator #(.width(22), .mode("unsigned")) comparator_1 (
    .a(\硬布线控制器组合逻辑单元_1_pcout ), .b(\硬布线控制器组合逻辑单元_测试_1_pcout ), .eq(comparator_1_eq));  // open: gt, lt
endmodule

module \状态机_测试  (
  input  LW,
  input  SW,
  input  BEQ,
  input  SLT,
  input  ADDI,
  input  S3,
  input  S2,
  input  S1,
  input  S0,
  output N3,
  output N2,
  output N1,
  output N0
);
endmodule

module \输出函数_测试  (
  input  S3,
  input  S2,
  input  S1,
  input  S0,
  output Mif,
  output Mcal,
  output Mex,
  output T1,
  output T2,
  output T3,
  output T4
);
endmodule

module \硬布线控制器组合逻辑单元_测试  (
  input  SLT,
  input  ADDI,
  input  LW,
  input  SW,
  input  BEQ,
  input  Mif,
  input  Mcal,
  input  Mex,
  input  T1,
  input  T2,
  input  T3,
  input  T4,
  input  EQUAL,
  output Pcout,
  output DRout,
  output Zout,
  output Rout,
  output IRiout,
  output IRaout,
  output DREout,
  output Pcin,
  output ARin,
  output DREin,
  output DRin,
  output Xin,
  output Rin,
  output IRin,
  output PSWin,
  output RegTgt,
  output RegDst,
  output Add,
  output Add4,
  output Slt_2,
  output READ,
  output WRITE
);
endmodule
