// Logisim project 单周期RISC-V处理器（硬布线控制器）（9条指令）.circ as structural Verilog: 12 circuits, main circuit 立即数扩展部件Ext
module \单周期RISC_V处理器_硬布线控制器_数据通路  (
);

  wire ALUASrc, and_1_out, Branch, Clk, Jump, MemtoReg, MemWr, or_1_out, RegWr, Rst, Zero;
  wire [1:0] ALUBSrc;
  wire [2:0] ExtOp, funct3;
  wire [3:0] ALUctr;
  wire [6:0] funct7;
  wire [11:0] PC_q_2;
  wire [24:0] Instr;
  wire [31:0] adder_1_out, busW, imm, multiplexer_1_out, multiplexer_2_out, multiplexer_3_out, PC_q,
       \寄存器堆regs_1_reg1out , \寄存器堆regs_1_reg2out , \数据存储器_data , \运算器alu_1_result ;

  Button \u_复位  (.out(Rst));
  Clock #(.highDuration(1), .lowDuration(1)) u_CLK (.out(Clk));
  \立即数扩展部件Ext  \u_立即数扩展部件ext_1  (.ExtOp(ExtOp), .Instr({funct7, Instr[24:15], funct3, Instr[11:0]}), .imm(imm));
  ROM #(.addrWidth(12), .dataWidth(32), .Select("low")) \u_指令存储器  (
    .addr(PC_q_2), .data({funct7, Instr[24:15], funct3, Instr[11:0]}), .sel(1'b0));
  Register #(.width(32), .trigger("rising"), .Select("low")) PC (
    .D(adder_1_out), .en(1'b1), .Q({PC_q[31:14], PC_q_2, PC_q[1:0]}), .clk(Clk), .clr(Rst), .cs(1'b0),
    .preset(1'b0));
  \寄存器堆Regs  \u_寄存器堆regs_1  (
    .R1_num(Instr[19:15]), .R2_num(Instr[24:20]), .Din(busW), .Write_Reg_num(Instr[11:7]),
    .Write_Enable(RegWr), .Clock(Clk), .Reg1Out(\寄存器堆regs_1_reg1out ), .Reg2Out(\寄存器堆regs_1_reg2out ));
  Multiplexer #(.select(1), .width(32), .disabled("Z"), .enable("false")) multiplexer_1 (
    .in0(32'h4), .in1(imm), .out(multiplexer_1_out), .sel(or_1_out));
  or or_1 (or_1_out, Jump, and_1_out);
  and and_1 (and_1_out, Branch, Zero);
  Multiplexer #(.select(1), .width(32), .disabled("Z"), .enable("false")) multiplexer_2 (
    .in0(\寄存器堆regs_1_reg1out ), .in1({PC_q[31:14], PC_q_2, PC_q[1:0]}), .out(multiplexer_2_out), .sel(ALUASrc));
  Multiplexer #(.select(2), .width(32), .disabled("Z"), .enable("false")) multiplexer_3 (
    .in0(\寄存器堆regs_1_reg2out ), .in1(32'h4), .in2(imm), .out(multiplexer_3_out), .sel(ALUBSrc));  // open: in3
  Adder #(.width(32)) adder_1 (
    .a({PC_q[31:14], PC_q_2, PC_q[1:0]}), .b(multiplexer_1_out), .out(adder_1_out), .cin(1'b0));  // open: cout
  \运算器ALU  \u_运算器alu_1  (
    .Zero(Zero), .Result(\运算器alu_1_result ), .A(multiplexer_2_out), .B(multiplexer_3_out), .ALUctr(ALUctr));
  \控制电路  \u_控制电路_1  (
    .funct3(funct3), .op(Instr[6:0]), .Branch(Branch), .Jump(Jump), .ALUASrc(ALUASrc), .ALUBSrc(ALUBSrc),
    .ALUctr(ALUctr), .MemtoReg(MemtoReg), .RegWr(RegWr), .MemWr(MemWr), .ExtOp(ExtOp));
  Multiplexer #(.select(1), .width(32), .disabled("Z"), .enable("false")) multiplexer_4 (
    .in0(\运算器alu_1_result ), .in1(\数据存储器_data ), .out(busW), .sel(MemtoReg));
  RAM #(.addrWidth(24), .dataWidth(32), .bus("separate"), .Select("low")) \u_数据存储器  (
    .addr(\运算器alu_1_result [25:2]), .din(\寄存器堆regs_1_reg2out ), .data(\数据存储器_data ), .str(MemWr), .sel(1'b0),
    .clk(Clk), .ld(1'b1), .clr(1'b0));

  // Other names for the same wires on the sheet: op[6:0] = Instr[6:0]; Rd[4:0] = Instr[11:7];
  //   Instr (some bits) = {funct7, funct3}; Rs1[4:0] = Instr[19:15]; Rs2[4:0] = Instr[24:20]

  // Notes on the sheet:
  //   contents of 指令存储器 (hex, n*v repeats v):
  //   a06693 106793 106613 6713 f70733 d78663 c787b3 ff5ff06f e02023 6f
  //   支持add、slt、sltu、ori、lw、lui、sw、beq、jal等9条指令
  //   单周期RISC-V处理器（硬布线控制器）数据通路
endmodule

module \控制电路  (
  input  [2:0] funct3,
  input  [6:0] op,
  output Branch,
  output Jump,
  output ALUASrc,
  output [1:0] ALUBSrc,
  output [3:0] ALUctr,
  output MemtoReg,
  output RegWr,
  output MemWr,
  output [2:0] ExtOp
);

  wire and_1_out, and_2_out, and_3_out, and_4_out, and_5_out, and_6_out, and_7_out, and_8_out, and_9_out,
       and_10_out, and_12_out, and_13_out, and_14_out, and_15_out, and_16_out;

  and and_1 (and_1_out, ~funct3[2], ~funct3[1], ~funct3[0]);  // AND_Gate
  and and_2 (and_2_out, ~funct3[2], funct3[1], ~funct3[0]);  // AND_Gate
  and and_3 (and_3_out, ~funct3[2], funct3[1], funct3[0]);  // AND_Gate
  and and_4 (and_4_out, funct3[2], funct3[1], ~funct3[0]);  // AND_Gate
  and and_5 (and_5_out, ~op[6], op[5], op[4], ~op[3], ~op[2], op[1], op[0]);  // AND_Gate
  and and_6 (and_6_out, ~op[6], ~op[5], op[4], ~op[3], ~op[2], op[1], op[0]);  // AND_Gate
  and and_7 (and_7_out, ~op[6], op[5], op[4], ~op[3], op[2], op[1], op[0]);  // AND_Gate
  and and_8 (and_8_out, ~op[6], ~op[5], ~op[4], ~op[3], ~op[2], op[1], op[0]);  // AND_Gate
  and and_9 (and_9_out, ~op[6], op[5], ~op[4], ~op[3], ~op[2], op[1], op[0]);  // AND_Gate
  and and_10 (and_10_out, op[6], op[5], ~op[4], ~op[3], ~op[2], op[1], op[0]);  // AND_Gate
  and and_11 (ALUBSrc[0], op[6], op[5], ~op[4], op[3], op[2], op[1], op[0]);  // AND_Gate
  and and_12 (and_12_out, ~op[6], ~op[5], op[4], ~op[3], op[2], op[1], op[0]);  // AND_Gate
  and and_13 (and_13_out, and_1_out, and_5_out);
  and and_14 (and_14_out, and_2_out, and_5_out);
  and and_15 (and_15_out, and_3_out, and_5_out);
  and and_16 (and_16_out, and_4_out, and_6_out);
  and and_17 (MemtoReg, and_2_out, and_8_out);
  and and_18 (MemWr, and_2_out, and_9_out);
  and and_19 (Branch, and_1_out, and_10_out);
  or or_1 (ALUASrc, ALUBSrc[0], and_12_out);
  or or_2 (ALUBSrc[1], and_16_out, and_7_out, MemtoReg, MemWr, and_12_out);
  or or_3 (ALUctr[0], and_15_out, and_7_out);
  or or_4 (ALUctr[1], and_14_out, and_15_out, and_16_out, and_7_out);
  or or_5 (ALUctr[2], and_16_out, and_7_out);
  or or_6 (ALUctr[3], and_7_out, Branch);
  or or_7 (RegWr, and_13_out, and_14_out, and_15_out, and_16_out, and_7_out, MemtoReg, ALUBSrc[0], and_12_out);
  or or_8 (ExtOp[0], and_7_out, Branch, and_12_out);
  or or_9 (ExtOp[1], MemWr, Branch);

  assign ExtOp[2] = ALUBSrc[0];
  assign Jump = ALUBSrc[0];

  // Notes on the sheet:
  //   输入信号
  //   输出信号
  //   控制电路
endmodule

// Regs
module \寄存器堆Regs  (
  input  [4:0] R1_num,
  input  [4:0] R2_num,
  input  [31:0] Din,
  input  [4:0] Write_Reg_num,
  input  Write_Enable,
  input  Clock,
  output [31:0] Reg1Out,
  output [31:0] Reg2Out
);

  wire and_1_out, and_2_out, and_3_out, and_4_out, and_5_out, and_6_out, and_7_out, and_8_out, and_9_out,
       and_10_out, and_11_out, and_12_out, and_13_out, and_14_out, and_15_out, and_16_out, and_17_out,
       and_18_out, and_19_out, and_20_out, and_21_out, and_22_out, and_23_out, and_24_out, and_25_out,
       and_26_out, and_27_out, and_28_out, and_29_out, and_30_out, and_31_out, decoder_1_out1,
       decoder_1_out2, decoder_1_out3, decoder_1_out4, decoder_1_out5, decoder_1_out6, decoder_1_out7,
       decoder_1_out8, decoder_1_out9, decoder_1_out10, decoder_1_out11, decoder_1_out12, decoder_1_out13,
       decoder_1_out14, decoder_1_out15, decoder_1_out16, decoder_1_out17, decoder_1_out18, decoder_1_out19,
       decoder_1_out20, decoder_1_out21, decoder_1_out22, decoder_1_out23, decoder_1_out24, decoder_1_out25,
       decoder_1_out26, decoder_1_out27, decoder_1_out28, decoder_1_out29, decoder_1_out30, decoder_1_out31;
  wire [31:0] register_1_q, register_2_q, register_3_q, register_4_q, register_5_q, register_6_q,
       register_7_q, register_8_q, register_9_q, register_10_q, register_11_q, register_12_q, register_13_q,
       register_14_q, register_15_q, register_16_q, register_17_q, register_18_q, register_19_q,
       register_20_q, register_21_q, register_22_q, register_23_q, register_24_q, register_25_q,
       register_26_q, register_27_q, register_28_q, register_29_q, register_30_q, register_31_q,
       register_32_q;

  Decoder #(.select(5), .tristate("false"), .disabled("Z"), .enable("false")) decoder_1 (
    .out1(decoder_1_out1), .out2(decoder_1_out2), .out3(decoder_1_out3), .out4(decoder_1_out4),
    .out5(decoder_1_out5), .out6(decoder_1_out6), .out7(decoder_1_out7), .out8(decoder_1_out8),
    .out9(decoder_1_out9), .out10(decoder_1_out10), .out11(decoder_1_out11), .out12(decoder_1_out12),
    .out13(decoder_1_out13), .out14(decoder_1_out14), .out15(decoder_1_out15), .out16(decoder_1_out16),
    .out17(decoder_1_out17), .out18(decoder_1_out18), .out19(decoder_1_out19), .out20(decoder_1_out20),
    .out21(decoder_1_out21), .out22(decoder_1_out22), .out23(decoder_1_out23), .out24(decoder_1_out24),
    .out25(decoder_1_out25), .out26(decoder_1_out26), .out27(decoder_1_out27), .out28(decoder_1_out28),
    .out29(decoder_1_out29), .out30(decoder_1_out30), .out31(decoder_1_out31), .sel(Write_Reg_num));  // open: out0
  and and_1 (and_1_out, decoder_1_out1, Write_Enable);
  and and_2 (and_2_out, decoder_1_out2, Write_Enable);
  and and_3 (and_3_out, decoder_1_out3, Write_Enable);
  and and_4 (and_4_out, decoder_1_out4, Write_Enable);
  and and_5 (and_5_out, decoder_1_out5, Write_Enable);
  and and_6 (and_6_out, decoder_1_out6, Write_Enable);
  and and_7 (and_7_out, decoder_1_out7, Write_Enable);
  and and_8 (and_8_out, decoder_1_out8, Write_Enable);
  and and_9 (and_9_out, decoder_1_out9, Write_Enable);
  and and_10 (and_10_out, decoder_1_out10, Write_Enable);
  and and_11 (and_11_out, decoder_1_out11, Write_Enable);
  and and_12 (and_12_out, decoder_1_out12, Write_Enable);
  and and_13 (and_13_out, decoder_1_out13, Write_Enable);
  and and_14 (and_14_out, decoder_1_out14, Write_Enable);
  and and_15 (and_15_out, decoder_1_out15, Write_Enable);
  and and_16 (and_16_out, decoder_1_out16, Write_Enable);
  and and_17 (and_17_out, decoder_1_out17, Write_Enable);
  and and_18 (and_18_out, decoder_1_out18, Write_Enable);
  and and_19 (and_19_out, decoder_1_out19, Write_Enable);
  and and_20 (and_20_out, decoder_1_out20, Write_Enable);
  and and_21 (and_21_out, decoder_1_out21, Write_Enable);
  and and_22 (and_22_out, decoder_1_out22, Write_Enable);
  and and_23 (and_23_out, decoder_1_out23, Write_Enable);
  and and_24 (and_24_out, decoder_1_out24, Write_Enable);
  and and_25 (and_25_out, decoder_1_out25, Write_Enable);
  and and_26 (and_26_out, decoder_1_out26, Write_Enable);
  and and_27 (and_27_out, decoder_1_out27, Write_Enable);
  and and_28 (and_28_out, decoder_1_out28, Write_Enable);
  and and_29 (and_29_out, decoder_1_out29, Write_Enable);
  and and_30 (and_30_out, decoder_1_out30, Write_Enable);
  and and_31 (and_31_out, decoder_1_out31, Write_Enable);
  Register #(.width(32), .trigger("rising"), .Select("low")) register_1 (
    .D({32{1'b0}}), .en(Write_Enable), .Q(register_1_q), .clk(Clock));  // open: clr
  Register #(.width(32), .trigger("rising"), .Select("low")) register_2 (
    .D(Din), .en(and_1_out), .Q(register_2_q), .clk(Clock));  // open: clr
  Register #(.width(32), .trigger("rising"), .Select("low")) register_3 (
    .D(Din), .en(and_2_out), .Q(register_3_q), .clk(Clock));  // open: clr
  Register #(.width(32), .trigger("rising"), .Select("low")) register_4 (
    .D(Din), .en(and_3_out), .Q(register_4_q), .clk(Clock));  // open: clr
  Register #(.width(32), .trigger("rising"), .Select("low")) register_5 (
    .D(Din), .en(and_4_out), .Q(register_5_q), .clk(Clock));  // open: clr
  Register #(.width(32), .trigger("rising"), .Select("low")) register_6 (
    .D(Din), .en(and_5_out), .Q(register_6_q), .clk(Clock));  // open: clr
  Register #(.width(32), .trigger("rising"), .Select("low")) register_7 (
    .D(Din), .en(and_6_out), .Q(register_7_q), .clk(Clock));  // open: clr
  Register #(.width(32), .trigger("rising"), .Select("low")) register_8 (
    .D(Din), .en(and_7_out), .Q(register_8_q), .clk(Clock));  // open: clr
  Register #(.width(32), .trigger("rising"), .Select("low")) register_9 (
    .D(Din), .en(and_8_out), .Q(register_9_q), .clk(Clock));  // open: clr
  Register #(.width(32), .trigger("rising"), .Select("low")) register_10 (
    .D(Din), .en(and_9_out), .Q(register_10_q), .clk(Clock));  // open: clr
  Register #(.width(32), .trigger("rising"), .Select("low")) register_11 (
    .D(Din), .en(and_10_out), .Q(register_11_q), .clk(Clock));  // open: clr
  Register #(.width(32), .trigger("rising"), .Select("low")) register_12 (
    .D(Din), .en(and_11_out), .Q(register_12_q), .clk(Clock));  // open: clr
  Register #(.width(32), .trigger("rising"), .Select("low")) register_13 (
    .D(Din), .en(and_12_out), .Q(register_13_q), .clk(Clock));  // open: clr
  Register #(.width(32), .trigger("rising"), .Select("low")) register_14 (
    .D(Din), .en(and_13_out), .Q(register_14_q), .clk(Clock));  // open: clr
  Register #(.width(32), .trigger("rising"), .Select("low")) register_15 (
    .D(Din), .en(and_14_out), .Q(register_15_q), .clk(Clock));  // open: clr
  Register #(.width(32), .trigger("rising"), .Select("low")) register_16 (
    .D(Din), .en(and_15_out), .Q(register_16_q), .clk(Clock));  // open: clr
  Register #(.width(32), .trigger("rising"), .Select("low")) register_17 (
    .D(Din), .en(and_16_out), .Q(register_17_q), .clk(Clock));  // open: clr
  Register #(.width(32), .trigger("rising"), .Select("low")) register_18 (
    .D(Din), .en(and_17_out), .Q(register_18_q), .clk(Clock));  // open: clr
  Register #(.width(32), .trigger("rising"), .Select("low")) register_19 (
    .D(Din), .en(and_18_out), .Q(register_19_q), .clk(Clock));  // open: clr
  Register #(.width(32), .trigger("rising"), .Select("low")) register_20 (
    .D(Din), .en(and_19_out), .Q(register_20_q), .clk(Clock));  // open: clr
  Register #(.width(32), .trigger("rising"), .Select("low")) register_21 (
    .D(Din), .en(and_20_out), .Q(register_21_q), .clk(Clock));  // open: clr
  Register #(.width(32), .trigger("rising"), .Select("low")) register_22 (
    .D(Din), .en(and_21_out), .Q(register_22_q), .clk(Clock));  // open: clr
  Register #(.width(32), .trigger("rising"), .Select("low")) register_23 (
    .D(Din), .en(and_22_out), .Q(register_23_q), .clk(Clock));  // open: clr
  Register #(.width(32), .trigger("rising"), .Select("low")) register_24 (
    .D(Din), .en(and_23_out), .Q(register_24_q), .clk(Clock));  // open: clr
  Register #(.width(32), .trigger("rising"), .Select("low")) register_25 (
    .D(Din), .en(and_24_out), .Q(register_25_q), .clk(Clock));  // open: clr
  Register #(.width(32), .trigger("rising"), .Select("low")) register_26 (
    .D(Din), .en(and_25_out), .Q(register_26_q), .clk(Clock));  // open: clr
  Register #(.width(32), .trigger("rising"), .Select("low")) register_27 (
    .D(Din), .en(and_26_out), .Q(register_27_q), .clk(Clock));  // open: clr
  Register #(.width(32), .trigger("rising"), .Select("low")) register_28 (
    .D(Din), .en(and_27_out), .Q(register_28_q), .clk(Clock));  // open: clr
  Register #(.width(32), .trigger("rising"), .Select("low")) register_29 (
    .D(Din), .en(and_28_out), .Q(register_29_q), .clk(Clock));  // open: clr
  Register #(.width(32), .trigger("rising"), .Select("low")) register_30 (
    .D(Din), .en(and_29_out), .Q(register_30_q), .clk(Clock));  // open: clr
  Register #(.width(32), .trigger("rising"), .Select("low")) register_31 (
    .D(Din), .en(and_30_out), .Q(register_31_q), .clk(Clock));  // open: clr
  Register #(.width(32), .trigger("rising"), .Select("low")) register_32 (
    .D(Din), .en(and_31_out), .Q(register_32_q), .clk(Clock));  // open: clr
  Multiplexer #(.select(5), .width(32), .disabled("Z"), .enable("false")) multiplexer_1 (
    .in0(register_1_q), .in1(register_2_q), .in2(register_3_q), .in3(register_4_q), .in4(register_5_q),
    .in5(register_6_q), .in6(register_7_q), .in7(register_8_q), .in8(register_9_q), .in9(register_10_q),
    .in10(register_11_q), .in11(register_12_q), .in12(register_13_q), .in13(register_14_q),
    .in14(register_15_q), .in15(register_16_q), .in16(register_17_q), .in17(register_18_q),
    .in18(register_19_q), .in19(register_20_q), .in20(register_21_q), .in21(register_22_q),
    .in22(register_23_q), .in23(register_24_q), .in24(register_25_q), .in25(register_26_q),
    .in26(register_27_q), .in27(register_28_q), .in28(register_29_q), .in29(register_30_q),
    .in30(register_31_q), .in31(register_32_q), .out(Reg1Out), .sel(R1_num));
  Multiplexer #(.select(5), .width(32), .disabled("Z"), .enable("false")) multiplexer_2 (
    .in0(register_1_q), .in1(register_2_q), .in2(register_3_q), .in3(register_4_q), .in4(register_5_q),
    .in5(register_6_q), .in6(register_7_q), .in7(register_8_q), .in8(register_9_q), .in9(register_10_q),
    .in10(register_11_q), .in11(register_12_q), .in12(register_13_q), .in13(register_14_q),
    .in14(register_15_q), .in15(register_16_q), .in16(register_17_q), .in17(register_18_q),
    .in18(register_19_q), .in19(register_20_q), .in20(register_21_q), .in21(register_22_q),
    .in22(register_23_q), .in23(register_24_q), .in24(register_25_q), .in25(register_26_q),
    .in26(register_27_q), .in27(register_28_q), .in28(register_29_q), .in29(register_30_q),
    .in30(register_31_q), .in31(register_32_q), .out(Reg2Out), .sel(R2_num));

  // Other names for the same wires on the sheet: CLK = Clock; RA[4:0] = R1_num; RB[4:0] = R2_num; RDA[31:0] = Reg1Out;
  //   RDB[31:0] = Reg2Out; RW[4:0] = Write_Reg_num; WE = Write_Enable

  // Notes on the sheet:
  //   输入端口
  //   寄存器堆Regs
  //   输出端口
endmodule

// Ext
module \立即数扩展部件Ext  (
  input  [2:0] ExtOp,
  input  [31:0] Instr,
  output [31:0] imm
);

  wire [11:0] bit_extender_4_out;
  wire [19:0] bit_extender_1_out, bit_extender_2_out, bit_extender_3_out;

  assign bit_extender_1_out = {{19{Instr[31]}}, Instr[31]};  // Bit_Extender bit_extender_1
  assign bit_extender_2_out = {{19{Instr[31]}}, Instr[31]};  // Bit_Extender bit_extender_2
  assign bit_extender_3_out = {{19{Instr[31]}}, Instr[31]};  // Bit_Extender bit_extender_3
  assign bit_extender_4_out = {{11{Instr[31]}}, Instr[31]};  // Bit_Extender bit_extender_4
  Multiplexer #(.select(3), .width(32), .disabled("Z"), .enable("false")) multiplexer_1 (
    .in0({bit_extender_1_out, Instr[31:20]}), .in1({Instr[31:12], {12{1'b0}}}),
    .in2({bit_extender_2_out, Instr[31:25], Instr[11:7]}),
    .in3({bit_extender_3_out, Instr[7], Instr[30:25], Instr[11:8], 1'b0}),
    .in4({bit_extender_4_out, Instr[19:12], Instr[20], Instr[30:21], 1'b0}), .in5({32{1'b0}}),
    .in6({32{1'b0}}), .in7({32{1'b0}}), .out(imm), .sel(ExtOp));

  // Notes on the sheet:
  //   立即数扩展部件Ext
endmodule

// ALU
module \运算器ALU  (
  input  [31:0] A,
  input  [31:0] B,
  input  [3:0] ALUctr,
  output Zero,
  output [31:0] Result
);

  wire \alu控制信号生成部件_1_sigctr , \alu控制信号生成部件_1_subctr , multiplexer_2_out, \n32位加法器_1_cf , \n32位加法器_1_of ,
       \n32位加法器_1_sf , xor_2_out, xor_3_out;
  wire [2:0] \alu控制信号生成部件_1_opctr ;
  wire [31:0] bit_extender_1_out, bit_extender_2_out, \n32位加法器_1_s , or_1_out, shifter_1_out, xor_1_out;

  assign bit_extender_1_out = {{31{\alu控制信号生成部件_1_subctr }}, \alu控制信号生成部件_1_subctr };  // Bit_Extender bit_extender_1
  \_32位加法器  \u_32位加法器_1  (
    .Cin(\alu控制信号生成部件_1_subctr ), .S(\n32位加法器_1_s ), .SF(\n32位加法器_1_sf ), .ZF(Zero), .CF(\n32位加法器_1_cf ),
    .OF(\n32位加法器_1_of ), .A(A), .B(xor_1_out));
  assign xor_1_out = B ^ bit_extender_1_out;  // XOR_Gate xor_1, 32 bits wide
  assign or_1_out = A | B;  // OR_Gate or_1, 32 bits wide
  Shifter #(.width(32), .shift("ll")) shifter_1 (.in(A), .\dist (B[4:0]), .out(shifter_1_out));
  \ALU控制信号生成部件  \alu控制信号生成部件_1  (
    .SUBctr(\alu控制信号生成部件_1_subctr ), .OPctr(\alu控制信号生成部件_1_opctr ), .SIGctr(\alu控制信号生成部件_1_sigctr ),
    .ALUctr(ALUctr));
  xor xor_2 (xor_2_out, ~\n32位加法器_1_cf , \alu控制信号生成部件_1_subctr );  // XOR_Gate
  xor xor_3 (xor_3_out, \n32位加法器_1_of , \n32位加法器_1_sf );
  Multiplexer #(.select(3), .width(32), .disabled("Z"), .enable("false")) multiplexer_1 (
    .in0(\n32位加法器_1_s ), .in1(or_1_out), .in2(B), .in3(bit_extender_2_out), .in4(shifter_1_out),
    .out(Result), .sel(\alu控制信号生成部件_1_opctr ));  // open: in5, in6, in7
  assign bit_extender_2_out = {{31{1'b0}}, multiplexer_2_out};  // Bit_Extender bit_extender_2
  Multiplexer #(.select(1), .width(1), .disabled("Z"), .enable("false")) multiplexer_2 (
    .in0(xor_2_out), .in1(xor_3_out), .out(multiplexer_2_out), .sel(\alu控制信号生成部件_1_sigctr ));

  // Notes on the sheet:
  //   逻辑左移
  //   运算器ALU
  //   ALU控制信号生成部件
endmodule

module \ALU控制信号生成部件  (
  input  [3:0] ALUctr,
  output SUBctr,
  output [2:0] OPctr,
  output SIGctr
);

  wire and_2_out;

  or or_1 (SUBctr, ALUctr[3], ALUctr[1]);
  and and_1 (OPctr[2], ~ALUctr[3], ALUctr[2], ~ALUctr[1]);  // AND_Gate
  or or_2 (OPctr[1], and_2_out, ALUctr[0]);
  and and_2 (and_2_out, ~ALUctr[2], ALUctr[1]);  // AND_Gate
  and and_3 (SIGctr, ~ALUctr[3], ~ALUctr[2], ALUctr[1], ~ALUctr[0]);  // AND_Gate
  and and_4 (OPctr[0], ~ALUctr[3], ALUctr[1]);  // AND_Gate

  // Notes on the sheet:
  //   ALU控制信号生成部件
endmodule

module \_32位加法器  (
  input  Cin,
  input  [31:0] A,
  input  [31:0] B,
  output SF,
  output ZF,
  output CF,
  output OF,
  output [31:0] S
);

  wire \n16位加法器_1_c16 , \n16位加法器_2_c16 ;
  wire [15:0] \n16位加法器_1_c ;

  \_16位加法器  \u_16位加法器_1  (
    .C0(\n16位加法器_2_c16 ), .A(A[31:16]), .B(B[31:16]), .S(S[31:16]), .C(\n16位加法器_1_c ), .C16(\n16位加法器_1_c16 ));
  \_16位加法器  \u_16位加法器_2  (.C0(Cin), .A(A[15:0]), .B(B[15:0]), .S(S[15:0]), .C16(\n16位加法器_2_c16 ));  // open: C
  nor nor_1 (ZF, S[31], S[30], S[29], S[28], S[27], S[26], S[25], S[24], S[23], S[22], S[21], S[20], S[19], S[18], S[17], S[16], S[15], S[14], S[13], S[12], S[11], S[10], S[9], S[8], S[7], S[6], S[5], S[4], S[3], S[2], S[1], S[0]);
  xor xor_1 (CF, \n16位加法器_1_c16 , Cin);
  xor xor_2 (OF, \n16位加法器_1_c [15], \n16位加法器_1_c16 );

  assign SF = S[31];

  // Notes on the sheet:
  //   16位加法器
  //   16位加法器
  //   32位加法器
endmodule

module \_16位加法器  (
  input  C0,
  input  [15:0] A,
  input  [15:0] B,
  output [15:0] S,
  output C16,
  output [15:0] C
);

  wire \n4位clu_1_c1 , \n4位clu_1_c2 , \n4位clu_1_c3 , \n4位加法器_1_gg , \n4位加法器_1_pg , \n4位加法器_2_gg ,
       \n4位加法器_2_pg , \n4位加法器_3_gg , \n4位加法器_3_pg , \n4位加法器_4_gg , \n4位加法器_4_pg ;

  \_4位加法器  \u_4位加法器_1  (
    .C0(C0), .A(A[3:0]), .B(B[3:0]), .Gg(\n4位加法器_1_gg ), .Pg(\n4位加法器_1_pg ), .S(S[3:0]), .C(C[3:0]));  // open: C4
  \_4位加法器  \u_4位加法器_2  (
    .C0(\n4位clu_1_c1 ), .A(A[7:4]), .B(B[7:4]), .Gg(\n4位加法器_2_gg ), .Pg(\n4位加法器_2_pg ), .S(S[7:4]), .C(C[7:4]));  // open: C4
  \_4位加法器  \u_4位加法器_3  (
    .C0(\n4位clu_1_c2 ), .A(A[11:8]), .B(B[11:8]), .Gg(\n4位加法器_3_gg ), .Pg(\n4位加法器_3_pg ), .S(S[11:8]),
    .C(C[11:8]));  // open: C4
  \_4位加法器  \u_4位加法器_4  (
    .C0(\n4位clu_1_c3 ), .A(A[15:12]), .B(B[15:12]), .Gg(\n4位加法器_4_gg ), .Pg(\n4位加法器_4_pg ), .S(S[15:12]),
    .C(C[15:12]), .C4(C16));
  \_4位CLU  \u_4位clu_1  (
    .C1(\n4位clu_1_c1 ), .C2(\n4位clu_1_c2 ), .C3(\n4位clu_1_c3 ), .C0(C0), .P0(\n4位加法器_1_pg ),
    .G0(\n4位加法器_1_gg ), .P1(\n4位加法器_2_pg ), .G1(\n4位加法器_2_gg ), .P2(\n4位加法器_3_pg ), .G2(\n4位加法器_3_gg ),
    .P3(\n4位加法器_4_pg ), .G3(\n4位加法器_4_gg ));  // open: C4

  // Notes on the sheet:
  //   16位加法器
endmodule

module \_4位加法器  (
  input  C0,
  input  [3:0] A,
  input  [3:0] B,
  output Gg,
  output Pg,
  output [3:0] S,
  output [3:0] C,
  output C4
);

  wire and_1_out, and_2_out, and_3_out, \n1位fa_1_gi , \n1位fa_1_pi , \n1位fa_2_gi , \n1位fa_2_pi , \n1位fa_3_gi ,
       \n1位fa_3_pi , \n1位fa_4_gi , \n1位fa_4_pi ;

  \_1位FA  \u_1位fa_1  (.Ci_1(1'b0), .Pi(\n1位fa_1_pi ), .Gi(\n1位fa_1_gi ), .Ai(A[3]), .Bi(B[3]));  // open: Si
  \_1位FA  \u_1位fa_2  (.Ci_1(1'b0), .Pi(\n1位fa_2_pi ), .Gi(\n1位fa_2_gi ), .Ai(A[2]), .Bi(B[2]));  // open: Si
  \_1位FA  \u_1位fa_3  (.Ci_1(1'b0), .Pi(\n1位fa_3_pi ), .Gi(\n1位fa_3_gi ), .Ai(A[1]), .Bi(B[1]));  // open: Si
  and and_1 (and_1_out, \n1位fa_2_gi , \n1位fa_1_pi );
  and and_2 (and_2_out, \n1位fa_3_gi , \n1位fa_1_pi , \n1位fa_2_pi );
  and and_3 (and_3_out, \n1位fa_4_gi , \n1位fa_1_pi , \n1位fa_2_pi , \n1位fa_3_pi );
  and and_4 (Pg, \n1位fa_1_pi , \n1位fa_2_pi , \n1位fa_3_pi , \n1位fa_4_pi );
  \_1位FA  \u_1位fa_4  (.Ci_1(1'b0), .Pi(\n1位fa_4_pi ), .Gi(\n1位fa_4_gi ), .Ai(A[0]), .Bi(B[0]));  // open: Si
  or or_1 (Gg, \n1位fa_1_gi , and_1_out, and_2_out, and_3_out);
  \_4位CLA  \u_4位cla_1  (
    .B3(A[3]), .A3(B[3]), .B2(A[2]), .A2(B[2]), .B1(A[1]), .A1(B[1]), .B0(A[0]), .A0(B[0]), .C0(C0), .C4(C4),
    .C0_3(C), .S3(S[3]), .S2(S[2]), .S1(S[1]), .S0(S[0]));

  // Notes on the sheet:
  //   4位加法器
endmodule

module \_4位CLU  (
  input  C0,
  input  P0,
  input  G0,
  input  P1,
  input  G1,
  input  P2,
  input  G2,
  input  P3,
  input  G3,
  output C1,
  output C2,
  output C3,
  output C4
);

  wire and_1_out, and_2_out, and_3_out, and_4_out, and_5_out, and_6_out, and_7_out, and_8_out, and_9_out,
       and_10_out;

  or or_1 (C1, and_1_out, G0);
  and and_1 (and_1_out, C0, P0);
  or or_2 (C2, and_2_out, and_3_out, G1);
  and and_2 (and_2_out, C0, P0, P1);
  and and_3 (and_3_out, G0, P1);
  or or_3 (C3, and_4_out, and_5_out, and_6_out, G2);
  and and_4 (and_4_out, C0, P0, P1, P2);
  and and_5 (and_5_out, G0, P1, P2);
  and and_6 (and_6_out, G1, P2);
  and and_7 (and_7_out, C0, P0, P1, P2, P3);
  and and_8 (and_8_out, G0, P1, P2, P3);
  or or_4 (C4, and_7_out, and_8_out, and_10_out, and_9_out, G3);
  and and_9 (and_9_out, G2, P3);
  and and_10 (and_10_out, G1, P2, P3);

  // Notes on the sheet:
  //   4位先行进位电路CLU
endmodule

module \_4位CLA  (
  input  B3,
  input  A3,
  input  B2,
  input  A2,
  input  B1,
  input  A1,
  input  B0,
  input  A0,
  input  C0,
  output C4,
  output [3:0] C0_3,
  output S3,
  output S2,
  output S1,
  output S0
);

  wire and_1_out, and_2_out, and_3_out, and_4_out, nand_1_out, nand_2_out, nand_3_out, nand_4_out,
       nand_5_out, nand_6_out, nand_7_out, nand_8_out, nand_9_out, nand_10_out, nand_11_out, nand_12_out,
       nand_13_out, nand_14_out, nor_1_out, nor_2_out, nor_3_out, nor_4_out, not_1_out, not_2_out, not_3_out,
       not_4_out, not_5_out;

  nand nand_1 (nand_1_out, B3, A3);
  nor nor_1 (nor_1_out, B3, A3);
  nand nand_2 (nand_2_out, B2, A2);
  nor nor_2 (nor_2_out, B2, A2);
  nand nand_3 (nand_3_out, B1, A1);
  nor nor_3 (nor_3_out, B1, A1);
  nand nand_4 (nand_4_out, B0, A0);
  nor nor_4 (nor_4_out, B0, A0);
  not not_1 (not_1_out, C0);
  not not_2 (not_2_out, nor_1_out);
  nand nand_5 (nand_5_out, nor_2_out, nand_1_out);
  nand nand_6 (nand_6_out, nor_3_out, nand_1_out, nand_2_out);
  nand nand_7 (nand_7_out, nor_4_out, nand_1_out, nand_2_out, nand_3_out);
  nand nand_8 (nand_8_out, nand_1_out, nand_2_out, nand_3_out, nand_4_out, not_1_out);
  and and_1 (and_1_out, nand_1_out, ~nor_1_out);  // AND_Gate
  not not_3 (not_3_out, nor_2_out);
  nand nand_9 (nand_9_out, nor_3_out, nand_2_out);
  nand nand_10 (nand_10_out, nor_4_out, nand_2_out, nand_3_out);
  nand nand_11 (nand_11_out, nand_2_out, nand_3_out, nand_4_out, not_1_out);
  and and_2 (and_2_out, nand_2_out, ~nor_2_out);  // AND_Gate
  not not_4 (not_4_out, nor_3_out);
  nand nand_12 (nand_12_out, nor_4_out, nand_3_out);
  nand nand_13 (nand_13_out, nand_3_out, nand_4_out, not_1_out);
  and and_3 (and_3_out, nand_3_out, ~nor_3_out);  // AND_Gate
  not not_5 (not_5_out, nor_4_out);
  nand nand_14 (nand_14_out, nand_4_out, not_1_out);
  and and_4 (and_4_out, nand_4_out, ~nor_4_out);  // AND_Gate
  not not_6 (C0_3[0], not_1_out);
  and and_5 (C4, not_2_out, nand_5_out, nand_6_out, nand_7_out, nand_8_out);
  and and_6 (C0_3[3], not_3_out, nand_9_out, nand_10_out, nand_11_out);
  and and_7 (C0_3[2], not_4_out, nand_12_out, nand_13_out);
  and and_8 (C0_3[1], not_5_out, nand_14_out);
  xor xor_1 (S3, and_1_out, C0_3[3]);
  xor xor_2 (S2, and_2_out, C0_3[2]);
  xor xor_3 (S1, and_3_out, C0_3[1]);
  xor xor_4 (S0, and_4_out, C0_3[0]);

  // Notes on the sheet:
  //   4位快速加法器 CLA
endmodule

// FA
module \_1位FA  (
  input  Ci_1,
  input  Ai,
  input  Bi,
  output Pi,
  output Gi,
  output Si
);

  wire xor_1_out;

  or or_1 (Pi, Bi, Ai);
  xor xor_1 (xor_1_out, Ai, Bi);
  and and_1 (Gi, Bi, Ai);
  xor xor_2 (Si, Ci_1, xor_1_out);

  // Notes on the sheet:
  //   1位全加器FA
endmodule
