// Logisim project Logisim的使用.circ as structural Verilog: 55 circuits, main circuit 隧道
module \隧道  (
  input  in_1,
  input  in_2,
  output out_3
);

  and and_1 (out_3, in_1, in_2);

  // Other names for the same wires on the sheet: A = in_1; B = in_2; Y = out_3
endmodule

module \探针  (
  input  A,
  input  B,
  output Y
);

  // Probe on A
  // Probe on Y
  xor xor_1 (Y, A, B);
  // Probe on B
endmodule

module \常量  (
  output out_1
);

  and and_1 (out_1, 1'b1, 1'b0);
endmodule

module \多位情况  (
  input  [7:0] A,
  input  [7:0] B,
  output [7:0] Y
);

  assign Y = A ^ B;  // XOR_Gate xor_1, 8 bits wide
endmodule

module \拼接  (
  input  [3:0] in_1,
  input  in_2,
  input  in_3,
  input  in_4,
  input  in_5,
  input  [3:0] in_6,
  input  [3:0] in_7,
  input  [7:0] in_8,
  output out_9,
  output out_10,
  output out_11,
  output out_12,
  output [3:0] out_13,
  output [7:0] out_14,
  output [3:0] out_15,
  output [3:0] out_16
);


  assign out_9 = in_1[0];
  assign out_10 = in_1[1];
  assign out_11 = in_1[2];
  assign out_12 = in_1[3];
  assign out_13 = {in_5, in_4, in_3, in_2};
  assign out_14 = {in_7, in_6};
  assign out_15 = in_8[3:0];
  assign out_16 = in_8[7:4];
endmodule

module \点阵  (
);

  ROM_part #(.addrWidth(8), .dataWidth(8), .Select("low")) rom_1 ();  // open: addr, data
  DotMatrix #(.inputtype("row"), .matrixcols(8), .matrixrows(8), .persist(0), .dotshape("square")) dotmatrix_1 ();  // open: row0, row1, row2, row3, row4, row5, row6, row7
endmodule

module \电路封装  (
  input  A,
  input  B,
  output Y
);

  wire and_1_out, and_2_out, not_1_out, not_2_out;

  not not_1 (not_1_out, B);
  not not_2 (not_2_out, A);
  and and_1 (and_1_out, not_1_out, A);
  and and_2 (and_2_out, B, not_2_out);
  or or_1 (Y, and_1_out, and_2_out);

  // Notes on the sheet:
  //   异或门
  //   Y = A 异或 B
endmodule

module \电路封装的应用  (
  input  A,
  input  B,
  output Y
);

  \电路封装  \u_异或门  (.A(A), .B(B), .Y(Y));
endmodule

module \上拉电阻  (
  input  X,
  input  X_2,
  output Y,
  output Y_2
);

  wire pull_resistor_1_node, pull_resistor_2_node;

  Pull_Resistor #(.pull(0)) pull_resistor_1 (.node(pull_resistor_1_node));
  Pull_Resistor #(.pull(1)) pull_resistor_2 (.node(pull_resistor_2_node));
  or or_1 (Y, X, pull_resistor_1_node);
  and and_1 (Y_2, X_2, pull_resistor_2_node);
endmodule

module \时钟  (
);

  wire CLK_out;

  Clock #(.highDuration(1), .lowDuration(1)) CLK (.out(CLK_out));
  LED #(.active("true")) LED (.in(CLK_out));
endmodule

module \电源_接地  (
  input  X,
  input  X_2,
  output Y,
  output Y_2
);

  or or_1 (Y, X, 1'b0);
  and and_1 (Y_2, X_2, 1'b1);
endmodule

module \位扩展器  (
  input  [7:0] in_1,
  input  [7:0] in_2,
  output [15:0] out_3,
  output [15:0] out_4
);

  assign out_3 = {{8{1'b0}}, in_1};  // Bit_Extender bit_extender_1
  assign out_4 = {{8{in_2[7]}}, in_2};  // Bit_Extender bit_extender_2
endmodule

module \缓冲器  (
  input  X,
  output Y
);

  buf buffer_1 (Y, X);
endmodule

module \可控缓冲器_可控反相器  (
  input  X,
  input  C,
  input  X_2,
  input  C_2,
  output Y,
  output Y_2
);

  assign Y = C ? X : 1'bz;  // Controlled_Buffer controlled_buffer_1
  assign Y_2 = C_2 ? ~X_2 : 1'bz;  // Controlled_Inverter controlled_inverter_1
endmodule

module \多路选择器  (
  input  A,
  input  B,
  input  SEL,
  input  A_2,
  input  B_2,
  input  C,
  input  D,
  input  [1:0] SEL_2,
  output Y,
  output Y_2
);

  Multiplexer #(.select(1), .width(1), .disabled("Z"), .enable("false")) multiplexer_1 (
    .in0(A), .in1(B), .out(Y), .sel(SEL));
  Multiplexer #(.select(2), .width(1), .disabled("Z"), .enable("false")) multiplexer_2 (
    .in0(A_2), .in1(B_2), .in2(C), .in3(D), .out(Y_2), .sel(SEL_2));
endmodule

module \多路分配器  (
  input  X,
  input  SEL,
  input  X_2,
  input  [1:0] SEL_2,
  output Y0,
  output Y1,
  output Y0_2,
  output Y1_2,
  output Y2,
  output Y3
);

  Demultiplexer #(.select(1), .width(1), .tristate("false"), .disabled("Z"), .enable("false")) demultiplexer_1 (
    .out0(Y0), .out1(Y1), .in(X), .sel(SEL));
  Demultiplexer #(.select(2), .width(1), .tristate("false"), .disabled("Z"), .enable("false")) demultiplexer_2 (
    .out0(Y0_2), .out1(Y1_2), .out2(Y2), .out3(Y3), .in(X_2), .sel(SEL_2));
endmodule

module \解码器  (
  input  SEL,
  input  [1:0] SEL_2,
  output Y0,
  output Y1,
  output Y0_2,
  output Y1_2,
  output Y2,
  output Y3
);

  Decoder #(.select(1), .tristate("false"), .disabled("Z"), .enable("false")) decoder_1 (
    .out0(Y0), .out1(Y1), .sel(SEL));
  Decoder #(.select(2), .tristate("false"), .disabled("Z"), .enable("false")) decoder_2 (
    .out0(Y0_2), .out1(Y1_2), .out2(Y2), .out3(Y3), .sel(SEL_2));
endmodule

module \七段码解码器  (
  input  EI,
  input  [3:0] Data,
  input  LT,
  input  BI,
  input  RBI,
  input  DP,
  output [6:0] Seg
);

  // Probe on Data
  // DisplayDecoder #(.multibit("true")) displaydecoder_1: pin names not known; wires that end beside it: Data, LT, EI, BI, RBI, Seg[0], Seg[1], Seg[2], Seg[3], Seg[4], Seg[5], Seg[6]
  _7_Segment_Display #(.active("true")) u_7_segment_display_1 (
    .g(Seg[6]), .f(Seg[5]), .a(Seg[0]), .b(Seg[1]), .e(Seg[4]), .d(Seg[3]), .c(Seg[2]), .dp(DP));
  // Probe on Seg
endmodule

module \位选择器  (
  input  [7:0] X,
  input  [2:0] SEL,
  output Y
);

  BitSelector #(.width(8), .group(1)) bitselector_1 (.in(X), .out(Y), .sel(SEL));
endmodule

module \加法器  (
  input  Cin,
  input  [7:0] A,
  input  [7:0] B,
  input  Cin_2,
  input  [7:0] A_2,
  input  [7:0] B_2,
  output [7:0] Y,
  output Cout,
  output [7:0] Y_2,
  output Cout_2
);

  // Probe on A
  // Probe on B
  // Probe on A_2
  // Probe on B_2
  // Probe on Y
  Adder #(.width(8)) adder_1 (.a(A), .b(B), .out(Y), .cin(Cin), .cout(Cout));
  // Probe on Y_2
  Adder #(.width(8)) adder_2 (.a(A_2), .b(B_2), .out(Y_2), .cin(Cin_2), .cout(Cout_2));
endmodule

module \减法器  (
  input  Cin,
  input  [7:0] A,
  input  [7:0] B,
  input  Cin_2,
  input  [7:0] A_2,
  input  [7:0] B_2,
  output [7:0] Y,
  output Cout,
  output [7:0] Y_2,
  output Cout_2
);

  // Probe on A
  // Probe on B
  // Probe on A_2
  // Probe on B_2
  // Probe on Y
  Subtractor #(.width(8)) subtractor_1 (.a(A), .b(B), .out(Y), .bin(Cin), .bout(Cout));
  // Probe on Y_2
  Subtractor #(.width(8)) subtractor_2 (.a(A_2), .b(B_2), .out(Y_2), .bin(Cin_2), .bout(Cout_2));
endmodule

module \乘法器  (
  input  [7:0] C,
  input  [7:0] A,
  input  [7:0] B,
  output [7:0] Y0,
  output [15:0] Y,
  output [7:0] Y1
);

  // Probe on C
  // Probe on A
  // Probe on B
  Multiplier #(.width(8)) multiplier_1 (.a(A), .b(B), .out(Y[7:0]), .cin(C), .cout(Y[15:8]));
  // Probe on Y

  assign Y0 = Y[7:0];
  assign Y1 = Y[15:8];
endmodule

module \除法器  (
  input  [15:0] A,
  input  [7:0] B,
  output [7:0] Q,
  output [7:0] R
);

  // Probe on A
  // Probe on B
  Divider #(.width(8)) divider_1 (.a(A[7:0]), .b(B), .out(Q), .upper(A[15:8]), .rem(R));
  // Probe on Q
  // Probe on R
endmodule

module \求补器  (
  input  [7:0] X,
  input  [7:0] X_2,
  output [7:0] Y,
  output [7:0] Y_2
);

  // Probe on X
  // Probe on X_2
  // Probe on Y
  Negator #(.width(8)) negator_1 (.in(X), .out(Y));
  // Probe on Y_2
  Negator #(.width(8)) negator_2 (.in(X_2), .out(Y_2));
endmodule

module \门电路  (
  input  A,
  input  in_2,
  input  B,
  input  in_4,
  input  in_5,
  input  in_6,
  input  in_7,
  input  in_8,
  input  in_9,
  input  in_10,
  input  in_11,
  output Y,
  output out_13,
  output out_14,
  output out_15,
  output out_16,
  output out_17
);

  and and_1 (Y, A, B);
  or or_1 (out_14, in_5, in_7);
  not not_1 (out_16, in_9);
  nand nand_1 (out_13, in_2, in_4);
  nor nor_1 (out_15, in_6, in_8);
  xor xor_1 (out_17, in_10, in_11);
endmodule

module \与门  (
  input  A,
  input  B,
  output Y
);

  and and_1 (Y, A, B);
endmodule

module \或门  (
  input  A,
  input  B,
  output Y
);

  or or_1 (Y, A, B);
endmodule

module \非门  (
  input  A,
  output Y
);

  not not_1 (Y, A);
endmodule

module \与非门  (
  input  A,
  input  B,
  input  A_2,
  input  B_2,
  input  A_3,
  input  B_3,
  output Y,
  output Y_2,
  output Y_3
);

  wire not_1_out, not_2_out;

  nand nand_1 (Y, A, B);
  not not_1 (not_1_out, A_2);
  or or_1 (Y_2, not_1_out, not_2_out);
  not not_2 (not_2_out, B_2);
  or or_2 (Y_3, ~A_3, ~B_3);  // OR_Gate
endmodule

module \或非门  (
  input  A,
  input  B,
  input  A_2,
  input  B_2,
  input  A_3,
  input  B_3,
  output Y,
  output Y_2,
  output Y_3
);

  wire not_1_out, not_2_out;

  nor nor_1 (Y, A, B);
  not not_1 (not_1_out, A_2);
  not not_2 (not_2_out, B_2);
  and and_1 (Y_3, ~A_3, ~B_3);  // AND_Gate
  and and_2 (Y_2, not_1_out, not_2_out);
endmodule

module \异或门  (
  input  A,
  input  B,
  input  A_2,
  input  B_2,
  output Y,
  output Y_2
);

  wire and_1_out, and_2_out;

  xor xor_1 (Y, A, B);
  and and_1 (and_1_out, ~A_2, B_2);  // AND_Gate
  and and_2 (and_2_out, A_2, ~B_2);  // AND_Gate
  or or_1 (Y_2, and_1_out, and_2_out);
endmodule

module \异或非门  (
  input  A,
  input  B,
  input  A_2,
  input  B_2,
  output Y,
  output Y_2
);

  wire and_1_out, and_2_out;

  xnor xnor_1 (Y, A, B);
  and and_1 (and_1_out, A_2, B_2);
  and and_2 (and_2_out, ~A_2, ~B_2);  // AND_Gate
  or or_1 (Y_2, and_1_out, and_2_out);
endmodule

module \输入_输出  (
  input  in_1,
  output out_2
);
endmodule

module \比较器  (
  input  [7:0] in_1,
  input  [7:0] in_2,
  input  [7:0] in_3,
  input  [7:0] in_4,
  input  [7:0] in_5,
  input  [7:0] in_6,
  input  [7:0] in_7,
  input  [7:0] in_8,
  input  [7:0] in_9,
  input  [7:0] in_10,
  input  [7:0] in_11,
  input  [7:0] in_12,
  output out_13,
  output out_14,
  output out_15,
  output out_16,
  output out_17,
  output out_18,
  output out_19,
  output out_20,
  output out_21,
  output out_22,
  output out_23,
  output out_24,
  output out_25,
  output out_26,
  output out_27,
  output out_28,
  output out_29,
  output out_30
);

  // Probe on in_1
  // Probe on in_3
  // Probe on in_5
  // Probe on in_7
  // Probe on in_10
  // Probe on in_12
  Comparator #(.width(8), .mode("twosComplement")) comparator_1 (
    .a(in_1), .b(in_3), .gt(out_13), .eq(out_15), .lt(out_17));
  Comparator #(.width(8), .mode("twosComplement")) comparator_2 (
    .a(in_5), .b(in_7), .gt(out_19), .eq(out_21), .lt(out_23));
  Comparator #(.width(8), .mode("twosComplement")) comparator_3 (
    .a(in_10), .b(in_12), .gt(out_26), .eq(out_28), .lt(out_30));
  // Probe on in_2
  // Probe on in_4
  // Probe on in_6
  // Probe on in_8
  // Probe on in_9
  // Probe on in_11
  Comparator #(.width(8), .mode("twosComplement")) comparator_4 (
    .a(in_2), .b(in_4), .gt(out_14), .eq(out_16), .lt(out_18));
  Comparator #(.width(8), .mode("twosComplement")) comparator_5 (
    .a(in_6), .b(in_8), .gt(out_20), .eq(out_22), .lt(out_24));
  Comparator #(.width(8), .mode("twosComplement")) comparator_6 (
    .a(in_9), .b(in_11), .gt(out_25), .eq(out_27), .lt(out_29));
endmodule

module \移位器  (
  input  [7:0] X,
  input  [7:0] X_2,
  input  [2:0] S,
  input  [2:0] S_2,
  input  [7:0] X_3,
  input  [7:0] X_4,
  input  [2:0] S_3,
  input  [2:0] S_4,
  input  [7:0] X_5,
  input  [2:0] S_5,
  output [7:0] Y,
  output [7:0] Y_2,
  output [7:0] Y_3,
  output [7:0] Y_4,
  output [7:0] Y_5
);

  Shifter #(.width(8), .shift("ll")) shifter_1 (.in(X), .\dist (S), .out(Y));
  Shifter #(.width(8), .shift("lr")) shifter_2 (.in(X_3), .\dist (S_3), .out(Y_3));
  Shifter #(.width(8), .shift("ar")) shifter_3 (.in(X_5), .\dist (S_5), .out(Y_5));
  Shifter #(.width(8), .shift("rl")) shifter_4 (.in(X_2), .\dist (S_2), .out(Y_2));
  Shifter #(.width(8), .shift("rr")) shifter_5 (.in(X_4), .\dist (S_4), .out(Y_4));

  // Notes on the sheet:
  //   逻辑左移
  //   逻辑右移
  //   算术右移
  //   循环左移
  //   循环右移
endmodule

module \位加法器  (
  input  [7:0] X,
  output [3:0] Y
);

  BitAdder #(.width(8)) bitadder_1 (.in0(X), .out(Y));
endmodule

module \位发现器  (
  input  [7:0] X,
  input  [7:0] X_2,
  output [2:0] Y,
  output [2:0] Y_2,
  output S,
  output S_2
);

  BitFinder #(.width(8), .\type ("low1")) bitfinder_1 (.in(X), .index(Y), .found(S));
  BitFinder #(.width(8), .\type ("low1")) bitfinder_2 (.in(X_2), .index(Y_2), .found(S_2));
endmodule

module \D触发器  (
  input  Set,
  input  D,
  input  Clr,
  output Q,
  output nQ
);

  wire CLK_out;

  Button CLK (.out(CLK_out));
  D_Flip_Flop #(.trigger("rising"), .Pre_Clr_Positions("ABOVE_BELOW"), .NegatePresetClear("false"), .enable("false"), .NewFFLayout("true")) d_ff_1 (
    .clk(CLK_out), .D(D), .Q(Q), .Qn(nQ), .preset(Set), .reset(Clr));
endmodule

module \T触发器  (
  input  Set,
  input  T,
  input  Clr,
  output Q,
  output nQ
);

  wire CLK_out;

  Button CLK (.out(CLK_out));
  T_Flip_Flop #(.trigger("rising"), .Pre_Clr_Positions("ABOVE_BELOW"), .NegatePresetClear("false"), .enable("false"), .NewFFLayout("true")) t_ff_1 (
    .clk(CLK_out), .T(T), .Q(Q), .Qn(nQ), .preset(Set), .reset(Clr));
endmodule

module \J_K_触发器  (
  input  Set,
  input  J,
  input  K,
  input  Clr,
  output Q,
  output nQ
);

  wire CLK_out;

  Button CLK (.out(CLK_out));
  J_K_Flip_Flop #(.trigger("rising"), .Pre_Clr_Positions("ABOVE_BELOW"), .NegatePresetClear("false"), .enable("false"), .NewFFLayout("true")) j_k_ff_1 (
    .J(J), .clk(CLK_out), .K(K), .Q(Q), .Qn(nQ), .preset(Set), .reset(Clr));
endmodule

module \S_R_触发器  (
  input  Set,
  input  S,
  input  R,
  input  Clr,
  output Q,
  output nQ
);

  wire CLK_out;

  Button CLK (.out(CLK_out));
  S_R_Flip_Flop #(.trigger("rising"), .Pre_Clr_Positions("ABOVE_BELOW"), .NegatePresetClear("false"), .enable("false"), .NewFFLayout("true")) s_r_ff_1 (
    .S(S), .clk(CLK_out), .R(R), .Q(Q), .Qn(nQ), .preset(Set), .reset(Clr));
endmodule

module \寄存器  (
  input  Set,
  input  CS,
  input  [7:0] D,
  input  EN,
  input  Clr,
  output [7:0] Q
);

  wire CLK_out;

  Button CLK (.out(CLK_out));
  Register #(.width(8), .trigger("rising"), .Select("low")) register_1 (
    .D(D), .en(EN), .Q(Q), .clk(CLK_out), .clr(Clr), .cs(CS), .preset(Set));
endmodule

module \计数器  (
  input  Set,
  input  EN,
  input  Load,
  input  [7:0] D,
  input  Rever,
  input  Clr,
  output [7:0] Q
);

  wire CLK_out;

  Button CLK (.out(CLK_out));
  Counter #(.width(8), .max('hff), .ongoal("wrap"), .trigger("rising"), .behavior("new")) counter_1 (
    .load(Load), .D(D), .count(EN), .Q(Q), .clk(CLK_out), .clr(Clr), .preset(Set), .down(Rever));  // open: carry
endmodule

module \移位寄存器  (
  input  [7:0] D,
  input  Load,
  input  Shift,
  input  Input,
  input  Clr,
  output Q0,
  output [7:0] Q
);

  wire CLK_out;

  Button CLK (.out(CLK_out));
  Shift_Register #(.width(1), .length(8), .parallel("true"), .trigger("rising")) shift_register_1 (
    .shift(Shift), .in(Input), .clk(CLK_out), .out(Q0), .load(Load), .clr(Clr), .d0(D[7]), .q0(Q[7]),
    .d1(D[6]), .q1(Q[6]), .d2(D[6]), .q2(Q[5]), .d3(D[4]), .q3(Q[4]), .d4(D[3]), .q4(Q[3]), .d5(D[2]),
    .q5(Q[2]), .d6(D[1]), .q6(Q[1]), .d7(D[0]), .q7(Q[0]));

  assign D[5] = D[6];
endmodule

module \随机数发生器  (
  input  EN,
  input  Clr,
  output [7:0] Q
);

  wire CLK_out;

  Button CLK (.out(CLK_out));
  Random #(.width(8), .seed(0), .trigger("rising")) random_1 (.clk(CLK_out), .next(EN), .out(Q), .clr(Clr));
  // Probe on Q
endmodule

module RAM (
  input  [7:0] A,
  input  Sel,
  input  Load,
  input  Clr,
  input  [7:0] A_2,
  input  Sel_2,
  input  Load_2,
  input  Clr_2,
  input  [7:0] A_3,
  input  [31:0] Din,
  input  Str,
  input  Sel_3,
  input  Load_3,
  input  Clr_3,
  output [31:0] D,
  output [31:0] D_2,
  output [31:0] Dout
);

  wire CLK_2_out, CLK_out;

  Button CLK (.out(CLK_out));
  Button CLK_2 (.out(CLK_2_out));
  RAM_part #(.addrWidth(8), .dataWidth(32), .bus("combined"), .Select("low")) ram_1 (
    .addr(A), .data(D), .sel(Sel), .clk(CLK_out), .ld(Load), .clr(Clr));
  RAM_part #(.addrWidth(8), .dataWidth(32), .bus("asynch"), .Select("low")) ram_2 (
    .addr(A_2), .data(D_2), .sel(Sel_2), .ld(Load_2), .clr(Clr_2));
  RAM_part #(.addrWidth(8), .dataWidth(32), .bus("separate"), .Select("low")) ram_3 (
    .addr(A_3), .din(Din), .data(Dout), .str(Str), .sel(Sel_3), .clk(CLK_2_out), .ld(Load_3), .clr(Clr_3));
endmodule

module ROM (
  input  [7:0] A,
  input  Sel,
  output [31:0] D
);

  ROM_part #(.addrWidth(8), .dataWidth(32), .Select("low")) rom_1 (.addr(A), .data(D), .sel(Sel));

  // Notes on the sheet:
  //   contents of rom_1 (hex, n*v repeats v):
  //   11111111 22222222 33333333 44444444 55555555 66666666 77777777 88888888 99999999 aaaaaaaa bbbbbbbb
  //   cccccccc dddddddd eeeeeeee ffffffff
endmodule

module PLA_ROM (
  input  [3:0] A,
  input  Sel,
  output [3:0] D
);

  // PlaRom #(.\and (4), .outputs(4), .Contents("2*16 1*16"), .Select("low")) plarom_1: pin names not known; wires that end beside it: A, Sel, D
endmodule

module \输入_输出部件  (
  input  in_1,
  input  EN,
  input  Clr,
  input  [13:0] Fre,
  input  EN_2,
  input  [6:0] Vol,
  input  R,
  input  G,
  input  B,
  input  IN1,
  input  IN2,
  input  IN3,
  input  EN_3,
  input  Clr_2,
  input  [3:0] in_15,
  input  DP,
  input  [3:0] in_17,
  input  DP_2,
  input  [6:0] in_19,
  input  [6:0] in_20,
  input  [6:0] in_21,
  input  [6:0] in_22,
  input  [6:0] in_23,
  input  [31:0] in_24,
  input  [31:0] in_25,
  input  [31:0] in_26,
  input  [31:0] in_27,
  input  [31:0] in_28,
  input  [31:0] in_29,
  input  [31:0] in_30,
  input  [31:0] in_31,
  input  [31:0] in_32,
  input  [31:0] in_33,
  input  [31:0] in_34,
  input  [31:0] in_35,
  input  [31:0] in_36,
  input  [31:0] in_37,
  input  [31:0] in_38,
  input  [31:0] in_39,
  input  [31:0] in_40,
  input  [31:0] in_41,
  input  [31:0] in_42,
  input  [31:0] in_43,
  input  [31:0] in_44,
  input  [31:0] in_45,
  input  [31:0] in_46,
  input  [31:0] in_47,
  input  [31:0] in_48,
  input  [31:0] in_49,
  input  [31:0] in_50,
  input  [31:0] in_51,
  input  [31:0] in_52,
  input  [31:0] in_53,
  input  [31:0] in_54,
  input  [31:0] in_55,
  input  [6:0] Data,
  input  EN_4,
  input  Clr_3,
  output out_59,
  output [3:0] out_60,
  output [7:0] out_61,
  output [3:0] out_62,
  output [3:0] out_63,
  output [6:0] Data_2,
  output Avai
);

  wire CLK_2_out, CLK_3_out, CLK_out, displaydecoder_1_p2, displaydecoder_1_p3, displaydecoder_1_p4,
       displaydecoder_1_p5, displaydecoder_1_p6, displaydecoder_1_p7, displaydecoder_1_p8, \按钮_Button_out ;

  Button CLK (.out(CLK_out));
  Button \u_按钮_Button  (.out(\按钮_Button_out ));
  // DipSwitch #(.NSwitches(4)) dipswitch_1: pin names not known; wires that end beside it: out_60[0], out_60[1], out_60[2], out_60[3]
  Joystick #(.bits(4)) joystick_1 (.x(out_62), .y(out_63));
  Button CLK_2 (.out(CLK_2_out));
  Button CLK_3 (.out(CLK_3_out));
  // Probe on in_15
  // Probe on \按钮_Button_out 
  // Switch #(.width(1)) 开关_Switch: pin names not known; wires that end beside it: in_1, out_59
  Slider #(.width(8), .Direction("left_to_right"), .value('h6b)) slider_1 (.out(out_61));
  Keyboard #(.Char_bit_width(7), .buflen(32), .trigger("rising")) keyboard_1 (
    .clk(CLK_2_out), .re(EN), .clr(Clr), .avail(Avai), .data(Data_2));
  // Digital_Oscilloscope #(.nState(10), .frontlines("rising"), .showclock("true")) 数字示波器_Digital_Oscilloscope: pin names not known; wires that end beside it: CLK_3_out, IN1, IN2, IN3, EN_3, Clr_2
  TTY #(.Char_bit_width(7), .rows(8), .cols(32), .trigger("rising")) tty_1 (
    .data(Data), .clk(CLK_out), .we(EN_4), .clr(Clr_3));
  LED #(.active("true")) LED (.in(\按钮_Button_out ));
  // RGBLed #(.multibit("false")) RGB_LED: pin names not known; wires that end beside it: R, G, B
  // DisplayDecoder #(.multibit("true")) displaydecoder_1: pin names not known; wires that end beside it: in_15, displaydecoder_1_p2, displaydecoder_1_p3, displaydecoder_1_p4, displaydecoder_1_p5, displaydecoder_1_p6, displaydecoder_1_p7, displaydecoder_1_p8
  // Probe on Data_2
  // Buzzer #(.freq_measure("Hz"), .vol_width(7)) 蜂鸣器_Buzzer: pin names not known; wires that end beside it: Fre, EN_2, Vol
  Hex_Digit_Display hex_digit_display_1 (.value(in_17), .dp(DP_2));
  DotMatrix #(.inputtype("column"), .matrixcols(5), .matrixrows(7), .persist(0), .dotshape("square")) dotmatrix_1 (
    .col0(in_19), .col1(in_20), .col2(in_21), .col3(in_22), .col4(in_23));
  _7_Segment_Display #(.active("true")) u_7_segment_display_1 (
    .g(displaydecoder_1_p8), .f(displaydecoder_1_p7), .a(displaydecoder_1_p2), .b(displaydecoder_1_p3),
    .e(displaydecoder_1_p6), .d(displaydecoder_1_p5), .c(displaydecoder_1_p4), .dp(DP));
  DotMatrix #(.inputtype("column"), .matrixcols(32), .matrixrows(32), .persist(0), .dotshape("square")) dotmatrix_2 (
    .col0(in_24), .col1(in_25), .col2(in_26), .col3(in_27), .col4(in_28), .col5(in_29), .col6(in_30),
    .col7(in_31), .col8(in_32), .col9(in_33), .col10(in_34), .col11(in_35), .col12(in_36), .col13(in_37),
    .col14(in_38), .col15(in_39), .col16(in_40), .col17(in_41), .col18(in_42), .col19(in_43), .col20(in_44),
    .col21(in_45), .col22(in_46), .col23(in_47), .col24(in_48), .col25(in_49), .col26(in_50), .col27(in_51),
    .col28(in_52), .col29(in_53), .col30(in_54), .col31(in_55));

  // Notes on the sheet:
  //   DIP开关（DIP Switch）
  //   滑杆（Slider）
  //   游戏杆（Joystick）
  //   键盘（Keyboard）
  //   七段码解码器
  //   终端（TTY）
  //   十六进制数码管（Hex Digital Display）
  //   LED点阵（LED Matrix）
  //   数码管（7-Segment Display）
  //   LED点阵（LED Matrix）
endmodule

module \优先级编码器  (
  input  In0,
  input  In1,
  input  In2,
  input  In3,
  input  In4,
  input  In5,
  input  In6,
  input  In7,
  input  EN,
  output EO,
  output [2:0] O,
  output GS
);

  Priority_Encoder #(.select(3), .disabled("Z")) priority_encoder_1 (
    .in0(In0), .in1(In1), .in2(In2), .in3(In3), .in4(In4), .in5(In5), .in6(In6), .in7(In7), .out(O), .gs(GS),
    .en_out(EO), .en_in(EN));
endmodule

module \奇偶校验  (
  input  A,
  input  B,
  input  A_2,
  input  B_2,
  output Y,
  output Y_2
);

  xor odd_parity_1 (Y, A, B);
  xnor even_parity_1 (Y_2, A_2, B_2);

  // Notes on the sheet:
  //   奇校验（Odd Parity）
  //   偶校验（Even Parity）
endmodule

module \晶体管  (
  input  C,
  input  X,
  output Y
);

  Transistor #(.\type ("p"), .gate("tl"), .width(1)) transistor_1 (.in(X), .out(Y), .gate(C));
endmodule

module \传输门  (
  input  L,
  input  X,
  input  H,
  output Y
);

  // Transmission_Gate #(.gate("tl"), .width(1)) transmission_1: pin names not known; wires that end beside it: X, L, H, Y
endmodule

module \函数发生器  (
  output out_1
);

  // ProgrammableGenerator #(.nState(4), .Contents("4 3 2 1 1 2 3 4")) programmablegenerator_1: pin names not known; wires that end beside it: out_1

  // Notes on the sheet:
  //   函数发生器
endmodule

module \TTL芯片  (
  input  A,
  input  B,
  input  A_2,
  input  B_2,
  input  A_3,
  input  A_4,
  input  B_3,
  input  A_5,
  input  B_4,
  input  [3:0] A_6,
  input  LT,
  input  BI,
  input  RBI,
  input  [3:0] A_7,
  input  [3:0] B_5,
  input  A_B,
  input  A_B_2,
  input  A_B_3,
  input  A_8,
  input  B_6,
  input  C,
  input  X,
  input  Serial_Input,
  input  Clk_Inhibit,
  input  [7:0] Data,
  input  Shift_Load,
  input  [3:0] A_9,
  input  [3:0] B_7,
  input  Cin,
  input  A_10,
  input  B_8,
  output Y,
  output Y_2,
  output Y_3,
  output Y_4,
  output Y_5,
  output [6:0] Y_6,
  output A_B_4,
  output A_B_5,
  output A_B_6,
  output Y_7,
  output Y_8,
  output Q7,
  output nQ7,
  output Cout,
  output [3:0] C_2,
  output Y_9
);

  wire CLK_out;

  Button CLK (.out(CLK_out));
  // _7400 #(.VccGndPorts("false"), .ShowInternalStructure("false")) 7400_1: pin names not known; wires that end beside it: 1'b1, A, B, Y, 1'b0
  // _7402 #(.VccGndPorts("false"), .ShowInternalStructure("false")) 7402_1: pin names not known; wires that end beside it: 1'b1, A_2, B_2, Y_2, 1'b0
  // _7404 #(.VccGndPorts("false"), .ShowInternalStructure("false")) 7404_1: pin names not known; wires that end beside it: 1'b1, A_3, Y_3, 1'b0
  // _7408 #(.VccGndPorts("false"), .ShowInternalStructure("false")) 7408_1: pin names not known; wires that end beside it: 1'b1, A_4, B_3, Y_4, 1'b0
  // _7432 #(.VccGndPorts("false"), .ShowInternalStructure("false")) 7432_1: pin names not known; wires that end beside it: 1'b1, A_5, B_4, Y_5, 1'b0
  _7447 #(.VccGndPorts("false"), .ShowInternalStructure("false")) u_7447_1 (
    .pin1(A_6[1]), .pin2(A_6[2]), .pin3(LT), .pin4(BI), .pin5(RBI), .pin6(A_6[3]), .pin7(A_6[0]),
    .pin15(Y_6[6]), .pin14(Y_6[5]), .pin13(Y_6[4]), .pin12(Y_6[3]), .pin11(Y_6[2]), .pin10(Y_6[1]),
    .pin9(Y_6[0]));
  _74283 #(.VccGndPorts("false"), .ShowInternalStructure("false")) u_74283_1 (
    .pin1(C_2[1]), .pin2(B_7[1]), .pin3(A_9[1]), .pin4(C_2[0]), .pin5(A_9[0]), .pin6(B_7[0]), .pin7(Cin),
    .pin15(B_7[2]), .pin14(A_9[2]), .pin13(C_2[2]), .pin12(A_9[3]), .pin11(B_7[3]), .pin10(C_2[3]),
    .pin9(Cout));
  // _747266 #(.VccGndPorts("false"), .ShowInternalStructure("false")) 747266_1: pin names not known; wires that end beside it: 1'b1, A_10, B_8, Y_9, 1'b0
  _7485 #(.VccGndPorts("false"), .ShowInternalStructure("false")) u_7485_1 (
    .pin1(B_5[3]), .pin2(A_B), .pin3(A_B_2), .pin4(A_B_3), .pin5(A_B_6), .pin6(A_B_5), .pin7(A_B_4),
    .pin15(A_7[3]), .pin14(B_5[2]), .pin13(A_7[2]), .pin12(A_7[1]), .pin11(B_5[1]), .pin10(A_7[0]),
    .pin9(B_5[0]));
  // _7486 #(.VccGndPorts("false"), .ShowInternalStructure("false")) 7486_1: pin names not known; wires that end beside it: 1'b1, A_8, B_6, Y_7, 1'b0
  _74165 #(.VccGndPorts("false"), .ShowInternalStructure("false")) u_74165_1 (
    .pin1(Shift_Load), .pin2(CLK_out), .pin3(Data[4]), .pin4(Data[5]), .pin5(Data[6]), .pin6(Data[7]),
    .pin7(nQ7), .pin15(Clk_Inhibit), .pin14(Data[3]), .pin13(Data[2]), .pin12(Data[1]), .pin11(Data[0]),
    .pin10(Serial_Input), .pin9(Q7));
  _7_Segment_Display #(.active("true")) u_7_segment_display_1 (
    .g(Y_6[5]), .f(Y_6[6]), .a(Y_6[4]), .b(Y_6[3]), .e(Y_6[0]), .d(Y_6[1]), .c(Y_6[2]), .dp(1'b0));

  // Notes on the sheet:
  //   7段码译码器
  //   4个与非门
  //   4个或非门
  //   6个非门
  //   4个与门
  //   4个或门
  //   4位加法器
  //   4个异或非门
  //   4个异或门
  //   4个三态门
  //   比较器
  //   并-串转换移位寄存器
  //   数码管
endmodule
